# Fritzing sketch 1PupTestCircuit (saved by Fritzing 0.8.7b)
breadboards: 1

parts:
  Inverter-NeckNorth = CD4066 Quad Analog Switch [part_number=4066 package="DIP (Dual Inline) [THT]"]
  VolTone-1a = CD4066 Quad Analog Switch [part_number=4066 package="DIP (Dual Inline) [THT]"]
  VolTone-1_2c = CD4066 Quad Analog Switch [part_number=4066 package="DIP (Dual Inline) [THT]"]
  VolTone-2b = CD4066 Quad Analog Switch [part_number=4066 package="DIP (Dual Inline) [THT]"]
  VolTone-2a = CD4066 Quad Analog Switch [part_number=4066 package="DIP (Dual Inline) [THT]"]
  Inverter-NeckSouth = CD4066 Quad Analog Switch [part_number=4066 package="DIP (Dual Inline) [THT]"]
  Combinator = CD4066 Quad Analog Switch [part_number=4066 package="DIP (Dual Inline) [THT]"]
  VolTone-1b = CD4066 Quad Analog Switch [part_number=4066 package="DIP (Dual Inline) [THT]"]
  R11 = Resistor [tolerance=±5% resistance=47k package=THT]
  R12 = Resistor [tolerance=±5% resistance=47k package=THT]
  R13 = Resistor [tolerance=±5% resistance=47k package=THT]
  R14 = Resistor [tolerance=±5% resistance=47k package=THT]
  R15 = Resistor [tolerance=±5% resistance=47k package=THT]
  C1 = Ceramic Capacitor [capacitance=10nF package="100 mil [THT, multilayer]"]
  R16 = Resistor [tolerance=±5% resistance=100k package=THT]
  C2 = Ceramic Capacitor [capacitance=22nF package="100 mil [THT, multilayer]"]
  C3 = Ceramic Capacitor [capacitance=33nF package="100 mil [THT, multilayer]"]
  C4 = Ceramic Capacitor [capacitance=47nF package="100 mil [THT, multilayer]"]
  R17 = Resistor [tolerance=±5% resistance=47k package=THT]
  R18 = Resistor [tolerance=±5% resistance=47k package=THT]
  R19 = Resistor [tolerance=±5% resistance=47k package=THT]
  R20 = Resistor [tolerance=±5% resistance=47k package=THT]
  R21 = Resistor [tolerance=±5% resistance=47k package=THT]
  C5 = Ceramic Capacitor [capacitance=22nF package="100 mil [THT, multilayer]"]
  C6 = Ceramic Capacitor [capacitance=10nF package="100 mil [THT, multilayer]"]
  C7 = Ceramic Capacitor [capacitance=33nF package="100 mil [THT, multilayer]"]
  C8 = Ceramic Capacitor [capacitance=47nF package="100 mil [THT, multilayer]"]
  R22 = Resistor [tolerance=±5% resistance=100k package=THT]

nets:
  N1: Inverter-NeckNorth.SIG_A_IN/OUT, Inverter-NeckNorth.SIG_D_IN/OUT
  N2: Inverter-NeckNorth.SIG_A_OUT/IN, Inverter-NeckNorth.SIG_B_IN/OUT, VolTone-1a.SIG_A_IN/OUT, R11.Pin_1
  N3: Inverter-NeckNorth.SIG_B_OUT/IN, Inverter-NeckNorth.SIG_C_OUT/IN
  N4: Inverter-NeckNorth.SIG_C_IN/OUT, Inverter-NeckNorth.SIG_D_OUT/IN, Combinator.SIG_B_IN/OUT, Combinator.SIG_D_IN/OUT
  N5: VolTone-1a.SIG_A_OUT/IN, VolTone-1a.SIG_B_IN/OUT, VolTone-1_2c.SIG_A_OUT/IN, VolTone-1_2c.SIG_B_IN/OUT, VolTone-2b.SIG_A_IN/OUT, VolTone-2b.SIG_B_OUT/IN, VolTone-2a.SIG_A_IN/OUT, VolTone-2a.SIG_B_OUT/IN, Combinator.SIG_A_OUT/IN, VolTone-1b.SIG_A_OUT/IN, VolTone-1b.SIG_B_IN/OUT
  N6: VolTone-1a.SIG_B_OUT/IN, R11.Pin_0, R12.Pin_1
  N7: VolTone-1a.SIG_C_IN/OUT, VolTone-1a.SIG_D_OUT/IN, VolTone-1_2c.SIG_C_IN/OUT, VolTone-1_2c.SIG_D_OUT/IN, VolTone-2b.SIG_C_OUT/IN, VolTone-2b.SIG_D_IN/OUT, VolTone-2a.SIG_C_OUT/IN, VolTone-2a.SIG_D_IN/OUT, Combinator.SIG_A_IN/OUT, Combinator.SIG_B_OUT/IN, VolTone-1b.SIG_C_IN/OUT, VolTone-1b.SIG_D_OUT/IN
  N8: VolTone-1a.SIG_C_OUT/IN, R20.Pin_1, R21.Pin_0
  N9: VolTone-1a.SIG_D_IN/OUT, Inverter-NeckSouth.SIG_C_IN/OUT, Inverter-NeckSouth.SIG_D_OUT/IN, R20.Pin_0
  N10: VolTone-1_2c.SIG_A_IN/OUT, R14.Pin_0, R15.Pin_1
  N11: VolTone-1_2c.SIG_B_OUT/IN, VolTone-1_2c.SIG_C_OUT/IN, R15.Pin_0, R16.Pin_1, R18.Pin_1, R22.Pin_0
  N12: VolTone-1_2c.SIG_D_IN/OUT, R18.Pin_0, R19.Pin_1
  N13: VolTone-2b.SIG_A_OUT/IN, C1.0
  N14: VolTone-2b.SIG_B_IN/OUT, C2.0
  N15: VolTone-2b.SIG_C_IN/OUT, C5.0
  N16: VolTone-2b.SIG_D_OUT/IN, C6.1
  N17: VolTone-2a.SIG_A_OUT/IN, C3.0
  N18: VolTone-2a.SIG_B_IN/OUT, C4.0
  N19: VolTone-2a.SIG_C_IN/OUT, C8.1
  N20: VolTone-2a.SIG_D_OUT/IN, C7.0
  N21: Inverter-NeckSouth.SIG_A_IN/OUT, Inverter-NeckSouth.SIG_B_OUT/IN, Combinator.SIG_D_OUT/IN
  N22: Inverter-NeckSouth.SIG_A_OUT/IN, Inverter-NeckSouth.SIG_C_OUT/IN
  N23: Inverter-NeckSouth.SIG_B_IN/OUT, Inverter-NeckSouth.SIG_D_IN/OUT
  N24: VolTone-1b.SIG_A_IN/OUT, R12.Pin_0, R13.Pin_1
  N25: VolTone-1b.SIG_B_OUT/IN, R13.Pin_0, R14.Pin_1
  N26: VolTone-1b.SIG_C_OUT/IN, R17.Pin_1, R19.Pin_0
  N27: VolTone-1b.SIG_D_IN/OUT, R17.Pin_0, R21.Pin_1
  N28: C1.1, R16.Pin_0, C2.1, C3.1, C4.1
  N29: C5.1, C6.0, C7.1, C8.0, R22.Pin_1

notes:
  NeckNorth Cold
  NeckNorth Hot
  NeckSouth Cold
  NeckSouth Hot
  NeckSouth Inverter
  Neg Output
  NeckNorth Inverter
  Neg Output
  Pos Output
  Neg Output

custom parts:
  CD4066 Quad Analog Switch: Quad Analog Switch
