# Fritzing sketch Ardu2 (saved by Fritzing 0.8.3b)
breadboards: 1

parts:
  H1_Coil_A = Inductor [package="400 mil [THT]"]
  H1_Coil_B = Inductor [package="400 mil [THT]"]
  H2_Coil_C = Inductor [package="400 mil [THT]"]
  H2_Coil_D = Inductor [package="400 mil [THT]"]
  Inverter_H1A = IC, DIP package, 4 pins [chip_label=Inverter]
  Inverter_H1B = IC, DIP package, 4 pins [chip_label=Inverter]
  Inverter_H2A = IC, DIP package, 4 pins [chip_label=Inverter]
  Inverter_H2B = IC, DIP package, 4 pins [chip_label=Inverter]
  VT_H1A = IC, DIP package, 4 pins [chip_label=Vol/Tone]
  VT_H1B = IC, DIP package, 4 pins [chip_label=Vol/Tone]
  VT_H2A = IC, DIP package, 4 pins [chip_label=Vol/Tone]
  VT_H2B = IC, DIP package, 4 pins [chip_label=Vol/Tone]
  Combinator_AB = IC, DIP package, 6 pins [chip_label=Combinator]
  Combinator_CD = IC, DIP package, 6 pins [chip_label=Combinator]
  Combinator_CDAB = IC, DIP package, 6 pins [chip_label=Combinator]
  Combinator_ABCD = IC, DIP package, 6 pins [chip_label=Combinator]
  Selector_1 = IC, DIP package, 6 pins [chip_label=Selector]
  VT_Master = IC, DIP package, 4 pins [chip_label=Vol/Tone]

nets:
  N1: H1_Coil_A.pin_0, Inverter_H1A.pin1
  N2: H1_Coil_A.pin_1, Inverter_H1A.pin2
  N3: H1_Coil_B.pin_0, Inverter_H1B.pin1
  N4: H1_Coil_B.pin_1, Inverter_H1B.pin2
  N5: H2_Coil_C.pin_0, Inverter_H2A.pin1
  N6: H2_Coil_C.pin_1, Inverter_H2A.pin2
  N7: H2_Coil_D.pin_0, Inverter_H2B.pin1
  N8: H2_Coil_D.pin_1, Inverter_H2B.pin2
  N9: Inverter_H1A.pin3, Combinator_AB.pin2
  N10: Inverter_H1A.pin4, VT_H1A.pin1
  N11: Inverter_H1B.pin3, Combinator_AB.pin5
  N12: Inverter_H1B.pin4, VT_H1B.pin1
  N13: Inverter_H2A.pin3, Combinator_CD.pin2
  N14: Inverter_H2A.pin4, VT_H2A.pin1
  N15: Inverter_H2B.pin3, Combinator_CD.pin5
  N16: Inverter_H2B.pin4, VT_H2B.pin1
  GND: VT_H1A.pin3, VT_H1B.pin3, VT_H2A.pin3, VT_H2B.pin3, Selector_1.pin4, VT_Master.pin3
  N17: VT_H1A.pin4, Combinator_AB.pin1
  N18: VT_H1B.pin4, Combinator_AB.pin6
  N19: VT_H2A.pin4, Combinator_CD.pin1
  N20: VT_H2B.pin4, Combinator_CD.pin6
  N21: Combinator_AB.pin3, Combinator_CDAB.pin6, Combinator_ABCD.pin1
  N22: Combinator_AB.pin4, Combinator_CDAB.pin5, Combinator_ABCD.pin2
  N23: Combinator_CD.pin3, Combinator_CDAB.pin1, Combinator_ABCD.pin6
  N24: Combinator_CD.pin4, Combinator_CDAB.pin2, Combinator_ABCD.pin5
  N25: Combinator_CDAB.pin3, Selector_1.pin6
  N26: Combinator_CDAB.pin4, Selector_1.pin5
  N27: Combinator_ABCD.pin3, Selector_1.pin1
  N28: Combinator_ABCD.pin4, Selector_1.pin2
  N29: Selector_1.pin3, VT_Master.pin1

notes:
  Amp Jack Hot
  Humbucker 1
  (Neck)
  Humbucker 2
  (Bridge)
  Component Requirements:
  Quad SPST:
  * Inverter : 1 Quad SPST * 4 = 4 Quad SPST
  * Vol/Tone: 1 SPST * 5 = 1.25 Quad SPST
  * Combinator: 3/4 Quad SPST * 4 = 3 Quad SPST
  * Selector: 1 Quad SPST
  Total 9.25 Quad SPST.
  --------------------------
  Vactrols:
  * Vol/Tone: 4 Vactrols + 1 Capacitor (+ 1 SPST) * 5
  = 20 Vactrols + 5 Capacitors + 5 SPST
