# Fritzing sketch Ardu2 layout test 01 (saved by Fritzing 0.8.7b)
circuit board: 7.95953cm x 10.4998cm
circuit board: 8.00217cm x 7.70403cm
circuit board: 5cm x 3.5cm
circuit board: 12cm x 3cm
breadboards: 1

parts:
  4066-1 = IC, DIP package, 14 pins [chip_label=IC]  # not connected
  ShiftReg_1 = IC, DIP package, 16 pins [chip_label=IC]  # not connected
  4066-2 = IC, DIP package, 14 pins [chip_label=IC]  # not connected
  4066-3 = IC, DIP package, 14 pins [chip_label=IC]  # not connected
  4066-4 = IC, DIP package, 14 pins [chip_label=IC]  # not connected
  ShiftReg_2 = IC, DIP package, 16 pins [chip_label=IC]  # not connected
  4066-5 = IC, DIP package, 14 pins [chip_label=IC]  # not connected
  4066-6 = IC, DIP package, 14 pins [chip_label=IC]  # not connected
  4066-7 = IC, DIP package, 14 pins [chip_label=IC]  # not connected
  4066-8 = IC, DIP package, 14 pins [chip_label=IC]  # not connected
  ShiftReg_3 = IC, DIP package, 16 pins [chip_label=IC]  # not connected
  ShiftReg_4 = IC, DIP package, 16 pins [chip_label=IC]  # not connected
  4066-9 = IC, DIP package, 14 pins [chip_label=IC]  # not connected
  4066-11 = IC, DIP package, 14 pins [chip_label=IC]  # not connected
  4066-13 = IC, DIP package, 14 pins [chip_label=IC]  # not connected
  4066-14 = IC, DIP package, 14 pins [chip_label=IC]  # not connected
  4066-16 = IC, DIP package, 14 pins [chip_label=IC]  # not connected
  ShiftReg_5 = IC, DIP package, 16 pins [chip_label=IC]  # not connected
  ShiftReg_6 = IC, DIP package, 16 pins [chip_label=IC]  # not connected
  ShiftReg_7 = IC, DIP package, 16 pins [chip_label=IC]  # not connected
  ShiftReg_8 = IC, DIP package, 16 pins [chip_label=IC]  # not connected
  4066-20 = IC, DIP package, 14 pins [chip_label=IC]  # not connected
  4066-24 = IC, DIP package, 14 pins [chip_label=IC]  # not connected
  4066-30 = IC, DIP package, 14 pins [chip_label=IC]  # not connected
  4066-31 = IC, DIP package, 14 pins [chip_label=IC]  # not connected
  C17 = Ceramic Capacitor [capacitance=100nF package="100 mil [THT, multilayer]"]  # not connected
  C18 = Ceramic Capacitor [capacitance=100nF package="100 mil [THT, multilayer]"]  # not connected
  C19 = Ceramic Capacitor [capacitance=100nF package="100 mil [THT, multilayer]"]  # not connected
  C20 = Ceramic Capacitor [capacitance=100nF package="100 mil [THT, multilayer]"]  # not connected
  R12 = Resistor [tolerance=±5% resistance=220 package=THT]  # not connected
  R13 = Resistor [tolerance=±5% resistance=220 package=THT]  # not connected
  R14 = Resistor [tolerance=±5% resistance=220 package=THT]  # not connected
  R15 = Resistor [tolerance=±5% resistance=220 package=THT]  # not connected
  R16 = Resistor [tolerance=±5% resistance=220 package=THT]  # not connected
  R17 = Resistor [tolerance=±5% resistance=220 package=THT]  # not connected
  C21 = Ceramic Capacitor [capacitance=100nF package="100 mil [THT, multilayer]"]
  C22 = Ceramic Capacitor [capacitance=100nF package="100 mil [THT, multilayer]"]
  C23 = Ceramic Capacitor [capacitance=100nF package="100 mil [THT, multilayer]"]
  C24 = Ceramic Capacitor [capacitance=100nF package="100 mil [THT, multilayer]"]
  R18 = Resistor [tolerance=±5% resistance=220 package=THT]
  R19 = Resistor [tolerance=±5% resistance=220 package=THT]
  R20 = Resistor [tolerance=±5% resistance=220 package=THT]
  R21 = Resistor [tolerance=±5% resistance=220 package=THT]
  R22 = Resistor [tolerance=±5% resistance=220 package=THT]
  R23 = Resistor [tolerance=±5% resistance=220 package=THT]
  C25 = Ceramic Capacitor [capacitance=100nF package="100 mil [THT, multilayer]"]  # not connected
  C26 = Ceramic Capacitor [capacitance=100nF package="100 mil [THT, multilayer]"]  # not connected
  C27 = Ceramic Capacitor [capacitance=100nF package="100 mil [THT, multilayer]"]  # not connected
  C28 = Ceramic Capacitor [capacitance=100nF package="100 mil [THT, multilayer]"]  # not connected
  R24 = Resistor [tolerance=±5% resistance=220 package=THT]  # not connected
  R25 = Resistor [tolerance=±5% resistance=220 package=THT]  # not connected
  R26 = Resistor [tolerance=±5% resistance=220 package=THT]  # not connected
  R27 = Resistor [tolerance=±5% resistance=220 package=THT]  # not connected
  R28 = Resistor [tolerance=±5% resistance=220 package=THT]  # not connected
  R29 = Resistor [tolerance=±5% resistance=220 package=THT]  # not connected
  C29 = Ceramic Capacitor [capacitance=100nF package="100 mil [THT, multilayer]"]
  C30 = Ceramic Capacitor [capacitance=100nF package="100 mil [THT, multilayer]"]  # not connected
  C31 = Ceramic Capacitor [capacitance=100nF package="100 mil [THT, multilayer]"]
  C32 = Ceramic Capacitor [capacitance=100nF package="100 mil [THT, multilayer]"]  # not connected
  C33 = Ceramic Capacitor [capacitance=100nF package="100 mil [THT, multilayer]"]
  C34 = Ceramic Capacitor [capacitance=100nF package="100 mil [THT, multilayer]"]  # not connected
  C35 = Ceramic Capacitor [capacitance=100nF package="100 mil [THT, multilayer]"]
  C36 = Ceramic Capacitor [capacitance=100nF package="100 mil [THT, multilayer]"]  # not connected
  R30 = Resistor [tolerance=±5% resistance=220 package=THT]
  R31 = Resistor [tolerance=±5% resistance=220 package=THT]  # not connected
  R32 = Resistor [tolerance=±5% resistance=220 package=THT]
  R33 = Resistor [tolerance=±5% resistance=220 package=THT]  # not connected
  R34 = Resistor [tolerance=±5% resistance=220 package=THT]
  R35 = Resistor [tolerance=±5% resistance=220 package=THT]  # not connected
  R36 = Resistor [tolerance=±5% resistance=220 package=THT]
  R37 = Resistor [tolerance=±5% resistance=220 package=THT]  # not connected
  R38 = Resistor [tolerance=±5% resistance=220 package=THT]
  R39 = Resistor [tolerance=±5% resistance=220 package=THT]  # not connected
  R40 = Resistor [tolerance=±5% resistance=220 package=THT]
  R41 = Resistor [tolerance=±5% resistance=220 package=THT]  # not connected
  Input_1_Neck_North = male pin header, 3 pins [form="♂ (male)"]  # not connected
  Input_3_Bridge_North = male pin header, 3 pins [form="♂ (male)"]  # not connected
  Input_2_Neck_South = male pin header, 3 pins [form="♂ (male)"]  # not connected
  Input_4_Bridge_South = male pin header, 3 pins [form="♂ (male)"]  # not connected
  Part1 = Bluetooth Mate Silver  # not connected
  Part3 = Arduino Pro Mini v13  # not connected
  IC1 = TC7660H Charge-Pump [part_number=TC7660H]  # not connected
  C37 = Ceramic Capacitor [capacitance=100nF package="100 mil [THT, multilayer]"]  # not connected
  C38 = Ceramic Capacitor [capacitance=100nF package="100 mil [THT, multilayer]"]  # not connected
  Output = male pin header, 2 pins [form="♂ (male)"]  # not connected
  4066-32 = IC, DIP package, 14 pins [chip_label=IC]  # not connected
  4066-33 = IC, DIP package, 14 pins [chip_label=IC]  # not connected
  4066-34 = IC, DIP package, 14 pins [chip_label=IC]  # not connected
  4066-35 = IC, DIP package, 14 pins [chip_label=IC]  # not connected
  ShiftReg_9 = IC, DIP package, 16 pins [chip_label=IC]  # not connected
  Audio_GND = male pin header, 1 pin [form="♂ (male)"]

nets:
  N1: C21.0, C22.0, C23.0, C24.0, R18.Pin_0
  N2: R18.Pin_1, R22.Pin_1, R30.Pin_1, R40.Pin_1, Audio_GND.pin1
  N3: R19.Pin_0, R21.Pin_1
  N4: R19.Pin_1, R20.Pin_0
  N5: R20.Pin_1, R23.Pin_0
  N6: R22.Pin_0, R23.Pin_1
  N7: C29.1, C31.1, C33.1, C35.1, R30.Pin_0
  N8: R32.Pin_0, R36.Pin_1
  N9: R32.Pin_1, R34.Pin_0
  N10: R34.Pin_1, R40.Pin_0
  N11: R36.Pin_0, R38.Pin_1
