# Fritzing sketch Combinator (saved by Fritzing 0.8.7b)
circuit board: 10cm x 5cm
breadboards: 1

parts:
  Output = female pin header, 2 pins [form="♀ (female)"]
  4660 = IC, DIP package, 14 pins [chip_label=CD4660]
  Input_B = female alternating pin header, 2 pins [form="♀ (female)"]
  Input_A = female alternating pin header, 2 pins [form="♀ (female)"]
  InputB1 = female alternating pin header, 2 pins [form="♀ (female)"]
  MAX4679 = IC, DIP package, 16 pins [chip_label=IC]
  Output1 = female pin header, 2 pins [form="♀ (female)"]
  InputA1 = female alternating pin header, 2 pins [form="♀ (female)"]
  Power2 = female pin header, 2 pins [form="♀ (female)"]
  Control4 = female pin header, 4 pins [form="♀ (female)"]
  Control5 = female pin header, 4 pins [form="♀ (female)"]

nets:
  N1: Output.pin1, Input_A.pin1, MAX4679.pin10
  N2: Output.pin2, Input_B.pin2, MAX4679.pin7
  N3: 4660.pin1, 4660.pin9, InputB1.pin1
  N4: 4660.pin2, 4660.pin3, InputA1.pin2
  N5: 4660.pin4, InputB1.pin2, Output1.pin2
  N6: 4660.pin5, Control5.pin4
  N7: 4660.pin6, Control5.pin3
  N8: 4660.pin7, MAX4679.pin4, Power2.pin2
  N9: 4660.pin8, Output1.pin1, InputA1.pin1
  N10: 4660.pin13, Control5.pin2
  N11: 4660.pin14, MAX4679.pin12, MAX4679.pin13, Power2.pin1
  N12: Input_B.pin1, MAX4679.pin2, MAX4679.pin11
  N13: Input_A.pin2, MAX4679.pin3, MAX4679.pin6
  N14: MAX4679.pin1, Control4.pin4
  N15: MAX4679.pin8, Control4.pin3
  N16: MAX4679.pin9, Control4.pin2

notes:
  Combinator
  1 series
  3 & 4 parallel
  3 turns on input  B alone
  4 turns on input A alone
  A series
  B & C parallel
  C turns on input B alone
  B turns on input A alone
  GND
  -5V
  +5V
  3
  1
  4
  C
  A
  B
