# Fritzing sketch R-Lattice 4066 7660 (saved by Fritzing 0.8.7b)
breadboards: 1

parts:
  IC1 = TC7660H Charge-Pump [part_number=TC1044]
  C1 = Electrolytic Capacitor [capacitance=1µF package="100 mil [THT, electrolytic]"]
  C2 = Electrolytic Capacitor [capacitance=1µF package="100 mil [THT, electrolytic]"]
  IC3 = MAX4677 Quad SPST Analog Switch [part_number=MAX4679]
  IC2 = MAX4677 Quad SPST Analog Switch [part_number=MAX4679]
  R1 = Resistor [tolerance=±5% resistance=68k package=THT]
  R2 = Resistor [tolerance=±5% resistance=68k package=THT]
  R3 = Resistor [tolerance=±5% resistance=68k package=THT]
  R4 = Resistor [tolerance=±5% resistance=68k package=THT]
  R5 = Resistor [tolerance=±5% resistance=68k package=THT]
  R6 = Resistor [tolerance=±5% resistance=68k package=THT]
  R7 = Resistor [tolerance=±5% resistance=68k package=THT]

nets:
  N1: IC1.no_name_yet#1, IC1.no_name_yet#8, IC3.no_name_yet#12, IC3.no_name_yet#13, IC2.no_name_yet#12, IC2.no_name_yet#13
  N2: IC1.no_name_yet#4, C2.-, IC3.no_name_yet#4, IC2.no_name_yet#4
  N3: IC1.no_name_yet#5, C1.-
  N4: IC1.no_name_yet#6, C2.+, IC3.no_name_yet#5, IC2.no_name_yet#5, IC2.no_name_yet#7, R7.Pin_1
  N5: IC1.no_name_yet#7, C1.+
  N6: IC3.no_name_yet#2, R1.Pin_0
  N7: IC3.no_name_yet#3, IC3.no_name_yet#8, IC3.no_name_yet#9, IC3.no_name_yet#14, IC2.no_name_yet#3, IC2.no_name_yet#8, IC2.no_name_yet#9, IC2.no_name_yet#14
  N8: IC3.no_name_yet#7, R3.Pin_0, R4.Pin_1
  N9: IC3.no_name_yet#10, R2.Pin_1, R4.Pin_0
  N10: IC3.no_name_yet#15, R1.Pin_1, R2.Pin_0
  N11: IC2.no_name_yet#2, R3.Pin_1, R6.Pin_0
  N12: IC2.no_name_yet#10, R5.Pin_1, R7.Pin_0
  N13: IC2.no_name_yet#15, R5.Pin_0, R6.Pin_1

notes:
  Arduino
  +5v Gnd
  -5v
  Vin
  Vout
