# Fritzing sketch Selector (saved by Fritzing 0.8.7b)
circuit board: 10.1903cm x 5.44773cm
breadboards: 1

parts:
  Output = female pin header, 2 pins [form="♀ (female)"]
  Input_B = female alternating pin header, 2 pins [form="♀ (female)"]
  Input_A = female alternating pin header, 2 pins [form="♀ (female)"]
  InputB1 = female alternating pin header, 2 pins [form="♀ (female)"]
  MAX4679 = IC, DIP package, 16 pins [chip_label=IC]
  Output1 = female pin header, 2 pins [form="♀ (female)"]
  InputA1 = female alternating pin header, 2 pins [form="♀ (female)"]
  Power1 = female pin header, 2 pins [form="♀ (female)"]
  Control2 = female pin header, 4 pins [form="♀ (female)"]
  Control3 = female pin header, 4 pins [form="♀ (female)"]
  4660 = IC, DIP package, 14 pins [chip_label=CD4660]

nets:
  N1: Output.pin1, MAX4679.pin3, MAX4679.pin10
  N2: Output.pin2, MAX4679.pin7, MAX4679.pin14
  N3: Input_B.pin1, MAX4679.pin2
  N4: Input_B.pin2, MAX4679.pin6
  N5: Input_A.pin1, MAX4679.pin11
  N6: Input_A.pin2, MAX4679.pin15
  N7: InputB1.pin1, 4660.pin11
  N8: InputB1.pin2, 4660.pin1
  N9: MAX4679.pin1, MAX4679.pin8, Control2.pin3
  N10: MAX4679.pin4, Power1.pin2, 4660.pin7
  N11: MAX4679.pin9, MAX4679.pin16, Control2.pin2
  N12: MAX4679.pin12, MAX4679.pin13, Power1.pin1, 4660.pin14
  N13: Output1.pin1, 4660.pin8, 4660.pin10
  N14: Output1.pin2, 4660.pin2, 4660.pin4
  N15: InputA1.pin1, 4660.pin9
  N16: InputA1.pin2, 4660.pin3
  N17: Control3.pin2, 4660.pin12, 4660.pin13
  N18: Control3.pin3, 4660.pin5, 4660.pin6

notes:
  Selector
  1 & 4 -> input B
  2 & 3 -> input A
  all -> inputs A & B
  A & D -> input B
  B & C -> input A
  none -> no output
  -5V
  +5V
  B
  C
  3
  4
  A
  D
  2
  GND
  1
