# Fritzing sketch Vol-Tone 4066 (saved by Fritzing 0.9.0b)
circuit board: 12.0705cm x 9.83657cm
breadboards: 1

parts:
  Input-1_Output-1_GND = female pin header, 3 pins [form="♀ (female)"]
  R1 = Resistor [tolerance=±5% resistance=47k package=THT]
  R2 = Resistor [tolerance=±5% resistance=47k package=THT]
  R3 = Resistor [tolerance=±5% resistance=47k package=THT]
  R4 = Resistor [tolerance=±5% resistance=47k package=THT]
  R5 = Resistor [tolerance=±5% resistance=47k package=THT]
  C1 = Ceramic Capacitor [capacitance=10nF package="100 mil [THT, multilayer]"]
  ?Tone_Resistor-1? = Resistor [tolerance=±5% resistance=100k package=THT]
  C3 = Ceramic Capacitor [capacitance=33nF package="100 mil [THT, multilayer]"]
  4066-0 = IC, DIP package, 14 pins [chip_label=4066]
  4066-1 = IC, DIP package, 14 pins [chip_label=4066]
  4066-2 = IC, DIP package, 14 pins [chip_label=4066]
  R6 = Resistor [tolerance=±5% resistance=47k package=THT]
  R7 = Resistor [tolerance=±5% resistance=47k package=THT]
  R8 = Resistor [tolerance=±5% resistance=47k package=THT]
  R9 = Resistor [tolerance=±5% resistance=47k package=THT]
  R10 = Resistor [tolerance=±5% resistance=47k package=THT]
  C8 = Ceramic Capacitor [capacitance=47nF package="100 mil [THT, multilayer]"]
  C7 = Ceramic Capacitor [capacitance=33nF package="100 mil [THT, multilayer]"]
  C6 = Ceramic Capacitor [capacitance=22nF package="100 mil [THT, multilayer]"]
  C5 = Ceramic Capacitor [capacitance=10nF package="100 mil [THT, multilayer]"]
  ?Tone_Resistor-2? = Resistor [tolerance=±5% resistance=100k package=THT]
  4066-4 = IC, DIP package, 14 pins [chip_label=4066]
  4066-3 = IC, DIP package, 14 pins [chip_label=4066]
  Input-2_Output-2 = female pin header, 2 pins [form="♀ (female)"]
  C4 = Ceramic Capacitor [capacitance=47nF package="100 mil [THT, multilayer]"]
  C2 = Ceramic Capacitor [capacitance=22nF package="100 mil [THT, multilayer]"]
  Power1 = female pin header, 2 pins [form="♀ (female)"]
  Vol-Tone = female pin header, 20 pins [form="♀ (female)"]

nets:
  N1: Input-1_Output-1_GND.pin1, R1.Pin_0, 4066-0.pin11
  N2: Input-1_Output-1_GND.pin2, 4066-0.pin2, 4066-0.pin3, 4066-0.pin9, 4066-0.pin10, 4066-1.pin2, 4066-1.pin3, 4066-1.pin9, 4066-1.pin10, 4066-2.pin9, 4066-2.pin10
  N3: Input-1_Output-1_GND.pin3, R5.Pin_1, ?Tone_Resistor-1?.Pin_0, 4066-2.pin4, 4066-2.pin8, R6.Pin_1, ?Tone_Resistor-2?.Pin_1
  N4: R1.Pin_1, R2.Pin_0, 4066-0.pin8
  N5: R2.Pin_1, R3.Pin_0, 4066-1.pin11
  N6: R3.Pin_1, R4.Pin_0, 4066-1.pin8
  N7: R4.Pin_1, R5.Pin_0, 4066-2.pin11
  N8: C1.0, 4066-0.pin1
  N9: C1.1, ?Tone_Resistor-1?.Pin_1, C3.1, C4.1, C2.1
  N10: C3.0, 4066-1.pin1
  N11: 4066-0.pin4, C2.0
  N12: 4066-0.pin5, Vol-Tone.pin10
  N13: 4066-0.pin6, Vol-Tone.pin9
  N14: 4066-0.pin7, 4066-1.pin7, 4066-2.pin7, 4066-4.pin7, 4066-3.pin7, Power1.pin2
  N15: 4066-0.pin12, Vol-Tone.pin2
  N16: 4066-0.pin13, Vol-Tone.pin1
  N17: 4066-0.pin14, 4066-1.pin14, 4066-2.pin14, 4066-4.pin14, 4066-3.pin14, Power1.pin1
  N18: 4066-1.pin4, C4.0
  N19: 4066-1.pin5, Vol-Tone.pin12
  N20: 4066-1.pin6, Vol-Tone.pin11
  N21: 4066-1.pin12, Vol-Tone.pin4
  N22: 4066-1.pin13, Vol-Tone.pin3
  N23: 4066-2.pin1, R6.Pin_0, R7.Pin_1
  N24: 4066-2.pin2, 4066-2.pin3, 4066-4.pin2, 4066-4.pin3, 4066-4.pin9, 4066-4.pin10, 4066-3.pin2, 4066-3.pin3, 4066-3.pin9, 4066-3.pin10, Input-2_Output-2.pin2
  N25: 4066-2.pin5, Vol-Tone.pin8
  N26: 4066-2.pin6, Vol-Tone.pin7
  N27: 4066-2.pin12, Vol-Tone.pin6
  N28: 4066-2.pin13, Vol-Tone.pin5
  N29: R7.Pin_0, R8.Pin_1, 4066-4.pin8
  N30: R8.Pin_0, R9.Pin_1, 4066-4.pin11
  N31: R9.Pin_0, R10.Pin_1, 4066-3.pin8
  N32: R10.Pin_0, 4066-3.pin11, Input-2_Output-2.pin1
  N33: C8.0, 4066-4.pin4
  N34: C8.1, C7.1, C6.1, C5.1, ?Tone_Resistor-2?.Pin_0
  N35: C7.0, 4066-4.pin1
  N36: C6.0, 4066-3.pin4
  N37: C5.0, 4066-3.pin1
  N38: 4066-4.pin5, Vol-Tone.pin18
  N39: 4066-4.pin6, Vol-Tone.pin17
  N40: 4066-4.pin12, Vol-Tone.pin16
  N41: 4066-4.pin13, Vol-Tone.pin15
  N42: 4066-3.pin5, Vol-Tone.pin20
  N43: 4066-3.pin6, Vol-Tone.pin19
  N44: 4066-3.pin12, Vol-Tone.pin14
  N45: 4066-3.pin13, Vol-Tone.pin13

notes:
  Volume-1
  Tone-1
  2x Vol/Tone pair - 4066
  Tone-2
  Volume-2
  +5V
  -5V
  V1-5
  C1-1
  C1-3
  V1-3
  V2-1
  V1-1
  C2-5
  V2-5
  C2-7
  V2-3
  V2-2
  C2-8
  V2-4
  C2-6
  V1-0
  V2-0
  V1-4
  C1-2
  V1-2
  C1-4
