# Fritzing sketch Vol-Tone Max4679 (saved by Fritzing 0.8.7b)
circuit board: 13.303cm x 11.267cm
breadboards: 1

parts:
  MAX4679-0 = IC, DIP package, 16 pins [chip_label=IC]
  Input-1_Output-1_GND = female pin header, 3 pins [form="♀ (female)"]
  MAX4679-1 = IC, DIP package, 16 pins [chip_label=IC]
  MAX4679-2 = IC, DIP package, 16 pins [chip_label=IC]
  R1 = Resistor [tolerance=±5% resistance=47k package=THT]
  R2 = Resistor [tolerance=±5% resistance=47k package=THT]
  R3 = Resistor [tolerance=±5% resistance=47k package=THT]
  R4 = Resistor [tolerance=±5% resistance=47k package=THT]
  R5 = Resistor [tolerance=±5% resistance=47k package=THT]
  C1 = Ceramic Capacitor [capacitance=10nF package="100 mil [THT, multilayer]"]
  ?Tone_Resistor-1? = Resistor [tolerance=±5% resistance=100k package=THT]
  C2 = Ceramic Capacitor [capacitance=22nF package="100 mil [THT, multilayer]"]
  C3 = Ceramic Capacitor [capacitance=33nF package="100 mil [THT, multilayer]"]
  C4 = Ceramic Capacitor [capacitance=47nF package="100 mil [THT, multilayer]"]
  MAX4679-4 = IC, DIP package, 16 pins [chip_label=IC]
  MAX4679-3 = IC, DIP package, 16 pins [chip_label=IC]
  R6 = Resistor [tolerance=±5% resistance=47k package=THT]
  R7 = Resistor [tolerance=±5% resistance=47k package=THT]
  R8 = Resistor [tolerance=±5% resistance=47k package=THT]
  R9 = Resistor [tolerance=±5% resistance=47k package=THT]
  R10 = Resistor [tolerance=±5% resistance=47k package=THT]
  C5 = Ceramic Capacitor [capacitance=10nF package="100 mil [THT, multilayer]"]
  C7 = Ceramic Capacitor [capacitance=33nF package="100 mil [THT, multilayer]"]
  C6 = Ceramic Capacitor [capacitance=22nF package="100 mil [THT, multilayer]"]
  C8 = Ceramic Capacitor [capacitance=47nF package="100 mil [THT, multilayer]"]
  ?Tone_Resistor-2? = Resistor [tolerance=±5% resistance=100k package=THT]
  Input-2_Output-2 = female pin header, 2 pins [form="♀ (female)"]

nets:
  N1: MAX4679-0.pin2, MAX4679-0.pin7, MAX4679-0.pin11, MAX4679-0.pin15, Input-1_Output-1_GND.pin2, MAX4679-1.pin3, MAX4679-1.pin7, MAX4679-1.pin11, MAX4679-1.pin15, MAX4679-2.pin10, MAX4679-2.pin15
  N2: MAX4679-0.pin3, C1.0
  N3: MAX4679-0.pin6, C2.0
  N4: MAX4679-0.pin10, R1.Pin_1, R2.Pin_0
  N5: MAX4679-0.pin12, Input-1_Output-1_GND.pin3, MAX4679-1.pin12, MAX4679-2.pin6, MAX4679-2.pin11, MAX4679-2.pin12, R5.Pin_1, ?Tone_Resistor-1?.Pin_0, MAX4679-4.pin12, MAX4679-3.pin12, R9.Pin_1, ?Tone_Resistor-2?.Pin_1
  N6: MAX4679-0.pin14, Input-1_Output-1_GND.pin1, R1.Pin_0
  N7: MAX4679-1.pin2, C3.0
  N8: MAX4679-1.pin6, C4.0
  N9: MAX4679-1.pin10, R3.Pin_1, R4.Pin_0
  N10: MAX4679-1.pin14, R2.Pin_1, R3.Pin_0
  N11: MAX4679-2.pin2, MAX4679-2.pin7, MAX4679-4.pin3, MAX4679-4.pin7, MAX4679-4.pin11, MAX4679-4.pin15, MAX4679-3.pin2, MAX4679-3.pin7, MAX4679-3.pin11, MAX4679-3.pin15, Input-2_Output-2.pin2
  N12: MAX4679-2.pin3, R9.Pin_0, R10.Pin_1
  N13: MAX4679-2.pin14, R4.Pin_1, R5.Pin_0
  N14: C1.1, ?Tone_Resistor-1?.Pin_1, C2.1, C3.1, C4.1
  N15: MAX4679-4.pin2, C7.0
  N16: MAX4679-4.pin6, C8.0
  N17: MAX4679-4.pin10, R8.Pin_1, R10.Pin_0
  N18: MAX4679-4.pin14, R7.Pin_1, R8.Pin_0
  N19: MAX4679-3.pin3, C5.0
  N20: MAX4679-3.pin6, C6.0
  N21: MAX4679-3.pin10, R6.Pin_1, R7.Pin_0
  N22: MAX4679-3.pin14, R6.Pin_0, Input-2_Output-2.pin1
  N23: C5.1, C7.1, C6.1, C8.1, ?Tone_Resistor-2?.Pin_0

notes:
  Volume-1
  Tone-1
  Vol/Tone pair - MAX4679
  Vol/Tone - MAX4679
  Tone-2
  Volume-2
