# Fritzing sketch InputStage_Vol_Tone 03 (saved by Fritzing 0.8.7b)
circuit board: 14.3639cm x 6.96137cm
breadboards: 1

parts:
  HousingConnect1 = female pin header, 10 pins [form="♀ (female)"]
  4660 = IC, DIP package, 14 pins [chip_label=CD4660]
  4660_2 = IC, DIP package, 14 pins [chip_label=CD4660]
  4660_3 = IC, DIP package, 14 pins [chip_label=CD4660]
  4660_4 = IC, DIP package, 14 pins [chip_label=CD4660]
  Con_INV3/4 = female pin header, 4 pins [form="♀ (female)"]
  InverterOutput = female pin header, 6 pins [form="♀ (female)"]
  Con_INV1/2_V+/- = female pin header, 6 pins [form="♀ (female)"]
  4660_5 = IC, DIP package, 14 pins [chip_label=CD4660]
  4660_6 = IC, DIP package, 14 pins [chip_label=CD4660]
  4660_7 = IC, DIP package, 14 pins [chip_label=CD4660]
  4660_8 = IC, DIP package, 14 pins [chip_label=CD4660]
  4660_9 = IC, DIP package, 14 pins [chip_label=CD4660]
  AD-3/4 = female pin header, 10 pins [form="♀ (female)"]
  BC-3/4 = female pin header, 10 pins [form="♀ (female)"]
  R1 = Resistor [tolerance=±5% resistance=100k package=THT]
  R2 = Resistor [tolerance=±5% resistance=100k package=THT]
  R3 = Resistor [tolerance=±5% resistance=100k package=THT]
  R4 = Resistor [tolerance=±5% resistance=100k package=THT]
  R5 = Resistor [tolerance=±5% resistance=100k package=THT]
  Tone4 = Resistor [tolerance=±5% resistance=220k package=THT]
  C4 = Ceramic Capacitor [capacitance=47nF package="100 mil [THT, multilayer]"]
  C3 = Ceramic Capacitor [capacitance=33nF package="100 mil [THT, multilayer]"]
  C2 = Ceramic Capacitor [capacitance=22nF package="100 mil [THT, multilayer]"]
  C1 = Ceramic Capacitor [capacitance=10nF package="100 mil [THT, multilayer]"]
  VolToneOut = female pin header, 4 pins [form="♀ (female)"]
  C5 = Ceramic Capacitor [capacitance=47nF package="100 mil [THT, multilayer]"]
  C6 = Ceramic Capacitor [capacitance=33nF package="100 mil [THT, multilayer]"]
  C7 = Ceramic Capacitor [capacitance=22nF package="100 mil [THT, multilayer]"]
  C8 = Ceramic Capacitor [capacitance=10nF package="100 mil [THT, multilayer]"]
  Tone3 = Resistor [tolerance=±5% resistance=220k package=THT]
  R6 = Resistor [tolerance=±5% resistance=100k package=THT]
  R7 = Resistor [tolerance=±5% resistance=100k package=THT]
  R8 = Resistor [tolerance=±5% resistance=100k package=THT]
  R9 = Resistor [tolerance=±5% resistance=100k package=THT]
  R10 = Resistor [tolerance=±5% resistance=100k package=THT]
  R11 = Resistor [tolerance=±5% resistance=100k package=THT]
  R12 = Resistor [tolerance=±5% resistance=100k package=THT]
  R13 = Resistor [tolerance=±5% resistance=100k package=THT]
  R14 = Resistor [tolerance=±5% resistance=100k package=THT]
  R15 = Resistor [tolerance=±5% resistance=100k package=THT]
  Tone5 = Resistor [tolerance=±5% resistance=220k package=THT]
  Tone6 = Resistor [tolerance=±5% resistance=220k package=THT]
  R16 = Resistor [tolerance=±5% resistance=100k package=THT]
  R17 = Resistor [tolerance=±5% resistance=100k package=THT]
  R18 = Resistor [tolerance=±5% resistance=100k package=THT]
  R19 = Resistor [tolerance=±5% resistance=100k package=THT]
  R20 = Resistor [tolerance=±5% resistance=100k package=THT]
  BC-3/5 = female pin header, 10 pins [form="♀ (female)"]
  AD-3/5 = female pin header, 10 pins [form="♀ (female)"]
  4660_10 = IC, DIP package, 14 pins [chip_label=CD4660]
  4660_11 = IC, DIP package, 14 pins [chip_label=CD4660]
  4660_12 = IC, DIP package, 14 pins [chip_label=CD4660]
  4660_13 = IC, DIP package, 14 pins [chip_label=CD4660]
  4660_14 = IC, DIP package, 14 pins [chip_label=CD4660]
  C9 = Ceramic Capacitor [capacitance=47nF package="100 mil [THT, multilayer]"]
  C10 = Ceramic Capacitor [capacitance=47nF package="100 mil [THT, multilayer]"]
  C11 = Ceramic Capacitor [capacitance=33nF package="100 mil [THT, multilayer]"]
  C12 = Ceramic Capacitor [capacitance=33nF package="100 mil [THT, multilayer]"]
  C13 = Ceramic Capacitor [capacitance=22nF package="100 mil [THT, multilayer]"]
  C14 = Ceramic Capacitor [capacitance=22nF package="100 mil [THT, multilayer]"]
  C15 = Ceramic Capacitor [capacitance=10nF package="100 mil [THT, multilayer]"]
  C16 = Ceramic Capacitor [capacitance=10nF package="100 mil [THT, multilayer]"]

nets:
  N1: HousingConnect1.pin1, 4660.pin2, 4660.pin3
  N2: HousingConnect1.pin2, 4660_2.pin9, 4660_2.pin10
  N3: HousingConnect1.pin3, 4660_2.pin2, 4660_2.pin3
  N4: HousingConnect1.pin4, 4660.pin9, 4660.pin10
  N5: HousingConnect1.pin5, InverterOutput.pin2
  N6: HousingConnect1.pin6, InverterOutput.pin3
  N7: HousingConnect1.pin7, 4660_4.pin2, 4660_4.pin3
  N8: HousingConnect1.pin8, 4660_4.pin9, 4660_4.pin10
  N9: HousingConnect1.pin9, 4660_3.pin2, 4660_3.pin3
  N10: HousingConnect1.pin10, 4660_3.pin9, 4660_3.pin10
  N11: 4660.pin1, 4660.pin8, 4660_9.pin11, R1.Pin_0
  N12: 4660.pin4, 4660.pin11, InverterOutput.pin1
  N13: 4660.pin5, 4660.pin6, Con_INV3/4.pin2
  N14: 4660.pin7, 4660_2.pin7, 4660_3.pin7, 4660_4.pin7, Con_INV1/2_V+/-.pin5, 4660_5.pin7, 4660_6.pin7, 4660_7.pin7, 4660_8.pin7, 4660_9.pin7, 4660_10.pin7, 4660_11.pin7, 4660_12.pin7, 4660_13.pin7, 4660_14.pin7
  N15: 4660.pin12, 4660.pin13, Con_INV3/4.pin1
  N16: 4660.pin14, 4660_2.pin14, 4660_3.pin14, 4660_4.pin14, Con_INV1/2_V+/-.pin6, 4660_5.pin14, 4660_6.pin14, 4660_7.pin14, 4660_8.pin14, 4660_9.pin14, 4660_10.pin14, 4660_11.pin14, 4660_12.pin14, 4660_13.pin14, 4660_14.pin14
  N17: 4660_2.pin1, 4660_2.pin8, 4660_9.pin1, R6.Pin_1
  N18: 4660_2.pin4, 4660_2.pin11, InverterOutput.pin4
  N19: 4660_2.pin5, 4660_2.pin6, Con_INV3/4.pin4
  N20: 4660_2.pin12, 4660_2.pin13, Con_INV3/4.pin3
  N21: 4660_3.pin1, 4660_3.pin8, R20.Pin_0, 4660_10.pin11
  N22: 4660_3.pin4, 4660_3.pin11, InverterOutput.pin5
  N23: 4660_3.pin5, 4660_3.pin6, Con_INV1/2_V+/-.pin3
  N24: 4660_3.pin12, 4660_3.pin13, Con_INV1/2_V+/-.pin4
  N25: 4660_4.pin1, 4660_4.pin8, R15.Pin_0, 4660_10.pin1
  N26: 4660_4.pin4, 4660_4.pin11, InverterOutput.pin6
  N27: 4660_4.pin5, 4660_4.pin6, Con_INV1/2_V+/-.pin1
  N28: 4660_4.pin12, 4660_4.pin13, Con_INV1/2_V+/-.pin2
  N29: 4660_5.pin1, R7.Pin_1, R8.Pin_0
  N30: 4660_5.pin2, 4660_5.pin3, 4660_6.pin2, 4660_6.pin3, 4660_7.pin2, 4660_7.pin3, 4660_8.pin2, 4660_8.pin3, 4660_9.pin2, 4660_9.pin3, VolToneOut.pin1
  N31: 4660_5.pin4, R8.Pin_1, R9.Pin_0
  N32: 4660_5.pin5, BC-3/4.pin1
  N33: 4660_5.pin6, BC-3/4.pin2
  N34: 4660_5.pin8, R3.Pin_1, R4.Pin_0
  N35: 4660_5.pin9, 4660_5.pin10, 4660_6.pin9, 4660_6.pin10, 4660_7.pin9, 4660_7.pin10, 4660_8.pin9, 4660_8.pin10, 4660_9.pin9, 4660_9.pin10, VolToneOut.pin2
  N36: 4660_5.pin11, R2.Pin_1, R3.Pin_0
  N37: 4660_5.pin12, AD-3/4.pin2
  N38: 4660_5.pin13, AD-3/4.pin1
  N39: 4660_6.pin1, R9.Pin_1, R10.Pin_0
  N40: 4660_6.pin5, BC-3/4.pin5
  N41: 4660_6.pin6, BC-3/4.pin6
  N42: 4660_6.pin8, R5.Pin_1
  N43: 4660_6.pin11, R4.Pin_1, R5.Pin_0
  N44: 4660_6.pin12, AD-3/4.pin6
  N45: 4660_6.pin13, AD-3/4.pin5
  N46: 4660_7.pin1, C6.0
  N47: 4660_7.pin4, C5.0
  N48: 4660_7.pin5, BC-3/4.pin8
  N49: 4660_7.pin6, BC-3/4.pin7
  N50: 4660_7.pin8, C4.1
  N51: 4660_7.pin11, C3.1
  N52: 4660_7.pin12, AD-3/4.pin7
  N53: 4660_7.pin13, AD-3/4.pin8
  N54: 4660_8.pin1, C8.0
  N55: 4660_8.pin4, C7.0
  N56: 4660_8.pin5, BC-3/4.pin9
  N57: 4660_8.pin6, BC-3/4.pin10
  N58: 4660_8.pin8, C2.1
  N59: 4660_8.pin11, C1.1
  N60: 4660_8.pin12, AD-3/4.pin10
  N61: 4660_8.pin13, AD-3/4.pin9
  N62: 4660_9.pin4, R6.Pin_0, R7.Pin_0
  N63: 4660_9.pin5, BC-3/4.pin4
  N64: 4660_9.pin6, BC-3/4.pin3
  N65: 4660_9.pin8, R1.Pin_1, R2.Pin_0
  N66: 4660_9.pin12, AD-3/4.pin3
  N67: 4660_9.pin13, AD-3/4.pin4
  N68: Tone4.Pin_1, C4.0, C3.0, C2.0, C1.0
  N69: VolToneOut.pin3, 4660_10.pin9, 4660_10.pin10, 4660_11.pin9, 4660_11.pin10, 4660_12.pin9, 4660_12.pin10, 4660_13.pin9, 4660_13.pin10, 4660_14.pin9, 4660_14.pin10
  N70: VolToneOut.pin4, 4660_10.pin2, 4660_10.pin3, 4660_11.pin2, 4660_11.pin3, 4660_12.pin2, 4660_12.pin3, 4660_13.pin2, 4660_13.pin3, 4660_14.pin2, 4660_14.pin3
  N71: C5.1, C6.1, C7.1, C8.1, Tone3.Pin_1
  N72: R11.Pin_0, R12.Pin_1, 4660_13.pin1
  N73: R12.Pin_0, R13.Pin_1, 4660_14.pin4
  N74: R13.Pin_0, R14.Pin_1, 4660_14.pin1
  N75: R14.Pin_0, R15.Pin_1, 4660_10.pin4
  N76: Tone5.Pin_1, C9.1
  N77: Tone6.Pin_1, C10.0, C12.0, C14.0, C16.0
  N78: R16.Pin_0, R17.Pin_1, 4660_13.pin11
  N79: R16.Pin_1, 4660_13.pin8
  N80: R17.Pin_0, R18.Pin_1, 4660_14.pin8
  N81: R18.Pin_0, R19.Pin_1, 4660_14.pin11
  N82: R19.Pin_0, R20.Pin_1, 4660_10.pin8
  N83: BC-3/5.pin1, 4660_14.pin5
  N84: BC-3/5.pin2, 4660_14.pin6
  N85: BC-3/5.pin3, 4660_10.pin6
  N86: BC-3/5.pin4, 4660_10.pin5
  N87: BC-3/5.pin5, 4660_13.pin5
  N88: BC-3/5.pin6, 4660_13.pin6
  N89: BC-3/5.pin7, 4660_12.pin6
  N90: BC-3/5.pin8, 4660_12.pin5
  N91: BC-3/5.pin9, 4660_11.pin5
  N92: BC-3/5.pin10, 4660_11.pin6
  N93: AD-3/5.pin1, 4660_14.pin13
  N94: AD-3/5.pin2, 4660_14.pin12
  N95: AD-3/5.pin3, 4660_10.pin12
  N96: AD-3/5.pin4, 4660_10.pin13
  N97: AD-3/5.pin5, 4660_13.pin13
  N98: AD-3/5.pin6, 4660_13.pin12
  N99: AD-3/5.pin7, 4660_12.pin12
  N100: AD-3/5.pin8, 4660_12.pin13
  N101: AD-3/5.pin9, 4660_11.pin13
  N102: AD-3/5.pin10, 4660_11.pin12
  N103: 4660_11.pin1, C15.0
  N104: 4660_11.pin4, C13.0
  N105: 4660_11.pin8, C14.1
  N106: 4660_11.pin11, C16.1
  N107: 4660_12.pin1, C11.0
  N108: 4660_12.pin4, C9.0
  N109: 4660_12.pin8, C10.1
  N110: 4660_12.pin11, C12.1

notes:
  A1
  B1
  Y1
  X1
  +V
  -V
  X2
  A2
  B2
  Y2
  Y3
  Y4
  B3
  A3
  A4
  B4
  Amp GND
  Amp HOT
  BC1
  AD1
  BC2
  AD2
  BC3
  BC4
  AD4
  AD3
  VT3
  VT4
