# Fritzing sketch Inverter (saved by Fritzing 0.8.7b)
circuit board: 10cm x 5cm
breadboards: 1

parts:
  Output = female pin header, 2 pins [form="♀ (female)"]
  Input = female alternating pin header, 2 pins [form="♀ (female)"]
  MAX4679 = IC, DIP package, 16 pins [chip_label=MAX4679]
  Input1 = female alternating pin header, 2 pins [form="♀ (female)"]
  Output1 = female pin header, 2 pins [form="♀ (female)"]
  4660 = IC, DIP package, 14 pins [chip_label=CD4660]

nets:
  N1: Output.pin1, MAX4679.pin3, MAX4679.pin10
  N2: Output.pin2, MAX4679.pin7, MAX4679.pin14
  N3: Input.pin1, MAX4679.pin11, MAX4679.pin15
  N4: Input.pin2, MAX4679.pin2, MAX4679.pin6
  N5: Input1.pin1, 4660.pin9, 4660.pin11
  N6: Input1.pin2, 4660.pin1, 4660.pin3
  N7: Output1.pin1, 4660.pin2, 4660.pin8
  N8: Output1.pin2, 4660.pin4, 4660.pin10

notes:
  Inverter
  1 & 2 to invert
  3 & 4 to go straight
  B & C to go straight
  A & D to invert
