# Fritzing sketch InputStage (saved by Fritzing 0.8.7b)
circuit board: 10.3434cm x 5.70443cm
breadboards: 1

parts:
  Output1 = female pin header, 2 pins [form="♀ (female)"]
  Input1 = female pin header, 2 pins [form="♀ (female)"]
  4660 = IC, DIP package, 14 pins [chip_label=CD4660]
  Power = female pin header, 2 pins [form="♀ (female)"]
  Input2 = female pin header, 2 pins [form="♀ (female)"]
  Output2 = female pin header, 2 pins [form="♀ (female)"]
  4660_2 = IC, DIP package, 14 pins [chip_label=CD4660]
  Input3 = female pin header, 2 pins [form="♀ (female)"]
  Input4 = female pin header, 2 pins [form="♀ (female)"]
  Output3 = female pin header, 2 pins [form="♀ (female)"]
  Output4 = female pin header, 2 pins [form="♀ (female)"]
  4660_3 = IC, DIP package, 14 pins [chip_label=CD4660]
  4660_4 = IC, DIP package, 14 pins [chip_label=CD4660]
  InputShield = female pin header, 1 pin [form="♀ (female)"]  # not connected
  AD1 = female pin header, 1 pin [form="♀ (female)"]
  BC1 = female pin header, 1 pin [form="♀ (female)"]
  AD2 = female pin header, 1 pin [form="♀ (female)"]
  BC2 = female pin header, 1 pin [form="♀ (female)"]
  AD3 = female pin header, 1 pin [form="♀ (female)"]
  BC3 = female pin header, 1 pin [form="♀ (female)"]
  AD4 = female pin header, 1 pin [form="♀ (female)"]
  BC4 = female pin header, 1 pin [form="♀ (female)"]

nets:
  N1: Output1.pin1, 4660.pin2, 4660.pin8
  N2: Output1.pin2, 4660.pin4, 4660.pin10
  N3: Input1.pin1, 4660.pin9, 4660.pin11
  N4: Input1.pin2, 4660.pin1, 4660.pin3
  N5: 4660.pin5, 4660.pin6, BC1.pin1
  N6: 4660.pin7, Power.pin2, 4660_2.pin7, 4660_3.pin7, 4660_4.pin7
  N7: 4660.pin12, 4660.pin13, AD1.pin1
  N8: 4660.pin14, Power.pin1, 4660_2.pin14, 4660_3.pin14, 4660_4.pin14
  N9: Input2.pin1, 4660_2.pin9, 4660_2.pin11
  N10: Input2.pin2, 4660_2.pin1, 4660_2.pin3
  N11: Output2.pin1, 4660_2.pin2, 4660_2.pin8
  N12: Output2.pin2, 4660_2.pin4, 4660_2.pin10
  N13: 4660_2.pin5, 4660_2.pin6, BC2.pin1
  N14: 4660_2.pin12, 4660_2.pin13, AD2.pin1
  N15: Input3.pin1, 4660_3.pin9, 4660_3.pin11
  N16: Input3.pin2, 4660_3.pin1, 4660_3.pin3
  N17: Input4.pin1, 4660_4.pin9, 4660_4.pin11
  N18: Input4.pin2, 4660_4.pin1, 4660_4.pin3
  N19: Output3.pin1, 4660_3.pin2, 4660_3.pin8
  N20: Output3.pin2, 4660_3.pin4, 4660_3.pin10
  N21: Output4.pin1, 4660_4.pin2, 4660_4.pin8
  N22: Output4.pin2, 4660_4.pin4, 4660_4.pin10
  N23: 4660_3.pin5, 4660_3.pin6, BC3.pin1
  N24: 4660_3.pin12, 4660_3.pin13, AD3.pin1
  N25: 4660_4.pin5, 4660_4.pin6, BC4.pin1
  N26: 4660_4.pin12, 4660_4.pin13, AD4.pin1

notes:
  Input Stage
  +5V
  -5V
