# Fritzing sketch InputStage_Vol_Tone 01 (saved by Fritzing 0.8.7b)
circuit board: 13.6869cm x 5.75091cm
breadboards: 1

parts:
  Input1 = female pin header, 2 pins [form="♀ (female)"]
  4660 = IC, DIP package, 14 pins [chip_label=CD4660]
  Power = female pin header, 2 pins [form="♀ (female)"]
  Input2 = female pin header, 2 pins [form="♀ (female)"]
  4660_2 = IC, DIP package, 14 pins [chip_label=CD4660]
  Input3 = female pin header, 2 pins [form="♀ (female)"]
  Input4 = female pin header, 2 pins [form="♀ (female)"]
  4660_3 = IC, DIP package, 14 pins [chip_label=CD4660]
  4660_4 = IC, DIP package, 14 pins [chip_label=CD4660]
  AD1 = female pin header, 1 pin [form="♀ (female)"]
  BC1 = female pin header, 1 pin [form="♀ (female)"]
  AD2 = female pin header, 1 pin [form="♀ (female)"]
  BC2 = female pin header, 1 pin [form="♀ (female)"]
  AD3 = female pin header, 1 pin [form="♀ (female)"]
  BC3 = female pin header, 1 pin [form="♀ (female)"]
  AD4 = female pin header, 1 pin [form="♀ (female)"]
  BC4 = female pin header, 1 pin [form="♀ (female)"]
  4660_5 = IC, DIP package, 14 pins [chip_label=CD4660]
  4660_6 = IC, DIP package, 14 pins [chip_label=CD4660]
  4660_7 = IC, DIP package, 14 pins [chip_label=CD4660]
  R6 = Resistor [tolerance=±5% resistance=47k package=THT]
  R7 = Resistor [tolerance=±5% resistance=47k package=THT]
  R8 = Resistor [tolerance=±5% resistance=47k package=THT]
  R9 = Resistor [tolerance=±5% resistance=47k package=THT]
  R10 = Resistor [tolerance=±5% resistance=47k package=THT]
  Output1Y = female pin header, 1 pin [form="♀ (female)"]
  Vout1 = female pin header, 2 pins [form="♀ (female)"]
  BC5 = female pin header, 2 pins [form="♀ (female)"]
  BC6 = female pin header, 2 pins [form="♀ (female)"]
  BC7 = female pin header, 2 pins [form="♀ (female)"]
  AD5 = female pin header, 2 pins [form="♀ (female)"]
  AD6 = female pin header, 2 pins [form="♀ (female)"]
  AD7 = female pin header, 2 pins [form="♀ (female)"]
  R11 = Resistor [tolerance=±5% resistance=47k package=THT]
  R12 = Resistor [tolerance=±5% resistance=47k package=THT]
  R13 = Resistor [tolerance=±5% resistance=47k package=THT]
  R14 = Resistor [tolerance=±5% resistance=47k package=THT]
  R15 = Resistor [tolerance=±5% resistance=47k package=THT]
  Output2Y = female pin header, 1 pin [form="♀ (female)"]
  AD8 = female pin header, 2 pins [form="♀ (female)"]
  BC8 = female pin header, 2 pins [form="♀ (female)"]
  BC9 = female pin header, 2 pins [form="♀ (female)"]
  AD9 = female pin header, 2 pins [form="♀ (female)"]
  Vout2 = female pin header, 2 pins [form="♀ (female)"]
  BC10 = female pin header, 2 pins [form="♀ (female)"]
  AD10 = female pin header, 2 pins [form="♀ (female)"]
  4660_8 = IC, DIP package, 14 pins [chip_label=CD4660]
  4660_9 = IC, DIP package, 14 pins [chip_label=CD4660]
  4660_10 = IC, DIP package, 14 pins [chip_label=CD4660]
  R16 = Resistor [tolerance=±5% resistance=47k package=THT]
  R17 = Resistor [tolerance=±5% resistance=47k package=THT]
  R18 = Resistor [tolerance=±5% resistance=47k package=THT]
  R19 = Resistor [tolerance=±5% resistance=47k package=THT]
  R20 = Resistor [tolerance=±5% resistance=47k package=THT]
  R21 = Resistor [tolerance=±5% resistance=47k package=THT]
  R22 = Resistor [tolerance=±5% resistance=47k package=THT]
  R23 = Resistor [tolerance=±5% resistance=47k package=THT]
  R24 = Resistor [tolerance=±5% resistance=47k package=THT]
  R25 = Resistor [tolerance=±5% resistance=47k package=THT]
  Output2Y1 = female pin header, 1 pin [form="♀ (female)"]
  Output2Y2 = female pin header, 1 pin [form="♀ (female)"]
  4660_11 = IC, DIP package, 14 pins [chip_label=CD4660]
  4660_12 = IC, DIP package, 14 pins [chip_label=CD4660]
  BC11 = female pin header, 2 pins [form="♀ (female)"]
  AD11 = female pin header, 2 pins [form="♀ (female)"]
  AD12 = female pin header, 2 pins [form="♀ (female)"]
  BC12 = female pin header, 2 pins [form="♀ (female)"]
  C9 = Ceramic Capacitor [capacitance=47nF package="100 mil [THT, multilayer]"]
  C10 = Ceramic Capacitor [capacitance=33nF package="100 mil [THT, multilayer]"]
  C11 = Ceramic Capacitor [capacitance=22nF package="100 mil [THT, multilayer]"]
  C12 = Ceramic Capacitor [capacitance=10nF package="100 mil [THT, multilayer]"]
  ToneR1 = Resistor [tolerance=±5% resistance=100k package=THT]
  C13 = Ceramic Capacitor [capacitance=47nF package="100 mil [THT, multilayer]"]
  C14 = Ceramic Capacitor [capacitance=33nF package="100 mil [THT, multilayer]"]
  C15 = Ceramic Capacitor [capacitance=22nF package="100 mil [THT, multilayer]"]
  C16 = Ceramic Capacitor [capacitance=10nF package="100 mil [THT, multilayer]"]
  ToneR2 = Resistor [tolerance=±5% resistance=100k package=THT]
  AD13 = female pin header, 2 pins [form="♀ (female)"]
  BC13 = female pin header, 2 pins [form="♀ (female)"]
  BC14 = female pin header, 2 pins [form="♀ (female)"]
  AD14 = female pin header, 2 pins [form="♀ (female)"]
  4660_13 = IC, DIP package, 14 pins [chip_label=CD4660]
  4660_14 = IC, DIP package, 14 pins [chip_label=CD4660]
  C17 = Ceramic Capacitor [capacitance=47nF package="100 mil [THT, multilayer]"]
  C18 = Ceramic Capacitor [capacitance=47nF package="100 mil [THT, multilayer]"]
  C19 = Ceramic Capacitor [capacitance=33nF package="100 mil [THT, multilayer]"]
  C20 = Ceramic Capacitor [capacitance=33nF package="100 mil [THT, multilayer]"]
  C21 = Ceramic Capacitor [capacitance=22nF package="100 mil [THT, multilayer]"]
  C22 = Ceramic Capacitor [capacitance=22nF package="100 mil [THT, multilayer]"]
  C23 = Ceramic Capacitor [capacitance=10nF package="100 mil [THT, multilayer]"]
  C24 = Ceramic Capacitor [capacitance=10nF package="100 mil [THT, multilayer]"]
  ToneR3 = Resistor [tolerance=±5% resistance=100k package=THT]
  ToneR4 = Resistor [tolerance=±5% resistance=100k package=THT]
  Amp = female pin header, 2 pins [form="♀ (female)"]  # not connected

nets:
  N1: Input1.pin1, 4660.pin9, 4660.pin11
  N2: Input1.pin2, 4660.pin1, 4660.pin3
  N3: 4660.pin2, 4660.pin8, 4660_5.pin1, R10.Pin_0
  N4: 4660.pin4, 4660.pin10, Output1Y.pin1
  N5: 4660.pin5, 4660.pin6, BC1.pin1
  N6: 4660.pin7, Power.pin2, 4660_2.pin7, 4660_3.pin7, 4660_4.pin7, 4660_5.pin7, 4660_6.pin7, 4660_7.pin7, 4660_8.pin7, 4660_9.pin7, 4660_10.pin7, 4660_11.pin7, 4660_12.pin7, 4660_13.pin7, 4660_14.pin7
  N7: 4660.pin12, 4660.pin13, AD1.pin1
  N8: 4660.pin14, Power.pin1, 4660_2.pin14, 4660_3.pin14, 4660_4.pin14, 4660_5.pin14, 4660_6.pin14, 4660_7.pin14, 4660_8.pin14, 4660_9.pin14, 4660_10.pin14, 4660_11.pin14, 4660_12.pin14, 4660_13.pin14, 4660_14.pin14
  N9: Input2.pin1, 4660_2.pin9, 4660_2.pin11
  N10: Input2.pin2, 4660_2.pin1, 4660_2.pin3
  N11: 4660_2.pin2, 4660_2.pin8, 4660_5.pin11, R15.Pin_0
  N12: 4660_2.pin4, 4660_2.pin10, Output2Y.pin1
  N13: 4660_2.pin5, 4660_2.pin6, BC2.pin1
  N14: 4660_2.pin12, 4660_2.pin13, AD2.pin1
  N15: Input3.pin1, 4660_3.pin9, 4660_3.pin11
  N16: Input3.pin2, 4660_3.pin1, 4660_3.pin3
  N17: Input4.pin1, 4660_4.pin9, 4660_4.pin11
  N18: Input4.pin2, 4660_4.pin1, 4660_4.pin3
  N19: 4660_3.pin2, 4660_3.pin8, 4660_9.pin1, R24.Pin_0
  N20: 4660_3.pin4, 4660_3.pin10, Output2Y1.pin1
  N21: 4660_3.pin5, 4660_3.pin6, BC3.pin1
  N22: 4660_3.pin12, 4660_3.pin13, AD3.pin1
  N23: 4660_4.pin2, 4660_4.pin8, 4660_9.pin11, R25.Pin_0
  N24: 4660_4.pin4, 4660_4.pin10, Output2Y2.pin1
  N25: 4660_4.pin5, 4660_4.pin6, BC4.pin1
  N26: 4660_4.pin12, 4660_4.pin13, AD4.pin1
  N27: 4660_5.pin2, 4660_5.pin3, 4660_6.pin2, 4660_6.pin3, 4660_6.pin4, 4660_7.pin2, 4660_7.pin3, R7.Pin_1, R8.Pin_0, Vout1.pin2, 4660_11.pin1, 4660_11.pin4, 4660_12.pin1, 4660_12.pin4
  N28: 4660_5.pin4, R9.Pin_0, R10.Pin_1
  N29: 4660_5.pin5, BC5.pin1
  N30: 4660_5.pin6, BC5.pin2
  N31: 4660_5.pin8, R14.Pin_0, R15.Pin_1
  N32: 4660_5.pin9, 4660_5.pin10, 4660_6.pin9, 4660_6.pin10, 4660_7.pin9, 4660_7.pin11, Vout1.pin1, 4660_11.pin8, 4660_11.pin11, 4660_12.pin8, 4660_12.pin11
  N33: 4660_5.pin12, AD5.pin2
  N34: 4660_5.pin13, AD5.pin1
  N35: 4660_6.pin1, R7.Pin_0, R9.Pin_1
  N36: 4660_6.pin5, BC6.pin1
  N37: 4660_6.pin6, BC6.pin2
  N38: 4660_6.pin8, R12.Pin_1, R13.Pin_0
  N39: 4660_6.pin11, R12.Pin_0, R14.Pin_1
  N40: 4660_6.pin12, AD6.pin2
  N41: 4660_6.pin13, AD6.pin1
  N42: 4660_7.pin1, R6.Pin_0, R8.Pin_1
  N43: 4660_7.pin4, R6.Pin_1, ToneR1.Pin_0
  N44: 4660_7.pin5, BC7.pin1
  N45: 4660_7.pin6, BC7.pin2
  N46: 4660_7.pin8, R11.Pin_1, ToneR2.Pin_0
  N47: 4660_7.pin10, R11.Pin_0, R13.Pin_1
  N48: 4660_7.pin12, AD7.pin2
  N49: 4660_7.pin13, AD7.pin1
  N50: AD8.pin1, 4660_9.pin13
  N51: AD8.pin2, 4660_9.pin12
  N52: BC8.pin1, 4660_10.pin5
  N53: BC8.pin2, 4660_10.pin6
  N54: BC9.pin1, 4660_9.pin5
  N55: BC9.pin2, 4660_9.pin6
  N56: AD9.pin1, 4660_10.pin13
  N57: AD9.pin2, 4660_10.pin12
  N58: Vout2.pin1, 4660_8.pin9, 4660_8.pin10, 4660_9.pin9, 4660_9.pin10, 4660_10.pin9, 4660_10.pin11, 4660_13.pin8, 4660_13.pin11, 4660_14.pin8, 4660_14.pin11
  N59: Vout2.pin2, 4660_8.pin2, 4660_8.pin3, 4660_8.pin4, 4660_9.pin2, 4660_9.pin3, 4660_10.pin2, 4660_10.pin3, R19.Pin_1, R21.Pin_0, 4660_13.pin1, 4660_13.pin4, 4660_14.pin1, 4660_14.pin4
  N60: BC10.pin1, 4660_8.pin5
  N61: BC10.pin2, 4660_8.pin6
  N62: AD10.pin1, 4660_8.pin13
  N63: AD10.pin2, 4660_8.pin12
  N64: 4660_8.pin1, R19.Pin_0, R23.Pin_1
  N65: 4660_8.pin8, R18.Pin_1, R20.Pin_0
  N66: 4660_8.pin11, R18.Pin_0, R22.Pin_1
  N67: 4660_9.pin4, R23.Pin_0, R24.Pin_1
  N68: 4660_9.pin8, R22.Pin_0, R25.Pin_1
  N69: 4660_10.pin1, R17.Pin_0, R21.Pin_1
  N70: 4660_10.pin4, R17.Pin_1, ToneR3.Pin_0
  N71: 4660_10.pin8, R16.Pin_1, ToneR4.Pin_0
  N72: 4660_10.pin10, R16.Pin_0, R20.Pin_1
  N73: 4660_11.pin2, C10.0
  N74: 4660_11.pin3, C9.0
  N75: 4660_11.pin5, BC12.pin1
  N76: 4660_11.pin6, BC12.pin2
  N77: 4660_11.pin9, C13.1
  N78: 4660_11.pin10, C14.1
  N79: 4660_11.pin12, AD12.pin2
  N80: 4660_11.pin13, AD12.pin1
  N81: 4660_12.pin2, C12.0
  N82: 4660_12.pin3, C11.0
  N83: 4660_12.pin5, BC11.pin1
  N84: 4660_12.pin6, BC11.pin2
  N85: 4660_12.pin9, C15.1
  N86: 4660_12.pin10, C16.1
  N87: 4660_12.pin12, AD11.pin2
  N88: 4660_12.pin13, AD11.pin1
  N89: C9.1, C10.1, C11.1, C12.1, ToneR1.Pin_1
  N90: C13.0, C14.0, C15.0, C16.0, ToneR2.Pin_1
  N91: AD13.pin1, 4660_14.pin13
  N92: AD13.pin2, 4660_14.pin12
  N93: BC13.pin1, 4660_14.pin5
  N94: BC13.pin2, 4660_14.pin6
  N95: BC14.pin1, 4660_13.pin5
  N96: BC14.pin2, 4660_13.pin6
  N97: AD14.pin1, 4660_13.pin13
  N98: AD14.pin2, 4660_13.pin12
  N99: 4660_13.pin2, C19.0
  N100: 4660_13.pin3, C18.0
  N101: 4660_13.pin9, C17.1
  N102: 4660_13.pin10, C20.1
  N103: 4660_14.pin2, C24.0
  N104: 4660_14.pin3, C21.0
  N105: 4660_14.pin9, C22.1
  N106: 4660_14.pin10, C23.1
  N107: C17.0, C20.0, C22.0, C23.0, ToneR4.Pin_1
  N108: C18.1, C19.1, C21.1, C24.1, ToneR3.Pin_1

notes:
  Input Stage
  +5V
  -5V
  VT3
  VT4
  VT2
  VT1
  Sig
  gnd
