# Fritzing sketch Inverter (saved by Fritzing 0.8.7b)
circuit board: 10cm x 5cm
breadboards: 1

parts:
  Output = female pin header, 2 pins [form="♀ (female)"]
  Output1 = female pin header, 2 pins [form="♀ (female)"]
  Input = female pin header, 2 pins [form="♀ (female)"]
  Input1 = female pin header, 2 pins [form="♀ (female)"]
  MAX4679 = IC, DIP package, 16 pins [chip_label=MAX4679]
  4660 = IC, DIP package, 14 pins [chip_label=CD4660]
  Power = female pin header, 2 pins [form="♀ (female)"]
  Control = female pin header, 4 pins [form="♀ (female)"]
  Control1 = female pin header, 4 pins [form="♀ (female)"]

nets:
  N1: Output.pin1, MAX4679.pin3, MAX4679.pin10
  N2: Output.pin2, MAX4679.pin7, MAX4679.pin14
  N3: Output1.pin1, 4660.pin2, 4660.pin8
  N4: Output1.pin2, 4660.pin4, 4660.pin10
  N5: Input.pin1, MAX4679.pin11, MAX4679.pin15
  N6: Input.pin2, MAX4679.pin2, MAX4679.pin6
  N7: Input1.pin1, 4660.pin9, 4660.pin11
  N8: Input1.pin2, 4660.pin1, 4660.pin3
  N9: MAX4679.pin1, MAX4679.pin16, Control1.pin1
  N10: MAX4679.pin4, 4660.pin7, Power.pin2
  N11: MAX4679.pin8, MAX4679.pin9, Control1.pin2
  N12: MAX4679.pin12, MAX4679.pin13, 4660.pin14, Power.pin1
  N13: 4660.pin5, Control.pin4
  N14: 4660.pin12, 4660.pin13, Control.pin1

notes:
  Inverter
  1 & 2 to invert
  B & C to go straight
  A & D to invert
  +5V
  -5V
  GND
  B
  C
  D
  A
  4
  3
  2
  1
  3 & 4 to go straight
