# Fritzing sketch OutputStage 04_03 (saved by Fritzing 0.8.7b)
circuit board: 14.4182cm x 6.14944cm
breadboards: 1

parts:
  Con_INV3/4 = female pin header, 4 pins [form="♀ (female)"]  # not connected
  InverterOutput = female pin header, 6 pins [form="♀ (female)"]
  Con_INV1/2_V+/- = female pin header, 6 pins [form="♀ (female)"]
  4660 = IC, DIP package, 14 pins [chip_label=CD4660]
  4660_2 = IC, DIP package, 14 pins [chip_label=CD4660]
  4660_3 = IC, DIP package, 14 pins [chip_label=CD4660]
  AD-4 = female pin header, 10 pins [form="♀ (female)"]  # not connected
  BC-3 = female pin header, 10 pins [form="♀ (female)"]  # not connected
  R1 = Resistor [tolerance=±5% resistance=100k package=THT]
  R2 = Resistor [tolerance=±5% resistance=100k package=THT]
  R3 = Resistor [tolerance=±5% resistance=100k package=THT]
  R4 = Resistor [tolerance=±5% resistance=100k package=THT]
  R5 = Resistor [tolerance=±5% resistance=100k package=THT]
  Tone4 = Resistor [tolerance=±5% resistance=220k package=THT]
  C4 = Ceramic Capacitor [capacitance=47nF package="100 mil [THT, multilayer]"]
  C3 = Ceramic Capacitor [capacitance=33nF package="100 mil [THT, multilayer]"]
  C2 = Ceramic Capacitor [capacitance=22nF package="100 mil [THT, multilayer]"]
  C1 = Ceramic Capacitor [capacitance=10nF package="100 mil [THT, multilayer]"]
  VolToneOut = female pin header, 4 pins [form="♀ (female)"]
  BC-1 = female pin header, 10 pins [form="♀ (female)"]  # not connected
  AD-2 = female pin header, 10 pins [form="♀ (female)"]  # not connected
  4660_4 = IC, DIP package, 14 pins [chip_label=CD4660]
  4660_5 = IC, DIP package, 14 pins [chip_label=CD4660]
  4660_6 = IC, DIP package, 14 pins [chip_label=CD4660]
  4660_7 = IC, DIP package, 14 pins [chip_label=CD4660]
  Controls_BC1 = female pin header, 6 pins [form="♀ (female)"]
  Controls_BC3 = female pin header, 8 pins [form="♀ (female)"]
  Controls_AD1_AmpGnd = female pin header, 6 pins [form="♀ (female)"]
  Controls_BC2 = female pin header, 6 pins [form="♀ (female)"]

nets:
  N1: InverterOutput.pin1, 4660.pin1, 4660_2.pin2, 4660_2.pin3, 4660_2.pin9, 4660_3.pin1
  N2: InverterOutput.pin3, 4660_5.pin2, 4660_5.pin3, 4660_5.pin9, 4660_5.pin10, 4660_6.pin3, 4660_6.pin9, 4660_7.pin2, 4660_7.pin3, 4660_7.pin9, 4660_7.pin10
  N3: InverterOutput.pin4, 4660.pin2, 4660.pin3
  N4: InverterOutput.pin5, 4660_2.pin1, 4660_2.pin4, 4660_2.pin10, 4660_3.pin4, 4660_4.pin1
  N5: InverterOutput.pin6, 4660_4.pin2, 4660_4.pin3
  N6: Con_INV1/2_V+/-.pin5, 4660.pin7, 4660_2.pin7, 4660_3.pin7, 4660_4.pin7, 4660_5.pin7, 4660_6.pin7, 4660_7.pin7
  N7: Con_INV1/2_V+/-.pin6, 4660.pin14, 4660_2.pin14, 4660_3.pin14, 4660_4.pin14, 4660_5.pin14, 4660_6.pin14, 4660_7.pin14
  N8: 4660.pin4, 4660.pin10, VolToneOut.pin2
  N9: 4660.pin5, Controls_BC2.pin6
  N10: 4660.pin6, Controls_BC2.pin5
  N11: 4660.pin8, 4660_2.pin8, 4660_3.pin8, VolToneOut.pin4, 4660_4.pin8, 4660_4.pin11
  N12: 4660.pin9, 4660.pin11, 4660_2.pin11, 4660_3.pin10, VolToneOut.pin1, 4660_4.pin9
  N13: 4660.pin12, Controls_BC3.pin2
  N14: 4660.pin13, Controls_BC3.pin1
  N15: 4660_2.pin5, Controls_BC3.pin4
  N16: 4660_2.pin6, Controls_BC3.pin3
  N17: 4660_2.pin12, Controls_BC3.pin5
  N18: 4660_2.pin13, Controls_BC3.pin6
  N19: 4660_3.pin2, 4660_3.pin3
  N20: 4660_3.pin5, 4660_3.pin12, Controls_BC2.pin4
  N21: 4660_3.pin6, 4660_3.pin13, Controls_BC2.pin3
  N22: 4660_3.pin9, 4660_3.pin11, R1.Pin_0, 4660_7.pin11
  N23: R1.Pin_1, R2.Pin_0, 4660_7.pin8
  N24: R2.Pin_1, R3.Pin_0, 4660_5.pin11
  N25: R3.Pin_1, R4.Pin_0, 4660_5.pin8
  N26: R4.Pin_1, R5.Pin_0, 4660_6.pin8
  N27: Tone4.Pin_0, C4.0, C3.0, C2.0, C1.0
  N28: C4.1, 4660_5.pin4
  N29: C3.1, 4660_5.pin1
  N30: C2.1, 4660_7.pin4
  N31: C1.1, 4660_7.pin1
  N32: VolToneOut.pin3, 4660_4.pin4, 4660_4.pin10
  N33: 4660_4.pin5, Controls_BC1.pin6
  N34: 4660_4.pin6, Controls_BC1.pin5
  N35: 4660_4.pin12, Controls_BC3.pin7
  N36: 4660_4.pin13, Controls_BC3.pin8
  N37: 4660_5.pin5, Controls_BC1.pin4
  N38: 4660_5.pin6, Controls_BC1.pin3
  N39: 4660_5.pin12, Controls_AD1_AmpGnd.pin4
  N40: 4660_5.pin13, Controls_AD1_AmpGnd.pin3
  N41: 4660_6.pin1, 4660_6.pin2
  N42: 4660_6.pin5, Controls_BC1.pin1
  N43: 4660_6.pin6, Controls_BC1.pin2
  N44: 4660_6.pin10, 4660_6.pin11, 4660_6.pin12, 4660_6.pin13
  N45: 4660_7.pin5, Controls_BC2.pin1
  N46: 4660_7.pin6, Controls_BC2.pin2
  N47: 4660_7.pin12, Controls_AD1_AmpGnd.pin2
  N48: 4660_7.pin13, Controls_AD1_AmpGnd.pin1

notes:
  Y1
  +V
  -V
  Y2
  Y3
  Y4
  Amp GND
  Amp HOT
  VT3
  VT4
  VT1
  VT2
  S1
