# Fritzing sketch POC Breadboard (saved by Fritzing 0.9.0b)
breadboards: 4

parts:
  CD3 = CD4066 Quad Analog Switch [part_number=4066 package="DIP (Dual Inline) [THT]"]
  CD6 = CD4066 Quad Analog Switch [part_number=4066 package="DIP (Dual Inline) [THT]"]
  CD7 = CD4066 Quad Analog Switch [part_number=4066 package="DIP (Dual Inline) [THT]"]
  CD8 = CD4066 Quad Analog Switch [part_number=4066 package="DIP (Dual Inline) [THT]"]
  CD9 = CD4066 Quad Analog Switch [part_number=4066 package="DIP (Dual Inline) [THT]"]
  CD10 = CD4066 Quad Analog Switch [part_number=4066 package="DIP (Dual Inline) [THT]"]
  CD11 = CD4066 Quad Analog Switch [part_number=4066 package="DIP (Dual Inline) [THT]"]
  CD12 = CD4066 Quad Analog Switch [part_number=4066 package="DIP (Dual Inline) [THT]"]
  CD13 = CD4066 Quad Analog Switch [part_number=4066 package="DIP (Dual Inline) [THT]"]
  CD14 = CD4066 Quad Analog Switch [part_number=4066 package="DIP (Dual Inline) [THT]"]
  CD17 = CD4066 Quad Analog Switch [part_number=4066 package="DIP (Dual Inline) [THT]"]
  CD18 = CD4066 Quad Analog Switch [part_number=4066 package="DIP (Dual Inline) [THT]"]
  CD19 = CD4066 Quad Analog Switch [part_number=4066 package="DIP (Dual Inline) [THT]"]
  CD20 = CD4066 Quad Analog Switch [part_number=4066 package="DIP (Dual Inline) [THT]"]
  CD21 = CD4066 Quad Analog Switch [part_number=4066 package="DIP (Dual Inline) [THT]"]
  CD22 = CD4066 Quad Analog Switch [part_number=4066 package="DIP (Dual Inline) [THT]"]
  CD23 = CD4066 Quad Analog Switch [part_number=4066 package="DIP (Dual Inline) [THT]"]
  R13 = Resistor [tolerance=±5% resistance=100k package=THT]
  R14 = Resistor [tolerance=±5% resistance=100k package=THT]
  R17 = Resistor [tolerance=±5% resistance=100k package=THT]
  R18 = Resistor [tolerance=±5% resistance=100k package=THT]
  R21 = Resistor [tolerance=±5% resistance=100k package=THT]
  R23 = Resistor [tolerance=±5% resistance=220k package=THT]
  C11 = Ceramic Capacitor [capacitance=4.7µF package="100 mil [THT, multilayer]"]
  C12 = Ceramic Capacitor [capacitance=22µF package="100 mil [THT, multilayer]"]
  C13 = Ceramic Capacitor [capacitance=47µF package="100 mil [THT, multilayer]"]
  C16 = Ceramic Capacitor [capacitance=10µF package="100 mil [THT, multilayer]"]
  R25 = Resistor [tolerance=±5% resistance=100k package=THT]
  R26 = Resistor [tolerance=±5% resistance=100k package=THT]
  R27 = Resistor [tolerance=±5% resistance=100k package=THT]
  R28 = Resistor [tolerance=±5% resistance=100k package=THT]
  R29 = Resistor [tolerance=±5% resistance=100k package=THT]
  R30 = Resistor [tolerance=±5% resistance=220k package=THT]
  C17 = Ceramic Capacitor [capacitance=22µF package="100 mil [THT, multilayer]"]
  C18 = Ceramic Capacitor [capacitance=47µF package="100 mil [THT, multilayer]"]
  C19 = Ceramic Capacitor [capacitance=4.7µF package="100 mil [THT, multilayer]"]
  C20 = Ceramic Capacitor [capacitance=10µF package="100 mil [THT, multilayer]"]
  R31 = Resistor [tolerance=±5% resistance=100k package=THT]
  R32 = Resistor [tolerance=±5% resistance=100k package=THT]
  R33 = Resistor [tolerance=±5% resistance=100k package=THT]
  R34 = Resistor [tolerance=±5% resistance=100k package=THT]
  R35 = Resistor [tolerance=±5% resistance=100k package=THT]
  R36 = Resistor [tolerance=±5% resistance=220k package=THT]
  C21 = Ceramic Capacitor [capacitance=4.7µF package="100 mil [THT, multilayer]"]
  C22 = Ceramic Capacitor [capacitance=10µF package="100 mil [THT, multilayer]"]
  C23 = Ceramic Capacitor [capacitance=22µF package="100 mil [THT, multilayer]"]
  C24 = Ceramic Capacitor [capacitance=47µF package="100 mil [THT, multilayer]"]
  CD24 = CD4066 Quad Analog Switch [part_number=4066 package="DIP (Dual Inline) [THT]"]
  CD25 = CD4066 Quad Analog Switch [part_number=4066 package="DIP (Dual Inline) [THT]"]
  CD26 = CD4066 Quad Analog Switch [part_number=4066 package="DIP (Dual Inline) [THT]"]
  CD27 = CD4066 Quad Analog Switch [part_number=4066 package="DIP (Dual Inline) [THT]"]
  CD28 = CD4066 Quad Analog Switch [part_number=4066 package="DIP (Dual Inline) [THT]"]
  R37 = Resistor [tolerance=±5% resistance=100k package=THT]
  R38 = Resistor [tolerance=±5% resistance=100k package=THT]
  R39 = Resistor [tolerance=±5% resistance=100k package=THT]
  R40 = Resistor [tolerance=±5% resistance=100k package=THT]
  R41 = Resistor [tolerance=±5% resistance=100k package=THT]
  R42 = Resistor [tolerance=±5% resistance=220k package=THT]
  C25 = Ceramic Capacitor [capacitance=4.7µF package="100 mil [THT, multilayer]"]
  C26 = Ceramic Capacitor [capacitance=10µF package="100 mil [THT, multilayer]"]
  C27 = Ceramic Capacitor [capacitance=22µF package="100 mil [THT, multilayer]"]
  C28 = Ceramic Capacitor [capacitance=47µF package="100 mil [THT, multilayer]"]
  R43 = Resistor [tolerance=±5% resistance=100k package=THT]
  R44 = Resistor [tolerance=±5% resistance=100k package=THT]
  R45 = Resistor [tolerance=±5% resistance=100k package=THT]
  R46 = Resistor [tolerance=±5% resistance=100k package=THT]
  R47 = Resistor [tolerance=±5% resistance=100k package=THT]
  R48 = Resistor [tolerance=±5% resistance=220k package=THT]
  C29 = Ceramic Capacitor [capacitance=4.7µF package="100 mil [THT, multilayer]"]
  C30 = Ceramic Capacitor [capacitance=10µF package="100 mil [THT, multilayer]"]
  C31 = Ceramic Capacitor [capacitance=22µF package="100 mil [THT, multilayer]"]
  C32 = Ceramic Capacitor [capacitance=47µF package="100 mil [THT, multilayer]"]

nets:
  N1: CD3.SIG_A_IN/OUT, CD3.SIG_B_OUT/IN
  N2: CD3.SIG_A_OUT/IN, CD3.SIG_C_IN/OUT
  N3: CD3.SIG_B_IN/OUT, CD3.SIG_D_OUT/IN
  N4: CD3.CONTROL_B, CD3.CONTROL_C
  N5: CD3.SIG_C_OUT/IN, CD3.SIG_D_IN/OUT
  N6: CD3.CONTROL_D, CD3.CONTROL_A
  VDD: CD3.VDD, CD6.VDD, CD7.VDD, CD8.VDD, CD9.VDD, CD10.VDD, CD11.VDD, CD12.VDD, CD13.VDD, CD14.VDD, CD17.VDD, CD18.VDD, CD19.VDD, CD20.VDD, CD21.VDD, CD22.VDD, CD23.VDD, CD24.VDD, CD25.VDD, CD26.VDD, CD27.VDD, CD28.VDD
  VSS: CD6.VSS, CD7.VSS, CD8.VSS, CD9.VSS, CD10.VSS, CD11.VSS, CD12.VSS, CD13.VSS, CD14.VSS, CD17.VSS, CD18.VSS, CD19.VSS, CD20.VSS, CD21.VSS, CD22.VSS, CD23.VSS, CD24.VSS, CD25.VSS, CD26.VSS, CD27.VSS, CD28.VSS
  N7: CD7.SIG_A_IN/OUT, CD7.SIG_B_OUT/IN
  N8: CD7.SIG_A_OUT/IN, CD7.SIG_C_IN/OUT
  N9: CD7.SIG_B_IN/OUT, CD7.SIG_D_OUT/IN, CD20.SIG_D_IN/OUT, R18.Pin_0
  N10: CD7.CONTROL_B, CD7.CONTROL_C
  N11: CD7.SIG_C_OUT/IN, CD7.SIG_D_IN/OUT
  N12: CD7.CONTROL_D, CD7.CONTROL_A
  N13: CD8.SIG_A_IN/OUT, CD8.SIG_B_OUT/IN
  N14: CD8.SIG_A_OUT/IN, CD8.SIG_C_IN/OUT
  N15: CD8.SIG_B_IN/OUT, CD8.SIG_D_OUT/IN
  N16: CD8.CONTROL_B, CD8.CONTROL_C
  N17: CD8.SIG_C_OUT/IN, CD8.SIG_D_IN/OUT
  N18: CD8.CONTROL_D, CD8.CONTROL_A
  N19: CD17.SIG_A_IN/OUT, CD17.SIG_B_OUT/IN
  N20: CD17.SIG_A_OUT/IN, CD17.SIG_C_IN/OUT
  N21: CD17.SIG_B_IN/OUT, CD17.SIG_D_OUT/IN
  N22: CD17.CONTROL_B, CD17.CONTROL_C
  N23: CD17.SIG_C_OUT/IN, CD17.SIG_D_IN/OUT
  N24: CD17.CONTROL_D, CD17.CONTROL_A
  N25: CD20.SIG_A_OUT/IN, CD20.SIG_B_OUT/IN, CD20.SIG_C_OUT/IN, CD20.SIG_D_OUT/IN, CD21.SIG_C_OUT/IN, CD21.SIG_D_OUT/IN, CD23.SIG_A_OUT/IN, CD23.SIG_B_OUT/IN, CD23.SIG_C_OUT/IN, CD23.SIG_D_OUT/IN
  N26: CD20.SIG_C_IN/OUT, R14.Pin_0, R18.Pin_1
  N27: CD21.SIG_A_OUT/IN, CD21.SIG_B_OUT/IN
  N28: CD21.SIG_C_IN/OUT, R17.Pin_1, R23.Pin_1, R26.Pin_1, R30.Pin_0, R31.Pin_1, R36.Pin_0, R37.Pin_1, R42.Pin_0, R43.Pin_1, R48.Pin_0
  N29: CD21.SIG_D_IN/OUT, R17.Pin_0, R21.Pin_1
  N30: CD23.SIG_C_IN/OUT, R13.Pin_1, R21.Pin_0
  N31: CD23.SIG_D_IN/OUT, R13.Pin_0, R14.Pin_1
  N32: R23.Pin_0, C11.1, C12.1, C13.1, C16.1
  N33: R25.Pin_1, R28.Pin_0
  N34: R26.Pin_0, R27.Pin_1
  N35: R27.Pin_0, R29.Pin_1
  N36: R28.Pin_1, R29.Pin_0
  N37: R30.Pin_1, C17.1, C18.1, C19.1, C20.1
  N38: R31.Pin_0, R35.Pin_1
  N39: R32.Pin_0, R33.Pin_1
  N40: R32.Pin_1, R35.Pin_0
  N41: R33.Pin_0, R34.Pin_1
  N42: R36.Pin_1, C21.1, C22.1, C23.1, C24.1
  N43: R37.Pin_0, R41.Pin_1
  N44: R38.Pin_0, R39.Pin_1
  N45: R38.Pin_1, R41.Pin_0
  N46: R39.Pin_0, R40.Pin_1
  N47: R42.Pin_1, C25.1, C26.1, C27.1, C28.1
  N48: R43.Pin_0, R47.Pin_1
  N49: R44.Pin_0, R45.Pin_1
  N50: R44.Pin_1, R47.Pin_0
  N51: R45.Pin_0, R46.Pin_1
  N52: R48.Pin_1, C29.1, C30.1, C31.1, C32.1

notes:
  Vol/tone 3
  Vol/tone 4
  Iverters 1,2,3,4
  Combinartor 1,2,3,4
  Vol/tone 5 (master)
  Vol/tone 2
  Vol/tone 1
  Selector
  -5v
  +5v
  Gnd
  Coil-1
  North
  Coil-1
  South
  Coil-2
  South
  Coil-3
  South
  Coil-4
  South
  Coil-2
  North
  Coil-4
  North
  Coil-3
  North
  Output
  South, North
  Control-2 A,D, B,C
  Control-3 A,D B,C
  Control-4 A,D, B,C
  Control-1 A,D, B,C
  Vol/Tone-1 Out

custom parts:
  CD4066 Quad Analog Switch: Quad Analog Switch
