# Fritzing sketch POC Inverter Breadboard (saved by Fritzing 0.9.0b)
breadboards: 1

parts:
  CD3 = CD4066 Quad Analog Switch [part_number=4066 package="DIP (Dual Inline) [THT]"]
  CD7 = CD4066 Quad Analog Switch [part_number=4066 package="DIP (Dual Inline) [THT]"]
  CD8 = CD4066 Quad Analog Switch [part_number=4066 package="DIP (Dual Inline) [THT]"]
  CD17 = CD4066 Quad Analog Switch [part_number=4066 package="DIP (Dual Inline) [THT]"]

nets:
  N1: CD3.SIG_A_IN/OUT, CD3.SIG_B_OUT/IN
  N2: CD3.SIG_A_OUT/IN, CD3.SIG_C_IN/OUT
  N3: CD3.SIG_B_IN/OUT, CD3.SIG_D_OUT/IN
  N4: CD3.CONTROL_B, CD3.CONTROL_C
  N5: CD3.SIG_C_OUT/IN, CD3.SIG_D_IN/OUT
  N6: CD3.CONTROL_D, CD3.CONTROL_A
  VDD: CD3.VDD, CD7.VDD, CD8.VDD, CD17.VDD
  N7: CD7.SIG_A_IN/OUT, CD7.SIG_B_OUT/IN
  N8: CD7.SIG_A_OUT/IN, CD7.SIG_C_IN/OUT
  N9: CD7.SIG_B_IN/OUT, CD7.SIG_D_OUT/IN
  N10: CD7.CONTROL_B, CD7.CONTROL_C
  VSS: CD7.VSS, CD8.VSS, CD17.VSS
  N11: CD7.SIG_C_OUT/IN, CD7.SIG_D_IN/OUT
  N12: CD7.CONTROL_D, CD7.CONTROL_A
  N13: CD8.SIG_A_IN/OUT, CD8.SIG_B_OUT/IN
  N14: CD8.SIG_A_OUT/IN, CD8.SIG_C_IN/OUT
  N15: CD8.SIG_B_IN/OUT, CD8.SIG_D_OUT/IN
  N16: CD8.CONTROL_B, CD8.CONTROL_C
  N17: CD8.SIG_C_OUT/IN, CD8.SIG_D_IN/OUT
  N18: CD8.CONTROL_D, CD8.CONTROL_A
  N19: CD17.SIG_A_IN/OUT, CD17.SIG_B_OUT/IN
  N20: CD17.SIG_A_OUT/IN, CD17.SIG_C_IN/OUT
  N21: CD17.SIG_B_IN/OUT, CD17.SIG_D_OUT/IN
  N22: CD17.CONTROL_B, CD17.CONTROL_C
  N23: CD17.SIG_C_OUT/IN, CD17.SIG_D_IN/OUT
  N24: CD17.CONTROL_D, CD17.CONTROL_A

notes:
  Iverters 1,2,3,4
  +5v
  Coil-1
  North
  Coil-1
  South
  Coil-2
  South
  Coil-3
  South
  Coil-4
  South
  Coil-2
  North
  Coil-4
  North
  Coil-3
  North
  Output-1
  North, South
  Control-2 A,D, B,C
  Control-3 A,D B,C
  Control-4 A,D, B,C
  Control-1 A,D, B,C
  -5v
  Output-2
  North, South
  Output-3
  North, South
  Output-4
  North, South

custom parts:
  CD4066 Quad Analog Switch: Quad Analog Switch
