# Fritzing sketch POC Switching Breadboard (saved by Fritzing 0.9.0b)
breadboards: 1

parts:
  CD1 = CD4066 Quad Analog Switch [part_number=4066 package="DIP (Dual Inline) [THT]"]
  CD2 = CD4066 Quad Analog Switch [part_number=4066 package="DIP (Dual Inline) [THT]"]
  CD3 = CD4066 Quad Analog Switch [part_number=4066 package="DIP (Dual Inline) [THT]"]
  CD4 = CD4066 Quad Analog Switch [part_number=4066 package="DIP (Dual Inline) [THT]"]
  CD5 = CD4066 Quad Analog Switch [part_number=4066 package="DIP (Dual Inline) [THT]"]
  CD6 = CD4066 Quad Analog Switch [part_number=4066 package="DIP (Dual Inline) [THT]"]
  CD7 = CD4066 Quad Analog Switch [part_number=4066 package="DIP (Dual Inline) [THT]"]
  CD8 = CD4066 Quad Analog Switch [part_number=4066 package="DIP (Dual Inline) [THT]"]
  C1 = Ceramic Capacitor [capacitance=100nF package="100 mil [THT, multilayer]"]
  C2 = Ceramic Capacitor [capacitance=100nF package="100 mil [THT, multilayer]"]
  C3 = Ceramic Capacitor [capacitance=100nF package="100 mil [THT, multilayer]"]
  C4 = Ceramic Capacitor [capacitance=100nF package="100 mil [THT, multilayer]"]
  C5 = Ceramic Capacitor [capacitance=100nF package="100 mil [THT, multilayer]"]
  C6 = Ceramic Capacitor [capacitance=100nF package="100 mil [THT, multilayer]"]
  C7 = Ceramic Capacitor [capacitance=100nF package="100 mil [THT, multilayer]"]
  C8 = Ceramic Capacitor [capacitance=100nF package="100 mil [THT, multilayer]"]

nets:
  N1: CD1.SIG_A_IN/OUT, CD6.SIG_A_OUT/IN, CD6.SIG_B_OUT/IN, CD6.SIG_C_OUT/IN, CD6.SIG_D_OUT/IN, CD8.SIG_A_IN/OUT, CD8.SIG_C_IN/OUT
  N2: CD1.SIG_A_OUT/IN, CD1.SIG_B_OUT/IN, CD1.SIG_C_OUT/IN, CD1.SIG_D_OUT/IN, CD2.SIG_A_OUT/IN, CD2.SIG_B_OUT/IN, CD2.SIG_D_IN/OUT
  N3: CD1.SIG_B_IN/OUT, CD3.SIG_B_IN/OUT, CD4.SIG_A_IN/OUT, CD6.SIG_A_IN/OUT, CD7.SIG_A_OUT/IN, CD7.SIG_B_OUT/IN, CD7.SIG_D_IN/OUT
  N4: CD1.VSS, C1.0
  N5: CD1.SIG_C_IN/OUT, CD3.SIG_C_IN/OUT, CD4.SIG_B_IN/OUT, CD5.SIG_A_IN/OUT, CD6.SIG_C_IN/OUT, CD7.SIG_B_IN/OUT, CD7.SIG_C_IN/OUT
  N6: CD1.SIG_D_IN/OUT, CD3.SIG_D_IN/OUT, CD4.SIG_C_IN/OUT, CD5.SIG_A_OUT/IN, CD5.SIG_B_OUT/IN, CD5.SIG_D_IN/OUT, CD6.SIG_D_IN/OUT
  N7: CD1.VDD, C1.1
  N8: CD2.SIG_A_IN/OUT, CD3.SIG_A_IN/OUT, CD5.SIG_B_IN/OUT, CD5.SIG_C_IN/OUT, CD6.SIG_B_IN/OUT, CD7.SIG_A_IN/OUT, CD8.SIG_B_IN/OUT
  N9: CD2.SIG_B_IN/OUT, CD2.SIG_C_IN/OUT, CD3.SIG_A_OUT/IN, CD3.SIG_B_OUT/IN, CD3.SIG_C_OUT/IN, CD3.SIG_D_OUT/IN, CD4.SIG_D_IN/OUT
  N10: CD2.VSS, C2.0
  N11: CD2.SIG_C_OUT/IN, CD2.SIG_D_OUT/IN, CD7.SIG_C_OUT/IN, CD7.SIG_D_OUT/IN
  N12: CD2.VDD, C2.1
  N13: CD3.VSS, C3.0
  N14: CD3.VDD, C3.1
  N15: CD4.SIG_A_OUT/IN, CD4.SIG_B_OUT/IN, CD4.SIG_C_OUT/IN, CD4.SIG_D_OUT/IN, CD8.SIG_A_OUT/IN, CD8.SIG_B_OUT/IN, CD8.SIG_D_IN/OUT
  N16: CD4.VSS, C4.0
  N17: CD4.VDD, C4.1
  N18: CD5.VSS, C8.0
  N19: CD5.SIG_C_OUT/IN, CD5.SIG_D_OUT/IN, CD8.SIG_C_OUT/IN, CD8.SIG_D_OUT/IN
  N20: CD5.VDD, C8.1
  N21: CD6.VSS, C6.0
  N22: CD6.VDD, C6.1
  N23: CD7.VSS, C7.0
  N24: CD7.VDD, C7.1
  N25: CD8.VSS, C5.0
  N26: CD8.VDD, C5.1

notes:
  GND
  Out+
  A+
  A-
  B+
  B-
  C+
  C-
  D+
  D-

custom parts:
  CD4066 Quad Analog Switch: Quad Analog Switch
