# Fritzing sketch POC Vol-Tone Breadboard resistive tone control (saved by Fritzing 0.9.0b)
breadboards: 1

parts:
  CD25 = CD4066 Quad Analog Switch [part_number=4066 package="DIP (Dual Inline) [THT]"]
  CD26 = CD4066 Quad Analog Switch [part_number=4066 package="DIP (Dual Inline) [THT]"]
  CD27 = CD4066 Quad Analog Switch [part_number=4066 package="DIP (Dual Inline) [THT]"]
  R40 = Resistor [tolerance=±5% resistance=100k package=THT]
  R41 = Resistor [tolerance=±5% resistance=100k package=THT]
  R42 = Resistor [tolerance=±5% resistance=100k package=THT]
  R43 = Resistor [tolerance=±5% resistance=100k package=THT]
  R44 = Resistor [tolerance=±5% resistance=200k package=THT]
  R45 = Resistor [tolerance=±5% resistance=100k package=THT]
  R46 = Resistor [tolerance=±5% resistance=50k package=THT]
  R47 = Resistor [tolerance=±5% resistance=22k package=THT]
  R48 = Resistor [tolerance=±5% resistance=100k package=THT]
  C32 = Ceramic Capacitor [capacitance=10nF package="100 mil [THT, multilayer]"]
  C33 = Ceramic Capacitor [capacitance=100nF package="100 mil [THT, multilayer]"]
  C34 = Ceramic Capacitor [capacitance=100nF package="100 mil [THT, multilayer]"]
  C35 = Ceramic Capacitor [capacitance=100nF package="100 mil [THT, multilayer]"]

nets:
  N1: CD25.SIG_A_IN/OUT, C32.1
  N2: CD25.SIG_A_OUT/IN, CD25.SIG_C_IN/OUT, R48.Pin_1
  N3: CD25.SIG_B_OUT/IN, CD25.SIG_B_IN/OUT
  VSS: CD25.CONTROL_B, CD25.VSS, CD26.VSS, CD27.VSS, C33.0, C34.0, C35.0
  N4: CD25.SIG_C_OUT/IN, CD25.SIG_D_OUT/IN, CD26.SIG_A_OUT/IN, CD26.SIG_B_OUT/IN, CD26.SIG_C_OUT/IN, CD26.SIG_D_OUT/IN, CD27.SIG_A_OUT/IN, CD27.SIG_B_OUT/IN, CD27.SIG_C_OUT/IN, CD27.SIG_D_OUT/IN
  N5: CD25.SIG_D_IN/OUT, R41.Pin_1, R48.Pin_0
  VDD: CD25.VDD, CD26.VDD, CD27.VDD, C33.1, C34.1, C35.1
  N6: CD26.SIG_A_IN/OUT, R46.Pin_1
  N7: CD26.SIG_C_IN/OUT, R41.Pin_0, R42.Pin_1
  N8: CD26.SIG_D_IN/OUT, R42.Pin_0, R43.Pin_1
  N9: CD27.SIG_A_IN/OUT, R44.Pin_1
  N10: CD27.SIG_B_IN/OUT, R45.Pin_1
  N11: CD27.SIG_C_IN/OUT, R40.Pin_1, R43.Pin_0
  N12: CD27.SIG_D_IN/OUT, R40.Pin_0
  N13: R44.Pin_0, R46.Pin_0, R47.Pin_0, C32.0

notes:
  Coil Output-1
  D on 1st 4066
  Coil Vol/tone
  Coil Output-2,
  Vol/tone output-2
  Vol/tone output-1

custom parts:
  CD4066 Quad Analog Switch: Quad Analog Switch
