# Fritzing sketch POC-1 Schematic (saved by Fritzing 0.9.0b)
breadboards: 1

parts:
  R7 = Rotary Potentiometer (Small) [maximum_resistance=500kΩ package=THT]
  R8 = Rotary Potentiometer (Small) [maximum_resistance=500kΩ package=THT]
  C4 = Ceramic Capacitor [capacitance=10nF package="100 mil [THT, multilayer]"]
  R6 = Rotary Potentiometer (Small) [maximum_resistance=500kΩ package=THT]
  R5 = Rotary Potentiometer (Small) [maximum_resistance=500kΩ package=THT]
  C3 = Ceramic Capacitor [capacitance=10nF package="100 mil [THT, multilayer]"]
  R2 = Rotary Potentiometer (Small) [maximum_resistance=500kΩ package=THT]
  R4 = Rotary Potentiometer (Small) [maximum_resistance=500kΩ package=THT]
  R3 = Rotary Potentiometer (Small) [maximum_resistance=500kΩ package=THT]
  R1 = Rotary Potentiometer (Small) [maximum_resistance=500kΩ package=THT]
  C1 = Ceramic Capacitor [capacitance=10nF package="100 mil [THT, multilayer]"]
  C2 = Ceramic Capacitor [capacitance=10nF package="100 mil [THT, multilayer]"]
  Switch_Array = IC, DIP package, 10 pins [chip_label=IC's]
  R9 = Rotary Potentiometer (Small) [maximum_resistance=500kΩ package=THT]
  R10 = Rotary Potentiometer (Small) [maximum_resistance=500kΩ package=THT]
  C5 = Ceramic Capacitor [capacitance=10nF package="100 mil [THT, multilayer]"]
  Inverter-A = IC, DIP package, 4 pins [chip_label=IC's]
  Coil-A = Inductor [package="400 mil [THT]"]
  Coil-C = Inductor [package="400 mil [THT]"]
  Inverter-C = IC, DIP package, 4 pins [chip_label=IC's]
  Coil-B = Inductor [package="400 mil [THT]"]
  Inverter-B = IC, DIP package, 4 pins [chip_label=IC's]
  Coil-D = Inductor [package="400 mil [THT]"]
  Inverter-D = IC, DIP package, 4 pins [chip_label=IC's]
  Amp = male pin header, 2 pins [form="♂ (male)"]

nets:
  N1: R7.leg1, C4.1, Switch_Array.pin5, Inverter-D.pin3
  N2: R7.wiper, R8.leg2, Switch_Array.pin4
  N3: R7.leg2, Inverter-D.pin4
  N4: R8.wiper, C4.0
  N5: R6.wiper, C3.0
  N6: R6.leg2, R5.wiper, Switch_Array.pin2
  N7: R5.leg1, C3.1, Switch_Array.pin3, Inverter-C.pin3
  N8: R5.leg2, Inverter-C.pin4
  N9: R2.wiper, C1.0
  N10: R2.leg2, R1.wiper, Switch_Array.pin8
  N11: R4.wiper, C2.0
  N12: R4.leg2, R3.wiper, Switch_Array.pin10
  N13: R3.leg1, C2.1, Switch_Array.pin1, Inverter-B.pin3
  N14: R3.leg2, Inverter-B.pin4
  N15: R1.leg1, C1.1, Switch_Array.pin9, Inverter-A.pin3
  N16: R1.leg2, Inverter-A.pin4
  GND: Switch_Array.pin6, R9.leg1, C5.1, Amp.pin2
  N17: Switch_Array.pin7, R9.leg2
  N18: R9.wiper, R10.leg2, Amp.pin1
  N19: R10.wiper, C5.0
  N20: Inverter-A.pin1, Coil-A.pin_0
  N21: Inverter-A.pin2, Coil-A.pin_1
  N22: Coil-C.pin_0, Inverter-C.pin1
  N23: Coil-C.pin_1, Inverter-C.pin2
  N24: Coil-B.pin_0, Inverter-B.pin1
  N25: Coil-B.pin_1, Inverter-B.pin2
  N26: Coil-D.pin_0, Inverter-D.pin1
  N27: Coil-D.pin_1, Inverter-D.pin2

notes:
  Amp1 is the +Input
  Amp2 is the GND output
  Each coil has its own
  Vol/Tone control
  Master Vol/Tone Control
