# Fritzing sketch POC-1 Single Inverter and resistive tone control breadboard  (saved by Fritzing 0.9.0b)
breadboards: 1

parts:
  CD17 = CD4066 Quad Analog Switch [part_number=4066 package="DIP (Dual Inline) [THT]"]
  CD21 = CD4066 Quad Analog Switch [part_number=4066 package="DIP (Dual Inline) [THT]"]
  CD22 = CD4066 Quad Analog Switch [part_number=4066 package="DIP (Dual Inline) [THT]"]
  CD23 = CD4066 Quad Analog Switch [part_number=4066 package="DIP (Dual Inline) [THT]"]
  CD24 = CD4066 Quad Analog Switch [part_number=4066 package="DIP (Dual Inline) [THT]"]
  R31 = Resistor [tolerance=±5% resistance=100k package=THT]
  R32 = Resistor [tolerance=±5% resistance=100k package=THT]
  R33 = Resistor [tolerance=±5% resistance=100k package=THT]
  R34 = Resistor [tolerance=±5% resistance=100k package=THT]
  R35 = Resistor [tolerance=±5% resistance=100k package=THT]
  C21 = Ceramic Capacitor [capacitance=10nF package="100 mil [THT, multilayer]"]
  C29 = Ceramic Capacitor [capacitance=100nF package="100 mil [THT, multilayer]"]
  C30 = Ceramic Capacitor [capacitance=100nF package="100 mil [THT, multilayer]"]
  C31 = Ceramic Capacitor [capacitance=100nF package="100 mil [THT, multilayer]"]
  R36 = Resistor [tolerance=±5% resistance=22k package=THT]
  R37 = Resistor [tolerance=±5% resistance=50k package=THT]
  R38 = Resistor [tolerance=±5% resistance=100k package=THT]
  R39 = Resistor [tolerance=±5% resistance=200k package=THT]
  L1 = Inductor [package="400 mil [THT]"]
  C32 = Ceramic Capacitor [capacitance=100nF package="100 mil [THT, multilayer]"]

nets:
  N1: CD17.SIG_A_IN/OUT, CD17.SIG_B_OUT/IN, CD21.SIG_A_IN/OUT, CD21.SIG_B_OUT/IN, L1.pin_0
  N2: CD17.SIG_A_OUT/IN, CD17.SIG_C_IN/OUT, CD21.SIG_A_OUT/IN, CD21.SIG_C_IN/OUT, CD22.SIG_A_OUT/IN, CD22.SIG_C_IN/OUT, R35.Pin_1
  N3: CD17.SIG_B_IN/OUT, CD17.SIG_D_OUT/IN, CD21.SIG_B_IN/OUT, CD21.SIG_D_OUT/IN, CD24.SIG_D_IN/OUT, R31.Pin_0
  N4: CD17.CONTROL_B, CD17.CONTROL_C, CD21.CONTROL_B, CD21.CONTROL_C
  VSS: CD17.VSS, CD21.VSS, CD22.CONTROL_B, CD22.VSS, CD23.VSS, CD24.VSS, C29.0, C30.0, C31.0, C32.0
  N5: CD17.SIG_C_OUT/IN, CD17.SIG_D_IN/OUT, CD21.SIG_C_OUT/IN, CD21.SIG_D_IN/OUT, L1.pin_1
  N6: CD17.CONTROL_D, CD17.CONTROL_A, CD21.CONTROL_D, CD21.CONTROL_A
  VDD: CD17.VDD, CD21.VDD, CD22.VDD, CD23.VDD, CD24.VDD, C29.1, C30.1, C31.1, C32.1
  N7: CD22.SIG_A_IN/OUT, C21.1
  N8: CD22.SIG_B_OUT/IN, CD22.SIG_B_IN/OUT
  N9: CD22.SIG_C_OUT/IN, CD22.SIG_D_OUT/IN, CD23.SIG_A_OUT/IN, CD23.SIG_B_OUT/IN, CD23.SIG_C_OUT/IN, CD23.SIG_D_OUT/IN, CD24.SIG_A_OUT/IN, CD24.SIG_B_OUT/IN, CD24.SIG_C_OUT/IN, CD24.SIG_D_OUT/IN
  N10: CD22.SIG_D_IN/OUT, R32.Pin_1, R35.Pin_0
  N11: CD23.SIG_A_IN/OUT, R37.Pin_1
  N12: CD23.SIG_C_IN/OUT, R32.Pin_0, R33.Pin_1
  N13: CD23.SIG_D_IN/OUT, R33.Pin_0, R34.Pin_1
  N14: CD24.SIG_A_IN/OUT, R39.Pin_1
  N15: CD24.SIG_B_IN/OUT, R38.Pin_1
  N16: CD24.SIG_C_IN/OUT, R31.Pin_1, R34.Pin_0
  N17: C21.0, R36.Pin_0, R37.Pin_0, R39.Pin_0

notes:
  +5v
  -5v
  AD: straight, BC: invert
  Gnd
  Coil-4
  North
  South
  Coil Vol/tone Control
  Coil V/T
  OUT+
  10 nF 200,100,50,22Kohm
  resistive tone control
  Coil V/T
  OUT-

custom parts:
  CD4066 Quad Analog Switch: Quad Analog Switch
