# Fritzing sketch POC-1 Switching Schematic (saved by Fritzing 0.9.0b)
breadboards: 1

parts:
  CD1 = CD4066 Quad Analog Switch [part_number=4066 package="DIP (Dual Inline) [THT]"]
  C1 = Ceramic Capacitor [capacitance=100nF package="100 mil [THT, multilayer]"]
  CD2 = CD4066 Quad Analog Switch [part_number=4066 package="DIP (Dual Inline) [THT]"]
  C2 = Ceramic Capacitor [capacitance=100nF package="100 mil [THT, multilayer]"]
  CD3 = CD4066 Quad Analog Switch [part_number=4066 package="DIP (Dual Inline) [THT]"]
  CD4 = CD4066 Quad Analog Switch [part_number=4066 package="DIP (Dual Inline) [THT]"]
  C3 = Ceramic Capacitor [capacitance=100nF package="100 mil [THT, multilayer]"]
  C4 = Ceramic Capacitor [capacitance=100nF package="100 mil [THT, multilayer]"]
  CD6 = CD4066 Quad Analog Switch [part_number=4066 package="DIP (Dual Inline) [THT]"]
  CD8 = CD4066 Quad Analog Switch [part_number=4066 package="DIP (Dual Inline) [THT]"]
  CD7 = CD4066 Quad Analog Switch [part_number=4066 package="DIP (Dual Inline) [THT]"]
  CD5 = CD4066 Quad Analog Switch [part_number=4066 package="DIP (Dual Inline) [THT]"]
  C6 = Ceramic Capacitor [capacitance=100nF package="100 mil [THT, multilayer]"]
  C5 = Ceramic Capacitor [capacitance=100nF package="100 mil [THT, multilayer]"]
  C8 = Ceramic Capacitor [capacitance=100nF package="100 mil [THT, multilayer]"]
  C7 = Ceramic Capacitor [capacitance=100nF package="100 mil [THT, multilayer]"]
  A+ = female pin header, 1 pin [form="♀ (female)"]
  A- = female pin header, 1 pin [form="♀ (female)"]
  B+ = female pin header, 1 pin [form="♀ (female)"]
  B- = female pin header, 1 pin [form="♀ (female)"]
  C+ = female pin header, 1 pin [form="♀ (female)"]
  C- = female pin header, 1 pin [form="♀ (female)"]
  D+ = female pin header, 1 pin [form="♀ (female)"]
  D- = female pin header, 1 pin [form="♀ (female)"]
  OUT- = male pin header, 1 pin [form="♂ (male)"]
  OUT+ = male pin header, 1 pin [form="♂ (male)"]

nets:
  N1: CD1.SIG_A_IN/OUT, CD6.SIG_A_OUT/IN, CD6.SIG_B_OUT/IN, CD6.SIG_C_OUT/IN, CD6.SIG_D_OUT/IN, CD5.SIG_A_IN/OUT, CD5.SIG_C_IN/OUT, B-.pin1
  N2: CD1.SIG_A_OUT/IN, CD1.SIG_B_OUT/IN, CD1.SIG_C_OUT/IN, CD1.SIG_D_OUT/IN, CD2.SIG_A_OUT/IN, CD2.SIG_B_OUT/IN, CD2.SIG_D_IN/OUT, A+.pin1
  N3: CD1.SIG_B_IN/OUT, CD3.SIG_B_IN/OUT, CD4.SIG_A_IN/OUT, CD6.SIG_A_IN/OUT, CD7.SIG_A_OUT/IN, CD7.SIG_B_OUT/IN, CD7.SIG_D_IN/OUT, C+.pin1
  N4: CD1.VSS, C1.0
  N5: CD1.SIG_C_IN/OUT, CD3.SIG_C_IN/OUT, CD4.SIG_B_IN/OUT, CD6.SIG_C_IN/OUT, CD8.SIG_A_IN/OUT, CD7.SIG_B_IN/OUT, CD7.SIG_C_IN/OUT, D+.pin1
  N6: CD1.SIG_D_IN/OUT, CD3.SIG_D_IN/OUT, CD4.SIG_C_IN/OUT, CD6.SIG_D_IN/OUT, CD8.SIG_A_OUT/IN, CD8.SIG_B_OUT/IN, C-.pin1
  N7: CD1.VDD, C1.1
  N8: CD2.SIG_A_IN/OUT, CD3.SIG_A_IN/OUT, CD6.SIG_B_IN/OUT, CD8.SIG_B_IN/OUT, CD8.SIG_C_IN/OUT, CD7.SIG_A_IN/OUT, CD5.SIG_B_IN/OUT, D-.pin1
  N9: CD2.SIG_B_IN/OUT, CD2.SIG_C_IN/OUT, CD3.SIG_A_OUT/IN, CD3.SIG_B_OUT/IN, CD3.SIG_C_OUT/IN, CD3.SIG_D_OUT/IN, CD4.SIG_D_IN/OUT, B+.pin1
  N10: CD2.VSS, C2.0
  N11: CD2.SIG_C_OUT/IN, CD2.SIG_D_OUT/IN, CD7.SIG_C_OUT/IN, CD7.SIG_D_OUT/IN, OUT+.pin1
  N12: CD2.VDD, C2.1
  N13: CD3.VSS, C3.0
  N14: CD3.VDD, C3.1
  N15: CD4.SIG_A_OUT/IN, CD4.SIG_B_OUT/IN, CD4.SIG_C_OUT/IN, CD4.SIG_D_OUT/IN, CD5.SIG_A_OUT/IN, CD5.SIG_B_OUT/IN, CD5.SIG_D_IN/OUT, A-.pin1
  N16: CD4.VSS, C4.0
  N17: CD4.VDD, C4.1
  N18: CD6.VSS, C6.0
  N19: CD6.VDD, C6.1
  N20: CD8.VSS, C8.0
  N21: CD8.SIG_C_OUT/IN, CD8.SIG_D_OUT/IN, OUT-.pin1
  N22: CD8.VDD, C8.1
  N23: CD7.VSS, C7.0
  N24: CD7.VDD, C7.1
  N25: CD5.VSS, C5.0
  GND: CD5.SIG_C_OUT/IN, CD5.SIG_D_OUT/IN
  N26: CD5.VDD, C5.1

custom parts:
  CD4066 Quad Analog Switch: Quad Analog Switch
