# Fritzing sketch 10PDT Mount (saved by Fritzing 0.8.7b)
circuit board: 3cm x 3.6cm
breadboards: 1

parts:
  J3 = female pin header, 9 pins [form="♀ (female)"]
  J2 = female pin header, 9 pins [form="♀ (female)"]

nets:
  N1: J3.pin2, J2.pin2
  N2: J3.pin4, J2.pin4
  N3: J3.pin6, J2.pin6
  N4: J3.pin8, J2.pin8
