# Fritzing sketch 4316a Master Vol-resistive-tone control schematic  (saved by Fritzing 0.9.1b)
breadboards: 1

parts:
  +5v = female pin header, 1 pin [form="♀ (female)"]
  -5v = female pin header, 1 pin [form="♀ (female)"]
  V100% = female pin header, 1 pin [form="♀ (female)"]
  V80% = female pin header, 1 pin [form="♀ (female)"]
  V40% = female pin header, 1 pin [form="♀ (female)"]
  V20% = female pin header, 1 pin [form="♀ (female)"]
  V0% = female pin header, 1 pin [form="♀ (female)"]
  Ton/off = female pin header, 1 pin [form="♀ (female)"]
  T300R = female pin header, 1 pin [form="♀ (female)"]
  T75R = female pin header, 1 pin [form="♀ (female)"]
  T37R = female pin header, 1 pin [form="♀ (female)"]
  C1 = Ceramic Capacitor [capacitance=100nF package="100 mil [THT, multilayer]"]
  4316-2 = IC, DIP package, 16 pins [chip_label=IC]
  C1_2 = Ceramic Capacitor [capacitance=100nF package="100 mil [THT, multilayer]"]
  4316-3 = IC, DIP package, 16 pins [chip_label=IC]
  C1_3 = Ceramic Capacitor [capacitance=100nF package="100 mil [THT, multilayer]"]
  4316-4 = IC, DIP package, 16 pins [chip_label=IC]
  RT3 = Resistor [tolerance=±5% resistance=75k package=THT]
  RT1 = Resistor [tolerance=±5% resistance=300k package=THT]
  RT2 = Resistor [tolerance=±5% resistance=150k package=THT]
  RT4 = Resistor [tolerance=±5% resistance=37k package=THT]
  RV = Resistor [tolerance=±5% resistance=100k package=THT]
  RV_2 = Resistor [tolerance=±5% resistance=100k package=THT]
  RV_3 = Resistor [tolerance=±5% resistance=100k package=THT]
  RV_4 = Resistor [tolerance=±5% resistance=100k package=THT]
  RV_5 = Resistor [tolerance=±5% resistance=100k package=THT]
  OUT+ = male pin header, 1 pin [form="♂ (male)"]
  OUT- = male pin header, 1 pin [form="♂ (male)"]
  T150R = female pin header, 1 pin [form="♀ (female)"]
  V60% = female pin header, 1 pin [form="♀ (female)"]
  CT = Ceramic Capacitor [capacitance=10nF package="100 mil [THT, multilayer]"]
  IN- = female pin header, 1 pin [form="♀ (female)"]
  IN+ = female pin header, 1 pin [form="♀ (female)"]

nets:
  N1: +5v.pin1, C1.1, 4316-2.pin16, C1_2.1, 4316-3.pin16, C1_3.1, 4316-4.pin16
  N2: -5v.pin1, C1.0, 4316-2.pin9, C1_2.0, 4316-3.pin9, C1_3.0, 4316-4.pin9
  N3: V100%.pin1, 4316-2.pin14
  N4: V80%.pin1, 4316-2.pin6
  N5: V40%.pin1, 4316-3.pin6
  N6: V20%.pin1, 4316-4.pin14
  N7: V0%.pin1, 4316-4.pin6
  N8: Ton/off.pin1, 4316-2.pin15
  N9: T300R.pin1, 4316-2.pin5
  N10: T75R.pin1, 4316-3.pin5
  N11: T37R.pin1, 4316-4.pin15
  N12: 4316-2.pin1, CT.1
  N13: 4316-2.pin2, 4316-2.pin13, RV_5.Pin_0, IN+.pin1
  N14: 4316-2.pin3, 4316-3.pin2, 4316-3.pin3, 4316-4.pin2, 4316-4.pin10, RV_4.Pin_1, OUT-.pin1, IN-.pin1
  N15: 4316-2.pin4, RT1.Pin_1
  N16: 4316-2.pin7, 4316-2.pin8
  N17: 4316-2.pin10, RV_2.Pin_0, RV_5.Pin_1
  N18: 4316-2.pin11, 4316-2.pin12, 4316-3.pin11, 4316-3.pin12, 4316-4.pin11, 4316-4.pin12, OUT+.pin1
  N19: 4316-3.pin1, RT2.Pin_1
  N20: 4316-3.pin4, RT3.Pin_1
  GND: 4316-3.pin7, 4316-3.pin8, 4316-4.pin3, 4316-4.pin4, 4316-4.pin5, 4316-4.pin7, 4316-4.pin8
  N21: 4316-3.pin10, RV.Pin_0, RV_3.Pin_1
  N22: 4316-3.pin13, RV_2.Pin_1, RV_3.Pin_0
  N23: 4316-3.pin14, V60%.pin1
  N24: 4316-3.pin15, T150R.pin1
  N25: 4316-4.pin1, RT4.Pin_1
  N26: 4316-4.pin13, RV.Pin_1, RV_4.Pin_0
  N27: RT3.Pin_0, RT1.Pin_0, RT2.Pin_0, RT4.Pin_0, CT.0
