# Fritzing sketch 4316d Single Inverter and resistive tone control pcb b (saved by Fritzing 0.9.2b)
circuit board: 13.6807cm x 6.31826cm
breadboards: 1

parts:
  CBoost = Ceramic Capacitor [capacitance=0.18nF package="100 mil [THT, multilayer]"]
  Cdc = Ceramic Capacitor [capacitance=100nF package="100 mil [THT, multilayer]"]
  Cdc_2 = Ceramic Capacitor [capacitance=100nF package="100 mil [THT, multilayer]"]
  Cdc_3 = Ceramic Capacitor [capacitance=100nF package="100 mil [THT, multilayer]"]
  Cdc_4 = Ceramic Capacitor [capacitance=100nF package="100 mil [THT, multilayer]"]
  RT1 = Resistor [tolerance=±1% resistance=16k package=THT]
  RV = Resistor [tolerance=±1% resistance=100k package=THT]
  RV_2 = Resistor [tolerance=±1% resistance=100k package=THT]
  RV_3 = Resistor [tolerance=±1% resistance=100k package=THT]
  RV_4 = Resistor [tolerance=±1% resistance=100k package=THT]
  RV_5 = Resistor [tolerance=±1% resistance=100k package=THT]
  RT4 = Resistor [tolerance=±1% resistance=64k package=THT]
  RT2 = Resistor [tolerance=±1% resistance=32k package=THT]
  RT1_2 = Resistor [tolerance=±1% resistance=16k package=THT]
  CT = Ceramic Capacitor [capacitance=10nF package="100 mil [THT, multilayer]"]
  4316-0 = IC, DIP package, 16 pins [chip_label=IC]
  4316-1 = IC, DIP package, 16 pins [chip_label=IC]
  4316-2 = IC, DIP package, 16 pins [chip_label=IC]
  J7 = female pin header, 1 pin [form="♀ (female)"]
  J7_2 = female pin header, 1 pin [form="♀ (female)"]
  J8 = female pin header, 1 pin [form="♀ (female)"]
  J8_2 = female pin header, 1 pin [form="♀ (female)"]
  J9 = female pin header, 1 pin [form="♀ (female)"]
  J9_2 = female pin header, 1 pin [form="♀ (female)"]
  Invert_T0_V4_T2_V2_T4_V0 = female pin header, 7 pins [form="♀ (female)"]
  Straight_Ton_V5_T1_V3_T3_V1 = female pin header, 7 pins [form="♀ (female)"]
  J6 = female pin header, 2 pins [form="♀ (female)"]
  J6_2 = female pin header, 2 pins [form="♀ (female)"]
  J5 = female pin header, 2 pins [form="♀ (female)"]
  J5_2 = female pin header, 2 pins [form="♀ (female)"]
  J4 = female pin header, 2 pins [form="♀ (female)"]
  J4_2 = female pin header, 2 pins [form="♀ (female)"]
  J13 = female pin header, 2 pins [form="♀ (female)"]
  J13_2 = female pin header, 2 pins [form="♀ (female)"]
  J14 = female pin header, 2 pins [form="♀ (female)"]
  J14_2 = female pin header, 2 pins [form="♀ (female)"]
  J15 = female pin header, 2 pins [form="♀ (female)"]
  J15_2 = female pin header, 2 pins [form="♀ (female)"]
  Out-_Out+ = female pin header, 2 pins [form="♀ (female)"]
  J3 = female pin header, 1 pin [form="♀ (female)"]
  J3_2 = female pin header, 1 pin [form="♀ (female)"]
  Coil+_Coil- = female pin header, 2 pins [form="♀ (female)"]
  J2 = female pin header, 1 pin [form="♀ (female)"]
  J10 = female pin header, 1 pin [form="♀ (female)"]
  J2_2 = female pin header, 1 pin [form="♀ (female)"]
  J10_2 = female pin header, 1 pin [form="♀ (female)"]
  J1 = female pin header, 1 pin [form="♀ (female)"]
  J1_2 = female pin header, 1 pin [form="♀ (female)"]
  V+_V-_GND_GND = female pin header, 4 pins [form="♀ (female)"]
  J12 = female pin header, 1 pin [form="♀ (female)"]
  J12_2 = female pin header, 1 pin [form="♀ (female)"]
  J12_3 = female pin header, 1 pin [form="♀ (female)"]
  J12_4 = female pin header, 1 pin [form="♀ (female)"]
  4316-3 = IC, DIP package, 16 pins [chip_label=IC]
  J0 = female pin header, 1 pin [form="♀ (female)"]
  J0_2 = female pin header, 1 pin [form="♀ (female)"]
  J0_3 = female pin header, 1 pin [form="♀ (female)"]
  J0_4 = female pin header, 1 pin [form="♀ (female)"]
  J11 = female pin header, 1 pin [form="♀ (female)"]
  J11_2 = female pin header, 1 pin [form="♀ (female)"]

nets:
  N1: CBoost.0, RV_3.Pin_0, 4316-0.pin11, 4316-0.pin12, 4316-1.pin2, 4316-1.pin13, J3.pin1, J3_2.pin1
  N2: CBoost.1, 4316-1.pin11, 4316-1.pin12, 4316-2.pin11, 4316-2.pin12, Out-_Out+.pin2, 4316-3.pin11, 4316-3.pin12
  N3: Cdc.0, Cdc_2.0, Cdc_3.0, Cdc_4.0, 4316-0.pin16, 4316-1.pin16, 4316-2.pin16, V+_V-_GND_GND.pin1, 4316-3.pin16
  N4: Cdc.1, Cdc_2.1, Cdc_3.1, Cdc_4.1, 4316-0.pin9, 4316-1.pin9, 4316-2.pin9, J7.pin1, J7_2.pin1, J8.pin1, J8_2.pin1, J9.pin1, J9_2.pin1, V+_V-_GND_GND.pin2, 4316-3.pin9
  N5: RT1.Pin_0, CT.1, 4316-1.pin4
  N6: RT1.Pin_1, RT1_2.Pin_0, 4316-2.pin1
  N7: RV.Pin_0, RV_2.Pin_1, 4316-2.pin13
  N8: RV.Pin_1, RV_4.Pin_0, 4316-2.pin10
  N9: RV_2.Pin_0, RV_3.Pin_1, 4316-1.pin10
  N10: RV_4.Pin_1, RV_5.Pin_0, 4316-3.pin13
  N11: RV_5.Pin_1, 4316-0.pin2, 4316-0.pin3, 4316-1.pin3, 4316-2.pin2, 4316-2.pin3, Out-_Out+.pin1, 4316-3.pin2, 4316-3.pin3, 4316-3.pin10
  N12: RT4.Pin_0, RT2.Pin_1, 4316-3.pin1
  N13: RT4.Pin_1, 4316-3.pin4
  N14: RT2.Pin_0, RT1_2.Pin_1, 4316-2.pin4
  N15: CT.0, 4316-1.pin1
  N16: 4316-0.pin1, 4316-0.pin10, Coil+_Coil-.pin2, J2.pin1, J2_2.pin1
  N17: 4316-0.pin4, 4316-0.pin13, Coil+_Coil-.pin1, J10.pin1, J10_2.pin1
  N18: 4316-0.pin5, 4316-0.pin6, Invert_T0_V4_T2_V2_T4_V0.pin1, J11.pin1, J11_2.pin1
  N19: 4316-0.pin14, 4316-0.pin15, Straight_Ton_V5_T1_V3_T3_V1.pin1, J1.pin1, J1_2.pin1
  N20: 4316-1.pin5, Invert_T0_V4_T2_V2_T4_V0.pin2, J13.pin1, J13_2.pin1
  N21: 4316-1.pin6, Invert_T0_V4_T2_V2_T4_V0.pin3, J13.pin2, J13_2.pin2
  N22: 4316-1.pin14, Straight_Ton_V5_T1_V3_T3_V1.pin3, J4.pin2, J4_2.pin2
  N23: 4316-1.pin15, Straight_Ton_V5_T1_V3_T3_V1.pin2, J4.pin1, J4_2.pin1
  N24: 4316-2.pin5, 4316-2.pin6, Invert_T0_V4_T2_V2_T4_V0.pin4, Invert_T0_V4_T2_V2_T4_V0.pin5, J14.pin1, J14.pin2, J14_2.pin1, J14_2.pin2
  N25: 4316-2.pin14, Straight_Ton_V5_T1_V3_T3_V1.pin5, J5.pin2, J5_2.pin2
  N26: 4316-2.pin15, Straight_Ton_V5_T1_V3_T3_V1.pin4, J5.pin1, J5_2.pin1
  N27: Invert_T0_V4_T2_V2_T4_V0.pin6, J15.pin1, J15_2.pin1, 4316-3.pin5
  N28: Invert_T0_V4_T2_V2_T4_V0.pin7, J15.pin2, J15_2.pin2, 4316-3.pin6
  N29: Straight_Ton_V5_T1_V3_T3_V1.pin6, J6.pin1, J6_2.pin1, 4316-3.pin15
  N30: Straight_Ton_V5_T1_V3_T3_V1.pin7, J6.pin2, J6_2.pin2, 4316-3.pin14
  N31: J12.pin1, J12_2.pin1, J12_3.pin1, J12_4.pin1
  N32: J0.pin1, J0_2.pin1, J0_3.pin1, J0_4.pin1
