# Fritzing sketch 4316d Single Inverter and resistive tone control schematic  (saved by Fritzing 0.9.2b)
breadboards: 1

parts:
  L1 = Inductor [package="400 mil [THT]"]
  C1 = Ceramic Capacitor [capacitance=100nF package="100 mil [THT, multilayer]"]
  +5v = female pin header, 1 pin [form="♀ (female)"]
  -5v = female pin header, 1 pin [form="♀ (female)"]
  Straight = female pin header, 1 pin [form="♀ (female)"]
  Invert = female pin header, 1 pin [form="♀ (female)"]
  V100% = female pin header, 1 pin [form="♀ (female)"]
  V80% = female pin header, 1 pin [form="♀ (female)"]
  V40% = female pin header, 1 pin [form="♀ (female)"]
  V20% = female pin header, 1 pin [form="♀ (female)"]
  V0% = female pin header, 1 pin [form="♀ (female)"]
  Ton/off = female pin header, 1 pin [form="♀ (female)"]
  T0R = female pin header, 1 pin [form="♀ (female)"]
  T32R = female pin header, 1 pin [form="♀ (female)"]
  T64R = female pin header, 1 pin [form="♀ (female)"]
  4316-0 = IC, DIP package, 16 pins [chip_label=IC]
  C1_2 = Ceramic Capacitor [capacitance=100nF package="100 mil [THT, multilayer]"]
  4316-1 = IC, DIP package, 16 pins [chip_label=IC]
  C1_3 = Ceramic Capacitor [capacitance=100nF package="100 mil [THT, multilayer]"]
  4316-2 = IC, DIP package, 16 pins [chip_label=IC]
  C1_4 = Ceramic Capacitor [capacitance=100nF package="100 mil [THT, multilayer]"]
  4316-3 = IC, DIP package, 16 pins [chip_label=IC]
  RT3 = Resistor [tolerance=±5% resistance=16k package=THT]
  RT1 = Resistor [tolerance=±5% resistance=64k package=THT]
  RT2 = Resistor [tolerance=±5% resistance=32k package=THT]
  RT4 = Resistor [tolerance=±5% resistance=16k package=THT]
  RV = Resistor [tolerance=±5% resistance=100k package=THT]
  RV_2 = Resistor [tolerance=±5% resistance=100k package=THT]
  RV_3 = Resistor [tolerance=±5% resistance=100k package=THT]
  RV_4 = Resistor [tolerance=±5% resistance=100k package=THT]
  RV_5 = Resistor [tolerance=±5% resistance=100k package=THT]
  OUT+ = male pin header, 1 pin [form="♂ (male)"]
  OUT- = male pin header, 1 pin [form="♂ (male)"]
  T16R = female pin header, 1 pin [form="♀ (female)"]
  V60% = female pin header, 1 pin [form="♀ (female)"]
  CT = Ceramic Capacitor [capacitance=10nF package="100 mil [THT, multilayer]"]
  C8 = Ceramic Capacitor [capacitance=0.18nF package="100 mil [THT, multilayer]"]
  T128R = female pin header, 1 pin [form="♀ (female)"]
  C9 = Ceramic Capacitor [capacitance=100nF package="100 mil [THT, multilayer]"]
  C10 = Ceramic Capacitor [capacitance=100nF package="100 mil [THT, multilayer]"]
  C11 = Ceramic Capacitor [capacitance=100nF package="100 mil [THT, multilayer]"]
  C12 = Ceramic Capacitor [capacitance=100nF package="100 mil [THT, multilayer]"]

nets:
  N1: L1.pin_0, 4316-0.pin4, 4316-0.pin13
  N2: L1.pin_1, 4316-0.pin1, 4316-0.pin10
  N3: C1.0, 4316-0.pin7, 4316-0.pin8, C1_2.0, 4316-1.pin7, 4316-1.pin8, C1_3.0, 4316-2.pin7, 4316-2.pin8, C1_4.0, C9.0, C10.0, C11.0
  N4: C1.1, +5v.pin1, 4316-0.pin16, C1_2.1, 4316-1.pin16, C1_3.1, 4316-2.pin16, C1_4.1, 4316-3.pin16
  N5: -5v.pin1, 4316-3.pin9, C12.1
  N6: Straight.pin1, 4316-0.pin14, 4316-0.pin15
  N7: Invert.pin1, 4316-0.pin5, 4316-0.pin6
  N8: V100%.pin1, 4316-1.pin14
  N9: V80%.pin1, 4316-1.pin6
  N10: V40%.pin1, 4316-2.pin6
  N11: V20%.pin1, 4316-3.pin14
  N12: V0%.pin1, 4316-3.pin6
  N13: Ton/off.pin1, 4316-1.pin15
  N14: T0R.pin1, 4316-1.pin5
  N15: T32R.pin1, 4316-2.pin5
  N16: T64R.pin1, 4316-3.pin15
  N17: 4316-0.pin2, 4316-0.pin3, 4316-1.pin3, 4316-2.pin2, 4316-2.pin3, 4316-3.pin2, 4316-3.pin3, 4316-3.pin10, RV_4.Pin_1, OUT-.pin1
  N18: 4316-0.pin9, C10.1
  N19: 4316-0.pin11, 4316-0.pin12, 4316-1.pin2, 4316-1.pin13, RV_5.Pin_0, C8.1
  N20: 4316-1.pin1, CT.1
  N21: 4316-1.pin4, RT4.Pin_0, CT.0
  N22: 4316-1.pin9, C9.1
  N23: 4316-1.pin10, RV_2.Pin_0, RV_5.Pin_1
  N24: 4316-1.pin11, 4316-1.pin12, 4316-2.pin11, 4316-2.pin12, 4316-3.pin11, 4316-3.pin12, OUT+.pin1, C8.0
  N25: 4316-2.pin1, RT3.Pin_0, RT4.Pin_1
  N26: 4316-2.pin4, RT3.Pin_1, RT2.Pin_0
  N27: 4316-2.pin9, C11.1
  N28: 4316-2.pin10, RV.Pin_0, RV_3.Pin_1
  N29: 4316-2.pin13, RV_2.Pin_1, RV_3.Pin_0
  N30: 4316-2.pin14, V60%.pin1
  N31: 4316-2.pin15, T16R.pin1
  N32: 4316-3.pin1, RT1.Pin_0, RT2.Pin_1
  N33: 4316-3.pin4, RT1.Pin_1
  N34: 4316-3.pin5, T128R.pin1
  GND: 4316-3.pin7, 4316-3.pin8, C12.0
  N35: 4316-3.pin13, RV.Pin_1, RV_4.Pin_0
