# Fritzing sketch 4316e IVT pcb e (saved by Fritzing 0.9.2b)
circuit board: 12.9466cm x 4.90025cm
breadboards: 1

parts:
  CBoost = Ceramic Capacitor [capacitance=0.18nF package="100 mil [THT, multilayer]"]
  Cdc = Ceramic Capacitor [capacitance=100nF package="100 mil [THT, multilayer]"]
  Cdc_2 = Ceramic Capacitor [capacitance=100nF package="100 mil [THT, multilayer]"]
  RT1 = Resistor [tolerance=±1% resistance=16k package=THT]
  RV = Resistor [tolerance=±1% resistance=100k package=THT]
  RV_2 = Resistor [tolerance=±1% resistance=100k package=THT]
  RV_3 = Resistor [tolerance=±1% resistance=100k package=THT]
  RV_4 = Resistor [tolerance=±1% resistance=100k package=THT]
  RV_5 = Resistor [tolerance=±1% resistance=100k package=THT]
  RT4 = Resistor [tolerance=±1% resistance=64k package=THT]
  RT2 = Resistor [tolerance=±1% resistance=32k package=THT]
  RT1_2 = Resistor [tolerance=±1% resistance=16k package=THT]
  CT = Ceramic Capacitor [capacitance=10nF package="100 mil [THT, multilayer]"]
  Out+_Out- = female pin header, 2 pins [form="♀ (female)"]
  Coil-_Coil+ = female pin header, 2 pins [form="♀ (female)"]
  Cdc_3 = Ceramic Capacitor [capacitance=100nF package="100 mil [THT, multilayer]"]
  Invert_V4_T0_T2_V2_T4_V0 = female pin header, 7 pins [form="♀ (female)"]
  V3_T1_V5_Ton_Strt_T3_V1 = female pin header, 7 pins [form="♀ (female)"]
  Cdc_4 = Ceramic Capacitor [capacitance=100nF package="100 mil [THT, multilayer]"]
  Cdc_5 = Ceramic Capacitor [capacitance=100nF package="100 mil [THT, multilayer]"]
  Cdc_6 = Ceramic Capacitor [capacitance=100nF package="100 mil [THT, multilayer]"]
  Cdc_7 = Ceramic Capacitor [capacitance=100nF package="100 mil [THT, multilayer]"]
  GND_GND_V-_V+ = female pin header, 4 pins [form="♀ (female)"]
  4316-0 = IC, DIP package, 16 pins [chip_label=IC]
  4316-1 = IC, DIP package, 16 pins [chip_label=IC]
  4316-2 = IC, DIP package, 16 pins [chip_label=IC]
  4316-3 = IC, DIP package, 16 pins [chip_label=IC]
  Cdc_8 = Ceramic Capacitor [capacitance=100nF package="100 mil [THT, multilayer]"]

nets:
  N1: CBoost.0, RV_3.Pin_0, 4316-0.pin11, 4316-0.pin12, 4316-1.pin2, 4316-1.pin13
  N2: CBoost.1, Out+_Out-.pin2, 4316-1.pin11, 4316-1.pin12, 4316-2.pin11, 4316-2.pin12, 4316-3.pin11, 4316-3.pin12
  N3: Cdc.0, Cdc_2.1, Cdc_4.1, Cdc_5.0
  N4: Cdc.1, Cdc_2.0, Cdc_3.0, Cdc_6.1, GND_GND_V-_V+.pin1, 4316-0.pin16, 4316-1.pin16, 4316-2.pin16, 4316-3.pin16
  N5: RT1.Pin_0, CT.1, 4316-1.pin4
  N6: RT1.Pin_1, RT1_2.Pin_0, 4316-2.pin1
  N7: RV.Pin_0, RV_2.Pin_1, 4316-2.pin13
  N8: RV.Pin_1, RV_4.Pin_0, 4316-2.pin10
  N9: RV_2.Pin_0, RV_3.Pin_1, 4316-1.pin10
  N10: RV_4.Pin_1, RV_5.Pin_0, 4316-3.pin13
  N11: RV_5.Pin_1, Out+_Out-.pin1, 4316-0.pin2, 4316-0.pin3, 4316-1.pin3, 4316-2.pin2, 4316-2.pin3, 4316-3.pin2, 4316-3.pin3, 4316-3.pin10
  N12: RT4.Pin_0, RT2.Pin_1, 4316-3.pin1
  N13: RT4.Pin_1, 4316-3.pin4
  N14: RT2.Pin_0, RT1_2.Pin_1, 4316-2.pin4
  N15: CT.0, 4316-1.pin1
  N16: Coil-_Coil+.pin1, 4316-0.pin4, 4316-0.pin13
  N17: Coil-_Coil+.pin2, 4316-0.pin1, 4316-0.pin10
  N18: Invert_V4_T0_T2_V2_T4_V0.pin1, 4316-0.pin5, 4316-0.pin6
  N19: Invert_V4_T0_T2_V2_T4_V0.pin2, 4316-1.pin6
  N20: Invert_V4_T0_T2_V2_T4_V0.pin3, 4316-1.pin5
  N21: Invert_V4_T0_T2_V2_T4_V0.pin4, 4316-2.pin5
  N22: Invert_V4_T0_T2_V2_T4_V0.pin5, 4316-2.pin6
  N23: Invert_V4_T0_T2_V2_T4_V0.pin6, 4316-3.pin5
  N24: Invert_V4_T0_T2_V2_T4_V0.pin7, 4316-3.pin6
  N25: V3_T1_V5_Ton_Strt_T3_V1.pin1, 4316-3.pin14
  N26: V3_T1_V5_Ton_Strt_T3_V1.pin2, 4316-3.pin15
  N27: V3_T1_V5_Ton_Strt_T3_V1.pin3, 4316-0.pin14, 4316-0.pin15
  N28: V3_T1_V5_Ton_Strt_T3_V1.pin4, 4316-1.pin15
  N29: V3_T1_V5_Ton_Strt_T3_V1.pin5, 4316-1.pin14
  N30: V3_T1_V5_Ton_Strt_T3_V1.pin6, 4316-2.pin15
  N31: V3_T1_V5_Ton_Strt_T3_V1.pin7, 4316-2.pin14
  N32: Cdc_4.0, Cdc_5.1, Cdc_7.1, GND_GND_V-_V+.pin2, 4316-0.pin9, 4316-1.pin9, 4316-2.pin9, 4316-3.pin9, Cdc_8.0
  N33: GND_GND_V-_V+.pin3, GND_GND_V-_V+.pin4
  N34: 4316-0.pin7, 4316-0.pin8
  N35: 4316-1.pin7, 4316-1.pin8
  N36: 4316-2.pin7, 4316-2.pin8
  N37: 4316-3.pin7, 4316-3.pin8, Cdc_8.1
