# Fritzing sketch POC-2a Schematic (saved by Fritzing 0.9.1b)
breadboards: 1

parts:
  C1 = Ceramic Capacitor [capacitance=10nF package="100 mil [THT, multilayer]"]
  Switch_Array = IC, DIP package, 10 pins [chip_label=IC's]
  Inverter-A = IC, DIP package, 4 pins [chip_label=IC's]
  Coil-A = Inductor [package="400 mil [THT]"]
  Coil-C = Inductor [package="400 mil [THT]"]
  Inverter-C = IC, DIP package, 4 pins [chip_label=IC's]
  Coil-B = Inductor [package="400 mil [THT]"]
  Inverter-B = IC, DIP package, 4 pins [chip_label=IC's]
  Coil-D = Inductor [package="400 mil [THT]"]
  Inverter-D = IC, DIP package, 4 pins [chip_label=IC's]
  Amp = male pin header, 2 pins [form="♂ (male)"]
  R1_linear = Rotary Potentiometer (Small) [maximum_resistance=500kΩ package=THT]
  C1_2 = Ceramic Capacitor [capacitance=10nF package="100 mil [THT, multilayer]"]
  R13 = Rotary Potentiometer (Small) [maximum_resistance=500kΩ package=THT]
  C1_3 = Ceramic Capacitor [capacitance=10nF package="100 mil [THT, multilayer]"]
  R1_linear_2 = Rotary Potentiometer (Small) [maximum_resistance=500kΩ package=THT]
  C1_4 = Ceramic Capacitor [capacitance=10nF package="100 mil [THT, multilayer]"]
  R1_linear_3 = Rotary Potentiometer (Small) [maximum_resistance=500kΩ package=THT]
  C1_5 = Ceramic Capacitor [capacitance=10nF package="100 mil [THT, multilayer]"]
  R2_log = Rotary Potentiometer (Large) [maximum_resistance=500kΩ package=THT]
  R1_linear_4 = Rotary Potentiometer (Large) [maximum_resistance=500kΩ package=THT]
  R2_log_2 = Rotary Potentiometer (Large) [maximum_resistance=500kΩ package=THT]
  R2_log_3 = Rotary Potentiometer (Large) [maximum_resistance=500kΩ package=THT]
  R2_log_4 = Rotary Potentiometer (Large) [maximum_resistance=500kΩ package=THT]
  R2_log_5 = Rotary Potentiometer (Large) [maximum_resistance=500kΩ package=THT]

nets:
  N1: C1.0, R2_log.wiper
  N2: C1.1, Switch_Array.pin9, Inverter-A.pin3, R1_linear_4.leg1
  N3: Switch_Array.pin1, Inverter-B.pin3, R1_linear.leg1, C1_2.1
  N4: Switch_Array.pin2, R13.wiper
  N5: Switch_Array.pin3, Inverter-C.pin3, R13.leg1, C1_3.1
  N6: Switch_Array.pin4, R1_linear_2.wiper
  N7: Switch_Array.pin5, Inverter-D.pin3, R1_linear_2.leg1, C1_4.1
  N8: Switch_Array.pin6, R1_linear_3.leg1, C1_5.1
  N9: Switch_Array.pin7, R1_linear_3.leg2, R2_log_5.leg2
  N10: Switch_Array.pin8, R1_linear_4.wiper
  N11: Switch_Array.pin10, R1_linear.wiper
  N12: Inverter-A.pin1, Coil-A.pin_0
  N13: Inverter-A.pin2, Coil-A.pin_1
  N14: Inverter-A.pin4, R2_log.leg2, R1_linear_4.leg2
  N15: Coil-C.pin_0, Inverter-C.pin1
  N16: Coil-C.pin_1, Inverter-C.pin2
  N17: Inverter-C.pin4, R13.leg2, R2_log_2.leg2
  N18: Coil-B.pin_0, Inverter-B.pin1
  N19: Coil-B.pin_1, Inverter-B.pin2
  N20: Inverter-B.pin4, R1_linear.leg2, R2_log_3.leg2
  N21: Coil-D.pin_0, Inverter-D.pin1
  N22: Coil-D.pin_1, Inverter-D.pin2
  N23: Inverter-D.pin4, R1_linear_2.leg2, R2_log_4.leg2
  N24: Amp.pin1, R1_linear_3.wiper
  GND: Amp.pin2
  N25: C1_2.0, R2_log_3.wiper
  N26: C1_3.0, R2_log_2.wiper
  N27: C1_4.0, R2_log_4.wiper
  N28: C1_5.0, R2_log_5.wiper

notes:
  Amp1 is the +Input
  Amp2 is the GND output
  Each coil has its own
  Vol/Tone control
  Master Vol/Tone Control
