# Fritzing sketch OutputStage 04_02 (saved by Fritzing 0.8.7b)
circuit board: 14.4182cm x 6.14944cm
breadboards: 1

parts:
  Con_INV3/4 = female pin header, 4 pins [form="♀ (female)"]  # not connected
  InverterOutput = female pin header, 6 pins [form="♀ (female)"]
  Con_INV1/2_V+/- = female pin header, 6 pins [form="♀ (female)"]  # not connected
  4660 = IC, DIP package, 14 pins [chip_label=CD4660]
  4660_2 = IC, DIP package, 14 pins [chip_label=CD4660]
  4660_3 = IC, DIP package, 14 pins [chip_label=CD4660]
  4660_4 = IC, DIP package, 14 pins [chip_label=CD4660]
  4660_5 = IC, DIP package, 14 pins [chip_label=CD4660]
  AD-4 = female pin header, 10 pins [form="♀ (female)"]  # not connected
  BC-3 = female pin header, 10 pins [form="♀ (female)"]  # not connected
  R1 = Resistor [tolerance=±5% resistance=100k package=THT]
  R2 = Resistor [tolerance=±5% resistance=100k package=THT]
  R3 = Resistor [tolerance=±5% resistance=100k package=THT]
  R4 = Resistor [tolerance=±5% resistance=100k package=THT]
  R5 = Resistor [tolerance=±5% resistance=100k package=THT]
  Tone4 = Resistor [tolerance=±5% resistance=220k package=THT]
  C4 = Ceramic Capacitor [capacitance=47nF package="100 mil [THT, multilayer]"]
  C3 = Ceramic Capacitor [capacitance=33nF package="100 mil [THT, multilayer]"]
  C2 = Ceramic Capacitor [capacitance=22nF package="100 mil [THT, multilayer]"]
  C1 = Ceramic Capacitor [capacitance=10nF package="100 mil [THT, multilayer]"]
  VolToneOut = female pin header, 4 pins [form="♀ (female)"]
  BC-1 = female pin header, 10 pins [form="♀ (female)"]  # not connected
  AD-2 = female pin header, 10 pins [form="♀ (female)"]  # not connected
  Controls_BC1 = female pin header, 4 pins [form="♀ (female)"]
  Controls_BC2 = female pin header, 4 pins [form="♀ (female)"]
  Controls_AD1 = female pin header, 4 pins [form="♀ (female)"]
  Controls_AD2 = female pin header, 4 pins [form="♀ (female)"]
  Controls_ABCD1 = female pin header, 4 pins [form="♀ (female)"]
  4660_6 = IC, DIP package, 14 pins [chip_label=CD4660]
  Controls_ABCD2 = female pin header, 4 pins [form="♀ (female)"]

nets:
  N1: InverterOutput.pin3, 4660.pin9, 4660.pin10, 4660_2.pin9, 4660_2.pin10, 4660_3.pin9, 4660_3.pin10, 4660_4.pin9, 4660_4.pin10, 4660_5.pin9, 4660_5.pin10
  N2: 4660.pin5, Controls_BC2.pin1
  N3: 4660.pin6, Controls_BC2.pin2
  N4: 4660.pin7, 4660_2.pin7, 4660_3.pin7, 4660_4.pin7, 4660_5.pin7
  N5: 4660.pin8, R3.Pin_1, R4.Pin_0
  N6: 4660.pin11, R2.Pin_1, R3.Pin_0
  N7: 4660.pin12, Controls_AD2.pin4
  N8: 4660.pin13, Controls_AD2.pin3
  N9: 4660.pin14, 4660_2.pin14, 4660_3.pin14, 4660_4.pin14, 4660_5.pin14
  N10: 4660_2.pin4, VolToneOut.pin1
  N11: 4660_2.pin5, Controls_BC2.pin3
  N12: 4660_2.pin6, Controls_BC2.pin4
  N13: 4660_2.pin11, R4.Pin_1, R5.Pin_0
  N14: 4660_2.pin12, Controls_AD1.pin2
  N15: 4660_2.pin13, Controls_AD1.pin1
  N16: 4660_3.pin5, 4660_3.pin12, Controls_BC1.pin3
  N17: 4660_3.pin6, Controls_BC1.pin4
  N18: 4660_3.pin8, C4.1
  N19: 4660_3.pin11, C3.1
  N20: 4660_4.pin4, VolToneOut.pin4
  N21: 4660_4.pin5, Controls_BC1.pin1
  N22: 4660_4.pin6, Controls_BC1.pin2
  N23: 4660_4.pin8, C2.1
  N24: 4660_4.pin11, C1.1
  N25: 4660_4.pin12, Controls_AD1.pin4
  N26: 4660_4.pin13, Controls_AD1.pin3
  N27: 4660_5.pin1, 4660_5.pin11, R1.Pin_0
  N28: 4660_5.pin2, 4660_5.pin3
  N29: 4660_5.pin5, Controls_ABCD1.pin4
  N30: 4660_5.pin6, Controls_ABCD1.pin3
  N31: 4660_5.pin8, R1.Pin_1, R2.Pin_0
  N32: 4660_5.pin12, Controls_AD2.pin1
  N33: 4660_5.pin13, Controls_AD2.pin2
  N34: Tone4.Pin_0, C4.0, C3.0, C2.0, C1.0
  N35: 4660_6.pin5, Controls_ABCD2.pin2
  N36: 4660_6.pin6, Controls_ABCD2.pin1
  N37: 4660_6.pin12, Controls_ABCD2.pin4
  N38: 4660_6.pin13, Controls_ABCD2.pin3

notes:
  Y1
  +V
  -V
  Y2
  Y3
  Y4
  Amp GND
  Amp HOT
  BC1
  AD1
  BC2
  AD2
  BC3
  BC4
  AD4
  AD3
  VT3
  VT4
  VT1
  VT2
  C1- out
  C1+ out
  A1+
  B1+
  B2+
  A2+
  B1-
  A2-
  A1-
  B2-
  C2- out
