# Fritzing sketch POC Combine-Select-Master-V-T Breadboard (saved by Fritzing 0.9.0b)
breadboards: 1

parts:
  CD6 = CD4066 Quad Analog Switch [part_number=4066 package="DIP (Dual Inline) [THT]"]
  CD9 = CD4066 Quad Analog Switch [part_number=4066 package="DIP (Dual Inline) [THT]"]
  CD10 = CD4066 Quad Analog Switch [part_number=4066 package="DIP (Dual Inline) [THT]"]
  CD11 = CD4066 Quad Analog Switch [part_number=4066 package="DIP (Dual Inline) [THT]"]
  CD12 = CD4066 Quad Analog Switch [part_number=4066 package="DIP (Dual Inline) [THT]"]
  CD13 = CD4066 Quad Analog Switch [part_number=4066 package="DIP (Dual Inline) [THT]"]
  CD14 = CD4066 Quad Analog Switch [part_number=4066 package="DIP (Dual Inline) [THT]"]
  CD18 = CD4066 Quad Analog Switch [part_number=4066 package="DIP (Dual Inline) [THT]"]
  R25 = Resistor [tolerance=±5% resistance=100k package=THT]
  R26 = Resistor [tolerance=±5% resistance=100k package=THT]
  R27 = Resistor [tolerance=±5% resistance=100k package=THT]
  R28 = Resistor [tolerance=±5% resistance=100k package=THT]
  R29 = Resistor [tolerance=±5% resistance=100k package=THT]
  R30 = Resistor [tolerance=±5% resistance=220k package=THT]
  C17 = Ceramic Capacitor [capacitance=22µF package="100 mil [THT, multilayer]"]
  C18 = Ceramic Capacitor [capacitance=47µF package="100 mil [THT, multilayer]"]
  C19 = Ceramic Capacitor [capacitance=4.7µF package="100 mil [THT, multilayer]"]
  C20 = Ceramic Capacitor [capacitance=10µF package="100 mil [THT, multilayer]"]

nets:
  N1: CD6.SIG_A_IN/OUT, C20.0
  N2: CD6.SIG_A_OUT/IN, CD6.SIG_B_OUT/IN, CD6.SIG_C_OUT/IN, CD6.SIG_D_OUT/IN, CD12.SIG_A_OUT/IN, CD12.SIG_B_OUT/IN, CD12.SIG_C_OUT/IN, CD12.SIG_D_OUT/IN, CD18.SIG_C_OUT/IN, CD18.SIG_D_OUT/IN
  N3: CD6.SIG_B_IN/OUT, C19.0
  VSS: CD6.VSS, CD9.VSS, CD10.VSS, CD11.VSS, CD12.VSS, CD13.VSS, CD14.VSS, CD18.VSS
  N4: CD6.SIG_C_IN/OUT, R27.Pin_0, R29.Pin_1
  N5: CD6.SIG_D_IN/OUT, R28.Pin_1, R29.Pin_0
  VDD: CD6.VDD, CD9.VDD, CD10.VDD, CD11.VDD, CD12.VDD, CD13.VDD, CD14.VDD, CD18.VDD
  N6: CD9.SIG_A_IN/OUT, CD9.SIG_C_OUT/IN
  N7: CD9.SIG_A_OUT/IN, CD9.SIG_B_OUT/IN
  N8: CD9.SIG_B_IN/OUT, CD10.SIG_B_IN/OUT, CD13.SIG_A_OUT/IN, CD13.SIG_B_OUT/IN, CD14.SIG_B_OUT/IN
  N9: CD9.SIG_C_IN/OUT, CD10.SIG_A_IN/OUT, CD10.SIG_C_OUT/IN, CD13.SIG_C_IN/OUT, CD14.SIG_D_IN/OUT
  N10: CD9.SIG_D_OUT/IN, CD9.SIG_D_IN/OUT, CD9.CONTROL_D, CD10.SIG_D_OUT/IN, CD10.SIG_D_IN/OUT, CD10.CONTROL_D, CD11.SIG_D_OUT/IN, CD11.SIG_D_IN/OUT, CD11.CONTROL_D, CD13.SIG_D_OUT/IN, CD13.SIG_D_IN/OUT, CD13.CONTROL_D, CD14.SIG_A_OUT/IN, CD14.SIG_B_IN/OUT, CD18.SIG_A_IN/OUT, CD18.SIG_A_OUT/IN, CD18.SIG_B_OUT/IN, CD18.SIG_B_IN/OUT, CD18.CONTROL_B, CD18.SIG_C_IN/OUT, CD18.CONTROL_A, R26.Pin_1, R30.Pin_1
  N11: CD10.SIG_A_OUT/IN, CD10.SIG_B_OUT/IN, CD11.SIG_B_IN/OUT, CD13.SIG_B_IN/OUT, CD14.SIG_A_IN/OUT
  N12: CD10.SIG_C_IN/OUT, CD11.SIG_C_IN/OUT, CD13.SIG_A_IN/OUT, CD13.SIG_C_OUT/IN, CD14.SIG_C_OUT/IN
  N13: CD11.SIG_A_IN/OUT, CD11.SIG_C_OUT/IN
  N14: CD11.SIG_A_OUT/IN, CD11.SIG_B_OUT/IN
  N15: CD12.SIG_A_IN/OUT, C18.0
  N16: CD12.SIG_B_IN/OUT, C17.0
  N17: CD12.SIG_C_IN/OUT, R25.Pin_1, R28.Pin_0
  N18: CD12.SIG_D_IN/OUT, CD14.SIG_C_IN/OUT, CD14.SIG_D_OUT/IN, R25.Pin_0
  N19: CD14.CONTROL_B, CD14.CONTROL_C
  N20: CD14.CONTROL_D, CD14.CONTROL_A
  N21: CD18.SIG_D_IN/OUT, R26.Pin_0, R27.Pin_1
  N22: R30.Pin_0, C17.1, C18.1, C19.1, C20.1

notes:
  Combinartor 1,2,3,4
  Vol/tone 5 (master)
  Selector Inputs
  A: B2
  B: A2
  C: A1
  D: B1
  -5v
  C1
  Input A1
  Output 1
  C2
  Input B1
  Input A2
  Input B2,
  Output 2
  C3
  Input B1
  Input A2
  Input B2,
  Output 2
  C4
  Input B1
  Input A2
  Input B2,
  Output 2
  C2
  Input A1
  Output 1
  C3
  Input A1
  Output 1
  C4
  Input A1
  Output 1
  C1
  Input B1
  Input A2
  Input B2,
  Output 2
  Selector
  C: Output 1
  Selector
  D: Output 2
  (GND)
  +5v
  Master Vol/Tone Out
  (to amp)
  Master Vol/Tone
  In (D on 1st 4066)

custom parts:
  CD4066 Quad Analog Switch: Quad Analog Switch
