# Fritzing sketch Full Conceptul View (saved by Fritzing 0.9.0b)
breadboards: 1

parts:
  Inv1 = IC, DIP package, 6 pins [chip_label=Inverter]
  VT1 = IC, DIP package, 14 pins [chip_label=Vol/Tone]
  SA1 = IC, DIP package, 42 pins [chip_label="Switch Array"]
  C1 = Inductor [part_number=Coil package="400 mil [THT]"]
  Inv2 = IC, DIP package, 6 pins [chip_label=Inverter]
  VT2 = IC, DIP package, 14 pins [chip_label=Vol/Tone]
  C2 = Inductor [part_number=Coil package="400 mil [THT]"]
  Inv3 = IC, DIP package, 6 pins [chip_label=Inverter]
  Inv4 = IC, DIP package, 6 pins [chip_label=Inverter]
  VT3 = IC, DIP package, 14 pins [chip_label=Vol/Tone]
  VT4 = IC, DIP package, 14 pins [chip_label=Vol/Tone]
  C3 = Inductor [part_number=Coil package="400 mil [THT]"]
  C4 = Inductor [part_number=Coil package="400 mil [THT]"]
  VT5 = IC, DIP package, 14 pins [chip_label=Vol/Tone]
  A1 = male pin header, 2 pins [form="♂ (male)" part_number=Amp]

nets:
  N1: Inv1.pin1, C1.pin_1
  N2: Inv1.pin3, VT1.pin1, SA1.pin41
  N3: Inv1.pin4, VT1.pin14
  N4: Inv1.pin6, C1.pin_0
  N5: VT1.pin7, SA1.pin42
  N6: SA1.pin33, VT5.pin1, A1.pin1
  N7: SA1.pin34, VT5.pin14
  N8: SA1.pin35, Inv3.pin3, VT4.pin1
  N9: SA1.pin36, VT4.pin7
  N10: SA1.pin37, Inv4.pin3, VT3.pin1
  N11: SA1.pin38, VT3.pin7
  N12: SA1.pin39, Inv2.pin3, VT2.pin1
  N13: SA1.pin40, VT2.pin7
  N14: Inv2.pin1, C2.pin_1
  N15: Inv2.pin4, VT2.pin14
  N16: Inv2.pin6, C2.pin_0
  N17: Inv3.pin1, C4.pin_1
  N18: Inv3.pin4, VT4.pin14
  N19: Inv3.pin6, C4.pin_0
  N20: Inv4.pin1, C3.pin_1
  N21: Inv4.pin4, VT3.pin14
  N22: Inv4.pin6, C3.pin_0
  N23: VT5.pin7, A1.pin2

notes:
  Output+ Gnd
  95x Control Pin = 12x Shift Reg
  +5v & -5v Rails
