# Fritzing sketch POC Inverter Breadboard (saved by Fritzing 0.9.0b)
breadboards: 1

parts:
  CD3 = CD4066 Quad Analog Switch [part_number=4066 package="DIP (Dual Inline) [THT]"]
  CD7 = CD4066 Quad Analog Switch [part_number=4066 package="DIP (Dual Inline) [THT]"]
  CD8 = CD4066 Quad Analog Switch [part_number=4066 package="DIP (Dual Inline) [THT]"]
  CD17 = CD4066 Quad Analog Switch [part_number=4066 package="DIP (Dual Inline) [THT]"]
  CD18 = CD4066 Quad Analog Switch [part_number=4066 package="DIP (Dual Inline) [THT]"]
  CD19 = CD4066 Quad Analog Switch [part_number=4066 package="DIP (Dual Inline) [THT]"]
  CD20 = CD4066 Quad Analog Switch [part_number=4066 package="DIP (Dual Inline) [THT]"]
  CD21 = CD4066 Quad Analog Switch [part_number=4066 package="DIP (Dual Inline) [THT]"]
  CD22 = CD4066 Quad Analog Switch [part_number=4066 package="DIP (Dual Inline) [THT]"]
  CD23 = CD4066 Quad Analog Switch [part_number=4066 package="DIP (Dual Inline) [THT]"]
  CD24 = CD4066 Quad Analog Switch [part_number=4066 package="DIP (Dual Inline) [THT]"]
  R31 = Resistor [tolerance=±5% resistance=100k package=THT]
  R32 = Resistor [tolerance=±5% resistance=100k package=THT]
  R33 = Resistor [tolerance=±5% resistance=100k package=THT]
  R34 = Resistor [tolerance=±5% resistance=100k package=THT]
  R35 = Resistor [tolerance=±5% resistance=100k package=THT]
  R36 = Resistor [tolerance=±5% resistance=100k package=THT]
  C21 = Ceramic Capacitor [capacitance=10nF package="100 mil [THT, multilayer]"]
  C22 = Ceramic Capacitor [capacitance=22nF package="100 mil [THT, multilayer]"]
  C23 = Ceramic Capacitor [capacitance=33nF package="100 mil [THT, multilayer]"]
  C24 = Ceramic Capacitor [capacitance=47nF package="100 mil [THT, multilayer]"]
  C25 = Ceramic Capacitor [capacitance=100nF package="100 mil [THT, multilayer]"]
  C26 = Ceramic Capacitor [capacitance=100nF package="100 mil [THT, multilayer]"]
  C27 = Ceramic Capacitor [capacitance=100nF package="100 mil [THT, multilayer]"]
  C28 = Ceramic Capacitor [capacitance=100nF package="100 mil [THT, multilayer]"]
  C29 = Ceramic Capacitor [capacitance=100nF package="100 mil [THT, multilayer]"]
  C30 = Ceramic Capacitor [capacitance=100nF package="100 mil [THT, multilayer]"]
  C31 = Ceramic Capacitor [capacitance=100nF package="100 mil [THT, multilayer]"]

nets:
  N1: CD3.SIG_A_IN/OUT, CD3.SIG_B_OUT/IN, CD19.SIG_A_IN/OUT, CD19.SIG_B_OUT/IN
  N2: CD3.SIG_A_OUT/IN, CD3.SIG_C_IN/OUT, CD19.SIG_A_OUT/IN, CD19.SIG_C_IN/OUT
  N3: CD3.SIG_B_IN/OUT, CD3.SIG_D_OUT/IN, CD19.SIG_B_IN/OUT, CD19.SIG_D_OUT/IN
  N4: CD3.CONTROL_B, CD3.CONTROL_C, CD19.CONTROL_B, CD19.CONTROL_C
  VSS: CD3.VSS, CD19.VSS, C26.0
  N5: CD3.SIG_C_OUT/IN, CD3.SIG_D_IN/OUT, CD19.SIG_C_OUT/IN, CD19.SIG_D_IN/OUT
  N6: CD3.CONTROL_D, CD3.CONTROL_A, CD19.CONTROL_D, CD19.CONTROL_A
  VDD: CD3.VDD, CD19.VDD, C26.1
  N7: CD7.SIG_A_IN/OUT, CD7.SIG_B_OUT/IN, CD18.SIG_A_IN/OUT, CD18.SIG_B_OUT/IN
  N8: CD7.SIG_A_OUT/IN, CD7.SIG_C_IN/OUT, CD18.SIG_A_OUT/IN, CD18.SIG_C_IN/OUT
  N9: CD7.SIG_B_IN/OUT, CD7.SIG_D_OUT/IN, CD18.SIG_B_IN/OUT, CD18.SIG_D_OUT/IN
  N10: CD7.CONTROL_B, CD7.CONTROL_C, CD18.CONTROL_B, CD18.CONTROL_C
  VSS_2: CD7.VSS, CD17.VSS, CD18.VSS, CD21.VSS, CD22.CONTROL_B, CD22.VSS, CD22.CONTROL_A, CD23.VSS, CD24.VSS, C25.0, C28.0, C29.0, C30.0, C31.0
  N11: CD7.SIG_C_OUT/IN, CD7.SIG_D_IN/OUT, CD18.SIG_C_OUT/IN, CD18.SIG_D_IN/OUT
  N12: CD7.CONTROL_D, CD7.CONTROL_A, CD18.CONTROL_D, CD18.CONTROL_A
  VDD_2: CD7.VDD, CD8.VDD, CD17.VDD, CD18.VDD, CD20.VDD, CD21.VDD, CD22.VDD, CD23.VDD, CD24.VDD, C25.1, C27.1, C28.1, C29.1, C30.1, C31.1
  N13: CD8.SIG_A_IN/OUT, CD8.SIG_B_OUT/IN, CD20.SIG_A_IN/OUT, CD20.SIG_B_OUT/IN
  N14: CD8.SIG_A_OUT/IN, CD8.SIG_C_IN/OUT, CD20.SIG_A_OUT/IN, CD20.SIG_C_IN/OUT
  N15: CD8.SIG_B_IN/OUT, CD8.SIG_D_OUT/IN, CD20.SIG_B_IN/OUT, CD20.SIG_D_OUT/IN
  N16: CD8.CONTROL_B, CD8.CONTROL_C, CD20.CONTROL_B, CD20.CONTROL_C
  VSS_3: CD8.VSS, CD20.VSS, C27.0
  N17: CD8.SIG_C_OUT/IN, CD8.SIG_D_IN/OUT, CD20.SIG_C_OUT/IN, CD20.SIG_D_IN/OUT
  N18: CD8.CONTROL_D, CD8.CONTROL_A, CD20.CONTROL_D, CD20.CONTROL_A
  N19: CD17.SIG_A_IN/OUT, CD17.SIG_B_OUT/IN, CD21.SIG_A_IN/OUT, CD21.SIG_B_OUT/IN
  N20: CD17.SIG_A_OUT/IN, CD17.SIG_C_IN/OUT, CD21.SIG_A_OUT/IN, CD21.SIG_C_IN/OUT
  N21: CD17.SIG_B_IN/OUT, CD17.SIG_D_OUT/IN, CD21.SIG_B_IN/OUT, CD21.SIG_D_OUT/IN
  N22: CD17.CONTROL_B, CD21.CONTROL_B
  N23: CD17.CONTROL_C, CD21.CONTROL_C
  N24: CD17.SIG_C_OUT/IN, CD17.SIG_D_IN/OUT, CD21.SIG_C_OUT/IN, CD21.SIG_D_IN/OUT
  N25: CD17.CONTROL_D, CD17.CONTROL_A, CD21.CONTROL_D, CD21.CONTROL_A
  N26: CD22.SIG_A_IN/OUT, CD22.SIG_A_OUT/IN, CD22.SIG_B_OUT/IN, CD22.SIG_B_IN/OUT, CD22.SIG_C_IN/OUT, R35.Pin_1, R36.Pin_1
  N27: CD22.SIG_C_OUT/IN, CD22.SIG_D_OUT/IN, CD23.SIG_A_OUT/IN, CD23.SIG_B_OUT/IN, CD23.SIG_C_OUT/IN, CD23.SIG_D_OUT/IN, CD24.SIG_A_OUT/IN, CD24.SIG_B_OUT/IN, CD24.SIG_C_OUT/IN, CD24.SIG_D_OUT/IN
  N28: CD22.SIG_D_IN/OUT, R32.Pin_1, R35.Pin_0
  N29: CD23.SIG_A_IN/OUT, C22.0
  N30: CD23.SIG_C_IN/OUT, R32.Pin_0, R33.Pin_1
  N31: CD23.SIG_D_IN/OUT, R33.Pin_0, R34.Pin_1
  N32: CD24.SIG_A_IN/OUT, C24.0
  N33: CD24.SIG_B_IN/OUT, C23.0
  N34: CD24.SIG_C_IN/OUT, R31.Pin_1, R34.Pin_0
  N35: CD24.SIG_D_IN/OUT, R31.Pin_0
  N36: R36.Pin_0, C21.1, C22.1, C23.1, C24.1

notes:
  Iverters 1,2,3,4
  +5v
  Coil-1
  North
  South
  Coil-2
  North
  South
  Coil-3
  North
  South
  Output-1
  North,
  South
  Control-2
  AD, BC
  Control-1
  AD, BC
  -5v
  Output-2
  North,
  South
  Output-3
  North,
  South
  Control-4
  AD, BC
  Control-3
  AD, BC
  Gnd
  Coil-4
  North
  South
  Output-4
  North,
  South
  Master Vol/Tone IN
  D on 1st 4066
  Master Vol/tone
  OUT
  Master Vol/Tone
  (to amp input)
  47-33-22-10 nF + 100KOhm

custom parts:
  CD4066 Quad Analog Switch: Quad Analog Switch
