# Fritzing sketch POC Switching Breadboard (saved by Fritzing 0.9.0b)
breadboards: 1

parts:
  CD1 = CD4066 Quad Analog Switch [part_number=4066 package="DIP (Dual Inline) [THT]"]
  CD2 = CD4066 Quad Analog Switch [part_number=4066 package="DIP (Dual Inline) [THT]"]
  CD3 = CD4066 Quad Analog Switch [part_number=4066 package="DIP (Dual Inline) [THT]"]
  CD4 = CD4066 Quad Analog Switch [part_number=4066 package="DIP (Dual Inline) [THT]"]
  CD5 = CD4066 Quad Analog Switch [part_number=4066 package="DIP (Dual Inline) [THT]"]
  CD6 = CD4066 Quad Analog Switch [part_number=4066 package="DIP (Dual Inline) [THT]"]
  CD7 = CD4066 Quad Analog Switch [part_number=4066 package="DIP (Dual Inline) [THT]"]
  CD8 = CD4066 Quad Analog Switch [part_number=4066 package="DIP (Dual Inline) [THT]"]

nets:
  N1: CD1.SIG_A_IN/OUT, CD6.SIG_A_OUT/IN, CD6.SIG_B_OUT/IN, CD6.SIG_C_OUT/IN, CD6.SIG_D_OUT/IN, CD8.SIG_A_IN/OUT, CD8.SIG_C_IN/OUT
  N2: CD1.SIG_A_OUT/IN, CD1.SIG_B_OUT/IN, CD1.SIG_C_OUT/IN, CD1.SIG_D_OUT/IN, CD2.SIG_A_OUT/IN, CD2.SIG_B_OUT/IN, CD2.SIG_D_IN/OUT
  N3: CD1.SIG_B_IN/OUT, CD3.SIG_B_IN/OUT, CD4.SIG_A_IN/OUT, CD6.SIG_A_IN/OUT, CD7.SIG_A_OUT/IN, CD7.SIG_B_OUT/IN, CD7.SIG_D_IN/OUT
  N4: CD1.SIG_C_IN/OUT, CD3.SIG_C_IN/OUT, CD4.SIG_B_IN/OUT, CD5.SIG_A_IN/OUT, CD6.SIG_C_IN/OUT, CD7.SIG_B_IN/OUT, CD7.SIG_C_IN/OUT
  N5: CD1.SIG_D_IN/OUT, CD3.SIG_D_IN/OUT, CD4.SIG_C_IN/OUT, CD5.SIG_A_OUT/IN, CD5.SIG_B_OUT/IN, CD5.SIG_D_IN/OUT, CD6.SIG_D_IN/OUT
  N6: CD2.SIG_A_IN/OUT, CD3.SIG_A_IN/OUT, CD5.SIG_B_IN/OUT, CD5.SIG_C_IN/OUT, CD6.SIG_B_IN/OUT, CD7.SIG_A_IN/OUT, CD8.SIG_B_IN/OUT
  N7: CD2.SIG_B_IN/OUT, CD2.SIG_C_IN/OUT, CD3.SIG_A_OUT/IN, CD3.SIG_B_OUT/IN, CD3.SIG_C_OUT/IN, CD3.SIG_D_OUT/IN, CD4.SIG_D_IN/OUT
  N8: CD2.SIG_C_OUT/IN, CD2.SIG_D_OUT/IN, CD7.SIG_C_OUT/IN, CD7.SIG_D_OUT/IN
  N9: CD4.SIG_A_OUT/IN, CD4.SIG_B_OUT/IN, CD4.SIG_C_OUT/IN, CD4.SIG_D_OUT/IN, CD8.SIG_A_OUT/IN, CD8.SIG_B_OUT/IN, CD8.SIG_D_IN/OUT
  N10: CD5.SIG_C_OUT/IN, CD5.SIG_D_OUT/IN, CD8.SIG_C_OUT/IN, CD8.SIG_D_OUT/IN

notes:
  GND
  Out+
  A+
  A-
  B+
  B-
  C+
  C-
  D+
  D-

custom parts:
  CD4066 Quad Analog Switch: Quad Analog Switch
