# Fritzing sketch POC Vol-Tone Breadboard resistive tone control (saved by Fritzing 0.9.0b)
breadboards: 1

parts:
  CD20 = CD4066 Quad Analog Switch [part_number=4066 package="DIP (Dual Inline) [THT]"]
  CD22 = CD4066 Quad Analog Switch [part_number=4066 package="DIP (Dual Inline) [THT]"]
  CD23 = CD4066 Quad Analog Switch [part_number=4066 package="DIP (Dual Inline) [THT]"]
  R13 = Resistor [tolerance=±5% resistance=100k package=THT]
  R14 = Resistor [tolerance=±5% resistance=100k package=THT]
  R18 = Resistor [tolerance=±5% resistance=100k package=THT]
  C25 = Ceramic Capacitor [capacitance=100nF package="100 mil [THT, multilayer]"]
  C26 = Ceramic Capacitor [capacitance=100nF package="100 mil [THT, multilayer]"]
  CD24 = CD4066 Quad Analog Switch [part_number=4066 package="DIP (Dual Inline) [THT]"]
  R40 = Resistor [tolerance=±5% resistance=100k package=THT]  # not connected
  R41 = Resistor [tolerance=±5% resistance=200k package=THT]  # not connected
  R42 = Resistor [tolerance=±5% resistance=22k package=THT]  # not connected
  R43 = Resistor [tolerance=±5% resistance=50k package=THT]  # not connected
  C30 = Ceramic Capacitor [capacitance=10nF package="100 mil [THT, multilayer]"]  # not connected
  C31 = Ceramic Capacitor [capacitance=100nF package="100 mil [THT, multilayer]"]
  R21 = Resistor [tolerance=±5% resistance=100k package=THT]
  C29 = Ceramic Capacitor [capacitance=100nF package="100 mil [THT, multilayer]"]
  R17 = Resistor [tolerance=±5% resistance=100k package=THT]
  C27 = Ceramic Capacitor [capacitance=100nF package="100 mil [THT, multilayer]"]
  R34 = Resistor [tolerance=±5% resistance=100k package=THT]
  C28 = Ceramic Capacitor [capacitance=100nF package="100 mil [THT, multilayer]"]
  R32 = Resistor [tolerance=±5% resistance=100k package=THT]
  R31 = Resistor [tolerance=±5% resistance=100k package=THT]
  CD21 = CD4066 Quad Analog Switch [part_number=4066 package="DIP (Dual Inline) [THT]"]
  R35 = Resistor [tolerance=±5% resistance=100k package=THT]
  R33 = Resistor [tolerance=±5% resistance=100k package=THT]
  CD19 = CD4066 Quad Analog Switch [part_number=4066 package="DIP (Dual Inline) [THT]"]

nets:
  N1: CD20.SIG_A_OUT/IN, CD20.SIG_B_OUT/IN, CD20.SIG_C_OUT/IN, CD20.SIG_D_OUT/IN, CD23.SIG_A_OUT/IN, CD23.SIG_B_OUT/IN, CD23.SIG_C_OUT/IN, CD23.SIG_D_OUT/IN, CD21.SIG_C_OUT/IN, CD21.SIG_D_OUT/IN
  VSS: CD20.VSS, CD22.VSS, CD23.VSS, C25.0, C26.0, CD24.VSS, C31.0, C29.0, C27.0, C28.0, CD21.VSS, CD19.CONTROL_B
  N2: CD20.SIG_C_IN/OUT, R14.Pin_0, R18.Pin_1
  N3: CD20.SIG_D_IN/OUT, R18.Pin_0
  VDD: CD20.VDD, CD22.VDD, CD23.VDD, C25.1, C26.1, CD24.VDD, C31.1, C29.1, C27.1, C28.1, CD21.VDD
  N4: CD23.SIG_C_IN/OUT, R13.Pin_1, R21.Pin_0
  N5: CD23.SIG_D_IN/OUT, R13.Pin_0, R14.Pin_1
  N6: CD24.SIG_A_OUT/IN, CD24.SIG_B_OUT/IN, CD24.SIG_C_OUT/IN, CD24.SIG_D_OUT/IN, R17.Pin_1, R31.Pin_1, CD21.SIG_B_IN/OUT, CD21.SIG_C_IN/OUT
  N7: R21.Pin_1, R17.Pin_0, CD21.SIG_D_IN/OUT
  N8: R34.Pin_0, CD19.CONTROL_A
  N9: R34.Pin_1, R33.Pin_0, CD19.SIG_D_OUT/IN
  N10: R32.Pin_0, R33.Pin_1
  N11: R32.Pin_1, R35.Pin_0
  N12: R31.Pin_0, CD21.SIG_A_IN/OUT, R35.Pin_1
  N13: CD21.SIG_A_OUT/IN, CD21.SIG_B_OUT/IN, CD19.SIG_A_IN/OUT, CD19.VSS, CD19.SIG_D_IN/OUT, CD19.CONTROL_D

notes:
  Vol/tone 1,2
  Gnd
  Vol/Tone-1 Out
  +5v
  -5v
  Vol/Tone-1 In
  (Inverter-1 North-Out)
  Vol/Tone-2 Out
  4x Tone on/off
  10 nF 200,100,50,22Kohm

custom parts:
  CD4066 Quad Analog Switch: Quad Analog Switch
