# Fritzing sketch POC Vol-Tone Breadboard (saved by Fritzing 0.9.0b)
breadboards: 1

parts:
  CD19 = CD4066 Quad Analog Switch [part_number=4066 package="DIP (Dual Inline) [THT]"]
  CD20 = CD4066 Quad Analog Switch [part_number=4066 package="DIP (Dual Inline) [THT]"]
  CD21 = CD4066 Quad Analog Switch [part_number=4066 package="DIP (Dual Inline) [THT]"]
  CD22 = CD4066 Quad Analog Switch [part_number=4066 package="DIP (Dual Inline) [THT]"]
  CD23 = CD4066 Quad Analog Switch [part_number=4066 package="DIP (Dual Inline) [THT]"]
  R13 = Resistor [tolerance=±5% resistance=100k package=THT]
  R14 = Resistor [tolerance=±5% resistance=100k package=THT]
  R17 = Resistor [tolerance=±5% resistance=100k package=THT]
  R18 = Resistor [tolerance=±5% resistance=100k package=THT]
  R21 = Resistor [tolerance=±5% resistance=100k package=THT]
  R23 = Resistor [tolerance=±5% resistance=100k package=THT]
  C11 = Ceramic Capacitor [capacitance=10nF package="100 mil [THT, multilayer]"]
  C12 = Ceramic Capacitor [capacitance=33nF package="100 mil [THT, multilayer]"]
  C13 = Ceramic Capacitor [capacitance=47nF package="100 mil [THT, multilayer]"]
  C16 = Ceramic Capacitor [capacitance=22nF package="100 mil [THT, multilayer]"]
  R31 = Resistor [tolerance=±5% resistance=100k package=THT]
  R32 = Resistor [tolerance=±5% resistance=100k package=THT]
  R33 = Resistor [tolerance=±5% resistance=100k package=THT]
  R34 = Resistor [tolerance=±5% resistance=100k package=THT]
  R35 = Resistor [tolerance=±5% resistance=100k package=THT]
  R36 = Resistor [tolerance=±5% resistance=100k package=THT]
  C21 = Ceramic Capacitor [capacitance=10nF package="100 mil [THT, multilayer]"]
  C22 = Ceramic Capacitor [capacitance=22nF package="100 mil [THT, multilayer]"]
  C23 = Ceramic Capacitor [capacitance=33nF package="100 mil [THT, multilayer]"]
  C24 = Ceramic Capacitor [capacitance=47nF package="100 mil [THT, multilayer]"]
  C25 = Ceramic Capacitor [capacitance=100nF package="100 mil [THT, multilayer]"]
  C26 = Ceramic Capacitor [capacitance=100nF package="100 mil [THT, multilayer]"]
  C27 = Ceramic Capacitor [capacitance=100nF package="100 mil [THT, multilayer]"]
  C28 = Ceramic Capacitor [capacitance=100nF package="100 mil [THT, multilayer]"]
  C29 = Ceramic Capacitor [capacitance=100nF package="100 mil [THT, multilayer]"]

nets:
  N1: CD19.SIG_A_IN/OUT, C24.0
  N2: CD19.SIG_A_OUT/IN, CD19.SIG_B_OUT/IN, CD19.SIG_C_OUT/IN, CD19.SIG_D_OUT/IN, CD21.SIG_A_OUT/IN, CD21.SIG_B_OUT/IN, CD22.SIG_A_OUT/IN, CD22.SIG_B_OUT/IN, CD22.SIG_C_OUT/IN, CD22.SIG_D_OUT/IN
  N3: CD19.SIG_B_IN/OUT, C23.0
  VSS: CD19.VSS, CD20.VSS, CD21.VSS, CD22.VSS, CD23.VSS, C25.0, C26.0, C27.0, C28.0, C29.0
  N4: CD19.SIG_C_IN/OUT, R33.Pin_0, R34.Pin_1
  N5: CD19.SIG_D_IN/OUT, R34.Pin_0
  VDD: CD19.VDD, CD20.VDD, CD21.VDD, CD22.VDD, CD23.VDD, C25.1, C26.1, C27.1, C28.1, C29.1
  N6: CD20.SIG_A_IN/OUT, C13.0
  N7: CD20.SIG_A_OUT/IN, CD20.SIG_B_OUT/IN, CD20.SIG_C_OUT/IN, CD20.SIG_D_OUT/IN, CD21.SIG_C_OUT/IN, CD21.SIG_D_OUT/IN, CD23.SIG_A_OUT/IN, CD23.SIG_B_OUT/IN, CD23.SIG_C_OUT/IN, CD23.SIG_D_OUT/IN
  N8: CD20.SIG_B_IN/OUT, C12.0
  N9: CD20.SIG_C_IN/OUT, R14.Pin_0, R18.Pin_1
  N10: CD20.SIG_D_IN/OUT, R18.Pin_0
  N11: CD21.SIG_A_IN/OUT, R31.Pin_0, R35.Pin_1
  N12: CD21.SIG_B_IN/OUT, CD21.SIG_C_IN/OUT, R17.Pin_1, R23.Pin_1, R31.Pin_1, R36.Pin_1
  N13: CD21.SIG_D_IN/OUT, R17.Pin_0, R21.Pin_1
  N14: CD22.SIG_A_IN/OUT, C22.0
  N15: CD22.SIG_B_IN/OUT, C21.0
  N16: CD22.SIG_C_IN/OUT, R32.Pin_1, R35.Pin_0
  N17: CD22.SIG_D_IN/OUT, R32.Pin_0, R33.Pin_1
  N18: CD23.SIG_A_IN/OUT, C16.0
  N19: CD23.SIG_B_IN/OUT, C11.0
  N20: CD23.SIG_C_IN/OUT, R13.Pin_1, R21.Pin_0
  N21: CD23.SIG_D_IN/OUT, R13.Pin_0, R14.Pin_1
  N22: R23.Pin_0, C11.1, C12.1, C13.1, C16.1
  N23: R36.Pin_0, C21.1, C22.1, C23.1, C24.1

notes:
  Vol/tone 1,2
  Gnd
  Vol/Tone-1 Out
  +5v
  -5v
  Vol/Tone-1 In
  (Inverter-1 North-Out)
  Vol/Tone-2 In
  (Inverter-2s North-Out)
  Vol/Tone-2 Out
  47-33-22-10 nF + 100KOhm

custom parts:
  CD4066 Quad Analog Switch: Quad Analog Switch
