# Fritzing sketch POC-1 Schematic (saved by Fritzing 0.9.0b)
breadboards: 1

parts:
  R1 = Rotary Potentiometer (Small) [maximum_resistance=500kΩ package=THT]
  R2 = Rotary Potentiometer (Small) [maximum_resistance=500kΩ package=THT]
  C1 = Ceramic Capacitor [capacitance=10nF package="100 mil [THT, multilayer]"]
  R3 = Rotary Potentiometer (Small) [maximum_resistance=500kΩ package=THT]
  R4 = Rotary Potentiometer (Small) [maximum_resistance=500kΩ package=THT]
  C2 = Ceramic Capacitor [capacitance=10nF package="100 mil [THT, multilayer]"]
  R5 = Rotary Potentiometer (Small) [maximum_resistance=500kΩ package=THT]
  R6 = Rotary Potentiometer (Small) [maximum_resistance=500kΩ package=THT]
  R7 = Rotary Potentiometer (Small) [maximum_resistance=500kΩ package=THT]
  R8 = Rotary Potentiometer (Small) [maximum_resistance=500kΩ package=THT]
  C3 = Ceramic Capacitor [capacitance=10nF package="100 mil [THT, multilayer]"]
  C4 = Ceramic Capacitor [capacitance=10nF package="100 mil [THT, multilayer]"]
  Switch_Array = IC, DIP package, 10 pins [chip_label=IC's]
  Amp = female pin header, 2 pins [form="♀ (female)"]
  R9 = Rotary Potentiometer (Small) [maximum_resistance=500kΩ package=THT]
  R10 = Rotary Potentiometer (Small) [maximum_resistance=500kΩ package=THT]
  C5 = Ceramic Capacitor [capacitance=10nF package="100 mil [THT, multilayer]"]
  Inverter = IC, DIP package, 4 pins [chip_label=IC's]
  L5 = Inductor [package="400 mil [THT]"]
  L6 = Inductor [package="400 mil [THT]"]
  Inverter1 = IC, DIP package, 4 pins [chip_label=IC's]
  L7 = Inductor [package="400 mil [THT]"]
  Inverter2 = IC, DIP package, 4 pins [chip_label=IC's]
  L8 = Inductor [package="400 mil [THT]"]
  Inverter3 = IC, DIP package, 4 pins [chip_label=IC's]

nets:
  N1: R1.leg1, C1.1, Switch_Array.pin5, Inverter3.pin3
  N2: R1.wiper, R2.leg2, Switch_Array.pin4
  N3: R1.leg2, Inverter3.pin4
  N4: R2.wiper, C1.0
  N5: R3.wiper, C2.0
  N6: R3.leg2, R4.wiper, Switch_Array.pin2
  N7: R4.leg1, C2.1, Switch_Array.pin3, Inverter1.pin3
  N8: R4.leg2, Inverter1.pin4
  N9: R5.wiper, C3.0
  N10: R5.leg2, R8.wiper, Switch_Array.pin8
  N11: R6.wiper, C4.0
  N12: R6.leg2, R7.wiper, Switch_Array.pin10
  N13: R7.leg1, C4.1, Switch_Array.pin1, Inverter2.pin3
  N14: R7.leg2, Inverter2.pin4
  N15: R8.leg1, C3.1, Switch_Array.pin9, Inverter.pin3
  N16: R8.leg2, Inverter.pin4
  GND: Switch_Array.pin6, Amp.pin2, R9.leg1, C5.1
  N17: Switch_Array.pin7, R9.leg2
  N18: Amp.pin1, R9.wiper, R10.leg2
  N19: R10.wiper, C5.0
  N20: Inverter.pin1, L5.pin_0
  N21: Inverter.pin2, L5.pin_1
  N22: L6.pin_0, Inverter1.pin1
  N23: L6.pin_1, Inverter1.pin2
  N24: L7.pin_0, Inverter2.pin1
  N25: L7.pin_1, Inverter2.pin2
  N26: L8.pin_0, Inverter3.pin1
  N27: L8.pin_1, Inverter3.pin2

notes:
  Amp1 is the +Input
  Amp2 is the GND output
  Each coil has its own
  Vol/Tone control
  Master Vol/Tone Control
