# Fritzing sketch POC-1 Single Inverter and resistive tone control schematic  (saved by Fritzing 0.9.0b)
breadboards: 1

parts:
  L1 = Inductor [package="400 mil [THT]"]
  C1 = Ceramic Capacitor [capacitance=100nF package="100 mil [THT, multilayer]"]
  CD1 = CD4066 Quad Analog Switch [part_number=4066 package="DIP (Dual Inline) [THT]"]
  C2 = Ceramic Capacitor [capacitance=100nF package="100 mil [THT, multilayer]"]
  CD2 = CD4066 Quad Analog Switch [part_number=4066 package="DIP (Dual Inline) [THT]"]
  C3 = Ceramic Capacitor [capacitance=100nF package="100 mil [THT, multilayer]"]
  CD3 = CD4066 Quad Analog Switch [part_number=4066 package="DIP (Dual Inline) [THT]"]
  C4 = Ceramic Capacitor [capacitance=100nF package="100 mil [THT, multilayer]"]
  CD4 = CD4066 Quad Analog Switch [part_number=4066 package="DIP (Dual Inline) [THT]"]
  R1 = Resistor [tolerance=±5% resistance=100k package=THT]
  R2 = Resistor [tolerance=±5% resistance=100k package=THT]
  R3 = Resistor [tolerance=±5% resistance=100k package=THT]
  R4 = Resistor [tolerance=±5% resistance=100k package=THT]
  R5 = Resistor [tolerance=±5% resistance=100k package=THT]
  R6 = Resistor [tolerance=±5% resistance=100k package=THT]
  R7 = Resistor [tolerance=±5% resistance=200k package=THT]
  R8 = Resistor [tolerance=±5% resistance=50k package=THT]
  R9 = Resistor [tolerance=±5% resistance=22k package=THT]
  C5 = Ceramic Capacitor [capacitance=10nF package="100 mil [THT, multilayer]"]
  +5v = female pin header, 1 pin [form="♀ (female)"]
  -5v = female pin header, 1 pin [form="♀ (female)"]
  Straight = female pin header, 1 pin [form="♀ (female)"]
  Invert = female pin header, 1 pin [form="♀ (female)"]
  OUT+ = female pin header, 1 pin [form="♀ (female)"]
  OUT- = female pin header, 1 pin [form="♀ (female)"]
  V100% = female pin header, 1 pin [form="♀ (female)"]
  V80% = female pin header, 1 pin [form="♀ (female)"]
  V40% = female pin header, 1 pin [form="♀ (female)"]
  V60% = female pin header, 1 pin [form="♀ (female)"]
  V20% = female pin header, 1 pin [form="♀ (female)"]
  V0% = female pin header, 1 pin [form="♀ (female)"]
  T200 = female pin header, 1 pin [form="♀ (female)"]
  T100 = female pin header, 1 pin [form="♀ (female)"]
  T22 = female pin header, 1 pin [form="♀ (female)"]
  T50 = female pin header, 1 pin [form="♀ (female)"]
  Ton/off = female pin header, 1 pin [form="♀ (female)"]

nets:
  N1: L1.pin_0, CD1.SIG_C_OUT/IN, CD1.SIG_D_IN/OUT
  N2: L1.pin_1, CD1.SIG_A_IN/OUT, CD1.SIG_B_OUT/IN
  VSS: C1.0, CD1.VSS, C2.0, CD2.VSS, C3.0, CD3.VSS, C4.0, CD4.CONTROL_B, CD4.VSS, -5v.pin1
  VDD: C1.1, CD1.VDD, C2.1, CD2.VDD, C3.1, CD3.VDD, C4.1, CD4.VDD, +5v.pin1
  N3: CD1.SIG_A_OUT/IN, CD1.SIG_C_IN/OUT, CD4.SIG_A_OUT/IN, CD4.SIG_C_IN/OUT, R5.Pin_1, OUT-.pin1
  N4: CD1.SIG_B_IN/OUT, CD1.SIG_D_OUT/IN, CD2.SIG_D_IN/OUT, R3.Pin_0
  N5: CD1.CONTROL_B, CD1.CONTROL_C, Invert.pin1
  N6: CD1.CONTROL_D, CD1.CONTROL_A, Straight.pin1
  N7: CD2.SIG_A_IN/OUT, R7.Pin_0
  N8: CD2.SIG_A_OUT/IN, CD2.SIG_B_OUT/IN, CD2.SIG_C_OUT/IN, CD2.SIG_D_OUT/IN, CD3.SIG_A_OUT/IN, CD3.SIG_B_OUT/IN, CD3.SIG_C_OUT/IN, CD3.SIG_D_OUT/IN, CD4.SIG_C_OUT/IN, CD4.SIG_D_OUT/IN, OUT+.pin1
  N9: CD2.SIG_B_IN/OUT, R6.Pin_0
  N10: CD2.CONTROL_B, T100.pin1
  N11: CD2.CONTROL_C, V80%.pin1
  N12: CD2.SIG_C_IN/OUT, R2.Pin_0, R3.Pin_1
  N13: CD2.CONTROL_D, V100%.pin1
  N14: CD2.CONTROL_A, T200.pin1
  N15: CD3.SIG_A_IN/OUT, R8.Pin_0
  N16: CD3.SIG_B_IN/OUT, R9.Pin_0
  N17: CD3.CONTROL_B, T22.pin1
  N18: CD3.CONTROL_C, V40%.pin1
  N19: CD3.SIG_C_IN/OUT, R1.Pin_0, R4.Pin_1
  N20: CD3.SIG_D_IN/OUT, R2.Pin_1, R4.Pin_0
  N21: CD3.CONTROL_D, V60%.pin1
  N22: CD3.CONTROL_A, T50.pin1
  N23: CD4.SIG_A_IN/OUT, C5.1
  GND: CD4.SIG_B_OUT/IN, CD4.SIG_B_IN/OUT
  N24: CD4.CONTROL_C, V0%.pin1
  N25: CD4.SIG_D_IN/OUT, R1.Pin_1, R5.Pin_0
  N26: CD4.CONTROL_D, V20%.pin1
  N27: CD4.CONTROL_A, Ton/off.pin1
  N28: R6.Pin_1, R7.Pin_1, R8.Pin_1, R9.Pin_1, C5.0

custom parts:
  CD4066 Quad Analog Switch: Quad Analog Switch
