# Fritzing sketch PSU -5v (saved by Fritzing 0.9.0b)
breadboards: 1

parts:
  LM2596_ADJ = female pin header, 5 pins [form="♀ (female)"]
  Cin = Electrolytic Capacitor [capacitance=470µF package="100 mil [THT, electrolytic]"]
  L1 = Inductor [package="400 mil [THT]"]
  Cout = Electrolytic Capacitor [capacitance=220µF package="100 mil [THT, electrolytic]"]
  R1 = Resistor [tolerance=±5% resistance=33k package=THT]
  R2 = Resistor [tolerance=±5% resistance=100k package=THT]
  Vout_-5V = male pin header, 1 pin [form="♂ (male)"]
  Vin = female pin header, 1 pin [form="♀ (female)"]
  D3 = Rectifier Diode [part_number="1N5400 (not schottky)" package="300 mil [THT]"]
  D4 = Schottky Diode [part_number=1N5823 package="Melf DO-213 AB [SMD]"]
  D2 = Schottky Diode [part_number=1N5825 package="Melf DO-213 AB [SMD]"]

nets:
  N1: LM2596_ADJ.pin1, Cin.+, D4.cathode
  N2: LM2596_ADJ.pin2, L1.pin_0, D2.cathode
  N3: LM2596_ADJ.pin3, LM2596_ADJ.pin5, Cin.-, Cout.-, R1.Pin_1, Vout_-5V.pin1, D3.anode, D2.anode
  N4: LM2596_ADJ.pin4, R1.Pin_0, R2.Pin_0
  GND: L1.pin_1, Cout.+, R2.Pin_1, D3.cathode
  N5: Vin.pin1, D4.anode

notes:
  Vin +9v, Vout -5v
  GND (Vin 0v)
