# Fritzing sketch SPDT Inverter-VT-PCB (saved by Fritzing 0.9.0b)
circuit board: 7.90338cm x 2.27336cm
breadboards: 1

parts:
  Controls = female pin header, 13 pins [form="♀ (female)" part_number=Controls]
  V100 = female pin header, 5 pins [form="♀ (female)"]
  Inv = female pin header, 5 pins [form="♀ (female)"]
  Str = female pin header, 5 pins [form="♀ (female)"]
  V80 = female pin header, 5 pins [form="♀ (female)"]
  V60 = female pin header, 5 pins [form="♀ (female)"]
  V40 = female pin header, 5 pins [form="♀ (female)"]
  V20 = female pin header, 5 pins [form="♀ (female)"]
  V0 = female pin header, 5 pins [form="♀ (female)"]
  T200 = female pin header, 5 pins [form="♀ (female)"]
  T100 = female pin header, 5 pins [form="♀ (female)"]
  T50 = female pin header, 5 pins [form="♀ (female)"]
  T25 = female pin header, 5 pins [form="♀ (female)"]
  Ton/off = female pin header, 5 pins [form="♀ (female)"]
  Vin = female pin header, 3 pins [form="♀ (female)"]

nets:
  N1: Controls.pin1, Str.pin3
  N2: Controls.pin2, Inv.pin3
  N3: Controls.pin3, V100.pin3
  N4: Controls.pin4, V80.pin3
  N5: Controls.pin5, V60.pin3
  N6: Controls.pin6, V40.pin3
  N7: Controls.pin7, V20.pin3
  N8: Controls.pin8, V0.pin3
  N9: Controls.pin9, T200.pin3
  N10: Controls.pin10, T100.pin3
  N11: Controls.pin11, T50.pin3
  N12: Controls.pin12, T25.pin3
  N13: Controls.pin13, Ton/off.pin3
  N14: V100.pin2, Inv.pin2, Str.pin2, V80.pin2, V60.pin2, V40.pin2, V20.pin2, V0.pin2, T200.pin2, T100.pin2, T50.pin2, T25.pin2, Ton/off.pin2, Vin.pin1
  N15: V100.pin4, Inv.pin4, Str.pin4, V80.pin4, V60.pin4, V40.pin4, V20.pin4, V0.pin4, T200.pin4, T100.pin4, T50.pin4, T25.pin4, Ton/off.pin4, Vin.pin3

notes:
  V+  V-
