# Fritzing sketch SPDT Switch-Array-PCB (saved by Fritzing 0.9.0b)
circuit board: 6.49408cm x 11.8787cm
breadboards: 1

parts:
  A+ = female pin header, 7 pins [form="♀ (female)"]
  D- = female pin header, 1 pin [form="♀ (female)"]
  D+ = female pin header, 1 pin [form="♀ (female)"]
  Vin = female pin header, 2 pins [form="♀ (female)"]
  C- = female pin header, 3 pins [form="♀ (female)"]
  C+ = female pin header, 3 pins [form="♀ (female)"]
  B- = female pin header, 5 pins [form="♀ (female)"]
  B+ = female pin header, 5 pins [form="♀ (female)"]
  A- = female pin header, 7 pins [form="♀ (female)"]
  Out+ = female pin header, 3 pins [form="♀ (female)"]
  D-_2 = female pin header, 3 pins [form="♀ (female)"]
  D+_2 = female pin header, 3 pins [form="♀ (female)"]
  C-_2 = female pin header, 3 pins [form="♀ (female)"]
  C+_2 = female pin header, 3 pins [form="♀ (female)"]
  B-_2 = female pin header, 3 pins [form="♀ (female)"]
  B+_2 = female pin header, 3 pins [form="♀ (female)"]
  Out- = female pin header, 3 pins [form="♀ (female)"]
  D-_3 = female pin header, 3 pins [form="♀ (female)"]
  D+_3 = female pin header, 3 pins [form="♀ (female)"]
  C-_3 = female pin header, 3 pins [form="♀ (female)"]
  C+_3 = female pin header, 3 pins [form="♀ (female)"]
  B-_3 = female pin header, 3 pins [form="♀ (female)"]
  B+_3 = female pin header, 3 pins [form="♀ (female)"]
  C+_4 = female pin header, 3 pins [form="♀ (female)"]
  C-_4 = female pin header, 3 pins [form="♀ (female)"]
  D+_4 = female pin header, 3 pins [form="♀ (female)"]
  D-_4 = female pin header, 3 pins [form="♀ (female)"]
  Out+_2 = female pin header, 3 pins [form="♀ (female)"]
  C+_5 = female pin header, 3 pins [form="♀ (female)"]
  C-_5 = female pin header, 3 pins [form="♀ (female)"]
  D+_5 = female pin header, 3 pins [form="♀ (female)"]
  D-_5 = female pin header, 3 pins [form="♀ (female)"]
  Out-_2 = female pin header, 3 pins [form="♀ (female)"]
  D+_6 = female pin header, 3 pins [form="♀ (female)"]
  D-_6 = female pin header, 3 pins [form="♀ (female)"]
  Out+_3 = female pin header, 3 pins [form="♀ (female)"]
  D+_7 = female pin header, 3 pins [form="♀ (female)"]
  D-_7 = female pin header, 3 pins [form="♀ (female)"]
  Out-_3 = female pin header, 3 pins [form="♀ (female)"]
  Out+_4 = female pin header, 3 pins [form="♀ (female)"]
  Out-_4 = female pin header, 3 pins [form="♀ (female)"]

nets:
  N1: A+.pin1, B+_2.pin2
  N2: A+.pin2, B-_2.pin2
  N3: A+.pin3, C+_2.pin2
  N4: A+.pin4, C-_2.pin2
  N5: A+.pin5, D+_2.pin2
  N6: A+.pin6, D-_2.pin2
  N7: A+.pin7, Out+.pin2
  N8: D-.pin1, Out-_4.pin2
  N9: D+.pin1, Out+_4.pin2
  N10: Vin.pin1, Out+.pin1, D-_2.pin1, D+_2.pin1, C-_2.pin1, C+_2.pin1, B-_2.pin1, B+_2.pin1, Out-.pin1, D-_3.pin1, D+_3.pin1, C-_3.pin1, C+_3.pin1, B-_3.pin1, B+_3.pin1, C+_4.pin1, C-_4.pin1, D+_4.pin1, D-_4.pin1, Out+_2.pin1, C+_5.pin1, C-_5.pin1, D+_5.pin1, D-_5.pin1, Out-_2.pin1, D+_6.pin1, D-_6.pin1, Out+_3.pin1, D+_7.pin1, D-_7.pin1, Out-_3.pin1, Out+_4.pin1, Out-_4.pin1
  N11: Vin.pin2, Out+.pin3, D-_2.pin3, D+_2.pin3, C-_2.pin3, C+_2.pin3, B-_2.pin3, B+_2.pin3, Out-.pin3, D-_3.pin3, D+_3.pin3, C-_3.pin3, C+_3.pin3, B-_3.pin3, B+_3.pin3, C+_4.pin3, C-_4.pin3, D+_4.pin3, D-_4.pin3, Out+_2.pin3, C+_5.pin3, C-_5.pin3, D+_5.pin3, D-_5.pin3, Out-_2.pin3, D+_6.pin3, D-_6.pin3, Out+_3.pin3, D+_7.pin3, D-_7.pin3, Out-_3.pin3, Out+_4.pin3, Out-_4.pin3
  N12: C-.pin1, D+_7.pin2
  N13: C-.pin2, D-_7.pin2
  N14: C-.pin3, Out-_3.pin2
  N15: C+.pin1, D+_6.pin2
  N16: C+.pin2, D-_6.pin2
  N17: C+.pin3, Out+_3.pin2
  N18: B-.pin1, C+_5.pin2
  N19: B-.pin2, C-_5.pin2
  N20: B-.pin3, D+_5.pin2
  N21: B-.pin4, D-_5.pin2
  N22: B-.pin5, Out-_2.pin2
  N23: B+.pin1, C+_4.pin2
  N24: B+.pin2, C-_4.pin2
  N25: B+.pin3, D+_4.pin2
  N26: B+.pin4, D-_4.pin2
  N27: B+.pin5, Out+_2.pin2
  N28: A-.pin1, B+_3.pin2
  N29: A-.pin2, B-_3.pin2
  N30: A-.pin3, C+_3.pin2
  N31: A-.pin4, C-_3.pin2
  N32: A-.pin5, D+_3.pin2
  N33: A-.pin6, D-_3.pin2
  N34: A-.pin7, Out-.pin2

notes:
  V+
  B+
  B-
  C+
  C-
  D+
  D-
  Out+
  Out-
  V-
  A+
  A-
