# Fritzing sketch defect POC Combinator Breadboard (saved by Fritzing 0.9.0b)
breadboards: 1

parts:
  CD6 = CD4066 Quad Analog Switch [part_number=4066 package="DIP (Dual Inline) [THT]"]
  CD12 = CD4066 Quad Analog Switch [part_number=4066 package="DIP (Dual Inline) [THT]"]
  CD18 = CD4066 Quad Analog Switch [part_number=4066 package="DIP (Dual Inline) [THT]"]
  CD13 = CD4066 Quad Analog Switch [part_number=4066 package="DIP (Dual Inline) [THT]"]
  CD10 = CD4066 Quad Analog Switch [part_number=4066 package="DIP (Dual Inline) [THT]"]
  CD14 = CD4066 Quad Analog Switch [part_number=4066 package="DIP (Dual Inline) [THT]"]
  CD11 = CD4066 Quad Analog Switch [part_number=4066 package="DIP (Dual Inline) [THT]"]
  CD9 = CD4066 Quad Analog Switch [part_number=4066 package="DIP (Dual Inline) [THT]"]
  CD19 = CD4066 Quad Analog Switch [part_number=4066 package="DIP (Dual Inline) [THT]"]

nets:
  N1: CD6.SIG_A_IN/OUT, CD6.SIG_C_OUT/IN, CD12.SIG_C_IN/OUT, CD13.SIG_A_IN/OUT, CD13.SIG_C_OUT/IN, CD9.SIG_A_IN/OUT, CD9.SIG_C_OUT/IN
  N2: CD6.SIG_A_OUT/IN, CD6.SIG_B_OUT/IN, CD13.SIG_A_OUT/IN, CD13.SIG_B_OUT/IN, CD14.SIG_A_OUT/IN, CD14.SIG_B_OUT/IN, CD11.SIG_B_IN/OUT
  N3: CD6.SIG_B_IN/OUT, CD12.SIG_B_IN/OUT, CD18.SIG_A_OUT/IN, CD18.SIG_B_OUT/IN, CD10.SIG_B_IN/OUT, CD14.SIG_B_IN/OUT, CD19.SIG_B_IN/OUT
  VSS: CD6.VSS, CD12.VSS, CD18.VSS, CD13.VSS, CD10.VSS, CD14.VSS, CD11.VSS, CD9.VSS, CD19.VSS
  N4: CD6.SIG_C_IN/OUT, CD18.SIG_C_IN/OUT, CD10.SIG_C_IN/OUT, CD11.SIG_C_IN/OUT, CD9.SIG_C_IN/OUT, CD19.SIG_C_IN/OUT
  N5: CD6.SIG_D_OUT/IN, CD6.SIG_D_IN/OUT, CD6.CONTROL_D, CD12.SIG_D_OUT/IN, CD12.SIG_D_IN/OUT, CD12.CONTROL_D, CD18.SIG_D_OUT/IN, CD18.SIG_D_IN/OUT, CD18.CONTROL_D, CD13.SIG_D_OUT/IN, CD13.SIG_D_IN/OUT, CD13.CONTROL_D, CD10.SIG_D_OUT/IN, CD10.SIG_D_IN/OUT, CD10.CONTROL_D, CD14.SIG_D_OUT/IN, CD14.SIG_D_IN/OUT, CD14.CONTROL_D, CD11.SIG_D_OUT/IN, CD11.SIG_D_IN/OUT, CD11.CONTROL_D, CD9.SIG_D_OUT/IN, CD9.SIG_D_IN/OUT, CD9.CONTROL_D, CD19.SIG_D_OUT/IN, CD19.SIG_D_IN/OUT, CD19.CONTROL_D
  VDD: CD6.VDD, CD12.VDD, CD18.VDD, CD13.VDD, CD10.VDD, CD14.VDD, CD11.VDD, CD9.VDD, CD19.VDD
  N6: CD12.SIG_A_IN/OUT, CD12.SIG_C_OUT/IN, CD10.SIG_A_IN/OUT, CD10.SIG_C_OUT/IN, CD14.SIG_A_IN/OUT, CD14.SIG_C_OUT/IN
  N7: CD12.SIG_A_OUT/IN, CD12.SIG_B_OUT/IN, CD18.SIG_B_IN/OUT, CD13.SIG_B_IN/OUT, CD9.SIG_B_IN/OUT, CD19.SIG_A_OUT/IN, CD19.SIG_B_OUT/IN
  N8: CD18.SIG_A_IN/OUT, CD18.SIG_C_OUT/IN, CD13.SIG_C_IN/OUT, CD14.SIG_C_IN/OUT, CD11.SIG_A_IN/OUT, CD11.SIG_C_OUT/IN, CD19.SIG_A_IN/OUT, CD19.SIG_C_OUT/IN
  N9: CD10.SIG_A_OUT/IN, CD10.SIG_B_OUT/IN, CD11.SIG_A_OUT/IN, CD11.SIG_B_OUT/IN, CD9.SIG_A_OUT/IN, CD9.SIG_B_OUT/IN

notes:
  -5v
  C2
  Input B1
  Input A2
  Input B2,
  Output 2
  C3
  Input B1
  Input A2
  Input B2,
  Output 2
  C4
  Input B1
  Input A2
  Input B2,
  Output 2
  C1
  Input B1
  Input A2
  Input B2,
  Output 2
  +5v
  Combinartor1,2,3,4,5,6
  unitary
  C4 [2/3]
  Input A1
  Output 1
  C1 [1/2]
  Input A1
  Output 1
  C3 [1/4]
  Input A1
  Output 1
  C2 [1/3]
  Input A1
  Output 1
  Combinartor
  7,8,9
  binary
  C5 [2/4]
  Input A1
  Output 1
  C6 [3/4]
  Input A1
  Output 1
  C7 [1/2]/[3/4]
  Input A1
  Output 1
  C8 [1/3]/[2/4]
  Input A1
  Output 1
  C9 [1/4]/[2/3]
  Input A1
  Output 1
  inverter-1
  white, green
  inverter-2
  blue, yellow
  inverter-3
  cyan, brown
  inverter-4
  grey, purple
  Output +
  Output -
  problem!!

custom parts:
  CD4066 Quad Analog Switch: Quad Analog Switch
