# Fritzing sketch 4316ArrayPCB (saved by Fritzing 0.9.1b)
circuit board: 20.0891cm x 7.59514cm
breadboards: 1

parts:
  4361-1 = IC, DIP package, 16 pins [chip_label=IC]
  4361-2 = IC, DIP package, 16 pins [chip_label=IC]
  4361-3 = IC, DIP package, 16 pins [chip_label=IC]
  4361-4 = IC, DIP package, 16 pins [chip_label=IC]
  4361-5 = IC, DIP package, 16 pins [chip_label=IC]
  4361-6 = IC, DIP package, 16 pins [chip_label=IC]
  4361-7 = IC, DIP package, 16 pins [chip_label=IC]
  4361-8 = IC, DIP package, 16 pins [chip_label=IC]
  C-2 = female pin header, 1 pin [form="♀ (female)"]
  C-4 = female pin header, 1 pin [form="♀ (female)"]
  C-6 = female pin header, 1 pin [form="♀ (female)"]
  C-7 = female pin header, 1 pin [form="♀ (female)"]
  C-8 = female pin header, 1 pin [form="♀ (female)"]
  C-9 = female pin header, 1 pin [form="♀ (female)"]
  C-10 = female pin header, 1 pin [form="♀ (female)"]
  C-11 = female pin header, 1 pin [form="♀ (female)"]
  C-12 = female pin header, 1 pin [form="♀ (female)"]
  C-13 = female pin header, 1 pin [form="♀ (female)"]
  C-14 = female pin header, 1 pin [form="♀ (female)"]
  C-15 = female pin header, 1 pin [form="♀ (female)"]
  V-8_1 = female pin header, 1 pin [form="♀ (female)"]
  C-5 = female pin header, 1 pin [form="♀ (female)"]
  1S4S-3 = female pin header, 2 pins [form="♀ (female)"]
  1S4S-4 = female pin header, 2 pins [form="♀ (female)"]
  1S4S-5 = female pin header, 2 pins [form="♀ (female)"]
  1S4S-6 = female pin header, 2 pins [form="♀ (female)"]
  1S4S-7 = female pin header, 2 pins [form="♀ (female)"]
  1S4S-8 = female pin header, 2 pins [form="♀ (female)"]
  1S4S-2 = female pin header, 2 pins [form="♀ (female)"]
  C-1 = female pin header, 1 pin [form="♀ (female)"]
  1S4S-1 = female pin header, 2 pins [form="♀ (female)"]
  C-3 = female pin header, 1 pin [form="♀ (female)"]
  2S3S-1 = female pin header, 2 pins [form="♀ (female)"]
  2S3S-2 = female pin header, 2 pins [form="♀ (female)"]
  2S3S-4 = female pin header, 2 pins [form="♀ (female)"]
  2S3S-5 = female pin header, 2 pins [form="♀ (female)"]
  2S3S-6 = female pin header, 2 pins [form="♀ (female)"]
  2S3S-7 = female pin header, 2 pins [form="♀ (female)"]
  2S3S-8 = female pin header, 2 pins [form="♀ (female)"]
  J4-1 = female pin header, 1 pin [form="♀ (female)"]
  J1-1 = female pin header, 1 pin [form="♀ (female)"]
  J1-5 = female pin header, 1 pin [form="♀ (female)"]
  J2-4 = female pin header, 1 pin [form="♀ (female)"]
  J4-2 = female pin header, 1 pin [form="♀ (female)"]
  J5-1 = female pin header, 1 pin [form="♀ (female)"]
  J2-1 = female pin header, 1 pin [form="♀ (female)"]
  J2-2 = female pin header, 1 pin [form="♀ (female)"]
  J6-2 = female pin header, 1 pin [form="♀ (female)"]
  J6-1 = female pin header, 1 pin [form="♀ (female)"]
  J2-3 = female pin header, 1 pin [form="♀ (female)"]
  J6-4 = female pin header, 1 pin [form="♀ (female)"]
  J6-3 = female pin header, 1 pin [form="♀ (female)"]
  J3-1 = female pin header, 1 pin [form="♀ (female)"]
  J3-2 = female pin header, 1 pin [form="♀ (female)"]
  J1-2 = female pin header, 1 pin [form="♀ (female)"]
  J4-3 = female pin header, 1 pin [form="♀ (female)"]
  J4-4 = female pin header, 1 pin [form="♀ (female)"]
  J8-1 = female pin header, 1 pin [form="♀ (female)"]
  J8-2 = female pin header, 1 pin [form="♀ (female)"]
  J5-2 = female pin header, 1 pin [form="♀ (female)"]
  J7-2 = female pin header, 1 pin [form="♀ (female)"]
  J7-1 = female pin header, 1 pin [form="♀ (female)"]
  J2-5 = female pin header, 1 pin [form="♀ (female)"]
  J2-6 = female pin header, 1 pin [form="♀ (female)"]
  J1-4 = female pin header, 1 pin [form="♀ (female)"]
  J1-3 = female pin header, 1 pin [form="♀ (female)"]
  J1-6 = female pin header, 1 pin [form="♀ (female)"]
  J3-3 = female pin header, 1 pin [form="♀ (female)"]
  J3-4 = female pin header, 1 pin [form="♀ (female)"]
  J4-5 = female pin header, 1 pin [form="♀ (female)"]
  J4-6 = female pin header, 1 pin [form="♀ (female)"]
  J7-4 = female pin header, 1 pin [form="♀ (female)"]
  J7-3 = female pin header, 1 pin [form="♀ (female)"]
  J3-5 = female pin header, 1 pin [form="♀ (female)"]
  J3-6 = female pin header, 1 pin [form="♀ (female)"]
  J4-8 = female pin header, 1 pin [form="♀ (female)"]
  J4-7 = female pin header, 1 pin [form="♀ (female)"]
  J2-8 = female pin header, 1 pin [form="♀ (female)"]
  J2-7 = female pin header, 1 pin [form="♀ (female)"]
  J6-6 = female pin header, 1 pin [form="♀ (female)"]
  J6-5 = female pin header, 1 pin [form="♀ (female)"]
  J8-3 = female pin header, 1 pin [form="♀ (female)"]
  J8-4 = female pin header, 1 pin [form="♀ (female)"]
  J5-3 = female pin header, 1 pin [form="♀ (female)"]
  J5-4 = female pin header, 1 pin [form="♀ (female)"]
  J6-8 = female pin header, 1 pin [form="♀ (female)"]
  J6-7 = female pin header, 1 pin [form="♀ (female)"]
  Coils = female pin header, 3 pins [form="♀ (female)"]
  Coils-Amp = female pin header, 7 pins [form="♀ (female)"]
  V-1_1 = female pin header, 1 pin [form="♀ (female)"]
  V-2_1 = female pin header, 1 pin [form="♀ (female)"]
  V-3_1 = female pin header, 1 pin [form="♀ (female)"]
  V-4_1 = female pin header, 1 pin [form="♀ (female)"]
  V-5_1 = female pin header, 1 pin [form="♀ (female)"]
  V-6_1 = female pin header, 1 pin [form="♀ (female)"]
  V-7_1 = female pin header, 1 pin [form="♀ (female)"]
  V- = female pin header, 1 pin [form="♀ (female)"]
  V-1_2 = female pin header, 1 pin [form="♀ (female)"]
  V-5_2 = female pin header, 1 pin [form="♀ (female)"]
  V-6_2 = female pin header, 1 pin [form="♀ (female)"]
  V-4_2 = female pin header, 1 pin [form="♀ (female)"]
  V-2_2 = female pin header, 1 pin [form="♀ (female)"]
  V-3_2 = female pin header, 1 pin [form="♀ (female)"]
  V-7_2 = female pin header, 1 pin [form="♀ (female)"]
  V+1_1 = female pin header, 1 pin [form="♀ (female)"]
  V+5_1 = female pin header, 1 pin [form="♀ (female)"]
  V+6_1 = female pin header, 1 pin [form="♀ (female)"]
  V+4_1 = female pin header, 1 pin [form="♀ (female)"]
  V+2_1 = female pin header, 1 pin [form="♀ (female)"]
  V+3_1 = female pin header, 1 pin [form="♀ (female)"]
  V+7_1 = female pin header, 1 pin [form="♀ (female)"]
  V+8_1 = female pin header, 1 pin [form="♀ (female)"]
  V+ = female pin header, 1 pin [form="♀ (female)"]
  V+8_2 = female pin header, 1 pin [form="♀ (female)"]
  V+6_2 = female pin header, 1 pin [form="♀ (female)"]
  V+7_2 = female pin header, 1 pin [form="♀ (female)"]
  V+4_2 = female pin header, 1 pin [form="♀ (female)"]
  V+2_2 = female pin header, 1 pin [form="♀ (female)"]
  V+5_2 = female pin header, 1 pin [form="♀ (female)"]
  V+3_2 = female pin header, 1 pin [form="♀ (female)"]
  GND = female pin header, 1 pin [form="♀ (female)"]  # not connected
  G1_1 = female pin header, 1 pin [form="♀ (female)"]
  G5_1 = female pin header, 1 pin [form="♀ (female)"]
  G6_1 = female pin header, 1 pin [form="♀ (female)"]
  G4_1 = female pin header, 1 pin [form="♀ (female)"]
  G2_1 = female pin header, 1 pin [form="♀ (female)"]
  G3_1 = female pin header, 1 pin [form="♀ (female)"]
  G7_1 = female pin header, 1 pin [form="♀ (female)"]
  G6_2 = female pin header, 1 pin [form="♀ (female)"]
  G5_2 = female pin header, 1 pin [form="♀ (female)"]
  G3_2 = female pin header, 1 pin [form="♀ (female)"]
  G2_2 = female pin header, 1 pin [form="♀ (female)"]
  G7_2 = female pin header, 1 pin [form="♀ (female)"]
  G4_2 = female pin header, 1 pin [form="♀ (female)"]
  G1_2 = female pin header, 1 pin [form="♀ (female)"]
  2S3S-3 = female pin header, 2 pins [form="♀ (female)"]

nets:
  N1: 4361-1.pin1, 4361-3.pin1, 4361-4.pin2, 4361-4.pin3, 4361-4.pin10, 4361-5.pin1, 4361-7.pin1, Coils.pin1
  N2: 4361-1.pin2, 4361-1.pin3, 4361-1.pin11, 4361-1.pin12, 4361-2.pin2, 4361-2.pin3, 4361-2.pin13, J2-5.pin1, J2-6.pin1, J1-4.pin1, J1-3.pin1, Coils.pin2
  N3: 4361-1.pin4, 4361-3.pin4, 4361-5.pin4, 4361-7.pin4, 4361-8.pin2, 4361-8.pin3, 4361-8.pin13, J1-1.pin1, J5-1.pin1, J3-1.pin1, J3-2.pin1, J1-2.pin1, J5-2.pin1, J7-2.pin1, J7-1.pin1, Coils.pin3
  N4: 4361-1.pin5, 2S3S-1.pin1
  N5: 4361-1.pin6, 2S3S-1.pin2
  N6: 4361-1.pin9, 4361-2.pin9, 4361-3.pin9, 4361-4.pin9, 4361-5.pin9, 4361-6.pin9, 4361-7.pin9, 4361-8.pin9, C-2.pin1, C-4.pin1, C-6.pin1, C-8.pin1, C-10.pin1, C-12.pin1, C-14.pin1, V-8_1.pin1, V-1_1.pin1, V-2_1.pin1, V-3_1.pin1, V-4_1.pin1, V-5_1.pin1, V-6_1.pin1, V-7_1.pin1, V-.pin1, V-1_2.pin1, V-5_2.pin1, V-6_2.pin1, V-4_2.pin1, V-2_2.pin1, V-3_2.pin1, V-7_2.pin1
  N7: 4361-1.pin10, 4361-5.pin10, 4361-6.pin10, 4361-7.pin2, 4361-7.pin3, 4361-7.pin11, 4361-7.pin12, J1-5.pin1, J1-6.pin1, Coils-Amp.pin2
  N8: 4361-1.pin13, 4361-2.pin10, 4361-3.pin2, 4361-3.pin3, 4361-3.pin11, 4361-3.pin12, 4361-5.pin13, Coils-Amp.pin1
  N9: 4361-1.pin14, 1S4S-1.pin2
  N10: 4361-1.pin15, 1S4S-1.pin1
  N11: 4361-1.pin16, 4361-2.pin16, 4361-3.pin16, 4361-4.pin16, 4361-5.pin16, 4361-6.pin16, 4361-7.pin16, 4361-8.pin16, C-7.pin1, C-9.pin1, C-11.pin1, C-13.pin1, C-15.pin1, C-5.pin1, C-1.pin1, C-3.pin1, V+1_1.pin1, V+5_1.pin1, V+6_1.pin1, V+4_1.pin1, V+2_1.pin1, V+3_1.pin1, V+7_1.pin1, V+8_1.pin1, V+.pin1, V+8_2.pin1, V+6_2.pin1, V+7_2.pin1, V+4_2.pin1, V+2_2.pin1, V+5_2.pin1, V+3_2.pin1
  N12: 4361-2.pin1, 4361-3.pin13, 4361-4.pin1, 4361-4.pin13, 4361-6.pin1, 4361-7.pin13, 4361-8.pin1, J2-1.pin1, J2-2.pin1, J6-2.pin1, J6-1.pin1, J4-3.pin1, J4-4.pin1, J8-1.pin1, J8-2.pin1, J3-3.pin1, J3-4.pin1, J4-5.pin1, J4-6.pin1, J7-4.pin1, J7-3.pin1, Coils-Amp.pin3
  N13: 4361-2.pin4, 4361-3.pin10, 4361-4.pin4, 4361-6.pin4, 4361-7.pin10, 4361-8.pin4, 4361-8.pin10, J4-1.pin1, J2-4.pin1, J4-2.pin1, J2-3.pin1, J6-4.pin1, J6-3.pin1, J3-5.pin1, J3-6.pin1, Coils-Amp.pin4
  N14: 4361-2.pin5, 2S3S-2.pin1
  N15: 4361-2.pin6, 2S3S-2.pin2
  N16: 4361-2.pin11, 4361-2.pin12, 4361-4.pin11, 4361-4.pin12, J4-8.pin1, J4-7.pin1, J2-8.pin1, J2-7.pin1, Coils-Amp.pin5
  N17: 4361-2.pin14, 1S4S-2.pin2
  N18: 4361-2.pin15, 1S4S-2.pin1
  N19: 4361-3.pin5, 2S3S-3.pin1
  N20: 4361-3.pin6, 2S3S-3.pin2
  N21: 4361-3.pin14, 1S4S-3.pin2
  N22: 4361-3.pin15, 1S4S-3.pin1
  N23: 4361-4.pin5, 2S3S-4.pin1
  N24: 4361-4.pin6, 2S3S-4.pin2
  N25: 4361-4.pin14, 1S4S-4.pin2
  N26: 4361-4.pin15, 1S4S-4.pin1
  N27: 4361-5.pin2, 4361-5.pin3, 4361-5.pin11, 4361-5.pin12, 4361-6.pin2, 4361-6.pin3, 4361-6.pin13, J5-3.pin1, J5-4.pin1, J6-8.pin1, J6-7.pin1, Coils-Amp.pin6
  N28: 4361-5.pin5, 2S3S-5.pin1
  N29: 4361-5.pin6, 2S3S-5.pin2
  N30: 4361-5.pin14, 1S4S-5.pin2
  N31: 4361-5.pin15, 1S4S-5.pin1
  N32: 4361-6.pin5, 2S3S-6.pin1
  N33: 4361-6.pin6, 2S3S-6.pin2
  N34: 4361-6.pin11, 4361-6.pin12, 4361-8.pin11, 4361-8.pin12, J6-6.pin1, J6-5.pin1, J8-3.pin1, J8-4.pin1, Coils-Amp.pin7
  N35: 4361-6.pin14, 1S4S-6.pin2
  N36: 4361-6.pin15, 1S4S-6.pin1
  N37: 4361-7.pin5, 2S3S-7.pin1
  N38: 4361-7.pin6, 2S3S-7.pin2
  N39: 4361-7.pin14, 1S4S-7.pin2
  N40: 4361-7.pin15, 1S4S-7.pin1
  N41: 4361-8.pin5, 2S3S-8.pin1
  N42: 4361-8.pin6, 2S3S-8.pin2
  N43: 4361-8.pin14, 1S4S-8.pin2
  N44: 4361-8.pin15, 1S4S-8.pin1
  N45: G1_1.pin1, G1_2.pin1
  N46: G5_1.pin1, G5_2.pin1
  N47: G6_1.pin1, G6_2.pin1
  N48: G4_1.pin1, G4_2.pin1
  N49: G2_1.pin1, G2_2.pin1
  N50: G3_1.pin1, G3_2.pin1
  N51: G7_1.pin1, G7_2.pin1

notes:
  A-
  C-
  C+
  B+
  A+
  B-
  D+
  D-
  Out-
  Out+
