# Fritzing sketch Carvin Wiring 00 (saved by Fritzing 0.9.2b)
breadboards: 1

parts:
  10PDT_Top = female pin header, 15 pins [form="♀ (female)"]
  10PDT_Bottom = female pin header, 15 pins [form="♀ (female)"]
  Coil_A_(N2) = Inductor [package="400 mil [THT]"]
  Coil_B_(_N1) = Inductor [package="400 mil [THT]"]
  Coil_C_(B2) = Inductor [package="400 mil [THT]"]
  Coil_D_(B1) = Inductor [package="400 mil [THT]"]
  5-Way_Switch = male pin header, 8 pins [form="♂ (male)"]
  ARDU2 = male pin header, 10 pins [form="♂ (male)"]
  Amp = male pin header, 2 pins [form="♂ (male)"]
  Neck_Shielding = female pin header, 1 pin [form="♀ (female)"]
  Bridge_Shielding = female pin header, 1 pin [form="♀ (female)"]
  Vol/tone = female pin header, 3 pins [form="♀ (female)"]

nets:
  N1: 10PDT_Top.pin1, ARDU2.pin3
  N2: 10PDT_Top.pin2, Coil_A_(N2).pin_0
  N3: 10PDT_Top.pin3, 10PDT_Bottom.pin12, 5-Way_Switch.pin4, 5-Way_Switch.pin5
  N4: 10PDT_Top.pin4, ARDU2.pin4
  N5: 10PDT_Top.pin5, Coil_A_(N2).pin_1
  N6: 10PDT_Top.pin6, 10PDT_Bottom.pin3, 5-Way_Switch.pin7
  N7: 10PDT_Top.pin7, ARDU2.pin7
  N8: 10PDT_Top.pin8, Coil_C_(B2).pin_0
  N9: 10PDT_Top.pin9, 5-Way_Switch.pin3, Vol/tone.pin1
  N10: 10PDT_Top.pin10, ARDU2.pin8
  N11: 10PDT_Top.pin11, Coil_C_(B2).pin_1
  N12: 10PDT_Top.pin12, 10PDT_Bottom.pin9, 5-Way_Switch.pin2
  N13: 10PDT_Top.pin13, ARDU2.pin1
  N14: 10PDT_Top.pin14, Amp.pin1
  N15: 10PDT_Top.pin15, Vol/tone.pin2
  N16: 10PDT_Bottom.pin1, ARDU2.pin5
  N17: 10PDT_Bottom.pin2, Coil_B_(_N1).pin_0
  N18: 10PDT_Bottom.pin4, ARDU2.pin6
  N19: 10PDT_Bottom.pin5, Coil_B_(_N1).pin_1
  N20: 10PDT_Bottom.pin7, ARDU2.pin9
  N21: 10PDT_Bottom.pin8, Coil_D_(B1).pin_0
  N22: 10PDT_Bottom.pin10, ARDU2.pin10
  N23: 10PDT_Bottom.pin11, Coil_D_(B1).pin_1
  N24: 10PDT_Bottom.pin13, ARDU2.pin2
  GND: 10PDT_Bottom.pin14, Amp.pin2, Neck_Shielding.pin1, Bridge_Shielding.pin1
  N25: 10PDT_Bottom.pin15, 5-Way_Switch.pin6, Vol/tone.pin3

notes:
  Out+
  Out-
  A+
  A-
  B+
  B-
  D-
  C-
  C+
  D+
