# Fritzing sketch 4316 Single Inverter and resistive tone control schematic  (saved by Fritzing 0.9.1b)
breadboards: 1

parts:
  L1 = Inductor [package="400 mil [THT]"]
  C1-1 = Ceramic Capacitor [capacitance=100nF package="100 mil [THT, multilayer]"]
  +5v = female pin header, 1 pin [form="♀ (female)"]
  -5v = female pin header, 1 pin [form="♀ (female)"]
  Straight = female pin header, 1 pin [form="♀ (female)"]
  Invert = female pin header, 1 pin [form="♀ (female)"]
  V100% = female pin header, 1 pin [form="♀ (female)"]
  V80% = female pin header, 1 pin [form="♀ (female)"]
  V40% = female pin header, 1 pin [form="♀ (female)"]
  V20% = female pin header, 1 pin [form="♀ (female)"]
  V0% = female pin header, 1 pin [form="♀ (female)"]
  T200R = female pin header, 1 pin [form="♀ (female)"]
  T100R = female pin header, 1 pin [form="♀ (female)"]
  T22R = female pin header, 1 pin [form="♀ (female)"]
  Ton/off = female pin header, 1 pin [form="♀ (female)"]
  4316-1 = IC, DIP package, 16 pins [chip_label=IC]
  C1-2 = Ceramic Capacitor [capacitance=100nF package="100 mil [THT, multilayer]"]
  4316-2 = IC, DIP package, 16 pins [chip_label=IC]
  Cc1-3 = Ceramic Capacitor [capacitance=100nF package="100 mil [THT, multilayer]"]
  4316-3 = IC, DIP package, 16 pins [chip_label=IC]
  C1-4 = Ceramic Capacitor [capacitance=100nF package="100 mil [THT, multilayer]"]
  4316-4 = IC, DIP package, 16 pins [chip_label=IC]
  CT = Ceramic Capacitor [capacitance=10nF package="100 mil [THT, multilayer]"]
  RT2 = Resistor [tolerance=±5% resistance=100k package=THT]
  RT4 = Resistor [tolerance=±5% resistance=22k package=THT]
  RT3 = Resistor [tolerance=±5% resistance=50k package=THT]
  RT1 = Resistor [tolerance=±5% resistance=200k package=THT]
  RV4 = Resistor [tolerance=±5% resistance=100k package=THT]
  RV2 = Resistor [tolerance=±5% resistance=100k package=THT]
  RV3 = Resistor [tolerance=±5% resistance=100k package=THT]
  RV5 = Resistor [tolerance=±5% resistance=100k package=THT]
  RV1 = Resistor [tolerance=±5% resistance=100k package=THT]
  OUT+ = male pin header, 1 pin [form="♂ (male)"]
  OUT- = male pin header, 1 pin [form="♂ (male)"]
  T50R = female pin header, 1 pin [form="♀ (female)"]
  V60% = female pin header, 1 pin [form="♀ (female)"]

nets:
  N1: L1.pin_0, 4316-1.pin4, 4316-1.pin13
  N2: L1.pin_1, 4316-1.pin1, 4316-1.pin10
  N3: C1-1.1, +5v.pin1, 4316-1.pin16, C1-2.1, 4316-2.pin16, Cc1-3.1, 4316-3.pin16, C1-4.1, 4316-4.pin16
  N4: -5v.pin1, 4316-1.pin9, C1-2.0, 4316-2.pin9, Cc1-3.0, 4316-3.pin9, C1-4.0, 4316-4.pin9
  N5: Straight.pin1, 4316-1.pin14, 4316-1.pin15
  N6: Invert.pin1, 4316-1.pin5, 4316-1.pin6
  N7: V100%.pin1, 4316-2.pin14
  N8: V80%.pin1, 4316-2.pin6
  N9: V40%.pin1, 4316-3.pin6
  N10: V20%.pin1, 4316-4.pin14
  N11: V0%.pin1, 4316-4.pin6
  N12: T200R.pin1, 4316-2.pin15
  N13: T100R.pin1, 4316-2.pin5
  N14: T22R.pin1, 4316-3.pin5
  N15: Ton/off.pin1, 4316-4.pin15
  N16: 4316-1.pin2, 4316-1.pin3, OUT-.pin1
  GND: 4316-1.pin7, 4316-1.pin8, 4316-2.pin7, 4316-2.pin8, 4316-3.pin7, 4316-3.pin8, 4316-4.pin3, 4316-4.pin4, 4316-4.pin5, 4316-4.pin7, 4316-4.pin8
  N17: 4316-1.pin11, 4316-1.pin12, 4316-2.pin13, RV1.Pin_0
  N18: 4316-2.pin1, RT1.Pin_0
  N19: 4316-2.pin2, 4316-2.pin3, 4316-2.pin11, 4316-2.pin12, 4316-3.pin2, 4316-3.pin3, 4316-3.pin11, 4316-3.pin12, 4316-4.pin11, 4316-4.pin12, OUT+.pin1
  N20: 4316-2.pin4, RT2.Pin_0
  N21: 4316-2.pin10, RV2.Pin_0, RV1.Pin_1
  N22: 4316-3.pin1, RT3.Pin_0
  N23: 4316-3.pin4, RT4.Pin_0
  N24: 4316-3.pin10, RV4.Pin_0, RV3.Pin_1
  N25: 4316-3.pin13, RV2.Pin_1, RV3.Pin_0
  N26: 4316-3.pin14, V60%.pin1
  N27: 4316-3.pin15, T50R.pin1
  N28: 4316-4.pin1, CT.1
  N29: 4316-4.pin2, 4316-4.pin10, RV5.Pin_1
  N30: 4316-4.pin13, RV4.Pin_1, RV5.Pin_0
  N31: CT.0, RT2.Pin_1, RT4.Pin_1, RT3.Pin_1, RT1.Pin_1
