# Fritzing sketch 4316-Inverter-Vol-Tone-PCB (saved by Fritzing 0.9.1b)
circuit board: 10.2374cm x 5.43208cm
breadboards: 1

parts:
  4316-2 = IC, DIP package, 16 pins [chip_label=IC]
  4316-3 = IC, DIP package, 16 pins [chip_label=IC]
  C-2 = female pin header, 1 pin [form="♀ (female)"]
  C-4 = female pin header, 1 pin [form="♀ (female)"]
  C-6 = female pin header, 1 pin [form="♀ (female)"]
  C-7 = female pin header, 1 pin [form="♀ (female)"]
  C-8 = female pin header, 1 pin [form="♀ (female)"]
  C-5 = female pin header, 1 pin [form="♀ (female)"]
  t50R_v60% = female pin header, 2 pins [form="♀ (female)"]
  tOn/Off_v20% = female pin header, 2 pins [form="♀ (female)"]
  t200R_v100% = female pin header, 2 pins [form="♀ (female)"]
  C-1 = female pin header, 1 pin [form="♀ (female)"]
  C-3 = female pin header, 1 pin [form="♀ (female)"]
  t100R_v80% = female pin header, 2 pins [form="♀ (female)"]
  V-1_1 = female pin header, 1 pin [form="♀ (female)"]
  V-2_1 = female pin header, 1 pin [form="♀ (female)"]
  V-3_1 = female pin header, 1 pin [form="♀ (female)"]
  V-1_2 = female pin header, 1 pin [form="♀ (female)"]
  V-2_2 = female pin header, 1 pin [form="♀ (female)"]
  V-3_2 = female pin header, 1 pin [form="♀ (female)"]
  V+4_1 = female pin header, 1 pin [form="♀ (female)"]
  V+2_1 = female pin header, 1 pin [form="♀ (female)"]
  V+3_1 = female pin header, 1 pin [form="♀ (female)"]
  V+ = female pin header, 1 pin [form="♀ (female)"]
  V+4_2 = female pin header, 1 pin [form="♀ (female)"]
  V+2_2 = female pin header, 1 pin [form="♀ (female)"]
  V+3_2 = female pin header, 1 pin [form="♀ (female)"]
  GND = female pin header, 1 pin [form="♀ (female)"]
  G1_1 = female pin header, 1 pin [form="♀ (female)"]
  G2_1 = female pin header, 1 pin [form="♀ (female)"]
  G3_1 = female pin header, 1 pin [form="♀ (female)"]
  G3_2 = female pin header, 1 pin [form="♀ (female)"]
  G2_2 = female pin header, 1 pin [form="♀ (female)"]
  G1_2 = female pin header, 1 pin [form="♀ (female)"]
  t22R_v40% = female pin header, 2 pins [form="♀ (female)"]
  4316-4 = IC, DIP package, 16 pins [chip_label=IC]
  V- = female pin header, 1 pin [form="♀ (female)"]
  J1-2 = female pin header, 1 pin [form="♀ (female)"]
  J1-1 = female pin header, 1 pin [form="♀ (female)"]
  Straight = female pin header, 1 pin [form="♀ (female)"]
  Invert = female pin header, 1 pin [form="♀ (female)"]
  22kR = Resistor [tolerance=±5% resistance=22k package=THT]
  50kR = Resistor [tolerance=±5% resistance=50k package=THT]
  100kR = Resistor [tolerance=±5% resistance=100k package=THT]
  200kR = Resistor [tolerance=±5% resistance=200k package=THT]
  ToneCap = Ceramic Capacitor [capacitance=10nF package="100 mil [THT, multilayer]"]
  v0% = female pin header, 1 pin [form="♀ (female)"]
  Out+ = female pin header, 1 pin [form="♀ (female)"]
  Out- = female pin header, 1 pin [form="♀ (female)"]
  100kR_2 = Resistor [tolerance=±5% resistance=100k package=THT]
  100kR_3 = Resistor [tolerance=±5% resistance=100k package=THT]
  100kR_4 = Resistor [tolerance=±5% resistance=100k package=THT]
  100kR_5 = Resistor [tolerance=±5% resistance=100k package=THT]
  100kR_6 = Resistor [tolerance=±5% resistance=100k package=THT]
  Coil = female pin header, 2 pins [form="♀ (female)"]
  4316-1 = IC, DIP package, 16 pins [chip_label=IC]

nets:
  N1: 4316-2.pin1, 200kR.Pin_0
  N2: 4316-2.pin2, 4316-2.pin3, 4316-2.pin11, 4316-2.pin12, 4316-3.pin2, 4316-3.pin3, 4316-3.pin11, 4316-3.pin12, 4316-4.pin11, 4316-4.pin12, Out+.pin1
  N3: 4316-2.pin4, 100kR.Pin_0
  N4: 4316-2.pin5, t100R_v80%.pin1
  N5: 4316-2.pin6, t100R_v80%.pin2
  N6: 4316-2.pin7, 4316-2.pin8, 4316-3.pin7, 4316-3.pin8, GND.pin1, G1_1.pin1, G2_1.pin1, G3_1.pin1, G3_2.pin1, G2_2.pin1, G1_2.pin1, 4316-4.pin3, 4316-4.pin4, 4316-4.pin5, 4316-4.pin7, 4316-4.pin8, 4316-1.pin7, 4316-1.pin8
  N7: 4316-2.pin9, 4316-3.pin9, C-2.pin1, C-4.pin1, C-6.pin1, C-8.pin1, V-1_1.pin1, V-2_1.pin1, V-3_1.pin1, V-1_2.pin1, V-2_2.pin1, V-3_2.pin1, 4316-4.pin9, V-.pin1, 4316-1.pin9
  N8: 4316-2.pin10, 100kR_5.Pin_0, 100kR_6.Pin_1
  N9: 4316-2.pin13, 100kR_6.Pin_0, 4316-1.pin11, 4316-1.pin12
  N10: 4316-2.pin14, t200R_v100%.pin2
  N11: 4316-2.pin15, t200R_v100%.pin1
  N12: 4316-2.pin16, 4316-3.pin16, C-7.pin1, C-5.pin1, C-1.pin1, C-3.pin1, V+4_1.pin1, V+2_1.pin1, V+3_1.pin1, V+.pin1, V+4_2.pin1, V+2_2.pin1, V+3_2.pin1, 4316-4.pin16, 4316-1.pin16
  N13: 4316-3.pin1, 50kR.Pin_0
  N14: 4316-3.pin4, 22kR.Pin_0
  N15: 4316-3.pin5, t22R_v40%.pin1
  N16: 4316-3.pin6, t22R_v40%.pin2
  N17: 4316-3.pin10, 100kR_3.Pin_0, 100kR_4.Pin_1
  N18: 4316-3.pin13, 100kR_4.Pin_0, 100kR_5.Pin_1
  N19: 4316-3.pin14, t50R_v60%.pin2
  N20: 4316-3.pin15, t50R_v60%.pin1
  N21: tOn/Off_v20%.pin1, 4316-4.pin15
  N22: tOn/Off_v20%.pin2, 4316-4.pin14
  N23: 4316-4.pin1, ToneCap.1
  N24: 4316-4.pin2, 4316-4.pin10, Out-.pin1, 100kR_2.Pin_1, 4316-1.pin2, 4316-1.pin3
  N25: 4316-4.pin6, v0%.pin1
  N26: 4316-4.pin13, 100kR_2.Pin_0, 100kR_3.Pin_1
  N27: J1-2.pin1, J1-1.pin1, Coil.pin1, 4316-1.pin4, 4316-1.pin13
  N28: Straight.pin1, 4316-1.pin14, 4316-1.pin15
  N29: Invert.pin1, 4316-1.pin5, 4316-1.pin6
  N30: 22kR.Pin_1, 50kR.Pin_1, 100kR.Pin_1, 200kR.Pin_1, ToneCap.0
  N31: Coil.pin2, 4316-1.pin1, 4316-1.pin10

notes:
  C+
  C-
