# Fritzing sketch 4316d Single Inverter and resistive tone control pcb a  (saved by Fritzing 0.9.2b)
circuit board: 10.6711cm x 8.09946cm
breadboards: 1

parts:
  4316-1 = IC, DIP package, 16 pins [chip_label=IC]
  4316-2 = IC, DIP package, 16 pins [chip_label=IC]
  4316-3 = IC, DIP package, 16 pins [chip_label=IC]
  C1 = Ceramic Capacitor [capacitance=100nF package="100 mil [THT, multilayer]"]
  C1_2 = Ceramic Capacitor [capacitance=100nF package="100 mil [THT, multilayer]"]
  C1_3 = Ceramic Capacitor [capacitance=100nF package="100 mil [THT, multilayer]"]
  C1_4 = Ceramic Capacitor [capacitance=100nF package="100 mil [THT, multilayer]"]
  4316-0 = IC, DIP package, 16 pins [chip_label=IC]
  J1 = female pin header, 14 pins [form="♀ (female)"]
  J2 = female pin header, 2 pins [form="♀ (female)"]
  R1 = Resistor [tolerance=±1% resistance=64k package=THT]
  R2 = Resistor [tolerance=±1% resistance=32k package=THT]
  R3 = Resistor [tolerance=±1% resistance=16k package=THT]
  R4 = Resistor [tolerance=±1% resistance=16k package=THT]
  R5 = Resistor [tolerance=±1% resistance=100k package=THT]
  C2 = Ceramic Capacitor [capacitance=0.18nF package="100 mil [THT, multilayer]"]
  R6 = Resistor [tolerance=±1% resistance=100k package=THT]

nets:
  N1: 4316-1.pin2, 4316-1.pin13
  N2: 4316-1.pin4, R4.Pin_1
  N3: 4316-1.pin5, J1.pin4
  N4: 4316-1.pin6, J1.pin3
  N5: 4316-1.pin7, 4316-1.pin8
  N6: 4316-1.pin9, 4316-2.pin9, 4316-3.pin9, C1.0, C1_2.0, C1_3.1, C1_4.0, 4316-0.pin9
  N7: 4316-1.pin10, R5.Pin_0, R6.Pin_1
  N8: 4316-1.pin11, 4316-1.pin12, C2.1
  N9: 4316-1.pin14, J1.pin2
  N10: 4316-1.pin15, J1.pin1
  N11: 4316-1.pin16, 4316-2.pin16, 4316-3.pin16, C1.1, C1_2.1, C1_3.0, C1_4.1, 4316-0.pin16
  N12: 4316-2.pin1, R3.Pin_0, R4.Pin_0
  N13: 4316-2.pin2, 4316-2.pin3
  N14: 4316-2.pin4, R2.Pin_1, R3.Pin_1
  N15: 4316-2.pin5, J1.pin6
  N16: 4316-2.pin6, J1.pin5
  N17: 4316-2.pin7, 4316-2.pin8
  N18: 4316-2.pin11, 4316-2.pin12
  N19: 4316-2.pin13, R6.Pin_0
  N20: 4316-2.pin14, J1.pin8
  N21: 4316-2.pin15, J1.pin7
  N22: 4316-3.pin1, R1.Pin_0, R2.Pin_0
  N23: 4316-3.pin2, 4316-3.pin3
  N24: 4316-3.pin4, R1.Pin_1
  N25: 4316-3.pin5, J1.pin12
  N26: 4316-3.pin6, J1.pin11
  N27: 4316-3.pin7, 4316-3.pin8
  N28: 4316-3.pin11, 4316-3.pin12
  N29: 4316-3.pin13, J1.pin10
  N30: 4316-3.pin14, J1.pin9
  N31: 4316-0.pin1, 4316-0.pin10, J2.pin1
  N32: 4316-0.pin2, 4316-0.pin3
  N33: 4316-0.pin4, 4316-0.pin13, J2.pin2
  N34: 4316-0.pin5, 4316-0.pin6, J1.pin13
  N35: 4316-0.pin7, 4316-0.pin8
  N36: 4316-0.pin11, 4316-0.pin12
  N37: 4316-0.pin14, 4316-0.pin15, J1.pin14
  N38: R5.Pin_1, C2.0
