# Fritzing sketch 4316d Single Inverter and resistive tone control pcb b (saved by Fritzing 0.9.2b)
circuit board: 13.6807cm x 6.31826cm
breadboards: 1

parts:
  C9 = Ceramic Capacitor [capacitance=0.18nF package="100 mil [THT, multilayer]"]
  C10 = Ceramic Capacitor [capacitance=100nF package="100 mil [THT, multilayer]"]
  C11 = Ceramic Capacitor [capacitance=100nF package="100 mil [THT, multilayer]"]
  C12 = Ceramic Capacitor [capacitance=100nF package="100 mil [THT, multilayer]"]
  C13 = Ceramic Capacitor [capacitance=100nF package="100 mil [THT, multilayer]"]
  RT5 = Resistor [tolerance=±1% resistance=16k package=THT]
  RV1 = Resistor [tolerance=±1% resistance=100k package=THT]
  RV2 = Resistor [tolerance=±1% resistance=100k package=THT]
  RV3 = Resistor [tolerance=±1% resistance=100k package=THT]
  RV4 = Resistor [tolerance=±1% resistance=100k package=THT]
  RV5 = Resistor [tolerance=±1% resistance=100k package=THT]
  RT6 = Resistor [tolerance=±1% resistance=64k package=THT]
  RT7 = Resistor [tolerance=±1% resistance=32k package=THT]
  RT8 = Resistor [tolerance=±1% resistance=16k package=THT]
  CT1 = Ceramic Capacitor [capacitance=10nF package="100 mil [THT, multilayer]"]
  4316-0 = IC, DIP package, 16 pins [chip_label=IC]
  4316-1 = IC, DIP package, 16 pins [chip_label=IC]
  4316-2 = IC, DIP package, 16 pins [chip_label=IC]
  j1 = female pin header, 1 pin [form="♀ (female)"]
  j2 = female pin header, 1 pin [form="♀ (female)"]
  j3 = female pin header, 1 pin [form="♀ (female)"]
  j4 = female pin header, 1 pin [form="♀ (female)"]
  j5 = female pin header, 1 pin [form="♀ (female)"]
  j6 = female pin header, 1 pin [form="♀ (female)"]
  Invert_T0_V4_T2_V2_T4_V0 = female pin header, 7 pins [form="♀ (female)"]
  Straight_Ton_V5_T1_V3_T3_V1 = female pin header, 7 pins [form="♀ (female)"]
  J1 = female pin header, 2 pins [form="♀ (female)"]
  J2 = female pin header, 2 pins [form="♀ (female)"]
  J3 = female pin header, 2 pins [form="♀ (female)"]
  J4 = female pin header, 2 pins [form="♀ (female)"]
  J5 = female pin header, 2 pins [form="♀ (female)"]
  J6 = female pin header, 2 pins [form="♀ (female)"]
  J7 = female pin header, 2 pins [form="♀ (female)"]
  J8 = female pin header, 2 pins [form="♀ (female)"]
  J9 = female pin header, 2 pins [form="♀ (female)"]
  J10 = female pin header, 2 pins [form="♀ (female)"]
  J11 = female pin header, 2 pins [form="♀ (female)"]
  J12 = female pin header, 2 pins [form="♀ (female)"]
  Out-_Out+ = female pin header, 2 pins [form="♀ (female)"]
  j7 = female pin header, 1 pin [form="♀ (female)"]
  j8 = female pin header, 1 pin [form="♀ (female)"]
  Coil+_Coil- = female pin header, 2 pins [form="♀ (female)"]
  j9 = female pin header, 1 pin [form="♀ (female)"]
  j10 = female pin header, 1 pin [form="♀ (female)"]
  j11 = female pin header, 1 pin [form="♀ (female)"]
  j12 = female pin header, 1 pin [form="♀ (female)"]
  j13 = female pin header, 1 pin [form="♀ (female)"]
  j14 = female pin header, 1 pin [form="♀ (female)"]
  V+_V-_GND_GND = female pin header, 4 pins [form="♀ (female)"]
  j15 = female pin header, 1 pin [form="♀ (female)"]
  j16 = female pin header, 1 pin [form="♀ (female)"]
  j17 = female pin header, 1 pin [form="♀ (female)"]
  j18 = female pin header, 1 pin [form="♀ (female)"]
  4316-3 = IC, DIP package, 16 pins [chip_label=IC]
  j19 = female pin header, 1 pin [form="♀ (female)"]
  j20 = female pin header, 1 pin [form="♀ (female)"]
  j21 = female pin header, 1 pin [form="♀ (female)"]
  j22 = female pin header, 1 pin [form="♀ (female)"]
  j23 = female pin header, 1 pin [form="♀ (female)"]
  j24 = female pin header, 1 pin [form="♀ (female)"]

nets:
  N1: C9.0, RV3.Pin_0, 4316-0.pin11, 4316-0.pin12, 4316-1.pin2, 4316-1.pin13, j7.pin1, j8.pin1
  N2: C9.1, 4316-1.pin11, 4316-1.pin12, 4316-2.pin11, 4316-2.pin12, Out-_Out+.pin2, 4316-3.pin11, 4316-3.pin12
  N3: C10.0, C11.0, C12.0, C13.0, 4316-0.pin16, 4316-1.pin16, 4316-2.pin16, V+_V-_GND_GND.pin1, 4316-3.pin16
  N4: C10.1, C11.1, C12.1, C13.1, 4316-0.pin9, 4316-1.pin9, 4316-2.pin9, j1.pin1, j2.pin1, j3.pin1, j4.pin1, j5.pin1, j6.pin1, V+_V-_GND_GND.pin2, 4316-3.pin9
  N5: RT5.Pin_0, CT1.1, 4316-1.pin4
  N6: RT5.Pin_1, RT8.Pin_0, 4316-2.pin1
  N7: RV1.Pin_0, RV2.Pin_1, 4316-2.pin13
  N8: RV1.Pin_1, RV4.Pin_0, 4316-2.pin10
  N9: RV2.Pin_0, RV3.Pin_1, 4316-1.pin10
  N10: RV4.Pin_1, RV5.Pin_0, 4316-3.pin13
  N11: RV5.Pin_1, 4316-0.pin2, 4316-0.pin3, 4316-1.pin3, 4316-2.pin2, 4316-2.pin3, Out-_Out+.pin1, 4316-3.pin2, 4316-3.pin3, 4316-3.pin10
  N12: RT6.Pin_0, RT7.Pin_1, 4316-3.pin1
  N13: RT6.Pin_1, 4316-3.pin4
  N14: RT7.Pin_0, RT8.Pin_1, 4316-2.pin4
  N15: CT1.0, 4316-1.pin1
  N16: 4316-0.pin1, 4316-0.pin10, Coil+_Coil-.pin2, j9.pin1, j11.pin1
  N17: 4316-0.pin4, 4316-0.pin13, Coil+_Coil-.pin1, j10.pin1, j12.pin1
  N18: 4316-0.pin5, 4316-0.pin6, Invert_T0_V4_T2_V2_T4_V0.pin1, j23.pin1, j24.pin1
  N19: 4316-0.pin14, 4316-0.pin15, Straight_Ton_V5_T1_V3_T3_V1.pin1, j13.pin1, j14.pin1
  N20: 4316-1.pin5, Invert_T0_V4_T2_V2_T4_V0.pin2, J7.pin1, J8.pin1
  N21: 4316-1.pin6, Invert_T0_V4_T2_V2_T4_V0.pin3, J7.pin2, J8.pin2
  N22: 4316-1.pin14, Straight_Ton_V5_T1_V3_T3_V1.pin3, J5.pin2, J6.pin2
  N23: 4316-1.pin15, Straight_Ton_V5_T1_V3_T3_V1.pin2, J5.pin1, J6.pin1
  N24: 4316-2.pin5, Invert_T0_V4_T2_V2_T4_V0.pin4, J9.pin1, J10.pin1
  N25: 4316-2.pin6, Invert_T0_V4_T2_V2_T4_V0.pin5, J9.pin2, J10.pin2
  N26: 4316-2.pin14, Straight_Ton_V5_T1_V3_T3_V1.pin5, J3.pin2, J4.pin2
  N27: 4316-2.pin15, Straight_Ton_V5_T1_V3_T3_V1.pin4, J3.pin1, J4.pin1
  N28: Invert_T0_V4_T2_V2_T4_V0.pin6, J11.pin1, J12.pin1, 4316-3.pin5
  N29: Invert_T0_V4_T2_V2_T4_V0.pin7, J11.pin2, J12.pin2, 4316-3.pin6
  N30: Straight_Ton_V5_T1_V3_T3_V1.pin6, J1.pin1, J2.pin1, 4316-3.pin15
  N31: Straight_Ton_V5_T1_V3_T3_V1.pin7, J1.pin2, J2.pin2, 4316-3.pin14
  N32: j15.pin1, j16.pin1, j17.pin1, j18.pin1
  N33: j19.pin1, j20.pin1, j21.pin1, j22.pin1
