# Fritzing sketch 4316d Single Inverter and resistive tone control pcb e (saved by Fritzing 0.9.2b)
circuit board: 13.1002cm x 5.19332cm
breadboards: 1

parts:
  CBoost = Ceramic Capacitor [capacitance=0.18nF package="100 mil [THT, multilayer]"]
  Cdc = Ceramic Capacitor [capacitance=100nF package="100 mil [THT, multilayer]"]
  Cdc_2 = Ceramic Capacitor [capacitance=100nF package="100 mil [THT, multilayer]"]
  RT1 = Resistor [tolerance=±1% resistance=16k package=THT]
  RV = Resistor [tolerance=±1% resistance=100k package=THT]
  RV_2 = Resistor [tolerance=±1% resistance=100k package=THT]
  RV_3 = Resistor [tolerance=±1% resistance=100k package=THT]
  RV_4 = Resistor [tolerance=±1% resistance=100k package=THT]
  RV_5 = Resistor [tolerance=±1% resistance=100k package=THT]
  RT4 = Resistor [tolerance=±1% resistance=64k package=THT]
  RT2 = Resistor [tolerance=±1% resistance=32k package=THT]
  RT1_2 = Resistor [tolerance=±1% resistance=16k package=THT]
  CT = Ceramic Capacitor [capacitance=10nF package="100 mil [THT, multilayer]"]
  Out+_Out- = female pin header, 2 pins [form="♀ (female)"]
  Coil-_Coil+ = female pin header, 2 pins [form="♀ (female)"]
  4316-0 = IC, DIP package, 16 pins [chip_label=IC]
  4316-1 = IC, DIP package, 16 pins [chip_label=IC]
  4316-2 = IC, DIP package, 16 pins [chip_label=IC]
  4316-3 = IC, DIP package, 16 pins [chip_label=IC]
  Cdc_3 = Ceramic Capacitor [capacitance=100nF package="100 mil [THT, multilayer]"]
  Invert_V4_T0_T2_V2_T4_V0 = female pin header, 7 pins [form="♀ (female)"]
  V3_T1_V5_Ton_Strt_T3_V1 = female pin header, 7 pins [form="♀ (female)"]
  Cdc_4 = Ceramic Capacitor [capacitance=100nF package="100 mil [THT, multilayer]"]
  Cdc_5 = Ceramic Capacitor [capacitance=100nF package="100 mil [THT, multilayer]"]
  Cdc1 = Ceramic Capacitor [capacitance=100nF package="100 mil [THT, multilayer]"]
  Cdc2 = Ceramic Capacitor [capacitance=100nF package="100 mil [THT, multilayer]"]
  Cdc3 = Ceramic Capacitor [capacitance=100nF package="100 mil [THT, multilayer]"]
  GND_GND_V-_V+ = female pin header, 4 pins [form="♀ (female)"]

nets:
  N1: CBoost.0, RV_3.Pin_0, 4316-0.pin11, 4316-0.pin12, 4316-1.pin2, 4316-1.pin13
  N2: CBoost.1, Out+_Out-.pin2, 4316-1.pin11, 4316-1.pin12, 4316-2.pin11, 4316-2.pin12, 4316-3.pin11, 4316-3.pin12
  N3: Cdc.1, Cdc_2.0, 4316-0.pin16, 4316-1.pin16, 4316-2.pin16, 4316-3.pin16, Cdc_3.0, Cdc1.1, GND_GND_V-_V+.pin1
  N4: RT1.Pin_0, CT.1, 4316-1.pin4
  N5: RT1.Pin_1, RT1_2.Pin_0, 4316-2.pin1
  N6: RV.Pin_0, RV_2.Pin_1, 4316-2.pin13
  N7: RV.Pin_1, RV_4.Pin_0, 4316-2.pin10
  N8: RV_2.Pin_0, RV_3.Pin_1, 4316-1.pin10
  N9: RV_4.Pin_1, RV_5.Pin_0, 4316-3.pin13
  N10: RV_5.Pin_1, Out+_Out-.pin1, 4316-0.pin2, 4316-0.pin3, 4316-1.pin3, 4316-2.pin2, 4316-2.pin3, 4316-3.pin2, 4316-3.pin3, 4316-3.pin10
  N11: RT4.Pin_0, RT2.Pin_1, 4316-3.pin1
  N12: RT4.Pin_1, 4316-3.pin4
  N13: RT2.Pin_0, RT1_2.Pin_1, 4316-2.pin4
  N14: CT.0, 4316-1.pin1
  N15: Coil-_Coil+.pin1, 4316-0.pin4, 4316-0.pin13
  N16: Coil-_Coil+.pin2, 4316-0.pin1, 4316-0.pin10
  N17: 4316-0.pin5, 4316-0.pin6, Invert_V4_T0_T2_V2_T4_V0.pin1
  N18: 4316-0.pin9, 4316-1.pin9, 4316-2.pin9, 4316-3.pin9, Cdc_4.0, Cdc_5.1, Cdc2.1, Cdc3.1, GND_GND_V-_V+.pin2
  N19: 4316-0.pin14, 4316-0.pin15, V3_T1_V5_Ton_Strt_T3_V1.pin3
  N20: 4316-1.pin5, Invert_V4_T0_T2_V2_T4_V0.pin3
  N21: 4316-1.pin6, Invert_V4_T0_T2_V2_T4_V0.pin2
  N22: 4316-1.pin14, V3_T1_V5_Ton_Strt_T3_V1.pin5
  N23: 4316-1.pin15, V3_T1_V5_Ton_Strt_T3_V1.pin4
  N24: 4316-2.pin5, Invert_V4_T0_T2_V2_T4_V0.pin4
  N25: 4316-2.pin6, Invert_V4_T0_T2_V2_T4_V0.pin5
  N26: 4316-2.pin14, V3_T1_V5_Ton_Strt_T3_V1.pin7
  N27: 4316-2.pin15, V3_T1_V5_Ton_Strt_T3_V1.pin6
  N28: 4316-3.pin5, Invert_V4_T0_T2_V2_T4_V0.pin6
  N29: 4316-3.pin6, Invert_V4_T0_T2_V2_T4_V0.pin7
  N30: 4316-3.pin8, Cdc3.0
  N31: 4316-3.pin14, V3_T1_V5_Ton_Strt_T3_V1.pin1
  N32: 4316-3.pin15, V3_T1_V5_Ton_Strt_T3_V1.pin2
