# Fritzing sketch 4316h MVT schematic  (saved by Fritzing 0.9.2b)
breadboards: 1

parts:
  +5v = female pin header, 1 pin [form="♀ (female)"]
  -5v = female pin header, 1 pin [form="♀ (female)"]
  V100% = female pin header, 1 pin [form="♀ (female)"]
  V80% = female pin header, 1 pin [form="♀ (female)"]
  V40% = female pin header, 1 pin [form="♀ (female)"]
  V20% = female pin header, 1 pin [form="♀ (female)"]
  V0% = female pin header, 1 pin [form="♀ (female)"]
  TR_10nF = female pin header, 1 pin [form="♀ (female)"]
  T0R = female pin header, 1 pin [form="♀ (female)"]
  T32R = female pin header, 1 pin [form="♀ (female)"]
  T64R = female pin header, 1 pin [form="♀ (female)"]
  C1 = Ceramic Capacitor [capacitance=100nF package="100 mil [THT, multilayer]"]
  4316-1 = IC, DIP package, 16 pins [chip_label=IC]
  C1_2 = Ceramic Capacitor [capacitance=100nF package="100 mil [THT, multilayer]"]
  4316-2 = IC, DIP package, 16 pins [chip_label=IC]
  C1_3 = Ceramic Capacitor [capacitance=100nF package="100 mil [THT, multilayer]"]
  4316-3 = IC, DIP package, 16 pins [chip_label=IC]
  RV = Resistor [tolerance=±5% resistance=100k package=THT]
  RV_2 = Resistor [tolerance=±5% resistance=100k package=THT]
  RV_3 = Resistor [tolerance=±5% resistance=100k package=THT]
  RV_4 = Resistor [tolerance=±5% resistance=100k package=THT]
  RV_5 = Resistor [tolerance=±5% resistance=100k package=THT]
  OUT+ = male pin header, 1 pin [form="♂ (male)"]
  OUT- = male pin header, 1 pin [form="♂ (male)"]
  T16R = female pin header, 1 pin [form="♀ (female)"]
  V60% = female pin header, 1 pin [form="♀ (female)"]
  IN- = female pin header, 1 pin [form="♀ (female)"]
  IN+ = female pin header, 1 pin [form="♀ (female)"]
  C1_4 = Ceramic Capacitor [capacitance=100nF package="100 mil [THT, multilayer]"]
  4316-0 = IC, DIP package, 16 pins [chip_label=IC]
  C6 = Ceramic Capacitor [capacitance=1nF package="100 mil [THT, multilayer]"]
  C5 = Ceramic Capacitor [capacitance=2nF package="100 mil [THT, multilayer]"]
  C4 = Ceramic Capacitor [capacitance=4nF package="100 mil [THT, multilayer]"]
  C3 = Ceramic Capacitor [capacitance=6.3nF package="100 mil [THT, multilayer]"]
  C2 = Ceramic Capacitor [capacitance=10nF package="100 mil [THT, multilayer]"]
  R2 = Resistor [tolerance=±1% resistance=32k package=THT]
  R4 = Resistor [tolerance=±0.5% resistance=64k package=THT]
  R1 = Resistor [tolerance=±1% resistance=16k package=THT]
  R1_2 = Resistor [tolerance=±1% resistance=16k package=THT]
  T128R = female pin header, 1 pin [form="♀ (female)"]
  TR_4nF = female pin header, 1 pin [form="♀ (female)"]
  TR_6_3nF = female pin header, 1 pin [form="♀ (female)"]
  TR_2nF = female pin header, 1 pin [form="♀ (female)"]
  TR_1nF = female pin header, 1 pin [form="♀ (female)"]
  R5 = Resistor [tolerance=±1% resistance=22k package=THT]
  C7 = Ceramic Capacitor [capacitance=0.18nF package="100 mil [THT, multilayer]"]
  C1_5 = Ceramic Capacitor [capacitance=100nF package="100 mil [THT, multilayer]"]
  C1_6 = Ceramic Capacitor [capacitance=100nF package="100 mil [THT, multilayer]"]
  C1_7 = Ceramic Capacitor [capacitance=100nF package="100 mil [THT, multilayer]"]
  C1_8 = Ceramic Capacitor [capacitance=100nF package="100 mil [THT, multilayer]"]

nets:
  N1: +5v.pin1, C1.1, 4316-1.pin16, C1_2.1, 4316-2.pin16, C1_3.1, 4316-3.pin16, C1_4.1, 4316-0.pin16
  N2: -5v.pin1, 4316-1.pin9, 4316-2.pin9, 4316-3.pin9, 4316-0.pin9, C1_5.1, C1_6.1, C1_7.1, C1_8.1
  N3: V100%.pin1, 4316-1.pin14
  N4: V80%.pin1, 4316-1.pin6
  N5: V40%.pin1, 4316-2.pin6
  N6: V20%.pin1, 4316-3.pin14
  N7: V0%.pin1, 4316-3.pin6
  N8: TR_10nF.pin1, 4316-1.pin15
  N9: T0R.pin1, 4316-1.pin5
  N10: T32R.pin1, 4316-2.pin5
  N11: T64R.pin1, 4316-3.pin15
  GND: C1.0, 4316-1.pin7, 4316-1.pin8, C1_2.0, 4316-2.pin7, 4316-2.pin8, C1_3.0, 4316-3.pin7, 4316-3.pin8, C1_4.0, 4316-0.pin7, 4316-0.pin8, C1_5.0, C1_6.0, C1_7.0, C1_8.0
  N12: 4316-1.pin1, C2.1
  N13: 4316-1.pin2, 4316-1.pin3, 4316-1.pin13, 4316-2.pin2, 4316-2.pin3, 4316-3.pin2, 4316-3.pin3, RV_5.Pin_0, IN+.pin1, 4316-0.pin2, 4316-0.pin3, 4316-0.pin11, 4316-0.pin12, C7.1
  N14: 4316-1.pin4, R1_2.Pin_0, R5.Pin_1
  N15: 4316-1.pin10, RV_2.Pin_0, RV_5.Pin_1
  N16: 4316-1.pin11, 4316-1.pin12, 4316-2.pin11, 4316-2.pin12, 4316-3.pin11, 4316-3.pin12, OUT+.pin1, C7.0
  N17: 4316-2.pin1, R1.Pin_0, R1_2.Pin_1
  N18: 4316-2.pin4, R2.Pin_0, R1.Pin_1
  N19: 4316-2.pin10, RV.Pin_0, RV_3.Pin_1
  N20: 4316-2.pin13, RV_2.Pin_1, RV_3.Pin_0
  N21: 4316-2.pin14, V60%.pin1
  N22: 4316-2.pin15, T16R.pin1
  N23: 4316-3.pin1, R2.Pin_1, R4.Pin_0
  N24: 4316-3.pin4, R4.Pin_1
  N25: 4316-3.pin5, T128R.pin1
  N26: 4316-3.pin10, RV_4.Pin_1, OUT-.pin1, IN-.pin1, C6.0, C5.0, C4.0, C3.0, C2.0, R5.Pin_0
  N27: 4316-3.pin13, RV.Pin_1, RV_4.Pin_0
  N28: 4316-0.pin1, C5.1
  N29: 4316-0.pin4, C4.1
  N30: 4316-0.pin5, TR_4nF.pin1
  N31: 4316-0.pin6, TR_6_3nF.pin1
  N32: 4316-0.pin10, C3.1
  N33: 4316-0.pin13, C6.1
  N34: 4316-0.pin14, TR_1nF.pin1
  N35: 4316-0.pin15, TR_2nF.pin1
