# Fritzing sketch SPDT-JUMPER-Inverter-Vol-tone-Switch-PCB-big-pads (saved by Fritzing 0.9.1b)
circuit board: 4.48278cm x 6.26061cm
breadboards: 1

parts:
  v100% = female pin header, 4 pins [form="♀ (female)"]
  v80% = female pin header, 4 pins [form="♀ (female)"]
  v60% = female pin header, 4 pins [form="♀ (female)"]
  v40% = female pin header, 4 pins [form="♀ (female)"]
  v0% = female pin header, 4 pins [form="♀ (female)"]
  v20% = female pin header, 4 pins [form="♀ (female)"]
  tON = female pin header, 4 pins [form="♀ (female)"]
  t200R = female pin header, 4 pins [form="♀ (female)"]
  t100R = female pin header, 4 pins [form="♀ (female)"]
  t50R = female pin header, 4 pins [form="♀ (female)"]
  t22R = female pin header, 3 pins [form="♀ (female)"]
  Invert = female pin header, 4 pins [form="♀ (female)"]
  Inverter = female pin header, 2 pins [form="♀ (female)"]
  Vol = female pin header, 6 pins [form="♀ (female)"]
  Vin = female pin header, 2 pins [form="♀ (female)"]
  Tone = female pin header, 5 pins [form="♀ (female)"]
  Straight = female pin header, 4 pins [form="♀ (female)"]

nets:
  N1: v100%.pin1, v100%.pin2, v80%.pin1, v80%.pin2, v60%.pin1, v60%.pin2, v40%.pin1, v40%.pin2, v0%.pin1, v0%.pin2, v20%.pin1, v20%.pin2, tON.pin1, tON.pin2, t200R.pin1, t200R.pin2, t100R.pin1, t100R.pin2, t50R.pin1, t50R.pin2, t22R.pin1, Invert.pin4, Vin.pin2, Straight.pin1
  N2: v100%.pin3, Vol.pin1
  N3: v100%.pin4, v80%.pin4, v60%.pin4, v40%.pin4, v0%.pin4, v20%.pin4, tON.pin4, t200R.pin4, t100R.pin4, t50R.pin4, t22R.pin3, Invert.pin1, Invert.pin2, Vin.pin1, Straight.pin3, Straight.pin4
  N4: v80%.pin3, Vol.pin2
  N5: v60%.pin3, Vol.pin3
  N6: v40%.pin3, Vol.pin4
  N7: v0%.pin3, Vol.pin6
  N8: v20%.pin3, Vol.pin5
  N9: tON.pin3, Tone.pin1
  N10: t200R.pin3, Tone.pin2
  N11: t100R.pin3, Tone.pin3
  N12: t50R.pin3, Tone.pin4
  N13: t22R.pin2, Tone.pin5
  N14: Invert.pin3, Inverter.pin2
  N15: Inverter.pin1, Straight.pin2

notes:
  V+
  Straight
  Invert
  v40%
  v60%
  v80%
  v0%
  v100%
  v20%
  tON
  t22R
  t200R
  t50R
  t100R
  GND
  Inverter
  Vol
  Tone
