# Fritzing sketch POC-2_4316_Switching Schematic (saved by Fritzing 0.9.1b)
breadboards: 1

parts:
  4316-1 = IC, DIP package, 16 pins [chip_label=HC4316]
  C1 = Ceramic Capacitor [capacitance=100nF package="100 mil [THT, multilayer]"]
  4316-2 = IC, DIP package, 16 pins [chip_label=HC4316]
  C2 = Ceramic Capacitor [capacitance=100nF package="100 mil [THT, multilayer]"]
  4316-3 = IC, DIP package, 16 pins [chip_label=HC4316]
  C3 = Ceramic Capacitor [capacitance=100nF package="100 mil [THT, multilayer]"]
  4316-4 = IC, DIP package, 16 pins [chip_label=HC4316]
  C4 = Ceramic Capacitor [capacitance=100nF package="100 mil [THT, multilayer]"]
  4316-5 = IC, DIP package, 16 pins [chip_label=HC4316]
  C5 = Ceramic Capacitor [capacitance=100nF package="100 mil [THT, multilayer]"]
  4316-6 = IC, DIP package, 16 pins [chip_label=HC4316]
  C6 = Ceramic Capacitor [capacitance=100nF package="100 mil [THT, multilayer]"]
  4316-7 = IC, DIP package, 16 pins [chip_label=HC4316]
  C7 = Ceramic Capacitor [capacitance=100nF package="100 mil [THT, multilayer]"]
  4316-8 = IC, DIP package, 16 pins [chip_label=HC4316]
  C8 = Ceramic Capacitor [capacitance=100nF package="100 mil [THT, multilayer]"]
  A+ = female pin header, 1 pin [form="♀ (female)"]
  B+ = female pin header, 1 pin [form="♀ (female)"]
  B- = female pin header, 1 pin [form="♀ (female)"]
  C+ = female pin header, 1 pin [form="♀ (female)"]
  C- = female pin header, 1 pin [form="♀ (female)"]
  A- = female pin header, 1 pin [form="♀ (female)"]
  D- = female pin header, 1 pin [form="♀ (female)"]
  D+ = female pin header, 1 pin [form="♀ (female)"]
  OUT+ = male pin header, 1 pin [form="♂ (male)"]
  OUT- = male pin header, 1 pin [form="♂ (male)"]

nets:
  N1: 4316-1.pin1, 4316-3.pin1, 4316-4.pin2, 4316-4.pin3, 4316-4.pin10, 4316-5.pin1, 4316-7.pin1, C+.pin1
  N2: 4316-1.pin2, 4316-1.pin3, 4316-1.pin11, 4316-1.pin12, 4316-2.pin2, 4316-2.pin3, 4316-2.pin13, A+.pin1
  N3: 4316-1.pin4, 4316-3.pin4, 4316-5.pin4, 4316-7.pin4, 4316-8.pin2, 4316-8.pin3, 4316-8.pin13, C-.pin1
  N4: 4316-1.pin7, 4316-1.pin8
  N5: 4316-1.pin9, C1.0
  N6: 4316-1.pin10, 4316-5.pin10, 4316-6.pin10, 4316-7.pin2, 4316-7.pin3, 4316-7.pin11, 4316-7.pin12, B-.pin1
  N7: 4316-1.pin13, 4316-2.pin10, 4316-3.pin2, 4316-3.pin3, 4316-3.pin11, 4316-3.pin12, 4316-5.pin13, B+.pin1
  N8: 4316-1.pin16, C1.1
  N9: 4316-2.pin1, 4316-3.pin13, 4316-4.pin1, 4316-4.pin13, 4316-6.pin1, 4316-7.pin13, 4316-8.pin1, D+.pin1
  N10: 4316-2.pin4, 4316-3.pin10, 4316-4.pin4, 4316-6.pin4, 4316-7.pin10, 4316-8.pin4, 4316-8.pin10, D-.pin1
  N11: 4316-2.pin7, 4316-2.pin8
  N12: 4316-2.pin9, C2.0
  N13: 4316-2.pin11, 4316-2.pin12, 4316-4.pin11, 4316-4.pin12, OUT+.pin1
  N14: 4316-2.pin16, C2.1
  N15: 4316-3.pin7, 4316-3.pin8
  N16: 4316-3.pin9, C3.0
  N17: 4316-3.pin16, C3.1
  N18: 4316-4.pin7, 4316-4.pin8
  N19: 4316-4.pin9, C4.0
  N20: 4316-4.pin16, C4.1
  N21: 4316-5.pin2, 4316-5.pin3, 4316-5.pin11, 4316-5.pin12, 4316-6.pin2, 4316-6.pin3, 4316-6.pin13, A-.pin1
  N22: 4316-5.pin7, 4316-5.pin8
  N23: 4316-5.pin9, C5.0
  N24: 4316-5.pin16, C5.1
  N25: 4316-6.pin7, 4316-6.pin8
  N26: 4316-6.pin9, C6.0
  N27: 4316-6.pin11, 4316-6.pin12, 4316-8.pin11, 4316-8.pin12, OUT-.pin1
  N28: 4316-6.pin16, C6.1
  N29: 4316-7.pin7, 4316-7.pin8
  N30: 4316-7.pin9, C7.0
  N31: 4316-7.pin16, C7.1
  N32: 4316-8.pin7, 4316-8.pin8
  N33: 4316-8.pin9, C8.0
  N34: 4316-8.pin16, C8.1
