# Fritzing sketch PSU +5v (saved by Fritzing 0.9.0b)
breadboards: 1

parts:
  LM2596_ADJ = female pin header, 5 pins [form="♀ (female)"]
  Cin = Electrolytic Capacitor [capacitance=470µF package="100 mil [THT, electrolytic]"]
  L1 = Inductor [package="400 mil [THT]"]
  Cout = Electrolytic Capacitor [capacitance=220µF package="100 mil [THT, electrolytic]"]
  R1 = Resistor [tolerance=±5% resistance=33k package=THT]
  R2 = Resistor [tolerance=±5% resistance=100k package=THT]
  Vin = female pin header, 1 pin [form="♀ (female)"]
  Vout = male pin header, 1 pin [form="♂ (male)"]
  D2 = Schottky Diode [part_number=1N5825 package="Melf DO-213 AB [SMD]"]

nets:
  N1: LM2596_ADJ.pin1, Cin.+, Vin.pin1
  N2: LM2596_ADJ.pin2, L1.pin_0, D2.cathode
  GND: LM2596_ADJ.pin3, LM2596_ADJ.pin5, Cin.-, Cout.-, R1.Pin_1, D2.anode
  N3: LM2596_ADJ.pin4, R1.Pin_0, R2.Pin_0
  N4: L1.pin_1, Cout.+, R2.Pin_1, Vout.pin1

notes:
  Vin +9v, Vout +5v
