# Fritzing sketch Working PSU -5v (saved by Fritzing 0.9.1b)
breadboards: 1

parts:
  LM2596_ADJ = female pin header, 5 pins [form="♀ (female)"]
  Cin = Electrolytic Capacitor [capacitance=220µF package="100 mil [THT, electrolytic]"]
  L1 = Inductor [package="400 mil [THT]"]
  Cout = Electrolytic Capacitor [capacitance=470µF package="100 mil [THT, electrolytic]"]
  R1 = Resistor [tolerance=±5% resistance=330 package=THT]
  Vout_-5V = male pin header, 1 pin [form="♂ (male)"]
  Vin = female pin header, 1 pin [form="♀ (female)"]
  D3 = Schottky Diode [part_number=1N5825 package="Melf DO-213 AB [SMD]"]
  R2 = Resistor [tolerance=±5% resistance=1k package=THT]

nets:
  N1: LM2596_ADJ.pin1, Cin.+, Vin.pin1
  N2: LM2596_ADJ.pin2, L1.pin_0, D3.cathode
  N3: LM2596_ADJ.pin3, LM2596_ADJ.pin5, Cin.-, Cout.-, R1.Pin_1, Vout_-5V.pin1, D3.anode
  N4: LM2596_ADJ.pin4, R1.Pin_0, R2.Pin_0
  N5: L1.pin_1, Cout.+
  GND: R2.Pin_1

notes:
  Vin +9v
  GND
  (Vin 0v)
  Vout -5v
