# Fritzing sketch SPDT JUMPER Switch-Array-PCB (saved by Fritzing 0.9.0b)
circuit board: 7.20605cm x 14.4947cm
breadboards: 1

parts:
  A+ = female pin header, 7 pins [form="♀ (female)"]
  D- = female pin header, 1 pin [form="♀ (female)"]
  D+ = female pin header, 1 pin [form="♀ (female)"]
  Vin = female pin header, 2 pins [form="♀ (female)"]
  C- = female pin header, 3 pins [form="♀ (female)"]
  C+ = female pin header, 3 pins [form="♀ (female)"]
  B- = female pin header, 5 pins [form="♀ (female)"]
  B+ = female pin header, 5 pins [form="♀ (female)"]
  A- = female pin header, 7 pins [form="♀ (female)"]
  Out+ = female pin header, 3 pins [form="♀ (female)"]
  Out- = female pin header, 3 pins [form="♀ (female)"]
  Out+_2 = female pin header, 3 pins [form="♀ (female)"]
  Out-_2 = female pin header, 3 pins [form="♀ (female)"]
  Out+_3 = female pin header, 3 pins [form="♀ (female)"]
  Out-_3 = female pin header, 3 pins [form="♀ (female)"]
  Out+_4 = female pin header, 3 pins [form="♀ (female)"]
  Out-_4 = female pin header, 3 pins [form="♀ (female)"]
  D-_2 = female pin header, 4 pins [form="♀ (female)"]
  D+_2 = female pin header, 4 pins [form="♀ (female)"]
  C-_2 = female pin header, 4 pins [form="♀ (female)"]
  C+_2 = female pin header, 4 pins [form="♀ (female)"]
  B-_2 = female pin header, 4 pins [form="♀ (female)"]
  B+_2 = female pin header, 4 pins [form="♀ (female)"]
  C-1 = female pin header, 4 pins [form="♀ (female)"]
  C+1 = female pin header, 4 pins [form="♀ (female)"]
  D+1 = female pin header, 4 pins [form="♀ (female)"]
  B-1 = female pin header, 4 pins [form="♀ (female)"]
  D-1 = female pin header, 4 pins [form="♀ (female)"]
  B+1 = female pin header, 4 pins [form="♀ (female)"]
  D+2 = female pin header, 4 pins [form="♀ (female)"]
  C-2 = female pin header, 4 pins [form="♀ (female)"]
  C+2 = female pin header, 4 pins [form="♀ (female)"]
  D-2 = female pin header, 4 pins [form="♀ (female)"]
  C+3 = female pin header, 4 pins [form="♀ (female)"]
  D+3 = female pin header, 4 pins [form="♀ (female)"]
  D-3 = female pin header, 4 pins [form="♀ (female)"]
  C-3 = female pin header, 4 pins [form="♀ (female)"]
  D+4 = female pin header, 4 pins [form="♀ (female)"]
  D-4 = female pin header, 4 pins [form="♀ (female)"]
  D-5 = female pin header, 4 pins [form="♀ (female)"]
  D+5 = female pin header, 4 pins [form="♀ (female)"]

nets:
  N1: A+.pin1, B+_2.pin3
  N2: A+.pin2, B-_2.pin3
  N3: A+.pin3, C+_2.pin3
  N4: A+.pin4, C-_2.pin3
  N5: A+.pin5, D+_2.pin3
  N6: A+.pin6, D-_2.pin3
  N7: A+.pin7, Out+.pin2
  N8: D-.pin1, Out-_4.pin2
  N9: D+.pin1, Out+_4.pin2
  N10: Vin.pin1, Out+_4.pin1, Out-_4.pin1, B+_2.pin1, B+_2.pin2, B+1.pin1, B+1.pin2, C+2.pin1, C+2.pin2, C+3.pin1, C+3.pin2, D+4.pin1, D+4.pin2, D+5.pin1, D+5.pin2
  N11: Vin.pin2, Out+.pin3, Out-.pin3, Out+_2.pin3, Out-_2.pin3, Out+_3.pin3, Out-_3.pin3, Out+_4.pin3, Out-_4.pin3, D-_2.pin4, D+_2.pin4, C-_2.pin4, C+_2.pin4, B-_2.pin4, B+_2.pin4, C-1.pin4, C+1.pin4, D+1.pin4, B-1.pin4, D-1.pin4, B+1.pin4, D+2.pin4, C-2.pin4, C+2.pin4, D-2.pin4, C+3.pin4, D+3.pin4, D-3.pin4, C-3.pin4, D+4.pin4, D-4.pin4, D-5.pin4, D+5.pin4
  N12: C-.pin1, D+5.pin3
  N13: C-.pin2, D-5.pin3
  N14: C-.pin3, Out-_3.pin2
  N15: C+.pin1, D+4.pin3
  N16: C+.pin2, D-4.pin3
  N17: C+.pin3, Out+_3.pin2
  N18: B-.pin1, C+3.pin3
  N19: B-.pin2, C-3.pin3
  N20: B-.pin3, D+3.pin3
  N21: B-.pin4, D-3.pin3
  N22: B-.pin5, Out-_2.pin2
  N23: B+.pin1, C+2.pin3
  N24: B+.pin2, C-2.pin3
  N25: B+.pin3, D+2.pin3
  N26: B+.pin4, D-2.pin3
  N27: B+.pin5, Out+_2.pin2
  N28: A-.pin1, B+1.pin3
  N29: A-.pin2, B-1.pin3
  N30: A-.pin3, C+1.pin3
  N31: A-.pin4, C-1.pin3
  N32: A-.pin5, D+1.pin3
  N33: A-.pin6, D-1.pin3
  N34: A-.pin7, Out-.pin2
  N35: Out+.pin1, D-_2.pin1, D-_2.pin2
  N36: Out-.pin1, D-1.pin1, D-1.pin2
  N37: Out+_2.pin1, D-2.pin1, D-2.pin2
  N38: Out-_2.pin1, D-3.pin1, D-3.pin2
  N39: Out+_3.pin1, D-4.pin1, D-4.pin2
  N40: Out-_3.pin1, D-5.pin1, D-5.pin2
  N41: D+_2.pin1, D+_2.pin2, C-_2.pin1, C-_2.pin2
  N42: C+_2.pin1, C+_2.pin2, B-_2.pin1, B-_2.pin2
  N43: C-1.pin1, C-1.pin2, D+1.pin1, D+1.pin2
  N44: C+1.pin1, C+1.pin2, B-1.pin1, B-1.pin2
  N45: D+2.pin1, D+2.pin2, C-2.pin1, C-2.pin2
  N46: D+3.pin1, D+3.pin2, C-3.pin1, C-3.pin2

notes:
  V+
  B+
  B-
  C+
  C-
  D+
  D-
  Out+
  Out-
  V-
  A+
  A-
