# Fritzing sketch SPDT-JUMPER-Switch-Array-PCB-big-pads (saved by Fritzing 0.9.1b)
circuit board: 7.20605cm x 14.4947cm
breadboards: 1

parts:
  Out+ = female pin header, 3 pins [form="♀ (female)"]
  A- = female pin header, 7 pins [form="♀ (female)"]
  B+ = female pin header, 5 pins [form="♀ (female)"]
  B- = female pin header, 5 pins [form="♀ (female)"]
  C+ = female pin header, 3 pins [form="♀ (female)"]
  C- = female pin header, 3 pins [form="♀ (female)"]
  D+ = female pin header, 1 pin [form="♀ (female)"]
  D- = female pin header, 1 pin [form="♀ (female)"]
  Vin = female pin header, 2 pins [form="♀ (female)"]
  D-_2 = female pin header, 4 pins [form="♀ (female)"]
  D+_2 = female pin header, 4 pins [form="♀ (female)"]
  C-_2 = female pin header, 4 pins [form="♀ (female)"]
  C+_2 = female pin header, 4 pins [form="♀ (female)"]
  B-_2 = female pin header, 4 pins [form="♀ (female)"]
  B+_2 = female pin header, 4 pins [form="♀ (female)"]
  A+ = female pin header, 7 pins [form="♀ (female)"]
  B+1 = female pin header, 4 pins [form="♀ (female)"]
  B-1 = female pin header, 4 pins [form="♀ (female)"]
  C+1 = female pin header, 4 pins [form="♀ (female)"]
  C-1 = female pin header, 4 pins [form="♀ (female)"]
  D-1 = female pin header, 4 pins [form="♀ (female)"]
  Out- = female pin header, 3 pins [form="♀ (female)"]
  D+1 = female pin header, 4 pins [form="♀ (female)"]
  C+2 = female pin header, 4 pins [form="♀ (female)"]
  C-2 = female pin header, 4 pins [form="♀ (female)"]
  D+2 = female pin header, 4 pins [form="♀ (female)"]
  D-2 = female pin header, 4 pins [form="♀ (female)"]
  Out+_2 = female pin header, 3 pins [form="♀ (female)"]
  Out-_2 = female pin header, 3 pins [form="♀ (female)"]
  D-3 = female pin header, 4 pins [form="♀ (female)"]
  D+3 = female pin header, 4 pins [form="♀ (female)"]
  C-3 = female pin header, 4 pins [form="♀ (female)"]
  C+3 = female pin header, 4 pins [form="♀ (female)"]
  D+4 = female pin header, 4 pins [form="♀ (female)"]
  D-4 = female pin header, 4 pins [form="♀ (female)"]
  Out+_3 = female pin header, 3 pins [form="♀ (female)"]
  Out-_3 = female pin header, 3 pins [form="♀ (female)"]
  D-5 = female pin header, 4 pins [form="♀ (female)"]
  D+5 = female pin header, 4 pins [form="♀ (female)"]
  Out+_4 = female pin header, 3 pins [form="♀ (female)"]
  Out-_4 = female pin header, 4 pins [form="♀ (female)"]
  Out-_5 = female pin header, 1 pin [form="♀ (female)"]  # not connected

nets:
  N1: Out+.pin1, D-_2.pin1, D-_2.pin2
  N2: Out+.pin2, A+.pin7
  N3: Out+.pin3, Vin.pin2, D-_2.pin4, D+_2.pin4, C-_2.pin4, C+_2.pin4, B-_2.pin4, B+_2.pin4, B+1.pin4, B-1.pin4, C+1.pin4, C-1.pin4, D-1.pin4, Out-.pin3, D+1.pin4, C+2.pin4, C-2.pin4, D+2.pin4, D-2.pin4, Out+_2.pin3, Out-_2.pin3, D-3.pin4, D+3.pin4, C-3.pin4, C+3.pin4, D+4.pin4, D-4.pin4, Out+_3.pin3, Out-_3.pin3, D-5.pin4, D+5.pin4, Out+_4.pin3, Out-_4.pin4
  N4: A-.pin1, B+1.pin3
  N5: A-.pin2, B-1.pin3
  N6: A-.pin3, C+1.pin3
  N7: A-.pin4, C-1.pin3
  N8: A-.pin5, D+1.pin3
  N9: A-.pin6, D-1.pin3
  N10: A-.pin7, Out-.pin2
  N11: B+.pin1, C+2.pin3
  N12: B+.pin2, B+.pin3, C-2.pin3, D+2.pin3
  N13: B+.pin4, D-2.pin3
  N14: B+.pin5, Out+_2.pin2
  N15: B-.pin1, B-.pin2, C-3.pin3, C+3.pin3
  N16: B-.pin3, D+3.pin3
  N17: B-.pin4, D-3.pin3
  N18: B-.pin5, Out-_2.pin2
  N19: C+.pin1, D+4.pin3
  N20: C+.pin2, D-4.pin3
  N21: C+.pin3, Out+_3.pin2
  N22: C-.pin1, D+5.pin3
  N23: C-.pin2, D-5.pin3
  N24: C-.pin3, Out-_3.pin2
  N25: D+.pin1, Out+_4.pin2
  N26: D-.pin1, Out-_4.pin1, Out-_4.pin3
  N27: Vin.pin1, B+_2.pin1, B+_2.pin2, B+1.pin1, B+1.pin2, C+2.pin1, C+2.pin2, C+3.pin1, C+3.pin2, D+4.pin1, D+4.pin2, D+5.pin1, D+5.pin2, Out+_4.pin1, Out-_4.pin2
  N28: D-_2.pin3, A+.pin6
  N29: D+_2.pin1, D+_2.pin2, C-_2.pin1, C-_2.pin2
  N30: D+_2.pin3, A+.pin5
  N31: C-_2.pin3, A+.pin4
  N32: C+_2.pin1, C+_2.pin2, B-_2.pin1, B-_2.pin2
  N33: C+_2.pin3, A+.pin3
  N34: B-_2.pin3, A+.pin2
  N35: B+_2.pin3, A+.pin1
  N36: B-1.pin1, B-1.pin2, C+1.pin1, C+1.pin2
  N37: C-1.pin1, C-1.pin2, D+1.pin1, D+1.pin2
  N38: D-1.pin1, D-1.pin2, Out-.pin1
  N39: C-2.pin1, C-2.pin2, D+2.pin1, D+2.pin2
  N40: D-2.pin1, D-2.pin2, Out+_2.pin1
  N41: Out-_2.pin1, D-3.pin1, D-3.pin2
  N42: D+3.pin1, D+3.pin2, C-3.pin1, C-3.pin2
  N43: D-4.pin1, D-4.pin2, Out+_3.pin1
  N44: Out-_3.pin1, D-5.pin1, D-5.pin2

notes:
  V+
  B+
  B-
  C+
  C-
  D+
  D-
  Out+
  Out-
  V-
  A+
  A-
