# Fritzing sketch VactrolNPN Shunt 00 (saved by Fritzing 0.9.2b)
breadboards: 1

parts:
  Vactrol = VTL5C4 [package=THT]
  2N2222 = TRANSISTOR_NPN [package=to-92]
  AMP = female pin header, 2 pins [form="♀ (female)"]
  R1 = Resistor [tolerance=±5% resistance=50 package=THT]
  5V = female pin header, 1 pin [form="♀ (female)"]
  R2 = Resistor [tolerance=±5% resistance=1k package=THT]
  PWM_(3_3V) = female pin header, 1 pin [form="♀ (female)"]
  Audio_Source_Ouptut = female pin header, 1 pin [form="♀ (female)"]

nets:
  N1: Vactrol.Pin_1, R1.Pin_1
  N2: Vactrol.Pin_2, 5V.pin1
  GND: Vactrol.Pin_4, 2N2222.E, AMP.pin2
  N3: Vactrol.Pin_3, AMP.pin1, Audio_Source_Ouptut.pin1
  N4: 2N2222.B, R2.Pin_1
  N5: 2N2222.C, R1.Pin_0
  N6: R2.Pin_0, PWM_(3_3V).pin1

custom parts:
  VTL5C4: Vactrol VTL5 C4 Optocoupler - keeps you from frying your stuff!
