# Fritzing sketch Inverter-Vol-Tone-Scematic-Digital-d (saved by Fritzing 0.9.2b)
breadboards: 1

parts:
  MAX395CNG-0 = IC, DIP package, 24 pins [chip_label=IC]
  MAX395CNG-1 = IC, DIP package, 24 pins [chip_label=IC]
  Rv = Resistor [tolerance=±1% resistance=100k package=THT]  # not connected
  Rv_2 = Resistor [tolerance=±1% resistance=100k package=THT]  # not connected
  Rv_3 = Resistor [tolerance=±1% resistance=100k package=THT]  # not connected
  Rv_4 = Resistor [tolerance=±1% resistance=100k package=THT]  # not connected
  Rv_5 = Resistor [tolerance=±1% resistance=100k package=THT]  # not connected
  Tone = Ceramic Capacitor [capacitance=10nF package="100 mil [THT, multilayer]"]  # not connected
  RT1 = Resistor [tolerance=±1% resistance=16k package=THT]  # not connected
  RT1_2 = Resistor [tolerance=±1% resistance=16k package=THT]  # not connected
  RT4 = Resistor [tolerance=±1% resistance=64k package=THT]  # not connected
  RT2 = Resistor [tolerance=±1% resistance=32k package=THT]  # not connected
  CDC = Ceramic Capacitor [capacitance=100nF package="100 mil [THT, multilayer]"]
  CDC_2 = Ceramic Capacitor [capacitance=100nF package="100 mil [THT, multilayer]"]
  Boost = Ceramic Capacitor [capacitance=0.18nF package="100 mil [THT, multilayer]"]  # not connected
  CDC_3 = Ceramic Capacitor [capacitance=100nF package="100 mil [THT, multilayer]"]
  CDC_4 = Ceramic Capacitor [capacitance=100nF package="100 mil [THT, multilayer]"]  # not connected
  IN+_IN- = female pin header, 2 pins [form="♀ (female)"]  # not connected
  OUT+_OUT- = female pin header, 2 pins [form="♀ (female)"]  # not connected
  GND = female pin header, 1 pin [form="♀ (female)"]  # not connected
  V- = female pin header, 1 pin [form="♀ (female)"]
  V+ = female pin header, 1 pin [form="♀ (female)"]
  DO = female pin header, 1 pin [form="♀ (female)"]
  V+_2 = female pin header, 1 pin [form="♀ (female)"]
  DI = female pin header, 1 pin [form="♀ (female)"]
  CLK = female pin header, 1 pin [form="♀ (female)"]
  CS = female pin header, 1 pin [form="♀ (female)"]

nets:
  N1: MAX395CNG-0.pin1, MAX395CNG-1.pin1, CLK.pin1
  N2: MAX395CNG-0.pin2, CDC_3.1, V+_2.pin1
  N3: MAX395CNG-0.pin3, MAX395CNG-1.pin22
  N4: MAX395CNG-0.pin21, V-.pin1
  N5: MAX395CNG-0.pin22, DO.pin1
  N6: MAX395CNG-0.pin23, V+.pin1
  N7: MAX395CNG-0.pin24, MAX395CNG-1.pin24, CS.pin1
  N8: MAX395CNG-1.pin2, CDC_2.1
  N9: MAX395CNG-1.pin3, DI.pin1
  N10: MAX395CNG-1.pin21, CDC.1

notes:
  All GND points connect to Ground Plane
