# Fritzing sketch Inverter-Vol-Tone-Scematic-Digital-e (saved by Fritzing 0.9.2b)
breadboards: 1

parts:
  MAX395CNG-1 = IC, DIP package, 24 pins [chip_label=IC]
  MAX395CNG-0 = IC, DIP package, 24 pins [chip_label=IC]
  CDC = Ceramic Capacitor [capacitance=100nF package="100 mil [THT, multilayer]"]
  CDC_2 = Ceramic Capacitor [capacitance=100nF package="100 mil [THT, multilayer]"]
  CDC_3 = Ceramic Capacitor [capacitance=100nF package="100 mil [THT, multilayer]"]
  CDC_4 = Ceramic Capacitor [capacitance=100nF package="100 mil [THT, multilayer]"]
  V- = female pin header, 1 pin [form="♀ (female)"]
  DO = female pin header, 1 pin [form="♀ (female)"]
  DI = female pin header, 1 pin [form="♀ (female)"]
  CLK = female pin header, 1 pin [form="♀ (female)"]
  CS = female pin header, 1 pin [form="♀ (female)"]

nets:
  N1: MAX395CNG-1.pin1, MAX395CNG-0.pin1, CLK.pin1
  N2: MAX395CNG-1.pin2, CDC_3.1
  N3: MAX395CNG-1.pin3, MAX395CNG-0.pin22
  N4: MAX395CNG-1.pin21, CDC_4.1, V-.pin1
  N5: MAX395CNG-1.pin22, DO.pin1
  N6: MAX395CNG-1.pin24, MAX395CNG-0.pin24, CS.pin1
  N7: MAX395CNG-0.pin2, CDC_2.1
  N8: MAX395CNG-0.pin3, DI.pin1
  N9: MAX395CNG-0.pin21, CDC.1
