# Fritzing sketch Inverter-Vol-Tone-Scematic-b (saved by Fritzing 0.9.2b)
breadboards: 1

parts:
  MAX395CNG-0 = IC, DIP package, 24 pins [chip_label=IC]
  MAX395CNG-1 = IC, DIP package, 24 pins [chip_label=IC]
  Coil = Inductor [package="400 mil [THT]"]
  R1 = Resistor [tolerance=±1% resistance=100k package=THT]
  R1_2 = Resistor [tolerance=±1% resistance=100k package=THT]
  R1_3 = Resistor [tolerance=±1% resistance=100k package=THT]
  R1_4 = Resistor [tolerance=±1% resistance=100k package=THT]
  R1_5 = Resistor [tolerance=±1% resistance=100k package=THT]
  OUT+ = female pin header, 1 pin [form="♀ (female)"]
  OUT- = female pin header, 1 pin [form="♀ (female)"]
  C1 = Ceramic Capacitor [capacitance=10nF package="100 mil [THT, multilayer]"]
  R2 = Resistor [tolerance=±1% resistance=37k package=THT]
  R2_2 = Resistor [tolerance=±1% resistance=37k package=THT]
  R4 = Resistor [tolerance=±1% resistance=150k package=THT]
  R3 = Resistor [tolerance=±1% resistance=75k package=THT]
  C2 = Ceramic Capacitor [capacitance=100nF package="100 mil [THT, multilayer]"]
  C2_2 = Ceramic Capacitor [capacitance=100nF package="100 mil [THT, multilayer]"]
  C8 = Ceramic Capacitor [capacitance=0.18nF package="100 mil [THT, multilayer]"]

nets:
  N1: MAX395CNG-0.pin1, MAX395CNG-1.pin1
  N2: MAX395CNG-0.pin2, MAX395CNG-0.pin23, C2.1
  N3: MAX395CNG-0.pin5, R1.Pin_1, R1_2.Pin_0
  N4: MAX395CNG-0.pin6, MAX395CNG-0.pin7, MAX395CNG-1.pin14, MAX395CNG-1.pin15, MAX395CNG-1.pin18, MAX395CNG-1.pin19, OUT+.pin1, C8.0
  N5: MAX395CNG-0.pin8, MAX395CNG-0.pin10, MAX395CNG-0.pin11, MAX395CNG-0.pin17, R1.Pin_0, C8.1
  N6: MAX395CNG-0.pin9, MAX395CNG-0.pin13, Coil.pin_1
  N7: MAX395CNG-0.pin12, MAX395CNG-0.pin16, Coil.pin_0
  N8: MAX395CNG-0.pin14, MAX395CNG-0.pin15
  N9: MAX395CNG-0.pin18, C1.1
  N10: MAX395CNG-0.pin19, MAX395CNG-1.pin6, MAX395CNG-1.pin8, MAX395CNG-1.pin9, MAX395CNG-1.pin11, MAX395CNG-1.pin13, R1_5.Pin_1, OUT-.pin1
  N11: MAX395CNG-0.pin20, C1.0, R2.Pin_0
  N12: MAX395CNG-0.pin21, C2.0
  N13: MAX395CNG-0.pin22, MAX395CNG-1.pin3
  N14: MAX395CNG-0.pin24, MAX395CNG-1.pin24
  N15: MAX395CNG-1.pin2, MAX395CNG-1.pin23, C2_2.0
  N16: MAX395CNG-1.pin5, R2.Pin_1, R2_2.Pin_0
  N17: MAX395CNG-1.pin7, R2_2.Pin_1, R3.Pin_0
  N18: MAX395CNG-1.pin10, R4.Pin_0, R3.Pin_1
  N19: MAX395CNG-1.pin12, R4.Pin_1
  N20: MAX395CNG-1.pin16, R1_4.Pin_1, R1_5.Pin_0
  N21: MAX395CNG-1.pin17, R1_3.Pin_1, R1_4.Pin_0
  N22: MAX395CNG-1.pin20, R1_2.Pin_1, R1_3.Pin_0
  N23: MAX395CNG-1.pin21, C2_2.1

notes:
  C+
  C-
