# Fritzing sketch Master-Vol-Tone-Scematic-e-with-SPI (saved by Fritzing 0.9.2b)
breadboards: 1

parts:
  MAX395CNG-0 = IC, DIP package, 24 pins [chip_label=IC]
  MAX395CNG-1 = IC, DIP package, 24 pins [chip_label=IC]
  R1 = Resistor [tolerance=±1% resistance=100k package=THT]
  R1_2 = Resistor [tolerance=±1% resistance=100k package=THT]
  R1_3 = Resistor [tolerance=±1% resistance=100k package=THT]
  R1_4 = Resistor [tolerance=±1% resistance=100k package=THT]
  R1_5 = Resistor [tolerance=±1% resistance=100k package=THT]
  AMP+ = female pin header, 1 pin [form="♀ (female)"]
  Amp-GND = female pin header, 1 pin [form="♀ (female)"]
  C1 = Ceramic Capacitor [capacitance=10nF package="100 mil [THT, multilayer]"]
  R2 = Resistor [tolerance=±1% resistance=16k package=THT]
  R2_2 = Resistor [tolerance=±1% resistance=16k package=THT]
  R4 = Resistor [tolerance=±1% resistance=64k package=THT]
  R3 = Resistor [tolerance=±1% resistance=32k package=THT]
  C2 = Ceramic Capacitor [capacitance=100nF package="100 mil [THT, multilayer]"]
  C2_2 = Ceramic Capacitor [capacitance=100nF package="100 mil [THT, multilayer]"]
  C3 = Ceramic Capacitor [capacitance=6.3nF package="100 mil [THT, multilayer]"]
  C4 = Ceramic Capacitor [capacitance=4nF package="100 mil [THT, multilayer]"]
  C5 = Ceramic Capacitor [capacitance=2nF package="100 mil [THT, multilayer]"]
  C6 = Ceramic Capacitor [capacitance=1nF package="100 mil [THT, multilayer]"]
  R5 = Resistor [tolerance=±1% resistance=22k package=THT]
  C7 = Ceramic Capacitor [capacitance=0.18nF package="100 mil [THT, multilayer]"]
  In+_In- = female pin header, 2 pins [form="♀ (female)"]
  CLK_CS_Di = female pin header, 3 pins [form="♀ (female)"]
  CLK_CS_Do = female pin header, 3 pins [form="♀ (female)"]
  +5v_-5v_GND = female pin header, 3 pins [form="♀ (female)"]  # not connected

nets:
  N1: MAX395CNG-0.pin1, MAX395CNG-1.pin1, CLK_CS_Di.pin1, CLK_CS_Do.pin1
  N2: MAX395CNG-0.pin2, MAX395CNG-0.pin23, C2.1
  N3: MAX395CNG-0.pin3, CLK_CS_Di.pin3
  N4: MAX395CNG-0.pin5, R1.Pin_1, R1_2.Pin_0
  N5: MAX395CNG-0.pin6, MAX395CNG-0.pin7, MAX395CNG-1.pin14, MAX395CNG-1.pin15, MAX395CNG-1.pin18, MAX395CNG-1.pin19, AMP+.pin1, C7.0
  N6: MAX395CNG-0.pin8, MAX395CNG-0.pin10, MAX395CNG-0.pin11, MAX395CNG-0.pin14, MAX395CNG-0.pin16, MAX395CNG-0.pin17, MAX395CNG-0.pin19, MAX395CNG-1.pin6, MAX395CNG-1.pin8, MAX395CNG-1.pin9, MAX395CNG-1.pin11, R1.Pin_0, C7.1, In+_In-.pin1
  N7: MAX395CNG-0.pin9, C6.1
  N8: MAX395CNG-0.pin12, C5.1
  N9: MAX395CNG-0.pin13, C4.1
  N10: MAX395CNG-0.pin15, C3.1
  N11: MAX395CNG-0.pin18, C1.1
  N12: MAX395CNG-0.pin20, R2.Pin_0, R5.Pin_1
  N13: MAX395CNG-0.pin21, C2.0
  N14: MAX395CNG-0.pin22, MAX395CNG-1.pin3
  N15: MAX395CNG-0.pin24, MAX395CNG-1.pin24, CLK_CS_Di.pin2, CLK_CS_Do.pin2
  N16: MAX395CNG-1.pin2, MAX395CNG-1.pin23, C2_2.0
  N17: MAX395CNG-1.pin5, R2.Pin_1, R2_2.Pin_0
  N18: MAX395CNG-1.pin7, R2_2.Pin_1, R3.Pin_0
  N19: MAX395CNG-1.pin10, R4.Pin_0, R3.Pin_1
  N20: MAX395CNG-1.pin12, R4.Pin_1
  N21: MAX395CNG-1.pin13, R1_5.Pin_1, Amp-GND.pin1, C1.0, C3.0, C4.0, C5.0, C6.0, R5.Pin_0, In+_In-.pin2
  N22: MAX395CNG-1.pin16, R1_4.Pin_1, R1_5.Pin_0
  N23: MAX395CNG-1.pin17, R1_3.Pin_1, R1_4.Pin_0
  N24: MAX395CNG-1.pin20, R1_2.Pin_1, R1_3.Pin_0
  N25: MAX395CNG-1.pin21, C2_2.1
  N26: MAX395CNG-1.pin22, CLK_CS_Do.pin3
