# Fritzing sketch Vactrol Direct Shunt a (saved by Fritzing 0.9.2b)
breadboards: 1

parts:
  Vactrol = VTL5C4 [package=THT]
  AMP = female pin header, 2 pins [form="♀ (female)"]
  R1 = Resistor [tolerance=±5% resistance=330 package=THT]
  Pyboard_Pin_Y1_(PWM) = female pin header, 1 pin [form="♀ (female)"]
  Audio_Source_Ouptut = female pin header, 1 pin [form="♀ (female)"]

nets:
  N1: Vactrol.Pin_1, R1.Pin_1
  N2: Vactrol.Pin_2, Pyboard_Pin_Y1_(PWM).pin1
  GND: Vactrol.Pin_4, AMP.pin2, R1.Pin_0
  N3: Vactrol.Pin_3, AMP.pin1, Audio_Source_Ouptut.pin1

notes:
  LED current limit resistor value TBD

custom parts:
  VTL5C4: Vactrol VTL5 C4 Optocoupler - keeps you from frying your stuff!
