# Fritzing sketch Full-Circuit-PCB-Digital-a (saved by Fritzing 0.9.2b)
circuit board: 3cm x 3.73218cm
circuit board: 23.5218cm x 15.4432cm
breadboards: 1

parts:
  MAX395CNG-10 = IC, DIP package, 24 pins [chip_label=IC]
  MAX395CNG-1 = IC, DIP package, 24 pins [chip_label=IC]
  CDC = Ceramic Capacitor [capacitance=100nF package="100 mil [THT, multilayer]"]  # not connected
  CDC_2 = Ceramic Capacitor [capacitance=100nF package="100 mil [THT, multilayer]"]  # not connected
  CDC_3 = Ceramic Capacitor [capacitance=100nF package="100 mil [THT, multilayer]"]  # not connected
  CDC_4 = Ceramic Capacitor [capacitance=100nF package="100 mil [THT, multilayer]"]  # not connected
  MAX395CNG-9 = IC, DIP package, 24 pins [chip_label=IC]
  MAX395CNG-8 = IC, DIP package, 24 pins [chip_label=IC]
  CDC1 = Ceramic Capacitor [capacitance=100nF package="100 mil [THT, multilayer]"]  # not connected
  CDC2 = Ceramic Capacitor [capacitance=100nF package="100 mil [THT, multilayer]"]  # not connected
  CDC3 = Ceramic Capacitor [capacitance=100nF package="100 mil [THT, multilayer]"]  # not connected
  CDC4 = Ceramic Capacitor [capacitance=100nF package="100 mil [THT, multilayer]"]  # not connected
  MAX395CNG-7 = IC, DIP package, 24 pins [chip_label=IC]
  MAX395CNG-5 = IC, DIP package, 24 pins [chip_label=IC]
  MAX395CNG-6 = IC, DIP package, 24 pins [chip_label=IC]
  MAX395CNG-4 = IC, DIP package, 24 pins [chip_label=IC]
  CDC5 = Ceramic Capacitor [capacitance=100nF package="100 mil [THT, multilayer]"]  # not connected
  CDC6 = Ceramic Capacitor [capacitance=100nF package="100 mil [THT, multilayer]"]
  CDC7 = Ceramic Capacitor [capacitance=100nF package="100 mil [THT, multilayer]"]  # not connected
  CDC8 = Ceramic Capacitor [capacitance=100nF package="100 mil [THT, multilayer]"]  # not connected
  CDC9 = Ceramic Capacitor [capacitance=100nF package="100 mil [THT, multilayer]"]  # not connected
  CDC10 = Ceramic Capacitor [capacitance=100nF package="100 mil [THT, multilayer]"]  # not connected
  CDC11 = Ceramic Capacitor [capacitance=100nF package="100 mil [THT, multilayer]"]  # not connected
  CDC12 = Ceramic Capacitor [capacitance=100nF package="100 mil [THT, multilayer]"]  # not connected
  MAX395CNG-13 = IC, DIP package, 24 pins [chip_label=IC]
  MAX395CNG-12 = IC, DIP package, 24 pins [chip_label=IC]
  CDC13 = Ceramic Capacitor [capacitance=100nF package="100 mil [THT, multilayer]"]  # not connected
  CDC14 = Ceramic Capacitor [capacitance=100nF package="100 mil [THT, multilayer]"]  # not connected
  CDC15 = Ceramic Capacitor [capacitance=100nF package="100 mil [THT, multilayer]"]  # not connected
  CDC16 = Ceramic Capacitor [capacitance=100nF package="100 mil [THT, multilayer]"]  # not connected
  MAX395CNG-2 = IC, DIP package, 24 pins [chip_label=IC]
  MAX395CNG-3 = IC, DIP package, 24 pins [chip_label=IC]
  CDC17 = Ceramic Capacitor [capacitance=100nF package="100 mil [THT, multilayer]"]  # not connected
  CDC19 = Ceramic Capacitor [capacitance=100nF package="100 mil [THT, multilayer]"]  # not connected
  CDC21 = Ceramic Capacitor [capacitance=100nF package="100 mil [THT, multilayer]"]
  CDC23 = Ceramic Capacitor [capacitance=100nF package="100 mil [THT, multilayer]"]  # not connected
  MAX395CNG-0 = IC, DIP package, 24 pins [chip_label=IC]
  MAX395CNG-1_2 = IC, DIP package, 24 pins [chip_label=IC]
  CDC25 = Ceramic Capacitor [capacitance=100nF package="100 mil [THT, multilayer]"]  # not connected
  CDC28 = Ceramic Capacitor [capacitance=100nF package="100 mil [THT, multilayer]"]  # not connected
  CDC29 = Ceramic Capacitor [capacitance=100nF package="100 mil [THT, multilayer]"]  # not connected
  CDC32 = Ceramic Capacitor [capacitance=100nF package="100 mil [THT, multilayer]"]  # not connected
  Shunt = female pin header, 1 pin [form="♀ (female)"]
  J7 = female pin header, 16 pins [form="♀ (female)"]  # not connected
  J9 = double row female pin header, 20 pins [form="♀ (female)"]  # not connected
  J8 = female pin header, 16 pins [form="♀ (female)"]
  Bat_+_- = female pin header, 2 pins [form="♀ (female)"]  # not connected
  Out_+_G_- = female pin header, 3 pins [form="♀ (female)"]  # not connected
  A_+_G_-1 = female pin header, 3 pins [form="♀ (female)"]  # not connected
  B_+_G_-2 = female pin header, 3 pins [form="♀ (female)"]  # not connected
  C_+_G_-3 = female pin header, 3 pins [form="♀ (female)"]  # not connected
  D_+_G_-4 = female pin header, 3 pins [form="♀ (female)"]  # not connected
  J10 = double row female pin header, 4 pins [form="♀ (female)"]  # not connected

nets:
  N1: MAX395CNG-10.pin1, MAX395CNG-1.pin1, MAX395CNG-9.pin1, MAX395CNG-8.pin1, MAX395CNG-7.pin1, MAX395CNG-5.pin1, MAX395CNG-6.pin1, MAX395CNG-4.pin1, MAX395CNG-13.pin1, MAX395CNG-12.pin1, MAX395CNG-2.pin1, MAX395CNG-3.pin1, J8.pin6
  N2: MAX395CNG-10.pin3, MAX395CNG-1.pin22
  N3: MAX395CNG-10.pin22, MAX395CNG-9.pin3
  N4: MAX395CNG-10.pin24, MAX395CNG-1.pin24, MAX395CNG-9.pin24, MAX395CNG-8.pin24, MAX395CNG-7.pin24, MAX395CNG-5.pin24, MAX395CNG-6.pin24, MAX395CNG-4.pin24, MAX395CNG-2.pin24, MAX395CNG-3.pin24, MAX395CNG-0.pin24, MAX395CNG-1_2.pin24, J8.pin5
  N5: MAX395CNG-1.pin3, MAX395CNG-12.pin22
  N6: MAX395CNG-9.pin22, MAX395CNG-8.pin3
  N7: MAX395CNG-8.pin22, MAX395CNG-7.pin3
  N8: MAX395CNG-7.pin22, MAX395CNG-6.pin3
  N9: MAX395CNG-5.pin3, MAX395CNG-6.pin22
  N10: MAX395CNG-5.pin22, MAX395CNG-4.pin3
  N11: MAX395CNG-4.pin22, MAX395CNG-3.pin3
  N12: CDC6.1, MAX395CNG-12.pin2
  N13: MAX395CNG-13.pin3, J8.pin8
  N14: MAX395CNG-13.pin22, MAX395CNG-12.pin3
  N15: MAX395CNG-13.pin24, MAX395CNG-12.pin24
  N16: MAX395CNG-12.pin21, CDC21.0
  N17: MAX395CNG-2.pin3, MAX395CNG-3.pin22
  N18: MAX395CNG-2.pin22, MAX395CNG-1_2.pin3
  N19: MAX395CNG-0.pin1, MAX395CNG-1_2.pin1
  N20: MAX395CNG-0.pin3, MAX395CNG-1_2.pin22
  N21: Shunt.pin1, J8.pin1

notes:
  PSU +/-5v
