# Fritzing sketch Full-Circuit-Scematic-Digital-b (saved by Fritzing 0.9.2b)
breadboards: 1

parts:
  MAX395CNG-3 = IC, DIP package, 24 pins [chip_label=IC]
  MAX395CNG-2 = IC, DIP package, 24 pins [chip_label=IC]
  CDC = Ceramic Capacitor [capacitance=100nF package="100 mil [THT, multilayer]"]
  CDC_2 = Ceramic Capacitor [capacitance=100nF package="100 mil [THT, multilayer]"]  # not connected
  CDC_3 = Ceramic Capacitor [capacitance=100nF package="100 mil [THT, multilayer]"]
  CDC_4 = Ceramic Capacitor [capacitance=100nF package="100 mil [THT, multilayer]"]  # not connected
  MAX395CNG-4 = IC, DIP package, 24 pins [chip_label=IC]
  MAX395CNG-5 = IC, DIP package, 24 pins [chip_label=IC]
  CDC1 = Ceramic Capacitor [capacitance=100nF package="100 mil [THT, multilayer]"]
  CDC2 = Ceramic Capacitor [capacitance=100nF package="100 mil [THT, multilayer]"]  # not connected
  CDC3 = Ceramic Capacitor [capacitance=100nF package="100 mil [THT, multilayer]"]  # not connected
  CDC4 = Ceramic Capacitor [capacitance=100nF package="100 mil [THT, multilayer]"]
  MAX395CNG-6 = IC, DIP package, 24 pins [chip_label=IC]
  MAX395CNG-8 = IC, DIP package, 24 pins [chip_label=IC]
  MAX395CNG-7 = IC, DIP package, 24 pins [chip_label=IC]
  MAX395CNG-9 = IC, DIP package, 24 pins [chip_label=IC]
  CDC5 = Ceramic Capacitor [capacitance=100nF package="100 mil [THT, multilayer]"]  # not connected
  CDC6 = Ceramic Capacitor [capacitance=100nF package="100 mil [THT, multilayer]"]
  CDC7 = Ceramic Capacitor [capacitance=100nF package="100 mil [THT, multilayer]"]  # not connected
  CDC8 = Ceramic Capacitor [capacitance=100nF package="100 mil [THT, multilayer]"]  # not connected
  CDC9 = Ceramic Capacitor [capacitance=100nF package="100 mil [THT, multilayer]"]
  CDC10 = Ceramic Capacitor [capacitance=100nF package="100 mil [THT, multilayer]"]  # not connected
  CDC11 = Ceramic Capacitor [capacitance=100nF package="100 mil [THT, multilayer]"]  # not connected
  CDC12 = Ceramic Capacitor [capacitance=100nF package="100 mil [THT, multilayer]"]
  MAX395CNG-0 = IC, DIP package, 24 pins [chip_label=IC]
  MAX395CNG-1 = IC, DIP package, 24 pins [chip_label=IC]
  CDC13 = Ceramic Capacitor [capacitance=100nF package="100 mil [THT, multilayer]"]
  CDC14 = Ceramic Capacitor [capacitance=100nF package="100 mil [THT, multilayer]"]  # not connected
  CDC15 = Ceramic Capacitor [capacitance=100nF package="100 mil [THT, multilayer]"]  # not connected
  CDC16 = Ceramic Capacitor [capacitance=100nF package="100 mil [THT, multilayer]"]
  MAX395CNG-11 = IC, DIP package, 24 pins [chip_label=IC]
  MAX395CNG-10 = IC, DIP package, 24 pins [chip_label=IC]
  CDC17 = Ceramic Capacitor [capacitance=100nF package="100 mil [THT, multilayer]"]
  CDC19 = Ceramic Capacitor [capacitance=100nF package="100 mil [THT, multilayer]"]  # not connected
  CDC21 = Ceramic Capacitor [capacitance=100nF package="100 mil [THT, multilayer]"]  # not connected
  CDC23 = Ceramic Capacitor [capacitance=100nF package="100 mil [THT, multilayer]"]
  MAX395CNG-13 = IC, DIP package, 24 pins [chip_label=IC]
  MAX395CNG-12 = IC, DIP package, 24 pins [chip_label=IC]
  CDC25 = Ceramic Capacitor [capacitance=100nF package="100 mil [THT, multilayer]"]
  CDC28 = Ceramic Capacitor [capacitance=100nF package="100 mil [THT, multilayer]"]  # not connected
  CDC29 = Ceramic Capacitor [capacitance=100nF package="100 mil [THT, multilayer]"]  # not connected
  CDC32 = Ceramic Capacitor [capacitance=100nF package="100 mil [THT, multilayer]"]
  Shunt = female pin header, 1 pin [form="♀ (female)"]
  CS = female pin header, 1 pin [form="♀ (female)"]
  DO = female pin header, 1 pin [form="♀ (female)"]
  CLK = female pin header, 1 pin [form="♀ (female)"]
  Shunt_2 = female pin header, 1 pin [form="♀ (female)"]

nets:
  N1: MAX395CNG-3.pin1, MAX395CNG-2.pin1, MAX395CNG-4.pin1, MAX395CNG-5.pin1, MAX395CNG-6.pin1, MAX395CNG-8.pin1, MAX395CNG-7.pin1, MAX395CNG-9.pin1, MAX395CNG-0.pin1, MAX395CNG-1.pin1, MAX395CNG-11.pin1, MAX395CNG-10.pin1, MAX395CNG-13.pin1, MAX395CNG-12.pin1, CLK.pin1
  N2: MAX395CNG-3.pin3, MAX395CNG-4.pin22
  N3: MAX395CNG-3.pin21, CDC_3.1
  N4: MAX395CNG-3.pin22, MAX395CNG-2.pin3
  N5: MAX395CNG-3.pin24, MAX395CNG-2.pin24, MAX395CNG-4.pin24, MAX395CNG-5.pin24, MAX395CNG-6.pin24, MAX395CNG-8.pin24, MAX395CNG-7.pin24, MAX395CNG-9.pin24, MAX395CNG-0.pin24, MAX395CNG-1.pin24, MAX395CNG-11.pin24, MAX395CNG-10.pin24, MAX395CNG-13.pin24, MAX395CNG-12.pin24, CS.pin1
  N6: MAX395CNG-2.pin21, CDC.1
  N7: MAX395CNG-2.pin22, MAX395CNG-1.pin3
  N8: MAX395CNG-4.pin3, MAX395CNG-5.pin22
  N9: MAX395CNG-4.pin21, CDC4.1
  N10: MAX395CNG-5.pin3, MAX395CNG-6.pin22
  N11: MAX395CNG-5.pin21, CDC1.1
  N12: MAX395CNG-6.pin3, MAX395CNG-7.pin22
  N13: MAX395CNG-8.pin3, MAX395CNG-9.pin22
  N14: MAX395CNG-8.pin21, CDC12.1
  N15: MAX395CNG-8.pin22, MAX395CNG-7.pin3
  N16: MAX395CNG-7.pin2, CDC9.1
  N17: MAX395CNG-9.pin3, MAX395CNG-10.pin22
  N18: MAX395CNG-9.pin21, CDC6.1
  N19: MAX395CNG-0.pin3, MAX395CNG-1.pin22
  N20: MAX395CNG-0.pin21, CDC16.1
  N21: MAX395CNG-1.pin21, CDC13.1
  N22: MAX395CNG-11.pin3, MAX395CNG-12.pin22
  N23: MAX395CNG-11.pin21, CDC23.1
  N24: MAX395CNG-11.pin22, MAX395CNG-10.pin3
  N25: MAX395CNG-10.pin21, CDC17.1
  N26: MAX395CNG-13.pin3, DO.pin1
  N27: MAX395CNG-13.pin21, CDC32.1
  N28: MAX395CNG-13.pin22, MAX395CNG-12.pin3
  N29: MAX395CNG-12.pin21, CDC25.1
  N30: Shunt.pin1, Shunt_2.pin1
