# Fritzing sketch Aux_Vibrato_Tremolo_2xPBs (saved by Fritzing 0.9.2b)
circuit board: 3.56901cm x 0.891497cm
circuit board: 3.85271cm x 0.891497cm
circuit board: 3.83498cm x 0.887951cm
breadboards: 1

parts:
  J7 = male pin header, 3 pins [form="♂ (male)"]
  J8 = male pin header, 3 pins [form="♂ (male)"]
  J13 = male pin header, 3 pins [form="♂ (male)"]
  S1 = Pushbutton [package="[THT]"]
  S2 = Pushbutton [package="[THT]"]
  S6 = Pushbutton [package="[THT]"]
  S4 = Pushbutton [package="[THT]"]
  S3 = Pushbutton [package="[THT]"]
  S5 = Pushbutton [package="[THT]"]

nets:
  N1: J7.pin1, S1.Pin_1, S1.Pin_2, S2.Pin_1, S2.Pin_2
  N2: J7.pin2, S2.Pin_3, S2.Pin_4
  N3: J7.pin3, S1.Pin_3, S1.Pin_4
  N4: J8.pin1, S3.Pin_1, S3.Pin_2
  N5: J8.pin2, S4.Pin_1, S4.Pin_2
  N6: J8.pin3, S4.Pin_3, S4.Pin_4, S3.Pin_3, S3.Pin_4
  N7: J13.pin1, S6.Pin_1, S6.Pin_2, S5.Pin_1, S5.Pin_2
  N8: J13.pin2, S6.Pin_3, S6.Pin_4
  N9: J13.pin3, S5.Pin_3, S5.Pin_4
