# Fritzing sketch HMI PCB 00 (saved by Fritzing 0.9.2b)
circuit board: 9.06069cm x 8.90875cm
breadboards: 1

parts:
  LED_ARRAY-0 = double row male pin header, 40 pins [form="♂ (male)"]
  LED_ARRAY-1 = double row male pin header, 40 pins [form="♂ (male)"]
  U1 = 74HC595 [package="DIP16 [THT]"]
  U2 = 74HC595 [package="DIP16 [THT]"]
  U3 = 74HC595 [package="DIP16 [THT]"]
  U4 = 74HC595 [package="DIP16 [THT]"]
  SPI = male pin header, 3 pins [form="♂ (male)"]
  +5V_GND = male pin header, 2 pins [form="♂ (male)"]
  R1 = Resistor [tolerance=±5% resistance=1k package=THT]
  R2 = Resistor [tolerance=±5% resistance=1k package=THT]
  R3 = Resistor [tolerance=±5% resistance=1k package=THT]
  R4 = Resistor [tolerance=±5% resistance=1k package=THT]
  R5 = Resistor [tolerance=±5% resistance=1k package=THT]
  R6 = Resistor [tolerance=±5% resistance=1k package=THT]
  R7 = Resistor [tolerance=±5% resistance=1k package=THT]
  R8 = Resistor [tolerance=±5% resistance=1k package=THT]
  R9 = Resistor [tolerance=±5% resistance=1k package=THT]
  R10 = Resistor [tolerance=±5% resistance=1k package=THT]
  R11 = Resistor [tolerance=±5% resistance=1k package=THT]
  R12 = Resistor [tolerance=±5% resistance=1k package=THT]
  R13 = Resistor [tolerance=±5% resistance=1k package=THT]
  R14 = Resistor [tolerance=±5% resistance=1k package=THT]
  R15 = Resistor [tolerance=±5% resistance=1k package=THT]
  R16 = Resistor [tolerance=±5% resistance=1k package=THT]
  R17 = Resistor [tolerance=±5% resistance=1k package=THT]
  R18 = Resistor [tolerance=±5% resistance=1k package=THT]
  R19 = Resistor [tolerance=±5% resistance=1k package=THT]
  R20 = Resistor [tolerance=±5% resistance=1k package=THT]
  R21 = Resistor [tolerance=±5% resistance=1k package=THT]
  R22 = Resistor [tolerance=±5% resistance=1k package=THT]
  R23 = Resistor [tolerance=±5% resistance=1k package=THT]
  R24 = Resistor [tolerance=±5% resistance=1k package=THT]
  R25 = Resistor [tolerance=±5% resistance=1k package=THT]
  R26 = Resistor [tolerance=±5% resistance=1k package=THT]
  R27 = Resistor [tolerance=±5% resistance=1k package=THT]
  R28 = Resistor [tolerance=±5% resistance=1k package=THT]
  R29 = Resistor [tolerance=±5% resistance=1k package=THT]
  R30 = Resistor [tolerance=±5% resistance=1k package=THT]
  R31 = Resistor [tolerance=±5% resistance=1k package=THT]
  R32 = Resistor [tolerance=±5% resistance=1k package=THT]
  R33 = Resistor [tolerance=±5% resistance=1k package=THT]
  R34 = Resistor [tolerance=±5% resistance=1k package=THT]
  R35 = Resistor [tolerance=±5% resistance=1k package=THT]
  R36 = Resistor [tolerance=±5% resistance=1k package=THT]
  R37 = Resistor [tolerance=±5% resistance=1k package=THT]
  R38 = Resistor [tolerance=±5% resistance=1k package=THT]
  R39 = Resistor [tolerance=±5% resistance=1k package=THT]
  R40 = Resistor [tolerance=±5% resistance=1k package=THT]
  U6 = 74HC595 [package="DIP16 [THT]"]
  C1 = Ceramic Capacitor [capacitance=100nF package="100 mil [THT, multilayer]"]
  C2 = Ceramic Capacitor [capacitance=100nF package="100 mil [THT, multilayer]"]
  C3 = Ceramic Capacitor [capacitance=100nF package="100 mil [THT, multilayer]"]
  C4 = Ceramic Capacitor [capacitance=100nF package="100 mil [THT, multilayer]"]
  C5 = Ceramic Capacitor [capacitance=100nF package="100 mil [THT, multilayer]"]

nets:
  N1: LED_ARRAY-0.pin1, R29.Pin_1
  N2: LED_ARRAY-0.pin2, R25.Pin_1
  N3: LED_ARRAY-0.pin3, R32.Pin_1
  N4: LED_ARRAY-0.pin4, R21.Pin_1
  N5: LED_ARRAY-0.pin5, R17.Pin_1
  N6: LED_ARRAY-0.pin6, R19.Pin_1
  N7: LED_ARRAY-0.pin7, R26.Pin_1
  N8: LED_ARRAY-0.pin8, R20.Pin_1
  N9: LED_ARRAY-0.pin9, R30.Pin_1
  N10: LED_ARRAY-0.pin10, R27.Pin_1
  N11: LED_ARRAY-0.pin11, R28.Pin_1
  N12: LED_ARRAY-0.pin12, R22.Pin_1
  N13: LED_ARRAY-0.pin13, R18.Pin_1
  N14: LED_ARRAY-0.pin14, R24.Pin_1
  N15: LED_ARRAY-0.pin15, R31.Pin_1
  N16: LED_ARRAY-0.pin16, R23.Pin_1
  N17: LED_ARRAY-0.pin17, R37.Pin_1
  N18: LED_ARRAY-0.pin18, R38.Pin_1
  N19: LED_ARRAY-0.pin19, R36.Pin_1
  N20: LED_ARRAY-0.pin20, R39.Pin_1
  N21: LED_ARRAY-0.pin21, LED_ARRAY-0.pin22, LED_ARRAY-0.pin23, LED_ARRAY-0.pin24, LED_ARRAY-0.pin25, LED_ARRAY-0.pin26, LED_ARRAY-0.pin27, LED_ARRAY-0.pin28, LED_ARRAY-0.pin29, LED_ARRAY-0.pin30, LED_ARRAY-0.pin31, LED_ARRAY-0.pin32, LED_ARRAY-0.pin33, LED_ARRAY-0.pin34, LED_ARRAY-0.pin35, LED_ARRAY-0.pin36, LED_ARRAY-0.pin37, LED_ARRAY-0.pin38, LED_ARRAY-0.pin39, LED_ARRAY-0.pin40, LED_ARRAY-1.pin1, LED_ARRAY-1.pin2, LED_ARRAY-1.pin3, LED_ARRAY-1.pin4, LED_ARRAY-1.pin5, LED_ARRAY-1.pin6, LED_ARRAY-1.pin7, LED_ARRAY-1.pin8, LED_ARRAY-1.pin9, LED_ARRAY-1.pin10, LED_ARRAY-1.pin11, LED_ARRAY-1.pin12, LED_ARRAY-1.pin13, LED_ARRAY-1.pin14, LED_ARRAY-1.pin15, LED_ARRAY-1.pin16, LED_ARRAY-1.pin17, LED_ARRAY-1.pin18, LED_ARRAY-1.pin19, LED_ARRAY-1.pin20
  N22: LED_ARRAY-1.pin21, R40.Pin_0
  N23: LED_ARRAY-1.pin22, R33.Pin_0
  N24: LED_ARRAY-1.pin23, R34.Pin_0
  N25: LED_ARRAY-1.pin24, R35.Pin_0
  N26: LED_ARRAY-1.pin25, R12.Pin_0
  N27: LED_ARRAY-1.pin26, R10.Pin_0
  N28: LED_ARRAY-1.pin27, R11.Pin_0
  N29: LED_ARRAY-1.pin28, R14.Pin_0
  N30: LED_ARRAY-1.pin29, R16.Pin_0
  N31: LED_ARRAY-1.pin30, R13.Pin_0
  N32: LED_ARRAY-1.pin31, R9.Pin_0
  N33: LED_ARRAY-1.pin32, R15.Pin_0
  N34: LED_ARRAY-1.pin33, R8.Pin_0
  N35: LED_ARRAY-1.pin34, R7.Pin_0
  N36: LED_ARRAY-1.pin35, R5.Pin_0
  N37: LED_ARRAY-1.pin36, R6.Pin_0
  N38: LED_ARRAY-1.pin37, R4.Pin_0
  N39: LED_ARRAY-1.pin38, R3.Pin_0
  N40: LED_ARRAY-1.pin39, R2.Pin_0
  N41: LED_ARRAY-1.pin40, R1.Pin_0
  N42: U1.Q1, R20.Pin_0
  N43: U1.Q2, R26.Pin_0
  N44: U1.Q3, R19.Pin_0
  N45: U1.Q4, R17.Pin_0
  N46: U1.Q5, R21.Pin_0
  N47: U1.Q6, R32.Pin_0
  N48: U1.Q7, R25.Pin_0
  N49: U1.SH_CP, U6.SH_CP
  N50: U1.DS, U6.Q7'
  N51: U1.Q0, R29.Pin_0
  N52: U1.VCC, C4.1
  N53: U2.Q1, R15.Pin_1
  N54: U2.Q2, R9.Pin_1
  N55: U2.Q3, R13.Pin_1
  N56: U2.Q4, R16.Pin_1
  N57: U2.Q5, R14.Pin_1
  N58: U2.Q6, R11.Pin_1
  N59: U2.Q7, R10.Pin_1
  N60: U2.Q7', U4.DS
  N61: U2.SH_CP, U3.SH_CP, SPI.pin3
  N62: U2.DS, U3.Q7'
  N63: U2.Q0, R12.Pin_1
  N64: U2.VCC, C2.0
  N65: U3.Q1, R1.Pin_1
  N66: U3.Q2, R2.Pin_1
  N67: U3.Q3, R3.Pin_1
  N68: U3.Q4, R4.Pin_1
  N69: U3.Q5, R6.Pin_1
  N70: U3.Q6, R5.Pin_1
  N71: U3.Q7, R7.Pin_1
  N72: U3.ST_CP, SPI.pin2
  N73: U3.DS, SPI.pin1
  N74: U3.Q0, R8.Pin_1
  N75: U3.VCC, C1.0
  N76: U4.Q1, R35.Pin_1
  N77: U4.Q2, R34.Pin_1
  N78: U4.Q3, R40.Pin_1
  N79: U4.Q4, R33.Pin_1
  N80: U4.Q5, R36.Pin_0
  N81: U4.Q6, R39.Pin_0
  N82: U4.Q7, R38.Pin_0
  N83: U4.Q7', U6.DS
  N84: U4.Q0, R37.Pin_0
  N85: U4.VCC, C5.1
  N86: +5V_GND.pin1, C1.1, C2.1, C3.0, C4.0, C5.0
  N87: R18.Pin_0, U6.Q3
  N88: R22.Pin_0, U6.Q4
  N89: R23.Pin_0, U6.Q0
  N90: R24.Pin_0, U6.Q2
  N91: R27.Pin_0, U6.Q6
  N92: R28.Pin_0, U6.Q5
  N93: R30.Pin_0, U6.Q7
  N94: R31.Pin_0, U6.Q1
  N95: U6.VCC, C3.1

notes:
  Pins:
  14: Data in
  13: Gnd (OE)
  12: Latch (CS)
  11: Clock
  10: +5v (MR)
  9 : Data out
