# Fritzing sketch Master-Vol-Tone-Scematic-Audio-e (saved by Fritzing 0.9.2b)
breadboards: 1

parts:
  MAX395CNG-1 = IC, DIP package, 24 pins [chip_label=IC]
  MAX395CNG-0 = IC, DIP package, 24 pins [chip_label=IC]
  Rv = Resistor [tolerance=±1% resistance=100k package=THT]
  Rv_2 = Resistor [tolerance=±1% resistance=100k package=THT]
  Rv_3 = Resistor [tolerance=±1% resistance=100k package=THT]
  Rv_4 = Resistor [tolerance=±1% resistance=100k package=THT]
  Rv_5 = Resistor [tolerance=±1% resistance=100k package=THT]
  Tone = Ceramic Capacitor [capacitance=10nF package="100 mil [THT, multilayer]"]
  RT1 = Resistor [tolerance=±1% resistance=16k package=THT]
  RT1_2 = Resistor [tolerance=±1% resistance=16k package=THT]
  RT4 = Resistor [tolerance=±1% resistance=64k package=THT]
  RT2 = Resistor [tolerance=±1% resistance=32k package=THT]
  CDC = Ceramic Capacitor [capacitance=100nF package="100 mil [THT, multilayer]"]  # not connected
  CDC_2 = Ceramic Capacitor [capacitance=100nF package="100 mil [THT, multilayer]"]  # not connected
  Boost = Ceramic Capacitor [capacitance=0.18nF package="100 mil [THT, multilayer]"]
  CDC_3 = Ceramic Capacitor [capacitance=100nF package="100 mil [THT, multilayer]"]  # not connected
  CDC_4 = Ceramic Capacitor [capacitance=100nF package="100 mil [THT, multilayer]"]  # not connected
  IN-_IN+ = female pin header, 2 pins [form="♀ (female)"]
  OUT+_OUT- = female pin header, 2 pins [form="♀ (female)"]
  RT0 = Resistor [tolerance=±1% resistance=22k package=THT]
  Tone_2 = Ceramic Capacitor [capacitance=1nF package="100 mil [THT, multilayer]"]
  Tone_3 = Ceramic Capacitor [capacitance=2nF package="100 mil [THT, multilayer]"]
  Tone_4 = Ceramic Capacitor [capacitance=4nF package="100 mil [THT, multilayer]"]
  Tone_5 = Ceramic Capacitor [capacitance=6.3nF package="100 mil [THT, multilayer]"]

nets:
  N1: MAX395CNG-1.pin5, MAX395CNG-1.pin8, MAX395CNG-1.pin9, MAX395CNG-1.pin11, MAX395CNG-1.pin14, MAX395CNG-1.pin15, MAX395CNG-1.pin18, MAX395CNG-1.pin19, MAX395CNG-0.pin6, MAX395CNG-0.pin7, MAX395CNG-0.pin20, Rv.Pin_1, Boost.1, IN-_IN+.pin2
  N2: MAX395CNG-1.pin6, Tone_2.1
  N3: MAX395CNG-1.pin7, Tone_3.1
  N4: MAX395CNG-1.pin10, Tone_4.1
  N5: MAX395CNG-1.pin12, Tone_5.1
  N6: MAX395CNG-1.pin13, Tone.0
  N7: MAX395CNG-1.pin16, RT1.Pin_0, RT0.Pin_1
  N8: MAX395CNG-1.pin17, RT1.Pin_1, RT1_2.Pin_0
  N9: MAX395CNG-1.pin20, RT1_2.Pin_1, RT2.Pin_0
  N10: MAX395CNG-0.pin5, RT4.Pin_0, RT2.Pin_1
  N11: MAX395CNG-0.pin8, RT4.Pin_1
  N12: MAX395CNG-0.pin9, Rv_5.Pin_0, Tone.1, IN-_IN+.pin1, OUT+_OUT-.pin2, RT0.Pin_0, Tone_2.0, Tone_3.0, Tone_4.0, Tone_5.0
  N13: MAX395CNG-0.pin10, MAX395CNG-0.pin11, MAX395CNG-0.pin13, MAX395CNG-0.pin15, MAX395CNG-0.pin18, MAX395CNG-0.pin19, Boost.0, OUT+_OUT-.pin1
  N14: MAX395CNG-0.pin12, Rv_4.Pin_0, Rv_5.Pin_1
  N15: MAX395CNG-0.pin14, Rv_3.Pin_0, Rv_4.Pin_1
  N16: MAX395CNG-0.pin16, Rv_2.Pin_0, Rv_3.Pin_1
  N17: MAX395CNG-0.pin17, Rv.Pin_0, Rv_2.Pin_1
