# Fritzing sketch Overview MAX395 (saved by Fritzing 0.9.2b)
breadboards: 1

parts:
  I/O_Board = IC, DIP package, 26 pins [chip_label="I/O Board"]
  Batt = DC Power [voltage=7.2 frequency=60]  # not connected
  Out-_Out+_D-_D+_C-_C+_B-_B+_A-_A+_GND = female pin header, 11 pins [form="♀ (female)"]
  IC2 = IC, DIP package, 16 pins [chip_label="PSU & Pyboard"]
  MVT = IC, DIP package, 22 pins [chip_label=I/MVT]
  IVT-3 = IC, DIP package, 20 pins [chip_label=I/MVT]
  IVT-2 = IC, DIP package, 20 pins [chip_label=I/MVT]
  IVT-1 = IC, DIP package, 20 pins [chip_label=I/MVT]
  IVT-0 = IC, DIP package, 20 pins [chip_label=I/MVT]
  IC1 = IC, DIP package, 30 pins [chip_label="Switch Array"]

nets:
  N1: I/O_Board.pin1, Out-_Out+_D-_D+_C-_C+_B-_B+_A-_A+_GND.pin10
  N2: I/O_Board.pin2, Out-_Out+_D-_D+_C-_C+_B-_B+_A-_A+_GND.pin9
  N3: I/O_Board.pin3, Out-_Out+_D-_D+_C-_C+_B-_B+_A-_A+_GND.pin8
  N4: I/O_Board.pin4, Out-_Out+_D-_D+_C-_C+_B-_B+_A-_A+_GND.pin7
  N5: I/O_Board.pin5, Out-_Out+_D-_D+_C-_C+_B-_B+_A-_A+_GND.pin6
  N6: I/O_Board.pin6, Out-_Out+_D-_D+_C-_C+_B-_B+_A-_A+_GND.pin5
  N7: I/O_Board.pin7, Out-_Out+_D-_D+_C-_C+_B-_B+_A-_A+_GND.pin4
  N8: I/O_Board.pin8, Out-_Out+_D-_D+_C-_C+_B-_B+_A-_A+_GND.pin3
  N9: I/O_Board.pin9, Out-_Out+_D-_D+_C-_C+_B-_B+_A-_A+_GND.pin2
  N10: I/O_Board.pin10, Out-_Out+_D-_D+_C-_C+_B-_B+_A-_A+_GND.pin1
  N11: I/O_Board.pin11, IVT-0.pin1
  N12: I/O_Board.pin12, IVT-0.pin2
  N13: I/O_Board.pin13, IVT-0.pin3
  N14: I/O_Board.pin14, IVT-1.pin1
  N15: I/O_Board.pin15, IVT-1.pin2
  N16: I/O_Board.pin16, IVT-1.pin3
  N17: I/O_Board.pin17, IVT-2.pin1
  N18: I/O_Board.pin18, IVT-2.pin2
  N19: I/O_Board.pin19, IVT-2.pin3
  N20: I/O_Board.pin20, IVT-3.pin1
  N21: I/O_Board.pin21, IVT-3.pin2
  N22: I/O_Board.pin22, IVT-3.pin3
  N23: I/O_Board.pin23, MVT.pin4
  N24: I/O_Board.pin24, MVT.pin5
  N25: I/O_Board.pin25, MVT.pin6
  N26: I/O_Board.pin26, Out-_Out+_D-_D+_C-_C+_B-_B+_A-_A+_GND.pin11
  N27: IC2.pin1, MVT.pin7
  N28: IC2.pin2, MVT.pin8
  N29: IC2.pin3, MVT.pin9
  N30: IC2.pin9, IC1.pin16
  N31: IC2.pin10, IC1.pin17
  N32: IC2.pin11, IC1.pin18
  N33: IC2.pin12, MVT.pin10
  N34: IC2.pin13, MVT.pin11
  N35: IC2.pin14, MVT.pin12
  N36: IC2.pin15, MVT.pin13
  N37: IC2.pin16, MVT.pin14
  N38: MVT.pin1, IC1.pin13
  N39: MVT.pin2, IC1.pin14
  N40: MVT.pin3, IC1.pin15
  N41: MVT.pin15, IVT-3.pin7
  N42: MVT.pin16, IVT-3.pin8
  N43: MVT.pin17, IVT-3.pin9
  N44: MVT.pin18, IVT-3.pin10
  N45: MVT.pin19, IVT-3.pin11
  N46: MVT.pin20, IVT-3.pin12
  N47: MVT.pin21, IVT-3.pin13
  N48: IVT-3.pin4, IC1.pin10
  N49: IVT-3.pin5, IC1.pin11
  N50: IVT-3.pin6, IC1.pin12
  N51: IVT-3.pin14, IVT-2.pin7
  N52: IVT-3.pin15, IVT-2.pin8
  N53: IVT-3.pin16, IVT-2.pin9
  N54: IVT-3.pin17, IVT-2.pin10
  N55: IVT-3.pin18, IVT-2.pin11
  N56: IVT-3.pin19, IVT-2.pin12
  N57: IVT-3.pin20, IVT-2.pin13
  N58: IVT-2.pin4, IC1.pin7
  N59: IVT-2.pin5, IC1.pin8
  N60: IVT-2.pin6, IC1.pin9
  N61: IVT-2.pin14, IVT-1.pin7
  N62: IVT-2.pin15, IVT-1.pin8
  N63: IVT-2.pin16, IVT-1.pin9
  N64: IVT-2.pin17, IVT-1.pin10
  N65: IVT-2.pin18, IVT-1.pin11
  N66: IVT-2.pin19, IVT-1.pin12
  N67: IVT-2.pin20, IVT-1.pin13
  N68: IVT-1.pin4, IC1.pin4
  N69: IVT-1.pin5, IC1.pin5
  N70: IVT-1.pin6, IC1.pin6
  N71: IVT-1.pin14, IVT-0.pin7
  N72: IVT-1.pin15, IVT-0.pin8
  N73: IVT-1.pin16, IVT-0.pin9
  N74: IVT-1.pin17, IVT-0.pin10
  N75: IVT-1.pin18, IVT-0.pin11
  N76: IVT-1.pin19, IVT-0.pin12
  N77: IVT-1.pin20, IVT-0.pin13
  N78: IVT-0.pin4, IC1.pin1
  N79: IVT-0.pin5, IC1.pin2
  N80: IVT-0.pin6, IC1.pin3
  N81: IVT-0.pin14, IC1.pin23
  N82: IVT-0.pin15, IC1.pin24
  N83: IVT-0.pin16, IC1.pin25
  N84: IVT-0.pin17, IC1.pin19
  N85: IVT-0.pin18, IC1.pin20
  N86: IVT-0.pin19, IC1.pin21
  N87: IVT-0.pin20, IC1.pin22

notes:
  Guitar
