# Fritzing sketch ReverseCurrentProtection (saved by Fritzing 0.9.2b)
breadboards: 1

parts:
  D = Rectifier Diode [part_number=1N4001 package="300 mil [THT]"]
  Fuse = Fuse with Handler [part_number=Htc-15m]
  Batt = DC Power [voltage=5]
  Circuit = female pin header, 2 pins [form="♀ (female)"]

nets:
  N1: D.cathode, Fuse.Connector2, Circuit.pin1
  GND: D.anode, Batt.V-, Circuit.pin2
  N2: Fuse.Connector1, Batt.V+

notes:
  GND  V+
