# Fritzing sketch SwitchArraySchematic (saved by Fritzing 0.9.1b)
breadboards: 1

parts:
  MAX395-0 = MAX395 Octal Analog Switch [package="DIP (Dual Inline) [THT]"]
  MAX395-1 = MAX395 Octal Analog Switch [package="DIP (Dual Inline) [THT]"]
  MAX395-3 = MAX395 Octal Analog Switch [package="DIP (Dual Inline) [THT]"]
  MAX395-2 = MAX395 Octal Analog Switch [package="DIP (Dual Inline) [THT]"]
  A+ = female pin header, 1 pin [form="♀ (female)"]
  A- = female pin header, 1 pin [form="♀ (female)"]
  B+ = female pin header, 1 pin [form="♀ (female)"]
  B- = female pin header, 1 pin [form="♀ (female)"]
  D+ = female pin header, 1 pin [form="♀ (female)"]
  C- = female pin header, 1 pin [form="♀ (female)"]
  C+ = female pin header, 1 pin [form="♀ (female)"]
  D- = female pin header, 1 pin [form="♀ (female)"]
  Out- = male pin header, 1 pin [form="♂ (male)"]
  Out+ = male pin header, 1 pin [form="♂ (male)"]
  C = Ceramic Capacitor [capacitance=100nF package="100 mil [THT, multilayer]"]
  C_2 = Ceramic Capacitor [capacitance=100nF package="100 mil [THT, multilayer]"]
  C_3 = Ceramic Capacitor [capacitance=100nF package="100 mil [THT, multilayer]"]
  C_4 = Ceramic Capacitor [capacitance=100nF package="100 mil [THT, multilayer]"]

nets:
  N1: MAX395-0.V+, C_3.1
  N2: MAX395-0.NO0, MAX395-0.NO7, MAX395-1.NO7, MAX395-3.NO6, MAX395-3.COM7, MAX395-2.NO2, MAX395-2.NO5, C-.pin1
  N3: MAX395-0.COM0, MAX395-0.NO1, MAX395-0.COM2, MAX395-0.NO3, MAX395-1.COM1, MAX395-1.COM2, MAX395-1.NO3, A+.pin1
  N4: MAX395-0.COM1, MAX395-0.COM6, MAX395-1.NO0, MAX395-3.COM0, MAX395-3.NO1, MAX395-2.COM3, MAX395-2.COM4, C+.pin1
  N5: MAX395-0.NO2, MAX395-0.NO5, MAX395-3.COM4, MAX395-2.NO4, MAX395-2.COM5, MAX395-2.NO6, MAX395-2.COM7, B-.pin1
  N6: MAX395-0.COM3, MAX395-0.COM4, MAX395-3.COM3, MAX395-2.COM0, MAX395-2.NO1, MAX395-2.COM2, MAX395-2.NO3, B+.pin1
  N7: MAX395-0.NO4, MAX395-0.COM5, MAX395-0.NO6, MAX395-0.COM7, MAX395-1.NO4, MAX395-1.COM5, MAX395-1.COM6, A-.pin1
  N8: MAX395-0.V-, C_3.0
  N9: MAX395-1.V+, C.1
  N10: MAX395-1.COM0, MAX395-1.NO1, MAX395-3.COM2, MAX395-3.NO3, Out+.pin1
  N11: MAX395-1.NO2, MAX395-1.NO5, MAX395-3.NO0, MAX395-3.NO5, MAX395-3.COM6, MAX395-2.NO0, MAX395-2.NO7, D-.pin1
  N12: MAX395-1.COM3, MAX395-1.COM4, MAX395-3.COM1, MAX395-3.NO2, MAX395-3.NO7, MAX395-2.COM1, MAX395-2.COM6, D+.pin1
  N13: MAX395-1.NO6, MAX395-1.COM7, MAX395-3.NO4, MAX395-3.COM5, Out-.pin1
  N14: MAX395-1.V-, C.0
  N15: MAX395-3.V+, C_4.1
  N16: MAX395-3.V-, C_4.0
  N17: MAX395-2.V+, C_2.1
  N18: MAX395-2.V-, C_2.0

custom parts:
  MAX395 Octal Analog Switch: An octal analog switch with SPI control. 24 pins on a 300mil dual inline package (DIP) footprint.
