# Fritzing sketch Temp IVT Max395 layout (saved by Fritzing 0.9.2b)
circuit board: 6.10262cm x 4.9722cm
breadboards: 1

parts:
  Power = female pin header, 3 pins [form="♀ (female)"]  # not connected
  R1 = Resistor [tolerance=±5% resistance=220 package=THT]
  R2 = Resistor [tolerance=±5% resistance=220 package=THT]
  R3 = Resistor [tolerance=±5% resistance=220 package=THT]
  R4 = Resistor [tolerance=±5% resistance=220 package=THT]
  R5 = Resistor [tolerance=±5% resistance=220 package=THT]
  R6 = Resistor [tolerance=±5% resistance=220 package=THT]
  R7 = Resistor [tolerance=±5% resistance=220 package=THT]
  R8 = Resistor [tolerance=±5% resistance=220 package=THT]
  R9 = Resistor [tolerance=±5% resistance=220 package=THT]
  C1 = Ceramic Capacitor [capacitance=100nF package="100 mil [THT, multilayer]"]  # not connected
  C2 = Ceramic Capacitor [capacitance=100nF package="100 mil [THT, multilayer]"]  # not connected
  C3 = Ceramic Capacitor [capacitance=100nF package="100 mil [THT, multilayer]"]  # not connected
  C4 = Ceramic Capacitor [capacitance=100nF package="100 mil [THT, multilayer]"]  # not connected
  MAX395-1 = MAX395 Octal Analog Switch [package="DIP (Dual Inline) [THT]"]  # not connected
  MAX395-0 = MAX395 Octal Analog Switch [package="DIP (Dual Inline) [THT]"]  # not connected
  MAX395 = MAX395 Octal Analog Switch [package="DIP (Dual Inline) [THT]"]  # not connected
  SPI_out = female pin header, 4 pins [form="♀ (female)"]  # not connected
  SPI_in = female pin header, 3 pins [form="♀ (female)"]  # not connected
  Coil_I/O = female pin header, 3 pins [form="♀ (female)"]  # not connected

nets:
  N1: R1.Pin_0, R4.Pin_1
  N2: R2.Pin_1, R5.Pin_0
  N3: R3.Pin_0, R5.Pin_1
  N4: R3.Pin_1, R4.Pin_0
  N5: R6.Pin_0, R9.Pin_1
  N6: R7.Pin_0, R8.Pin_1
  N7: R7.Pin_1, R9.Pin_0

custom parts:
  MAX395 Octal Analog Switch: An octal analog switch with SPI control. 24 pins on a 300mil dual inline package (DIP) footprint.
  MAX395 Octal Analog Switch: Octal Analog switch with SPI control. 24 pins on a 300mil dual inline package (DIP) footprint.
