# Fritzing sketch PyboardPins (saved by Fritzing 0.9.2b)
breadboards: 1

parts:
  Host_Clock_IN = female pin header, 1 pin [form="♀ (female)"]
  Host_Clock_Out = female pin header, 1 pin [form="♀ (female)"]
  Host_Data_IN = female pin header, 1 pin [form="♀ (female)"]
  Host_Data_Out = female pin header, 1 pin [form="♀ (female)"]
  R1 = Resistor [tolerance=±5% resistance=1k package=THT]
  R2 = Resistor [tolerance=±5% resistance=1k package=THT]
  Device_Data = female pin header, 1 pin [form="♀ (female)"]
  Device_Clock = female pin header, 1 pin [form="♀ (female)"]

nets:
  N1: Host_Clock_IN.pin1, Host_Clock_Out.pin1, R1.Pin_0, Device_Clock.pin1
  N2: Host_Data_IN.pin1, Host_Data_Out.pin1, R2.Pin_1, Device_Data.pin1
  3.3V: R1.Pin_1, R2.Pin_0
