# Fritzing sketch Selector (saved by Fritzing 0.8.7b)
circuit board: 10cm x 5cm
breadboards: 1

parts:
  Output = female pin header, 2 pins [form="♀ (female)"]
  4660 = IC, DIP package, 14 pins [chip_label=CD4660]
  Input_B = female alternating pin header, 2 pins [form="♀ (female)"]
  Input_A = female alternating pin header, 2 pins [form="♀ (female)"]
  InputB1 = female alternating pin header, 2 pins [form="♀ (female)"]
  MAX4679 = IC, DIP package, 16 pins [chip_label=IC]
  Output1 = female pin header, 2 pins [form="♀ (female)"]
  InputA1 = female alternating pin header, 2 pins [form="♀ (female)"]

nets:
  N1: Output.pin1, MAX4679.pin3, MAX4679.pin10
  N2: Output.pin2, MAX4679.pin7, MAX4679.pin14
  N3: 4660.pin1, InputB1.pin2
  N4: 4660.pin2, 4660.pin4, Output1.pin2
  N5: 4660.pin3, InputA1.pin2
  N6: 4660.pin8, 4660.pin10, Output1.pin1
  N7: 4660.pin9, InputA1.pin1
  N8: 4660.pin11, InputB1.pin1
  N9: Input_B.pin1, MAX4679.pin2
  N10: Input_B.pin2, MAX4679.pin6
  N11: Input_A.pin1, MAX4679.pin11
  N12: Input_A.pin2, MAX4679.pin15

notes:
  Selector
  1 & 4 -> input B
  2 & 3 -> input A
  all -> inputs A & B
  A & D -> input B
  B & C -> input A
  none -> no output
