# Fritzing sketch Vol-Tone 4066 (saved by Fritzing 0.8.7b)
circuit board: 10.0569cm x 9.84856cm
breadboards: 1

parts:
  Input-1_Output-1_GND = female pin header, 3 pins [form="♀ (female)"]
  R1 = Resistor [tolerance=±5% resistance=47k package=THT]
  R2 = Resistor [tolerance=±5% resistance=47k package=THT]
  R3 = Resistor [tolerance=±5% resistance=47k package=THT]
  R4 = Resistor [tolerance=±5% resistance=47k package=THT]
  R5 = Resistor [tolerance=±5% resistance=47k package=THT]
  C1 = Ceramic Capacitor [capacitance=10nF package="100 mil [THT, multilayer]"]
  ?Tone_Resistor-1? = Resistor [tolerance=±5% resistance=100k package=THT]
  C3 = Ceramic Capacitor [capacitance=33nF package="100 mil [THT, multilayer]"]
  4066-0 = IC, DIP package, 14 pins [chip_label=4066]
  4066-1 = IC, DIP package, 14 pins [chip_label=4066]
  4066-2 = IC, DIP package, 14 pins [chip_label=4066]
  R6 = Resistor [tolerance=±5% resistance=47k package=THT]
  R7 = Resistor [tolerance=±5% resistance=47k package=THT]
  R8 = Resistor [tolerance=±5% resistance=47k package=THT]
  R9 = Resistor [tolerance=±5% resistance=47k package=THT]
  R10 = Resistor [tolerance=±5% resistance=47k package=THT]
  C8 = Ceramic Capacitor [capacitance=47nF package="100 mil [THT, multilayer]"]
  C7 = Ceramic Capacitor [capacitance=33nF package="100 mil [THT, multilayer]"]
  C6 = Ceramic Capacitor [capacitance=22nF package="100 mil [THT, multilayer]"]
  C5 = Ceramic Capacitor [capacitance=10nF package="100 mil [THT, multilayer]"]
  ?Tone_Resistor-2? = Resistor [tolerance=±5% resistance=100k package=THT]
  4066-4 = IC, DIP package, 14 pins [chip_label=4066]
  4066-3 = IC, DIP package, 14 pins [chip_label=4066]
  Input-2_Output-2 = female pin header, 2 pins [form="♀ (female)"]
  C4 = Ceramic Capacitor [capacitance=47nF package="100 mil [THT, multilayer]"]
  C2 = Ceramic Capacitor [capacitance=22nF package="100 mil [THT, multilayer]"]

nets:
  N1: Input-1_Output-1_GND.pin1, R1.Pin_0, 4066-0.pin11
  N2: Input-1_Output-1_GND.pin2, 4066-0.pin2, 4066-0.pin3, 4066-0.pin9, 4066-0.pin10, 4066-1.pin2, 4066-1.pin3, 4066-1.pin9, 4066-1.pin10, 4066-2.pin9, 4066-2.pin10
  N3: Input-1_Output-1_GND.pin3, R5.Pin_1, ?Tone_Resistor-1?.Pin_0, 4066-2.pin4, 4066-2.pin8, R6.Pin_1, ?Tone_Resistor-2?.Pin_1
  N4: R1.Pin_1, R2.Pin_0, 4066-0.pin8
  N5: R2.Pin_1, R3.Pin_0, 4066-1.pin11
  N6: R3.Pin_1, R4.Pin_0, 4066-1.pin8
  N7: R4.Pin_1, R5.Pin_0, 4066-2.pin11
  N8: C1.0, 4066-0.pin1
  N9: C1.1, ?Tone_Resistor-1?.Pin_1, C3.1, C4.1, C2.1
  N10: C3.0, 4066-1.pin1
  N11: 4066-0.pin4, C2.0
  N12: 4066-1.pin4, C4.0
  N13: 4066-2.pin1, R6.Pin_0, R7.Pin_1
  N14: 4066-2.pin2, 4066-2.pin3, 4066-4.pin2, 4066-4.pin3, 4066-4.pin9, 4066-4.pin10, 4066-3.pin2, 4066-3.pin3, 4066-3.pin9, 4066-3.pin10, Input-2_Output-2.pin2
  N15: R7.Pin_0, R8.Pin_1, 4066-4.pin8
  N16: R8.Pin_0, R9.Pin_1, 4066-4.pin11
  N17: R9.Pin_0, R10.Pin_1, 4066-3.pin8
  N18: R10.Pin_0, 4066-3.pin11, Input-2_Output-2.pin1
  N19: C8.0, 4066-4.pin4
  N20: C8.1, C7.1, C6.1, C5.1, ?Tone_Resistor-2?.Pin_0
  N21: C7.0, 4066-4.pin1
  N22: C6.0, 4066-3.pin4
  N23: C5.0, 4066-3.pin1

notes:
  Volume-1
  Tone-1
  Vol/Tone pair - 4066
  Tone-2
  Volume-2
