# Fritzing sketch Vol-Tone (saved by Fritzing 0.8.7b)
circuit board: 10.1315cm x 5.73702cm
breadboards: 1

parts:
  MAX4679-0 = IC, DIP package, 16 pins [chip_label=IC]
  Input_Output_GND = female pin header, 3 pins [form="♀ (female)"]
  MAX4679-1 = IC, DIP package, 16 pins [chip_label=IC]
  MAX4679-2 = IC, DIP package, 16 pins [chip_label=IC]
  R1 = Resistor [tolerance=±5% resistance=47k package=THT]
  R2 = Resistor [tolerance=±5% resistance=47k package=THT]
  R3 = Resistor [tolerance=±5% resistance=47k package=THT]
  R4 = Resistor [tolerance=±5% resistance=47k package=THT]
  R5 = Resistor [tolerance=±5% resistance=47k package=THT]
  C1 = Ceramic Capacitor [capacitance=10nF package="100 mil [THT, multilayer]"]
  ?Tone_Resistor? = Resistor [tolerance=±5% resistance=100k package=THT]
  C2 = Ceramic Capacitor [capacitance=22nF package="100 mil [THT, multilayer]"]
  C3 = Ceramic Capacitor [capacitance=33nF package="100 mil [THT, multilayer]"]
  C4 = Ceramic Capacitor [capacitance=47nF package="100 mil [THT, multilayer]"]

nets:
  N1: MAX4679-0.pin2, MAX4679-0.pin7, MAX4679-0.pin11, MAX4679-0.pin15, Input_Output_GND.pin2, MAX4679-1.pin3, MAX4679-1.pin7, MAX4679-1.pin11, MAX4679-1.pin15, MAX4679-2.pin10, MAX4679-2.pin15
  N2: MAX4679-0.pin3, C1.0
  N3: MAX4679-0.pin6, C2.0
  N4: MAX4679-0.pin10, R2.Pin_0
  N5: MAX4679-0.pin12, Input_Output_GND.pin3, MAX4679-1.pin12, MAX4679-2.pin11, MAX4679-2.pin12, R5.Pin_1, ?Tone_Resistor?.Pin_0
  N6: MAX4679-0.pin14, Input_Output_GND.pin1, R1.Pin_0
  N7: MAX4679-1.pin2, C3.0
  N8: MAX4679-1.pin6, C4.0
  N9: MAX4679-1.pin10, R4.Pin_0
  N10: MAX4679-1.pin14, R3.Pin_0
  N11: MAX4679-2.pin14, R5.Pin_0
  N12: C1.1, C2.1, C3.1, C4.1

notes:
  Volume
  Tone
