# Fritzing sketch ArduStomp (saved by Fritzing 0.7.12b)
breadboards: 3

parts:
  S1 = Pushbutton [package=THT]
  R1 = Resistor [tolerance=±5% resistance=10k package=THT]
  S2 = Pushbutton [package=THT]
  R2 = Resistor [tolerance=±5% resistance=10k package=THT]
  S3 = Pushbutton [package=THT]
  R3 = Resistor [tolerance=±5% resistance=10k package=THT]
  S4 = Pushbutton [package=THT]
  S5 = Pushbutton [package=THT]
  R5 = Resistor [tolerance=±5% resistance=10k package=THT]
  S6 = Pushbutton [package=THT]
  R6 = Resistor [tolerance=±5% resistance=10k package=THT]
  S7 = Pushbutton [package=THT]
  R7 = Resistor [tolerance=±5% resistance=10k package=THT]
  S8 = Pushbutton [package=THT]
  R8 = Resistor [tolerance=±5% resistance=10k package=THT]
  S9 = Pushbutton [package=THT]
  R9 = Resistor [tolerance=±5% resistance=10k package=THT]
  ARDUINO1 = Arduino Micro
  U1 = 74HC595 [package="DIP16 [THT]"]
  U2 = 74HC595 [package="DIP16 [THT]"]
  U3 = 74HC595 [package="DIP16 [THT]"]
  C1 = Electrolytic Capacitor [capacitance=1µF package="200 mil [THT, electrolytic]"]
  LED1 = yellow LED - 5mm [package="5 mm [THT]"]
  LED7 = yellow LED - 5mm [package="5 mm [THT]"]
  LED11 = yellow LED - 5mm [package="5 mm [THT]"]
  LED12 = yellow LED - 5mm [package="5 mm [THT]"]
  LED13 = yellow LED - 5mm [package="5 mm [THT]"]
  LED14 = yellow LED - 5mm [package="5 mm [THT]"]
  LED21 = yellow LED - 5mm [package="5 mm [THT]"]
  LED22 = white LED - 5mm [package="5 mm [THT]"]
  LED16 = Red LED - 5mm [package="5 mm [THT]"]
  LED19 = Blue LED - 5mm [package="5 mm [THT]"]
  LED20 = green LED - 5mm [package="5 mm [THT]"]
  LED17 = Red LED - 5mm [package="5 mm [THT]"]
  LED18 = Red LED - 5mm [package="5 mm [THT]"]
  LED4 = Blue LED - 5mm [package="5 mm [THT]"]
  LED2 = green LED - 5mm [package="5 mm [THT]"]
  LED15 = yellow LED - 5mm [package="5 mm [THT]"]
  LED6 = Red LED - 5mm [package="5 mm [THT]"]
  LED23 = Red LED - 5mm [package="5 mm [THT]"]
  LED24 = Red LED - 5mm [package="5 mm [THT]"]
  LED25 = Red LED - 5mm [package="5 mm [THT]"]
  LED26 = Red LED - 5mm [package="5 mm [THT]"]
  R10 = Resistor [tolerance=±5% resistance=1k package=THT]
  R11 = Resistor [tolerance=±5% resistance=1k package=THT]
  R12 = Resistor [tolerance=±5% resistance=1k package=THT]
  R13 = Resistor [tolerance=±5% resistance=1k package=THT]
  R14 = Resistor [tolerance=±5% resistance=1k package=THT]
  R15 = Resistor [tolerance=±5% resistance=1k package=THT]
  R16 = Resistor [tolerance=±5% resistance=1k package=THT]
  R17 = Resistor [tolerance=±5% resistance=1k package=THT]
  R18 = Resistor [tolerance=±5% resistance=1k package=THT]
  R19 = Resistor [tolerance=±5% resistance=1k package=THT]
  R20 = Resistor [tolerance=±5% resistance=1k package=THT]
  R21 = Resistor [tolerance=±5% resistance=1k package=THT]
  R22 = Resistor [tolerance=±5% resistance=1k package=THT]  # not connected
  R23 = Resistor [tolerance=±5% resistance=1k package=THT]  # not connected
  R24 = Resistor [tolerance=±5% resistance=1k package=THT]  # not connected
  R25 = Resistor [tolerance=±5% resistance=1k package=THT]  # not connected
  R26 = Resistor [tolerance=±5% resistance=1k package=THT]
  R27 = Resistor [tolerance=±5% resistance=1k package=THT]
  R28 = Resistor [tolerance=±5% resistance=1k package=THT]
  R29 = Resistor [tolerance=±5% resistance=1k package=THT]
  R30 = Resistor [tolerance=±5% resistance=10k package=THT]
  R31 = Resistor [tolerance=±5% resistance=1k package=THT]
  R32 = Resistor [tolerance=±5% resistance=1k package=THT]
  R33 = Resistor [tolerance=±5% resistance=1k package=THT]
  R34 = Resistor [tolerance=±5% resistance=1k package=THT]
  R35 = Resistor [tolerance=±5% resistance=1k package=THT]

nets:
  N1: S1.Pin_1, S1.Pin_2, R1.Pin_1, ARDUINO1.D2
  VCC: S1.Pin_3, S1.Pin_4, S2.Pin_3, S2.Pin_4, S3.Pin_3, S3.Pin_4, S4.Pin_3, S4.Pin_4, S5.Pin_3, S5.Pin_4, S6.Pin_3, S6.Pin_4, S7.Pin_3, S7.Pin_4, S8.Pin_3, S8.Pin_4, S9.Pin_3, S9.Pin_4, ARDUINO1.5V, U1.MR, U1.VCC, U2.MR, U2.VCC, U3.MR, U3.VCC
  GND: R1.Pin_0, R2.Pin_0, R3.Pin_0, R5.Pin_0, R7.Pin_0, R8.Pin_0, R9.Pin_0, ARDUINO1.GND#31, U1.GND, U1.OE, U2.GND, U2.OE, U3.GND, U3.OE, C1.+, LED1.cathode, LED7.cathode, LED11.cathode, LED12.cathode, LED13.cathode, LED14.cathode, LED21.cathode, LED22.cathode, LED16.cathode, LED19.cathode, LED20.cathode, LED17.cathode, LED18.cathode, LED4.cathode, LED2.cathode, LED15.cathode, LED6.cathode, LED23.cathode, LED24.cathode, LED25.cathode, LED26.cathode, R30.Pin_0
  N2: S2.Pin_1, S2.Pin_2, R2.Pin_1, ARDUINO1.D3
  N3: S3.Pin_1, S3.Pin_2, R3.Pin_1, ARDUINO1.D4
  N4: S4.Pin_1, S4.Pin_2, ARDUINO1.D5, R30.Pin_1
  N5: S5.Pin_1, S5.Pin_2, R5.Pin_1, ARDUINO1.D6
  N6: S6.Pin_1, S6.Pin_2, R6.Pin_1, ARDUINO1.D7
  N7: S7.Pin_1, S7.Pin_2, R7.Pin_1, ARDUINO1.D8
  N8: S8.Pin_1, S8.Pin_2, R8.Pin_1, ARDUINO1.D9
  N9: S9.Pin_1, S9.Pin_2, R9.Pin_1, ARDUINO1.D10
  N10: ARDUINO1.D11, U1.DS
  N11: ARDUINO1.D12, ARDUINO1.D13, U1.SH_CP, U1.ST_CP, U2.SH_CP, U2.ST_CP, U3.SH_CP, C1.-
  N12: U1.Q1, R10.Pin_0
  N13: U1.Q3, R13.Pin_0
  N14: U1.Q4, R12.Pin_0
  N15: U1.Q5, R14.Pin_0
  N16: U1.Q6, R15.Pin_0
  N17: U1.Q7, R16.Pin_0
  N18: U1.Q7', U2.DS
  N19: U2.Q1, R17.Pin_0
  N20: U2.Q2, R34.Pin_0
  N21: U2.Q3, R18.Pin_0
  N22: U2.Q4, R19.Pin_0
  N23: U2.Q5, R20.Pin_0
  N24: U2.Q6, R21.Pin_0
  N25: U2.Q7, R26.Pin_0
  N26: U2.Q7', U3.DS
  N27: U3.Q1, R27.Pin_0
  N28: U3.Q2, R28.Pin_0
  N29: U3.Q3, R29.Pin_0
  N30: U3.Q4, R33.Pin_0
  N31: U3.Q5, R32.Pin_0
  N32: U3.Q6, R35.Pin_0
  N33: U3.Q7, R31.Pin_0
  N34: LED1.anode, R31.Pin_1
  N35: LED7.anode, R33.Pin_1
  N36: LED11.anode, R14.Pin_1
  N37: LED12.anode, R10.Pin_1
  N38: LED13.anode, R11.Pin_1
  N39: LED14.anode, R12.Pin_1
  N40: LED21.anode, R35.Pin_1
  N41: LED22.anode, R32.Pin_1
  N42: LED16.anode, R21.Pin_1
  N43: LED19.anode, R28.Pin_1
  N44: LED20.anode, R27.Pin_1
  N45: LED17.anode, R29.Pin_1
  N46: LED18.anode, R26.Pin_1
  N47: LED4.anode, R20.Pin_1
  N48: LED2.anode, R19.Pin_1
  N49: LED15.anode, R13.Pin_1
  N50: LED6.anode, R18.Pin_1
  N51: LED23.anode, R17.Pin_1
  N52: LED24.anode, R16.Pin_1
  N53: LED25.anode, R15.Pin_1
  N54: LED26.anode, R34.Pin_1

notes:
  LEDs:
  C P A P P P P B B M N T T T T T V V V V V
  o o u r r r r s n i e 5 4 3 2 1 5 4 3 2 1
  n w t 4 3 2 1 d k
  Buttons:
  V+ V- T+ T- N M B P A

custom parts:
  Arduino Micro: Arduino Micro Microcontroller
