# Fritzing sketch ArduStomp01 (saved by Fritzing 0.7.12b)
breadboards: 3

parts:
  S1 = Pushbutton [package=THT]
  R1 = Resistor [tolerance=±5% resistance=10k package=THT]
  S2 = Pushbutton [package=THT]
  R2 = Resistor [tolerance=±5% resistance=10k package=THT]
  S3 = Pushbutton [package=THT]
  R3 = Resistor [tolerance=±5% resistance=10k package=THT]
  S4 = Pushbutton [package=THT]
  S5 = Pushbutton [package=THT]
  R5 = Resistor [tolerance=±5% resistance=10k package=THT]
  S6 = Pushbutton [package=THT]
  R6 = Resistor [tolerance=±5% resistance=10k package=THT]
  S7 = Pushbutton [package=THT]
  R7 = Resistor [tolerance=±5% resistance=10k package=THT]
  S8 = Pushbutton [package=THT]
  R8 = Resistor [tolerance=±5% resistance=10k package=THT]
  S9 = Pushbutton [package=THT]
  R9 = Resistor [tolerance=±5% resistance=10k package=THT]
  ARDUINO1 = Arduino Micro
  U1 = 74HC595 [package="DIP16 [THT]"]  # not connected
  U2 = 74HC595 [package="DIP16 [THT]"]  # not connected
  C1 = Electrolytic Capacitor [capacitance=1µF package="200 mil [THT, electrolytic]"]
  R15 = Resistor [tolerance=±5% resistance=1k package=THT]  # not connected
  R16 = Resistor [tolerance=±5% resistance=1k package=THT]  # not connected
  R17 = Resistor [tolerance=±5% resistance=1k package=THT]  # not connected
  R18 = Resistor [tolerance=±5% resistance=1k package=THT]  # not connected
  R19 = Resistor [tolerance=±5% resistance=1k package=THT]  # not connected
  R20 = Resistor [tolerance=±5% resistance=1k package=THT]  # not connected
  R21 = Resistor [tolerance=±5% resistance=1k package=THT]  # not connected
  R26 = Resistor [tolerance=±5% resistance=1k package=THT]  # not connected
  R27 = Resistor [tolerance=±5% resistance=1k package=THT]  # not connected
  R28 = Resistor [tolerance=±5% resistance=1k package=THT]  # not connected
  R29 = Resistor [tolerance=±5% resistance=1k package=THT]  # not connected
  R30 = Resistor [tolerance=±5% resistance=10k package=THT]
  R31 = Resistor [tolerance=±5% resistance=1k package=THT]  # not connected
  R32 = Resistor [tolerance=±5% resistance=1k package=THT]  # not connected
  R33 = Resistor [tolerance=±5% resistance=1k package=THT]  # not connected
  R34 = Resistor [tolerance=±5% resistance=1k package=THT]  # not connected
  R35 = Resistor [tolerance=±5% resistance=1k package=THT]  # not connected
  LED27 = yellow LED - 5mm [package="5 mm [THT]"]
  LED28 = yellow LED - 5mm [package="5 mm [THT]"]
  LED29 = Red LED - 5mm [package="5 mm [THT]"]
  LED30 = Red LED - 5mm [package="5 mm [THT]"]
  LED31 = Red LED - 5mm [package="5 mm [THT]"]
  LED33 = yellow LED - 5mm [package="5 mm [THT]"]
  LED32 = yellow LED - 5mm [package="5 mm [THT]"]
  LED35 = white LED - 5mm [package="5 mm [THT]"]
  LED39 = yellow LED - 5mm [package="5 mm [THT]"]
  LED36 = yellow LED - 5mm [package="5 mm [THT]"]
  LED37 = yellow LED - 5mm [package="5 mm [THT]"]
  LED38 = yellow LED - 5mm [package="5 mm [THT]"]
  LED41 = Red LED - 5mm [package="5 mm [THT]"]
  LED42 = Blue LED - 5mm [package="5 mm [THT]"]
  LED40 = green LED - 5mm [package="5 mm [THT]"]
  LED43 = green LED - 5mm [package="5 mm [THT]"]
  microSD1 = MicroSD Breakout
  Part1 = Bluetooth Mate Silver
  S10 = Pushbutton [package=THT]
  R36 = Resistor [tolerance=±5% resistance=10k package=THT]

nets:
  N1: S1.Pin_1, S1.Pin_2, R1.Pin_1, ARDUINO1.D2
  5V: S1.Pin_3, S1.Pin_4, S2.Pin_3, S2.Pin_4, S3.Pin_3, S3.Pin_4, S4.Pin_3, S4.Pin_4, S5.Pin_3, S5.Pin_4, S6.Pin_3, S6.Pin_4, S7.Pin_3, S7.Pin_4, S8.Pin_3, S8.Pin_4, S9.Pin_3, S9.Pin_4, ARDUINO1.5V, microSD1.5V, Part1.VCC
  GND: R1.Pin_0, R2.Pin_0, R3.Pin_0, R5.Pin_0, R7.Pin_0, R8.Pin_0, R9.Pin_0, ARDUINO1.GND#31, R30.Pin_0, microSD1.GND, Part1.GND, R36.Pin_0
  N2: S2.Pin_1, S2.Pin_2, R2.Pin_1, ARDUINO1.D3
  N3: S3.Pin_1, S3.Pin_2, R3.Pin_1, ARDUINO1.D4
  N4: S4.Pin_1, S4.Pin_2, ARDUINO1.D5, R30.Pin_1
  N5: S5.Pin_1, S5.Pin_2, R5.Pin_1, ARDUINO1.D6
  N6: S6.Pin_1, S6.Pin_2, R6.Pin_1, ARDUINO1.D7
  N7: S7.Pin_1, S7.Pin_2, R7.Pin_1, ARDUINO1.D8
  N8: S8.Pin_1, S8.Pin_2, R8.Pin_1, ARDUINO1.D9
  N9: S9.Pin_1, S9.Pin_2, R9.Pin_1, ARDUINO1.D11
  N10: ARDUINO1.MOSI, microSD1.DI
  N11: ARDUINO1.TX, Part1.RX_5V
  N12: ARDUINO1.RX, Part1.TX_5V
  N13: ARDUINO1.D10, microSD1.CS
  N14: ARDUINO1.D12, S10.Pin_1, S10.Pin_2, R36.Pin_1
  N15: ARDUINO1.D13, C1.-
  N16: ARDUINO1.MISO, microSD1.DO
  N17: ARDUINO1.SCK, microSD1.CLK
  N18: LED27.cathode, LED28.cathode, LED29.cathode, LED30.cathode, LED31.cathode, LED33.cathode, LED32.cathode, LED35.cathode, LED39.cathode, LED36.cathode, LED37.cathode, LED38.cathode, LED41.cathode, LED42.cathode, LED40.cathode, LED43.cathode
  N19: S10.Pin_3, S10.Pin_4

notes:
  LEDs:
  MSB,
  Unsigned int :
  Byte 2: || Byte 1:
  7 6 5 4 3 2 1 0 || 7 6 5 4 0 1 2 3
  C P T T T V V V || A P P P N M B B
  o o 2 1 0 2 1 0|| u r r r 1 0
  n w t 2 1 0
  Buttons:
  V+ V- T+ T- N M B P A S
  ArduConf00::nbLeds[] =
  {1, // neck led
  1, // middle led
  2, // bridge leds 00 11 10 !!
  3, // presets leds in binary !!!
  1, // auto led
  // end of first byte
  3, // vol leds in binary !!!
  3, // tone leds in binary !!!
  1, // power led
  1}; // connect led
  // end of second byte!

custom parts:
  Arduino Micro: Arduino Micro Microcontroller
  MicroSD Breakout: 5V-ready microSD Breakout with Level Shifter
