# Fritzing sketch ArduStomp02 (saved by Fritzing 0.8.3b)
circuit board: 16.9333cm x 5.64444cm
breadboards: 3

parts:
  S1 = Pushbutton [package=THT]
  R1 = Resistor [tolerance=±5% resistance=10k package=THT]
  S2 = Pushbutton [package=THT]
  R2 = Resistor [tolerance=±5% resistance=10k package=THT]
  S3 = Pushbutton [package=THT]
  R3 = Resistor [tolerance=±5% resistance=10k package=THT]
  S4 = Pushbutton [package=THT]
  S5 = Pushbutton [package=THT]
  R5 = Resistor [tolerance=±5% resistance=10k package=THT]
  S6 = Pushbutton [package=THT]
  R6 = Resistor [tolerance=±5% resistance=10k package=THT]
  S7 = Pushbutton [package=THT]
  R7 = Resistor [tolerance=±5% resistance=10k package=THT]
  S8 = Pushbutton [package=THT]
  R8 = Resistor [tolerance=±5% resistance=10k package=THT]
  S9 = Pushbutton [package=THT]
  R9 = Resistor [tolerance=±5% resistance=10k package=THT]
  ARDUINO1 = Arduino Micro
  U1 = 74HC595 [package="DIP16 [THT]"]
  U2 = 74HC595 [package="DIP16 [THT]"]
  C1 = Electrolytic Capacitor [capacitance=1µF package="200 mil [THT, electrolytic]"]
  R15 = Resistor [tolerance=±5% resistance=1k package=THT]
  R16 = Resistor [tolerance=±5% resistance=1k package=THT]
  R17 = Resistor [tolerance=±5% resistance=1k package=THT]
  R18 = Resistor [tolerance=±5% resistance=1k package=THT]
  R19 = Resistor [tolerance=±5% resistance=1k package=THT]
  R20 = Resistor [tolerance=±5% resistance=1k package=THT]
  R21 = Resistor [tolerance=±5% resistance=1k package=THT]
  R26 = Resistor [tolerance=±5% resistance=1k package=THT]
  R27 = Resistor [tolerance=±5% resistance=1k package=THT]
  R28 = Resistor [tolerance=±5% resistance=1k package=THT]
  R29 = Resistor [tolerance=±5% resistance=1k package=THT]
  R30 = Resistor [tolerance=±5% resistance=10k package=THT]
  R31 = Resistor [tolerance=±5% resistance=1k package=THT]
  R32 = Resistor [tolerance=±5% resistance=1k package=THT]
  R33 = Resistor [tolerance=±5% resistance=1k package=THT]
  R34 = Resistor [tolerance=±5% resistance=1k package=THT]
  R35 = Resistor [tolerance=±5% resistance=1k package=THT]
  LED29 = Red LED - 5mm [package="5 mm [THT]"]
  LED30 = Red LED - 5mm [package="5 mm [THT]"]
  LED31 = Red LED - 5mm [package="5 mm [THT]"]
  LED33 = yellow LED - 5mm [package="5 mm [THT]"]
  LED32 = yellow LED - 5mm [package="5 mm [THT]"]
  LED35 = white LED - 5mm [package="5 mm [THT]"]
  LED39 = yellow LED - 5mm [package="5 mm [THT]"]
  LED41 = Red LED - 5mm [package="5 mm [THT]"]
  LED42 = Blue LED - 5mm [package="5 mm [THT]"]
  LED40 = green LED - 5mm [package="5 mm [THT]"]
  LED43 = green LED - 5mm [package="5 mm [THT]"]
  microSD1 = MicroSD Breakout
  Part1 = Bluetooth Mate Silver
  S10 = Pushbutton [package=THT]
  R36 = Resistor [tolerance=±5% resistance=10k package=THT]
  LED38 = green LED - 5mm [package="5 mm [THT]"]
  LED37 = green LED - 5mm [package="5 mm [THT]"]
  LED36 = green LED - 5mm [package="5 mm [THT]"]
  LED44 = Blue LED - 5mm [package="5 mm [THT]"]
  LED45 = Red LED - 5mm [package="5 mm [THT]"]

nets (from the schematic view):
  N1: S1.Pin_1, S1.Pin_2, R1.Pin_1, ARDUINO1.D2
  N2: S1.Pin_3, S1.Pin_4
  GND: R1.Pin_0, R2.Pin_0, R3.Pin_0, R5.Pin_0, R6.Pin_0, R7.Pin_0, R8.Pin_0, R9.Pin_0, ARDUINO1.GND#31, U1.OE, U2.OE, C1.+, R30.Pin_0, LED29.cathode, LED30.cathode, LED31.cathode, LED33.cathode, LED32.cathode, LED35.cathode, LED39.cathode, LED41.cathode, LED42.cathode, LED40.cathode, LED43.cathode, microSD1.GND, Part1.GND, R36.Pin_0, LED38.cathode, LED37.cathode, LED36.cathode, LED44.cathode, LED45.cathode
  N3: S2.Pin_1, S2.Pin_2, ARDUINO1.D3
  N4: S2.Pin_3, S2.Pin_4
  N5: S3.Pin_1, S3.Pin_2, R3.Pin_1, ARDUINO1.D4
  N6: S3.Pin_3, S3.Pin_4
  N7: S4.Pin_1, S4.Pin_2, ARDUINO1.D5, R30.Pin_1
  N8: S4.Pin_3, S4.Pin_4
  N9: S5.Pin_1, S5.Pin_2
  N10: S5.Pin_3, S5.Pin_4
  N11: S6.Pin_1, S6.Pin_2, R6.Pin_1, ARDUINO1.D7
  N12: S6.Pin_3, S6.Pin_4
  N13: S7.Pin_1, S7.Pin_2, R7.Pin_1, ARDUINO1.D8
  N14: S7.Pin_3, S7.Pin_4
  N15: S8.Pin_1, S8.Pin_2, R8.Pin_1, ARDUINO1.D9
  N16: S8.Pin_3, S8.Pin_4
  N17: S9.Pin_1, S9.Pin_2, R9.Pin_1, ARDUINO1.D11
  N18: S9.Pin_3, S9.Pin_4
  N19: ARDUINO1.MOSI, U1.DS, microSD1.DI
  N20: ARDUINO1.TX, Part1.RX_5V
  N21: ARDUINO1.RX, Part1.TX_5V
  N22: ARDUINO1.D10, microSD1.CS
  N23: ARDUINO1.D12, S10.Pin_1, S10.Pin_2, R36.Pin_1
  N24: ARDUINO1.D13, U1.ST_CP, U2.ST_CP, C1.-
  N25: ARDUINO1.MISO, microSD1.DO
  N26: ARDUINO1.SCK, U1.SH_CP, U2.SH_CP, microSD1.CLK
  N27: U1.Q1, R27.Pin_0
  N28: U1.Q2, R18.Pin_0
  N29: U1.Q3, R19.Pin_0
  N30: U1.Q4, R21.Pin_0
  N31: U1.Q5, R32.Pin_0
  N32: U1.Q6, R34.Pin_0
  N33: U1.Q7, R28.Pin_0
  N34: U1.Q7', U2.DS
  N35: U1.Q0, R26.Pin_0
  N36: U2.Q1, R33.Pin_0
  N37: U2.Q2, R20.Pin_0
  N38: U2.Q3, R15.Pin_0
  N39: U2.Q4, R16.Pin_0
  N40: U2.Q5, R17.Pin_0
  N41: U2.Q6, R35.Pin_0
  N42: U2.Q7, R31.Pin_0
  N43: U2.Q0, R29.Pin_0
  N44: R15.Pin_1, LED33.anode
  N45: R16.Pin_1, LED39.anode
  N46: R18.Pin_1, LED44.anode
  N47: R19.Pin_1, LED42.anode
  N48: R20.Pin_1, LED32.anode
  N49: R21.Pin_1, LED45.anode
  N50: R26.Pin_1, LED43.anode
  N51: R27.Pin_1, LED40.anode
  N52: R28.Pin_1, LED36.anode
  N53: R29.Pin_1, LED37.anode
  N54: R31.Pin_1, LED31.anode
  N55: R32.Pin_1, LED41.anode
  N56: R33.Pin_1, LED38.anode
  N57: R34.Pin_1, LED35.anode
  N58: R35.Pin_1, LED29.anode
  N59: S10.Pin_3, S10.Pin_4

notes:
  LEDs:
  MSB,
  Unsigned int :
  Byte 2: || Byte 1:
  7 6 5 4 3 2 1 0 || 7 6 0 1 3 2 5 4
  V V V T T T P P || P A N N M M B B
  2 1 0 2 1 0 2 1 || 0 0 1 0 1 0 1 0
  Buttons:
  V+ V- T+ T- N M B P A S
  ArduConf00::nbLeds[] =
  {2, // neck led
  2, // middle led
  2, // bridge leds 00 11 10 !!
  1, // auto led
  3, // 1st of the presets leds
  // end of first byte
  // 2 more presets leds
  3, // tone leds in binary !!!
  3} // vol leds in binary !!!
  ; // end of second byte!

custom parts:
  Arduino Micro: Arduino Micro Microcontroller
  MicroSD Breakout: 5V-ready microSD Breakout with Level Shifter
