# Fritzing sketch ArduStompPCB02 (saved by Fritzing 0.8.3b)
circuit board: 10.7439cm x 9.43453cm
breadboards: 1

parts:
  Arduino_MICRO = Arduino Micro
  Shift-00 = SHIFT REGISTER [package=dil16]
  9v_in = female pin header, 2 pins [form="♀ (female)"]
  5v_GND_out = female pin header, 2 pins [form="♀ (female)"]
  R00 = Resistor [tolerance=±5% resistance=1k package=THT]
  R01 = Resistor [tolerance=±5% resistance=1k package=THT]
  R02 = Resistor [tolerance=±5% resistance=1k package=THT]
  R03 = Resistor [tolerance=±5% resistance=1k package=THT]
  R04 = Resistor [tolerance=±5% resistance=1k package=THT]
  R05 = Resistor [tolerance=±5% resistance=1k package=THT]
  R06 = Resistor [tolerance=±5% resistance=1k package=THT]
  R07 = Resistor [tolerance=±5% resistance=1k package=THT]
  R17 = Resistor [tolerance=±5% resistance=10k package=THT]
  R18 = Resistor [tolerance=±5% resistance=10k package=THT]
  R19 = Resistor [tolerance=±5% resistance=10k package=THT]
  R20 = Resistor [tolerance=±5% resistance=10k package=THT]
  R21 = Resistor [tolerance=±5% resistance=10k package=THT]
  R22 = Resistor [tolerance=±5% resistance=10k package=THT]
  R23 = Resistor [tolerance=±5% resistance=10k package=THT]
  R24 = Resistor [tolerance=±5% resistance=10k package=THT]
  R25 = Resistor [tolerance=±5% resistance=10k package=THT]
  R26 = Resistor [tolerance=±5% resistance=10k package=THT]
  Shift-01 = SHIFT REGISTER [package=dil16]
  R14 = Resistor [tolerance=±5% resistance=1k package=THT]
  R10 = Resistor [tolerance=±5% resistance=1k package=THT]
  R09 = Resistor [tolerance=±5% resistance=1k package=THT]
  R12 = Resistor [tolerance=±5% resistance=1k package=THT]
  R13 = Resistor [tolerance=±5% resistance=1k package=THT]
  R15 = Resistor [tolerance=±5% resistance=1k package=THT]
  R08 = Resistor [tolerance=±5% resistance=1k package=THT]
  R11 = Resistor [tolerance=±5% resistance=1k package=THT]
  Bluetooth = male pin header, 6 pins [form="♂ (male)"]
  Switches = female pin header, 10 pins [form="♀ (female)"]
  LED-01 = female pin header, 8 pins [form="♀ (female)"]
  SD_card = male pin header, 8 pins [form="♂ (male)"]
  LED-00 = female pin header, 8 pins [form="♀ (female)"]

nets:
  N1: Arduino_MICRO.MOSI, Shift-00.SER, SD_card.pin3
  N2: Arduino_MICRO.TX, Bluetooth.pin5
  N3: Arduino_MICRO.RX, Bluetooth.pin4
  GND: Arduino_MICRO.GND#6, Shift-00.GND, Shift-00.G, 5v_GND_out.pin2, R17.Pin_1, R18.Pin_1, R19.Pin_1, R20.Pin_1, R21.Pin_1, R22.Pin_1, R23.Pin_1, R24.Pin_1, R25.Pin_1, R26.Pin_1, Shift-01.GND, Shift-01.G, SD_card.pin6
  N4: Arduino_MICRO.D2, R17.Pin_0, Switches.pin1
  N5: Arduino_MICRO.D3, R18.Pin_0, Switches.pin2
  N6: Arduino_MICRO.D4, R19.Pin_0, Switches.pin3
  N7: Arduino_MICRO.D5, R20.Pin_0, Switches.pin4
  N8: Arduino_MICRO.D6, R21.Pin_0, Switches.pin5
  N9: Arduino_MICRO.D7, R22.Pin_0, Switches.pin6
  N10: Arduino_MICRO.D8, R23.Pin_0, Switches.pin7
  N11: Arduino_MICRO.D9, R24.Pin_0, Switches.pin8
  N12: Arduino_MICRO.D10, SD_card.pin2
  N13: Arduino_MICRO.D11, R25.Pin_0, Switches.pin9
  N14: Arduino_MICRO.D12, R26.Pin_0, Switches.pin10
  N15: Arduino_MICRO.D13, Shift-00.RCK, Shift-01.RCK
  VCC: Arduino_MICRO.5V, Shift-00.SCL, Shift-00.VCC, 5v_GND_out.pin1, Shift-01.SCL, Shift-01.VCC, Bluetooth.pin2, SD_card.pin8
  N16: Arduino_MICRO.GND#31, 9v_in.pin1, Bluetooth.pin3
  N17: Arduino_MICRO.VIN, 9v_in.pin2
  N18: Arduino_MICRO.MISO, SD_card.pin4
  N19: Arduino_MICRO.SCK, Shift-00.SCK, Shift-01.SCK, SD_card.pin5
  N20: Shift-00.QB, R01.Pin_0
  N21: Shift-00.QC, R02.Pin_0
  N22: Shift-00.QD, R03.Pin_0
  N23: Shift-00.QE, R04.Pin_0
  N24: Shift-00.QF, R05.Pin_0
  N25: Shift-00.QG, R06.Pin_0
  N26: Shift-00.QH, R07.Pin_0
  N27: Shift-00.QH*, Shift-01.SER
  N28: Shift-00.QA, R00.Pin_0
  N29: R00.Pin_1, LED-00.pin8
  N30: R01.Pin_1, LED-00.pin7
  N31: R02.Pin_1, LED-00.pin6
  N32: R03.Pin_1, LED-00.pin5
  N33: R04.Pin_1, LED-00.pin4
  N34: R05.Pin_1, LED-00.pin3
  N35: R06.Pin_1, LED-00.pin2
  N36: R07.Pin_1, LED-00.pin1
  N37: Shift-01.QB, R09.Pin_0
  N38: Shift-01.QC, R10.Pin_0
  N39: Shift-01.QD, R11.Pin_0
  N40: Shift-01.QE, R12.Pin_0
  N41: Shift-01.QF, R13.Pin_0
  N42: Shift-01.QG, R14.Pin_0
  N43: Shift-01.QH, R15.Pin_0
  N44: Shift-01.QA, R08.Pin_0
  N45: R14.Pin_1, LED-01.pin2
  N46: R10.Pin_1, LED-01.pin6
  N47: R09.Pin_1, LED-01.pin7
  N48: R12.Pin_1, LED-01.pin4
  N49: R13.Pin_1, LED-01.pin3
  N50: R15.Pin_1, LED-01.pin1
  N51: R08.Pin_1, LED-01.pin8
  N52: R11.Pin_1, LED-01.pin5

notes:
  ArduGuitar
  ArduStomp
  AREF
  MISO
  GND
  A0
  A4
  A5
  SCK
  3V3
  NC
  A2
  VIN
  A3
  RST
  13
  A1
  5V
  04
  12
  SS
  MOSI
  TX
  05
  RX
  10
  06
  08
  02
  07
  03
  09
  11
  RTS-O
  VCC
  TX-O
  RX-I
  CTS-I
  -VOL
  PRESET
  -TONE
  NECK
  +VOL
  SAVE
  +TONE
  AUTO
  MIDDLE
  BRIDGE
  T0
  T2
  P1
  V0
  V2
  T1
  V1
  P2
  N0
  M1
  M0
  B1
  N1
  B0
  P0
  9V
  CLK
  CS
  DO
  CD
  DI

custom parts:
  Arduino Micro: Arduino Micro Microcontroller
