# Fritzing sketch ArduStomp02schematic (saved by Fritzing 0.8.3b)
breadboards: 1

parts:
  Part1 = Bluetooth Mate Silver
  ARDUINO1 = Arduino Micro
  microSD1 = MicroSD Breakout
  U1 = 74HC595 [package="DIP16 [THT]"]
  U2 = 74HC595 [package="DIP16 [THT]"]
  JACK1 = 2.1mm DC Barrel Jack
  C1 = Electrolytic Capacitor [capacitance=1μF package="0405 [SMD, electrolytic]"]
  R1 = Resistor [tolerance=±5% resistance=10k package=THT]
  R2 = Resistor [tolerance=±5% resistance=10k package=THT]
  R3 = Resistor [tolerance=±5% resistance=10k package=THT]
  R4 = Resistor [tolerance=±5% resistance=10k package=THT]
  R5 = Resistor [tolerance=±5% resistance=10k package=THT]
  R6 = Resistor [tolerance=±5% resistance=10k package=THT]
  R7 = Resistor [tolerance=±5% resistance=10k package=THT]
  R8 = Resistor [tolerance=±5% resistance=10k package=THT]
  R9 = Resistor [tolerance=±5% resistance=10k package=THT]
  R10 = Resistor [tolerance=±5% resistance=10k package=THT]
  S1 = Pushbutton [part_number="Vol +" package="[THT]"]
  S2 = Pushbutton [part_number="Vol -" package="[THT]"]
  S3 = Pushbutton [part_number="Tone -" package="[THT]"]
  S4 = Pushbutton [part_number="Tone +" package="[THT]"]
  S5 = Pushbutton [part_number=Bridge package="[THT]"]
  S6 = Pushbutton [part_number=Neck package="[THT]"]
  S7 = Pushbutton [part_number=Presets package="[THT]"]
  S8 = Pushbutton [part_number=Middle package="[THT]"]
  S9 = Pushbutton [part_number=Save package="[THT]"]
  S10 = Pushbutton [part_number=Auto package="[THT]"]
  R11 = Resistor [tolerance=±5% resistance=1k package=THT]
  R12 = Resistor [tolerance=±5% resistance=1k package=THT]
  R13 = Resistor [tolerance=±5% resistance=1k package=THT]
  R14 = Resistor [tolerance=±5% resistance=1k package=THT]
  R15 = Resistor [tolerance=±5% resistance=1k package=THT]
  R16 = Resistor [tolerance=±5% resistance=1k package=THT]
  R17 = Resistor [tolerance=±5% resistance=1k package=THT]
  R18 = Resistor [tolerance=±5% resistance=1k package=THT]
  R19 = Resistor [tolerance=±5% resistance=1k package=THT]
  R20 = Resistor [tolerance=±5% resistance=1k package=THT]
  R21 = Resistor [tolerance=±5% resistance=1k package=THT]
  R22 = Resistor [tolerance=±5% resistance=1k package=THT]
  R23 = Resistor [tolerance=±5% resistance=1k package=THT]
  R24 = Resistor [tolerance=±5% resistance=1k package=THT]
  R25 = Resistor [tolerance=±5% resistance=1k package=THT]
  R26 = Resistor [tolerance=±5% resistance=1k package=THT]
  LED1 = LED - 5mm [color="Red (633nm)" part_number="Vol 2" package="5 mm [THT]"]
  LED2 = LED - 5mm [color="Red (633nm)" part_number="Vol 1" package="5 mm [THT]"]
  LED3 = LED - 5mm [color="Red (633nm)" part_number="Vol 0" package="5 mm [THT]"]
  LED4 = LED - 5mm [color="Red (633nm)" part_number="Bridge 1" package="5 mm [THT]"]
  LED5 = LED - 5mm [color="Yellow (592nm)" part_number="Bridge 0" package="5 mm [THT]"]
  LED6 = LED - 5mm [color="Yellow (595nm)" part_number="Tone 1" package="5 mm [THT]"]
  LED7 = LED - 5mm [color="Yellow (595nm)" part_number="Tone 0" package="5 mm [THT]"]
  LED8 = LED - 5mm [color="Yellow (595nm)" part_number="Tone 2" package="5 mm [THT]"]
  LED9 = LED - 5mm [color="Green (570nm)" part_number="Neck 0" package="5 mm [THT]"]
  LED10 = LED - 5mm [color="Green (570nm)" part_number="Neck 1" package="5 mm [THT]"]
  LED11 = LED - 5mm [color="Green (570nm)" part_number="Preset 1" package="5 mm [THT]"]
  LED12 = LED - 5mm [color="Green (570nm)" part_number="Preset 0" package="5 mm [THT]"]
  LED13 = LED - 5mm [color="Green (570nm)" part_number="Preset 2" package="5 mm [THT]"]
  LED14 = LED - 5mm [color="White (4500K)" part_number="Aurto 0" package="5 mm [THT]"]
  LED15 = LED - 5mm [color="Blue (525nm)" part_number="Middle 0" package="5 mm [THT]"]
  LED16 = LED - 5mm [color="Blue (525nm)" part_number="Middle 1" package="5 mm [THT]"]

nets:
  N1: Part1.RX_5V, ARDUINO1.TX
  N2: Part1.TX_5V, ARDUINO1.RX
  VCC: Part1.VCC, ARDUINO1.5V, microSD1.5V, U1.MR, U1.VCC, U2.MR, U2.VCC, S1.Pin_1, S2.Pin_1, S2.Pin_2, S3.Pin_1, S3.Pin_2, S4.Pin_1, S4.Pin_2, S5.Pin_1, S5.Pin_2, S6.Pin_1, S6.Pin_2, S7.Pin_1, S7.Pin_2, S8.Pin_1, S8.Pin_2, S9.Pin_1, S9.Pin_2, S10.Pin_1, S10.Pin_2
  GND: Part1.GND, ARDUINO1.GND, microSD1.GND, U1.GND, U1.OE, U2.GND, U2.OE, JACK1.center, C1.-, R1.Pin_0, R2.Pin_0, R3.Pin_0, R4.Pin_0, R5.Pin_0, R6.Pin_0, R7.Pin_0, R8.Pin_0, R9.Pin_0, R10.Pin_0, LED1.cathode, LED2.cathode, LED3.cathode, LED4.cathode, LED5.cathode, LED6.cathode, LED7.cathode, LED8.cathode, LED9.cathode, LED10.cathode, LED11.cathode, LED12.cathode, LED13.cathode, LED14.cathode, LED15.cathode, LED16.cathode
  N3: ARDUINO1.MOSI, microSD1.DI, U1.DS
  N4: ARDUINO1.D2, R1.Pin_1, S9.Pin_3, S9.Pin_4
  N5: ARDUINO1.D3, R2.Pin_1, S10.Pin_3, S10.Pin_4
  N6: ARDUINO1.D4, R3.Pin_1, S7.Pin_3, S7.Pin_4
  N7: ARDUINO1.D5, R5.Pin_1, S5.Pin_3, S5.Pin_4
  N8: ARDUINO1.D6, R6.Pin_1, S8.Pin_3, S8.Pin_4
  N9: ARDUINO1.D7, R4.Pin_1, S6.Pin_3, S6.Pin_4
  N10: ARDUINO1.D8, R8.Pin_1, S3.Pin_3, S3.Pin_4
  N11: ARDUINO1.D9, R7.Pin_1, S4.Pin_3, S4.Pin_4
  N12: ARDUINO1.D10, microSD1.CS
  N13: ARDUINO1.D11, R9.Pin_1, S2.Pin_3, S2.Pin_4
  N14: ARDUINO1.D12, R10.Pin_1, S1.Pin_3, S1.Pin_4
  N15: ARDUINO1.D13, U1.ST_CP, U2.ST_CP, C1.+
  N16: ARDUINO1.VIN, JACK1.sleeve
  N17: ARDUINO1.MISO, microSD1.DO
  N18: ARDUINO1.SCK, microSD1.CLK, U1.SH_CP, U2.SH_CP
  N19: U1.Q1, R22.Pin_0
  N20: U1.Q2, R26.Pin_0
  N21: U1.Q3, R23.Pin_0
  N22: U1.Q4, R19.Pin_0
  N23: U1.Q5, R21.Pin_0
  N24: U1.Q6, R24.Pin_0
  N25: U1.Q7, R25.Pin_0
  N26: U1.Q7', U2.DS
  N27: U1.Q0, R20.Pin_0
  N28: U2.Q1, R15.Pin_0
  N29: U2.Q2, R17.Pin_0
  N30: U2.Q3, R18.Pin_0
  N31: U2.Q4, R13.Pin_0
  N32: U2.Q5, R14.Pin_0
  N33: U2.Q6, R12.Pin_0
  N34: U2.Q7, R11.Pin_0
  N35: U2.Q0, R16.Pin_0
  N36: R11.Pin_1, LED1.anode
  N37: R12.Pin_1, LED2.anode
  N38: R13.Pin_1, LED8.anode
  N39: R14.Pin_1, LED3.anode
  N40: R15.Pin_1, LED13.anode
  N41: R16.Pin_1, LED11.anode
  N42: R17.Pin_1, LED7.anode
  N43: R18.Pin_1, LED6.anode
  N44: R19.Pin_1, LED9.anode
  N45: R20.Pin_1, LED5.anode
  N46: R21.Pin_1, LED10.anode
  N47: R22.Pin_1, LED4.anode
  N48: R23.Pin_1, LED16.anode
  N49: R24.Pin_1, LED14.anode
  N50: R25.Pin_1, LED12.anode
  N51: R26.Pin_1, LED15.anode

custom parts:
  Arduino Micro: Arduino Micro Microcontroller
  MicroSD Breakout: 5V-ready microSD Breakout with Level Shifter
  2.1mm DC Barrel Jack: 2.1mm DC Barrel Jack with Thru-Hole Connectors (breadboardable)
