# Fritzing sketch ArduStompPCB0OLD (saved by Fritzing 0.8.3b)
circuit board: 10.74cm x 9.43453cm
breadboards: 2

parts:
  Shift-01 = SHIFT REGISTER [package=dil16]
  R08 = Resistor [tolerance=±5% resistance=1k package=THT]
  R22 = Resistor [tolerance=±5% resistance=10k package=THT]
  LED-01 = male pin header, 8 pins [form="♂ (male)"]
  R10 = Resistor [tolerance=±5% resistance=1k package=THT]
  R18 = Resistor [tolerance=±5% resistance=10k package=THT]
  R13 = Resistor [tolerance=±5% resistance=1k package=THT]
  LED-00 = male pin header, 8 pins [form="♂ (male)"]
  R25 = Resistor [tolerance=±5% resistance=10k package=THT]
  5v_GND_OUT = male pin header, 2 pins [form="♂ (male)"]
  Arduino_MICRO_(digital) = female pin header, 17 pins [form="♀ (female)"]
  R00 = Resistor [tolerance=±5% resistance=1k package=THT]
  R06 = Resistor [tolerance=±5% resistance=1k package=THT]
  R19 = Resistor [tolerance=±5% resistance=10k package=THT]
  Shift-00 = SHIFT REGISTER [package=dil16]
  R23 = Resistor [tolerance=±5% resistance=10k package=THT]
  R03 = Resistor [tolerance=±5% resistance=1k package=THT]
  R17 = Resistor [tolerance=±5% resistance=10k package=THT]
  R14 = Resistor [tolerance=±5% resistance=1k package=THT]
  R05 = Resistor [tolerance=±5% resistance=1k package=THT]
  R12 = Resistor [tolerance=±5% resistance=1k package=THT]
  9v_IN = male pin header, 2 pins [form="♂ (male)"]
  Switches = male pin header, 10 pins [form="♂ (male)"]
  Bluetooth = female pin header, 6 pins [form="♀ (female)"]
  Arduino_MICRO_(analog) = female pin header, 17 pins [form="♀ (female)"]
  R02 = Resistor [tolerance=±5% resistance=1k package=THT]
  R07 = Resistor [tolerance=±5% resistance=1k package=THT]
  R09 = Resistor [tolerance=±5% resistance=1k package=THT]
  R16 = Resistor [tolerance=±5% resistance=10k package=THT]
  R04 = Resistor [tolerance=±5% resistance=1k package=THT]
  SD_card = male pin header, 8 pins [form="♂ (male)"]
  R01 = Resistor [tolerance=±5% resistance=1k package=THT]
  R22_2 = Resistor [tolerance=±5% resistance=10k package=THT]
  R11 = Resistor [tolerance=±5% resistance=1k package=THT]
  R15 = Resistor [tolerance=±5% resistance=1k package=THT]
  R24 = Resistor [tolerance=±5% resistance=10k package=THT]
  R21 = Resistor [tolerance=±5% resistance=10k package=THT]

nets:
  N1: Shift-01.QB, R09.Pin_0
  N2: Shift-01.QC, R10.Pin_0
  N3: Shift-01.QD, R11.Pin_0
  N4: Shift-01.QE, R12.Pin_0
  N5: Shift-01.QF, R13.Pin_0
  N6: Shift-01.QG, R14.Pin_0
  N7: Shift-01.QH, R15.Pin_0
  GND: Shift-01.GND, Shift-01.G, R22.Pin_1, R18.Pin_1, R25.Pin_1, 5v_GND_OUT.pin2, Arduino_MICRO_(digital).pin12, R19.Pin_1, Shift-00.GND, Shift-00.G, R23.Pin_1, R17.Pin_1, 9v_IN.pin1, Bluetooth.pin3, Arduino_MICRO_(analog).pin14, R16.Pin_1, SD_card.pin6, R22_2.Pin_1, R24.Pin_1, R21.Pin_1
  VCC: Shift-01.SCL, Shift-01.VCC, 5v_GND_OUT.pin1, Shift-00.SCL, Shift-00.VCC, Bluetooth.pin2, Arduino_MICRO_(analog).pin12, SD_card.pin8
  N8: Shift-01.SCK, Shift-00.SCK, Arduino_MICRO_(analog).pin17, SD_card.pin5
  N9: Shift-01.RCK, Shift-00.RCK, Arduino_MICRO_(analog).pin1
  N10: Shift-01.SER, Shift-00.QH*
  N11: Shift-01.QA, R08.Pin_0
  N12: R08.Pin_1, LED-01.pin8
  N13: R22.Pin_0, Arduino_MICRO_(digital).pin6, Switches.pin6
  N14: LED-01.pin1, R15.Pin_1
  N15: LED-01.pin2, R14.Pin_1
  N16: LED-01.pin3, R13.Pin_1
  N17: LED-01.pin4, R12.Pin_1
  N18: LED-01.pin5, R11.Pin_1
  N19: LED-01.pin6, R10.Pin_1
  N20: LED-01.pin7, R09.Pin_1
  N21: R18.Pin_0, Arduino_MICRO_(digital).pin9, Switches.pin3
  N22: LED-00.pin1, R07.Pin_1
  N23: LED-00.pin2, R06.Pin_1
  N24: LED-00.pin3, R05.Pin_1
  N25: LED-00.pin4, R04.Pin_1
  N26: LED-00.pin5, R03.Pin_1
  N27: LED-00.pin6, R02.Pin_1
  N28: LED-00.pin7, R01.Pin_1
  N29: LED-00.pin8, R00.Pin_1
  N30: R25.Pin_0, Arduino_MICRO_(digital).pin1, Switches.pin10
  N31: Arduino_MICRO_(digital).pin2, Switches.pin9, R24.Pin_0
  N32: Arduino_MICRO_(digital).pin3, SD_card.pin2
  N33: Arduino_MICRO_(digital).pin4, R23.Pin_0, Switches.pin8
  N34: Arduino_MICRO_(digital).pin5, Switches.pin7, R22_2.Pin_0
  N35: Arduino_MICRO_(digital).pin7, Switches.pin5, R21.Pin_0
  N36: Arduino_MICRO_(digital).pin8, R19.Pin_0, Switches.pin4
  N37: Arduino_MICRO_(digital).pin10, R17.Pin_0, Switches.pin2
  N38: Arduino_MICRO_(digital).pin11, Switches.pin1, R16.Pin_0
  N39: Arduino_MICRO_(digital).pin14, Bluetooth.pin4
  N40: Arduino_MICRO_(digital).pin15, Bluetooth.pin5
  N41: Arduino_MICRO_(digital).pin17, Shift-00.SER, SD_card.pin3
  N42: R00.Pin_0, Shift-00.QA
  N43: R06.Pin_0, Shift-00.QG
  N44: Shift-00.QB, R01.Pin_0
  N45: Shift-00.QC, R02.Pin_0
  N46: Shift-00.QD, R03.Pin_0
  N47: Shift-00.QE, R04.Pin_0
  N48: Shift-00.QF, R05.Pin_0
  N49: Shift-00.QH, R07.Pin_0
  N50: 9v_IN.pin2, Arduino_MICRO_(analog).pin15
  N51: Arduino_MICRO_(analog).pin16, SD_card.pin4

notes:
  ArduGuitar
  ArduStomp
  12
  11
  10
  09
  08
  07
  06
  05
  04
  03
  02
  GND
  RST
  RX
  TX
  SS
  MOSI
  A5
  SCK
  MISO
  13
  VIN
  A4
  AREF
  A3
  5V
  3V3
  A2
  A1
  NC
  A0
  RX-I
  TX-O
  VCC
  CTS-I
  RTS-O
  NECK
  +TONE
  -TONE
  -VOL
  MIDDLE
  PRESET
  AUTO
  SAVE
  BRIDGE
  T1
  V2
  N1
  T2
  V1
  M0
  N0
  T0
  P2
  B0
  P1
  P0
  B1
  V0
  M1
  9V
  CD
  DI
  CS
  DO
  CLK
  +VOL
  5V GND OUT
  SD CARD
  BLUETOOTH
  SWITCHES
  V+V-T+T- N M  B  P  A S
  GND 9V IN
  ARDUINO DIGITAL
  ARDUINO ANALOG
  SHIFT-0
  SHIFT-1
  LED-1
  LED-0
  NECK-0
  NECK-1
  MIDDLE-0
  MIDDLE-1
  BRIDGE-0
  BRIDGE-1
  PRESET-0
  PRESET-1
  PRESET-2
  TONE-1
  TONE-0
  TONE-2
  VOL-2
  VOL-0
  VOL-1
  CDCSDIDOCLKGN3V5V
  D13
  D12
  D10
  D11
  D09
  D08
  D07
  D06
  D05
  D04
  D03
  D02
  5V     3V      GND      CLK    DO     DI     CS      CD
