# Fritzing sketch ArduStompPCB03 (saved by Fritzing 0.8.3b)
circuit board: 10.7439cm x 9.43453cm
breadboards: 1

parts:
  Shift-00 = SHIFT REGISTER [package=dil16]
  9v_in = female pin header, 2 pins [form="♀ (female)"]
  5v_GND_out = female pin header, 2 pins [form="♀ (female)"]
  R00 = Resistor [tolerance=±5% resistance=1k package=THT]
  R01 = Resistor [tolerance=±5% resistance=1k package=THT]
  R02 = Resistor [tolerance=±5% resistance=1k package=THT]
  R03 = Resistor [tolerance=±5% resistance=1k package=THT]
  R04 = Resistor [tolerance=±5% resistance=1k package=THT]
  R05 = Resistor [tolerance=±5% resistance=1k package=THT]
  R06 = Resistor [tolerance=±5% resistance=1k package=THT]
  R07 = Resistor [tolerance=±5% resistance=1k package=THT]
  R17 = Resistor [tolerance=±5% resistance=10k package=THT]
  R18 = Resistor [tolerance=±5% resistance=10k package=THT]
  R19 = Resistor [tolerance=±5% resistance=10k package=THT]
  R20 = Resistor [tolerance=±5% resistance=10k package=THT]
  R21 = Resistor [tolerance=±5% resistance=10k package=THT]
  R22 = Resistor [tolerance=±5% resistance=10k package=THT]
  R23 = Resistor [tolerance=±5% resistance=10k package=THT]
  R24 = Resistor [tolerance=±5% resistance=10k package=THT]
  R25 = Resistor [tolerance=±5% resistance=10k package=THT]
  R26 = Resistor [tolerance=±5% resistance=10k package=THT]
  Shift-01 = SHIFT REGISTER [package=dil16]
  R14 = Resistor [tolerance=±5% resistance=1k package=THT]
  R10 = Resistor [tolerance=±5% resistance=1k package=THT]
  R09 = Resistor [tolerance=±5% resistance=1k package=THT]
  R12 = Resistor [tolerance=±5% resistance=1k package=THT]
  R13 = Resistor [tolerance=±5% resistance=1k package=THT]
  R15 = Resistor [tolerance=±5% resistance=1k package=THT]
  R08 = Resistor [tolerance=±5% resistance=1k package=THT]
  R11 = Resistor [tolerance=±5% resistance=1k package=THT]
  Bluetooth = male pin header, 6 pins [form="♂ (male)"]
  Switches = female pin header, 10 pins [form="♀ (female)"]
  LED-01 = female pin header, 8 pins [form="♀ (female)"]
  SD_card = male pin header, 8 pins [form="♂ (male)"]
  LED-00 = female pin header, 8 pins [form="♀ (female)"]
  part = female pin header, 17 pins [form="♀ (female)"]
  Arduino_MICRO = female pin header, 17 pins [form="♀ (female)"]

nets:
  N1: Shift-00.QB, R01.Pin_0
  N2: Shift-00.QC, R02.Pin_0
  N3: Shift-00.QD, R03.Pin_0
  N4: Shift-00.QE, R04.Pin_0
  N5: Shift-00.QF, R05.Pin_0
  N6: Shift-00.QG, R06.Pin_0
  N7: Shift-00.QH, R07.Pin_0
  GND: Shift-00.GND, Shift-00.G, 5v_GND_out.pin2, R17.Pin_1, R18.Pin_1, R19.Pin_1, R20.Pin_1, R21.Pin_1, R22.Pin_1, R23.Pin_1, R24.Pin_1, R25.Pin_1, R26.Pin_1, Shift-01.GND, Shift-01.G, SD_card.pin6, part.pin12
  N8: Shift-00.QH*, Shift-01.SER
  VCC: Shift-00.SCL, Shift-00.VCC, 5v_GND_out.pin1, Shift-01.SCL, Shift-01.VCC, Bluetooth.pin2, SD_card.pin8, Arduino_MICRO.pin12
  N9: Shift-00.SCK, Shift-01.SCK, SD_card.pin5, Arduino_MICRO.pin17
  N10: Shift-00.RCK, Shift-01.RCK, Arduino_MICRO.pin1
  N11: Shift-00.SER, SD_card.pin3, part.pin17
  N12: Shift-00.QA, R00.Pin_0
  N13: 9v_in.pin1, Bluetooth.pin3, Arduino_MICRO.pin14
  N14: 9v_in.pin2, Arduino_MICRO.pin15
  N15: R00.Pin_1, LED-00.pin8
  N16: R01.Pin_1, LED-00.pin7
  N17: R02.Pin_1, LED-00.pin6
  N18: R03.Pin_1, LED-00.pin5
  N19: R04.Pin_1, LED-00.pin4
  N20: R05.Pin_1, LED-00.pin3
  N21: R06.Pin_1, LED-00.pin2
  N22: R07.Pin_1, LED-00.pin1
  N23: R17.Pin_0, Switches.pin1, part.pin11
  N24: R18.Pin_0, Switches.pin2, part.pin10
  N25: R19.Pin_0, Switches.pin3, part.pin9
  N26: R20.Pin_0, Switches.pin4, part.pin8
  N27: R21.Pin_0, Switches.pin5, part.pin7
  N28: R22.Pin_0, Switches.pin6, part.pin6
  N29: R23.Pin_0, Switches.pin7, part.pin5
  N30: R24.Pin_0, Switches.pin8, part.pin4
  N31: R25.Pin_0, Switches.pin9, part.pin2
  N32: R26.Pin_0, Switches.pin10, part.pin1
  N33: Shift-01.QB, R09.Pin_0
  N34: Shift-01.QC, R10.Pin_0
  N35: Shift-01.QD, R11.Pin_0
  N36: Shift-01.QE, R12.Pin_0
  N37: Shift-01.QF, R13.Pin_0
  N38: Shift-01.QG, R14.Pin_0
  N39: Shift-01.QH, R15.Pin_0
  N40: Shift-01.QA, R08.Pin_0
  N41: R14.Pin_1, LED-01.pin2
  N42: R10.Pin_1, LED-01.pin6
  N43: R09.Pin_1, LED-01.pin7
  N44: R12.Pin_1, LED-01.pin4
  N45: R13.Pin_1, LED-01.pin3
  N46: R15.Pin_1, LED-01.pin1
  N47: R08.Pin_1, LED-01.pin8
  N48: R11.Pin_1, LED-01.pin5
  N49: Bluetooth.pin4, part.pin14
  N50: Bluetooth.pin5, part.pin15
  N51: SD_card.pin2, part.pin3
  N52: SD_card.pin4, Arduino_MICRO.pin16

notes:
  ArduGuitar
  ArduStomp
  12
  11
  10
  09
  08
  07
  06
  05
  04
  03
  02
  GND
  RST
  RX
  TX
  SS
  MOSI
  A5
  SCK
  MISO
  13
  VIN
  A4
  AREF
  A3
  5V
  3V3
  A2
  A1
  NC
  A0
  RX-I
  TX-O
  VCC
  CTS-I
  RTS-O
  NECK
  +TONE
  -TONE
  -VOL
  MIDDLE
  PRESET
  AUTO
  SAVE
  BRIDGE
  T1
  V2
  N1
  T2
  V1
  M0
  N0
  T0
  P2
  B0
  P1
  P0
  B1
  V0
  M1
  9V
  CD
  DI
  CS
  DO
  CLK
  +VOL
