# Fritzing sketch ArduGuitarMicro08 (saved by Fritzing 0.8.3b)
breadboards: 1

parts:
  micro = Arduino Micro
  R6 = Resistor [tolerance=±5% resistance=51k package=THT]
  R7 = Resistor [tolerance=±5% resistance=51k package=THT]
  R8 = Resistor [tolerance=±5% resistance=100 package=THT]
  R9 = Resistor [tolerance=±5% resistance=100 package=THT]
  R10 = Resistor [tolerance=±5% resistance=100 package=THT]
  R11 = Resistor [tolerance=±5% resistance=100 package=THT]
  Tone_Cap = Ceramic Capacitor [capacitance=22nF package="0603 [SMD, multilayer]"]
  R12 = Resistor [tolerance=±5% resistance=100 package=THT]
  Split_VTL = VTL5C4 [package=THT]
  Neck_VTL = VTL5C4 [package=THT]
  Bridge_VTL = VTL5C4 [package=THT]
  Middle_VTL = VTL5C4 [package=THT]
  Max_Vol_VTL = VTL5C4 [package=THT]
  Tone_VTL = VTL5C4 [package=THT]
  Vol2_VTL = VTL5C4 [package=THT]
  Vol1_VTL = VTL5C4 [package=THT]
  R5 = Resistor [tolerance=±5% resistance=51k package=THT]
  J4 = male pin header, 2 pins [form="♂ (male)"]
  J2 = female pin header, 4 pins [form="♀ (female)"]
  J3 = rounded female pin header, 2 pins [form="♀ (female rounded)"]
  J5 = rounded female pin header, 2 pins [form="♀ (female rounded)"]
  V1 = DC Power [voltage=9]
  BT = Bluetooth Mate Silver

nets (from the schematic view):
  N1: micro.TX, BT.RX_5V
  N2: micro.RX, BT.TX_5V
  N3: micro.D2, Neck_VTL.Pin_2
  N4: micro.D3, Middle_VTL.Pin_2
  N5: micro.D4, Bridge_VTL.Pin_2
  N6: micro.D5, Split_VTL.Pin_2
  N7: micro.D9, Vol1_VTL.Pin_2
  N8: micro.D10, Vol2_VTL.Pin_2
  N9: micro.D11, Tone_VTL.Pin_2
  N10: micro.D12, Max_Vol_VTL.Pin_2
  5V: micro.5V, BT.VCC
  N11: micro.GND#31, R12.Pin_1, V1.V-, BT.GND
  N12: micro.VIN, V1.V+
  N13: R6.Pin_0, R5.Pin_0
  N14: R6.Pin_1, Vol2_VTL.Pin_1
  N15: R7.Pin_0, Tone_VTL.Pin_1
  N16: R8.Pin_0, Split_VTL.Pin_1
  N17: R9.Pin_0, Bridge_VTL.Pin_1
  N18: R10.Pin_0, Middle_VTL.Pin_1
  N19: R11.Pin_0, Neck_VTL.Pin_1
  N20: Tone_Cap.0, Split_VTL.Pin_4, Vol2_VTL.Pin_4, J4.pin2, J2.pin1, J3.pin1, J5.pin1
  N21: Tone_Cap.1, Tone_VTL.Pin_4
  N22: R12.Pin_0, Max_Vol_VTL.Pin_1
  N23: Split_VTL.Pin_3, J2.pin2, J2.pin3
  N24: Neck_VTL.Pin_4, Bridge_VTL.Pin_4, Middle_VTL.Pin_4, Max_Vol_VTL.Pin_3, Vol1_VTL.Pin_3
  N25: Neck_VTL.Pin_3, J3.pin2
  N26: Bridge_VTL.Pin_3, J2.pin4
  N27: Middle_VTL.Pin_3, J5.pin2
  N28: Max_Vol_VTL.Pin_4, Tone_VTL.Pin_3, Vol2_VTL.Pin_3, Vol1_VTL.Pin_4, J4.pin1
  N29: Vol1_VTL.Pin_1, R5.Pin_1

notes:
  Bridge Middle Neck
  blue orange yellow orange
  Guitar Guitar
  out gnd
  Neck
  Middle
  Brdige
  Guitar Out GND
  Hot
  9 V
  100 Ohm
  51K Ohm

custom parts:
  Arduino Micro: Arduino Micro Microcontroller
  VTL5C4: Vactrol VTL5 C4 Optocoupler - keeps you from frying your stuff!
