# Fritzing sketch ArduGuitarMicro01 (saved by Fritzing 0.7.12b)
breadboards: 1

parts:
  ARDUINO1 = Arduino Micro
  R6 = Resistor [tolerance=±5% resistance=51k package=THT]
  R7 = Resistor [tolerance=±5% resistance=51k package=THT]  # not connected
  R8 = Resistor [tolerance=±5% resistance=100 package=THT]  # not connected
  R9 = Resistor [tolerance=±5% resistance=100 package=THT]  # not connected
  R10 = Resistor [tolerance=±5% resistance=100 package=THT]  # not connected
  R11 = Resistor [tolerance=±5% resistance=100 package=THT]  # not connected
  J2 = male pin header, 6 pins [form="♂ (male)"]  # not connected
  J3 = male pin header, 6 pins [form="♂ (male)"]  # not connected
  J4 = male pin header, 6 pins [form="♂ (male)"]  # not connected
  C1 = Ceramic Capacitor [capacitance=22nF package="0603 [SMD, multilayer]"]  # not connected
  R12 = Resistor [tolerance=±5% resistance=100 package=THT]  # not connected
  U7 = VTL5C4 [package=THT]  # not connected
  U8 = VTL5C4 [package=THT]  # not connected
  U9 = VTL5C4 [package=THT]
  U10 = VTL5C4 [package=THT]
  U11 = VTL5C4 [package=THT]
  U12 = VTL5C4 [package=THT]
  U13 = VTL5C4 [package=THT]
  U14 = VTL5C4 [package=THT]
  R5 = Resistor [tolerance=±5% resistance=51k package=THT]

nets:
  N1: ARDUINO1.D3, U10.Pin_2
  N2: ARDUINO1.D4, U9.Pin_2
  N3: ARDUINO1.D9, U14.Pin_2
  N4: ARDUINO1.D11, U12.Pin_2
  N5: ARDUINO1.D12, U11.Pin_2
  N6: R6.Pin_0, R5.Pin_0
  N7: R6.Pin_1, U13.Pin_1
  N8: U13.Pin_4, U14.Pin_3
  N9: U14.Pin_1, R5.Pin_1

notes:
  Bridge Middle Neck
  blue orange yellow orange
  Guitar Guitar
  out gnd

custom parts:
  Arduino Micro: Arduino Micro Microcontroller
  VTL5C4: Vactrol VTL5 C4 Optocoupler - keeps you from frying your stuff!
